// Logisim project ram256.circ as structural Verilog: 8 circuits, main circuit Reg4
module DLatch (
  input  d,
  input  set,
  output o
);

  wire nand_1_out, nand_2_out, nand_4_out;

  nand nand_1 (nand_1_out, d, set);
  nand nand_2 (nand_2_out, nand_1_out, set);
  nand nand_3 (o, nand_1_out, nand_4_out);
  nand nand_4 (nand_4_out, o, nand_2_out);
endmodule

module Reg4 (
  input  [3:0] data,
  input  write,
  input  read,
  output [3:0] out
);

  wire dlatch_1_o, dlatch_2_o, dlatch_3_o, dlatch_4_o;

  DLatch dlatch_1 (.d(data[0]), .set(write), .o(dlatch_1_o));
  DLatch dlatch_2 (.d(data[1]), .set(write), .o(dlatch_2_o));
  DLatch dlatch_3 (.d(data[2]), .set(write), .o(dlatch_3_o));
  DLatch dlatch_4 (.d(data[3]), .set(write), .o(dlatch_4_o));
  assign out[0] = read ? dlatch_1_o : 1'bz;  // Controlled_Buffer controlled_buffer_1
  assign out[1] = read ? dlatch_2_o : 1'bz;  // Controlled_Buffer controlled_buffer_2
  assign out[2] = read ? dlatch_3_o : 1'bz;  // Controlled_Buffer controlled_buffer_3
  assign out[3] = read ? dlatch_4_o : 1'bz;  // Controlled_Buffer controlled_buffer_4
endmodule

module Reg8 (
  input  [7:0] data,
  input  read,
  input  write,
  output [7:0] out
);

  Reg4 reg4_1 (.write(write), .read(read), .data(data[3:0]), .out(out[3:0]));
  Reg4 reg4_2 (.write(write), .read(read), .data(data[7:4]), .out(out[7:4]));
endmodule

module Enabler4 (
  input  [3:0] data,
  input  enable,
  output [3:0] out
);

  assign out[0] = enable ? data[0] : 1'bz;  // Controlled_Buffer controlled_buffer_1
  assign out[1] = enable ? data[1] : 1'bz;  // Controlled_Buffer controlled_buffer_2
  assign out[2] = enable ? data[2] : 1'bz;  // Controlled_Buffer controlled_buffer_3
  assign out[3] = enable ? data[3] : 1'bz;  // Controlled_Buffer controlled_buffer_4
endmodule

module Dec2x4 (
  input  in_1,
  input  in_2,
  output [3:0] out
);

  wire not_1_out, not_2_out;

  not not_1 (not_1_out, in_1);
  not not_2 (not_2_out, in_2);
  and and_1 (out[0], not_1_out, not_2_out);
  and and_2 (out[1], in_1, not_2_out);
  and and_3 (out[2], not_1_out, in_2);
  and and_4 (out[3], in_1, in_2);
endmodule

module Dec3x8 (
  input  in_1,
  input  in_2,
  input  in_3,
  output [7:0] out
);

  wire not_1_out, not_2_out, not_3_out;

  not not_1 (not_1_out, in_1);
  not not_2 (not_2_out, in_2);
  not not_3 (not_3_out, in_3);
  and and_1 (out[0], not_1_out, not_2_out, not_3_out);
  and and_2 (out[1], in_1, not_2_out, not_3_out);
  and and_3 (out[2], not_1_out, in_2, not_3_out);
  and and_4 (out[3], in_1, in_2, not_3_out);
  and and_5 (out[4], not_1_out, not_2_out, in_3);
  and and_6 (out[5], in_1, not_2_out, in_3);
  and and_7 (out[6], not_1_out, in_2, in_3);
  and and_8 (out[7], in_1, in_2, in_3);
endmodule

module RamCell8 (
  input  row,
  input  [7:0] data,
  input  column,
  input  read,
  input  write,
  output [7:0] data_2
);

  wire and_1_out, and_2_out, and_3_out;
  wire [7:0] reg8_1_out;

  and and_1 (and_1_out, row, column);
  and and_2 (and_2_out, read, and_1_out);
  Reg8 reg8_1 (.data(reg8_1_out), .read(and_2_out), .write(and_3_out), .out(reg8_1_out));
  and and_3 (and_3_out, and_1_out, write);
  assign reg8_1_out = write ? data : 8'bz;  // Controlled_Buffer controlled_buffer_1
  assign data_2 = read ? reg8_1_out : 8'bz;  // Controlled_Buffer controlled_buffer_2
endmodule

module Ram256 (
  input  [7:0] mar,
  input  marw,
  input  datar,
  input  dataw,
  input  [7:0] in_5,
  output [7:0] out_6
);

  wire decoder_1_out0, decoder_1_out1, decoder_1_out2, decoder_1_out3, decoder_1_out4, decoder_1_out5,
       decoder_1_out6, decoder_1_out7, decoder_1_out8, decoder_1_out9, decoder_1_out10, decoder_1_out11,
       decoder_1_out12, decoder_1_out13, decoder_1_out14, decoder_1_out15, decoder_2_out0, decoder_2_out1,
       decoder_2_out2, decoder_2_out3, decoder_2_out4, decoder_2_out5, decoder_2_out6, decoder_2_out7,
       decoder_2_out8, decoder_2_out9, decoder_2_out10, decoder_2_out11, decoder_2_out12, decoder_2_out13,
       decoder_2_out14, decoder_2_out15;
  wire [7:0] reg8_1_out;

  assign out_6 = dataw ? in_5 : 8'bz;  // Controlled_Buffer controlled_buffer_1
  Reg8 reg8_1 (.data(mar), .read(1'b1), .write(marw), .out(reg8_1_out));
  Decoder #(.select(4)) decoder_1 (
    .out0(decoder_1_out0), .out1(decoder_1_out1), .out2(decoder_1_out2), .out3(decoder_1_out3),
    .out4(decoder_1_out4), .out5(decoder_1_out5), .out6(decoder_1_out6), .out7(decoder_1_out7),
    .out8(decoder_1_out8), .out9(decoder_1_out9), .out10(decoder_1_out10), .out11(decoder_1_out11),
    .out12(decoder_1_out12), .out13(decoder_1_out13), .out14(decoder_1_out14), .out15(decoder_1_out15),
    .sel(reg8_1_out[7:4]), .en(1'b1));
  RamCell8 ramcell8_1 (
    .row(decoder_1_out0), .column(decoder_2_out0), .data(out_6), .data_2(out_6), .read(datar), .write(dataw));
  RamCell8 ramcell8_2 (
    .row(decoder_1_out1), .column(decoder_2_out0), .data(out_6), .data_2(out_6), .read(datar), .write(dataw));
  RamCell8 ramcell8_3 (
    .row(decoder_1_out2), .column(decoder_2_out0), .data(out_6), .data_2(out_6), .read(datar), .write(dataw));
  RamCell8 ramcell8_4 (
    .row(decoder_1_out3), .column(decoder_2_out0), .data(out_6), .data_2(out_6), .read(datar), .write(dataw));
  RamCell8 ramcell8_5 (
    .row(decoder_1_out4), .column(decoder_2_out0), .data(out_6), .data_2(out_6), .read(datar), .write(dataw));
  RamCell8 ramcell8_6 (
    .row(decoder_1_out5), .column(decoder_2_out0), .data(out_6), .data_2(out_6), .read(datar), .write(dataw));
  RamCell8 ramcell8_7 (
    .row(decoder_1_out6), .column(decoder_2_out0), .data(out_6), .data_2(out_6), .read(datar), .write(dataw));
  RamCell8 ramcell8_8 (
    .row(decoder_1_out7), .column(decoder_2_out0), .data(out_6), .data_2(out_6), .read(datar), .write(dataw));
  RamCell8 ramcell8_9 (
    .row(decoder_1_out8), .column(decoder_2_out0), .data(out_6), .data_2(out_6), .read(datar), .write(dataw));
  RamCell8 ramcell8_10 (
    .row(decoder_1_out9), .column(decoder_2_out0), .data(out_6), .data_2(out_6), .read(datar), .write(dataw));
  RamCell8 ramcell8_11 (
    .row(decoder_1_out10), .column(decoder_2_out0), .data(out_6), .data_2(out_6), .read(datar), .write(dataw));
  RamCell8 ramcell8_12 (
    .row(decoder_1_out11), .column(decoder_2_out0), .data(out_6), .data_2(out_6), .read(datar), .write(dataw));
  RamCell8 ramcell8_13 (
    .row(decoder_1_out12), .column(decoder_2_out0), .data(out_6), .data_2(out_6), .read(datar), .write(dataw));
  RamCell8 ramcell8_14 (
    .row(decoder_1_out13), .column(decoder_2_out0), .data(out_6), .data_2(out_6), .read(datar), .write(dataw));
  RamCell8 ramcell8_15 (
    .row(decoder_1_out14), .column(decoder_2_out0), .data(out_6), .data_2(out_6), .read(datar), .write(dataw));
  RamCell8 ramcell8_16 (
    .row(decoder_1_out15), .column(decoder_2_out0), .data(out_6), .data_2(out_6), .read(datar), .write(dataw));
  RamCell8 ramcell8_17 (
    .row(decoder_1_out0), .column(decoder_2_out1), .data(out_6), .data_2(out_6), .read(datar), .write(dataw));
  RamCell8 ramcell8_18 (
    .row(decoder_1_out1), .column(decoder_2_out1), .data(out_6), .data_2(out_6), .read(datar), .write(dataw));
  RamCell8 ramcell8_19 (
    .row(decoder_1_out2), .column(decoder_2_out1), .data(out_6), .data_2(out_6), .read(datar), .write(dataw));
  RamCell8 ramcell8_20 (
    .row(decoder_1_out3), .column(decoder_2_out1), .data(out_6), .data_2(out_6), .read(datar), .write(dataw));
  RamCell8 ramcell8_21 (
    .row(decoder_1_out4), .column(decoder_2_out1), .data(out_6), .data_2(out_6), .read(datar), .write(dataw));
  RamCell8 ramcell8_22 (
    .row(decoder_1_out5), .column(decoder_2_out1), .data(out_6), .data_2(out_6), .read(datar), .write(dataw));
  RamCell8 ramcell8_23 (
    .row(decoder_1_out6), .column(decoder_2_out1), .data(out_6), .data_2(out_6), .read(datar), .write(dataw));
  RamCell8 ramcell8_24 (
    .row(decoder_1_out7), .column(decoder_2_out1), .data(out_6), .data_2(out_6), .read(datar), .write(dataw));
  RamCell8 ramcell8_25 (
    .row(decoder_1_out8), .column(decoder_2_out1), .data(out_6), .data_2(out_6), .read(datar), .write(dataw));
  RamCell8 ramcell8_26 (
    .row(decoder_1_out9), .column(decoder_2_out1), .data(out_6), .data_2(out_6), .read(datar), .write(dataw));
  RamCell8 ramcell8_27 (
    .row(decoder_1_out10), .column(decoder_2_out1), .data(out_6), .data_2(out_6), .read(datar), .write(dataw));
  RamCell8 ramcell8_28 (
    .row(decoder_1_out11), .column(decoder_2_out1), .data(out_6), .data_2(out_6), .read(datar), .write(dataw));
  RamCell8 ramcell8_29 (
    .row(decoder_1_out12), .column(decoder_2_out1), .data(out_6), .data_2(out_6), .read(datar), .write(dataw));
  RamCell8 ramcell8_30 (
    .row(decoder_1_out13), .column(decoder_2_out1), .data(out_6), .data_2(out_6), .read(datar), .write(dataw));
  RamCell8 ramcell8_31 (
    .row(decoder_1_out14), .column(decoder_2_out1), .data(out_6), .data_2(out_6), .read(datar), .write(dataw));
  RamCell8 ramcell8_32 (
    .row(decoder_1_out15), .column(decoder_2_out1), .data(out_6), .data_2(out_6), .read(datar), .write(dataw));
  RamCell8 ramcell8_33 (
    .row(decoder_1_out0), .column(decoder_2_out2), .data(out_6), .data_2(out_6), .read(datar), .write(dataw));
  RamCell8 ramcell8_34 (
    .row(decoder_1_out1), .column(decoder_2_out2), .data(out_6), .data_2(out_6), .read(datar), .write(dataw));
  RamCell8 ramcell8_35 (
    .row(decoder_1_out2), .column(decoder_2_out2), .data(out_6), .data_2(out_6), .read(datar), .write(dataw));
  RamCell8 ramcell8_36 (
    .row(decoder_1_out3), .column(decoder_2_out2), .data(out_6), .data_2(out_6), .read(datar), .write(dataw));
  RamCell8 ramcell8_37 (
    .row(decoder_1_out4), .column(decoder_2_out2), .data(out_6), .data_2(out_6), .read(datar), .write(dataw));
  RamCell8 ramcell8_38 (
    .row(decoder_1_out5), .column(decoder_2_out2), .data(out_6), .data_2(out_6), .read(datar), .write(dataw));
  RamCell8 ramcell8_39 (
    .row(decoder_1_out6), .column(decoder_2_out2), .data(out_6), .data_2(out_6), .read(datar), .write(dataw));
  RamCell8 ramcell8_40 (
    .row(decoder_1_out7), .column(decoder_2_out2), .data(out_6), .data_2(out_6), .read(datar), .write(dataw));
  RamCell8 ramcell8_41 (
    .row(decoder_1_out8), .column(decoder_2_out2), .data(out_6), .data_2(out_6), .read(datar), .write(dataw));
  RamCell8 ramcell8_42 (
    .row(decoder_1_out9), .column(decoder_2_out2), .data(out_6), .data_2(out_6), .read(datar), .write(dataw));
  RamCell8 ramcell8_43 (
    .row(decoder_1_out10), .column(decoder_2_out2), .data(out_6), .data_2(out_6), .read(datar), .write(dataw));
  RamCell8 ramcell8_44 (
    .row(decoder_1_out11), .column(decoder_2_out2), .data(out_6), .data_2(out_6), .read(datar), .write(dataw));
  RamCell8 ramcell8_45 (
    .row(decoder_1_out12), .column(decoder_2_out2), .data(out_6), .data_2(out_6), .read(datar), .write(dataw));
  RamCell8 ramcell8_46 (
    .row(decoder_1_out13), .column(decoder_2_out2), .data(out_6), .data_2(out_6), .read(datar), .write(dataw));
  RamCell8 ramcell8_47 (
    .row(decoder_1_out14), .column(decoder_2_out2), .data(out_6), .data_2(out_6), .read(datar), .write(dataw));
  RamCell8 ramcell8_48 (
    .row(decoder_1_out15), .column(decoder_2_out2), .data(out_6), .data_2(out_6), .read(datar), .write(dataw));
  RamCell8 ramcell8_49 (
    .row(decoder_1_out0), .column(decoder_2_out3), .data(out_6), .data_2(out_6), .read(datar), .write(dataw));
  RamCell8 ramcell8_50 (
    .row(decoder_1_out1), .column(decoder_2_out3), .data(out_6), .data_2(out_6), .read(datar), .write(dataw));
  RamCell8 ramcell8_51 (
    .row(decoder_1_out2), .column(decoder_2_out3), .data(out_6), .data_2(out_6), .read(datar), .write(dataw));
  RamCell8 ramcell8_52 (
    .row(decoder_1_out3), .column(decoder_2_out3), .data(out_6), .data_2(out_6), .read(datar), .write(dataw));
  RamCell8 ramcell8_53 (
    .row(decoder_1_out4), .column(decoder_2_out3), .data(out_6), .data_2(out_6), .read(datar), .write(dataw));
  RamCell8 ramcell8_54 (
    .row(decoder_1_out5), .column(decoder_2_out3), .data(out_6), .data_2(out_6), .read(datar), .write(dataw));
  RamCell8 ramcell8_55 (
    .row(decoder_1_out6), .column(decoder_2_out3), .data(out_6), .data_2(out_6), .read(datar), .write(dataw));
  RamCell8 ramcell8_56 (
    .row(decoder_1_out7), .column(decoder_2_out3), .data(out_6), .data_2(out_6), .read(datar), .write(dataw));
  RamCell8 ramcell8_57 (
    .row(decoder_1_out8), .column(decoder_2_out3), .data(out_6), .data_2(out_6), .read(datar), .write(dataw));
  RamCell8 ramcell8_58 (
    .row(decoder_1_out9), .column(decoder_2_out3), .data(out_6), .data_2(out_6), .read(datar), .write(dataw));
  RamCell8 ramcell8_59 (
    .row(decoder_1_out10), .column(decoder_2_out3), .data(out_6), .data_2(out_6), .read(datar), .write(dataw));
  RamCell8 ramcell8_60 (
    .row(decoder_1_out11), .column(decoder_2_out3), .data(out_6), .data_2(out_6), .read(datar), .write(dataw));
  RamCell8 ramcell8_61 (
    .row(decoder_1_out12), .column(decoder_2_out3), .data(out_6), .data_2(out_6), .read(datar), .write(dataw));
  RamCell8 ramcell8_62 (
    .row(decoder_1_out13), .column(decoder_2_out3), .data(out_6), .data_2(out_6), .read(datar), .write(dataw));
  RamCell8 ramcell8_63 (
    .row(decoder_1_out14), .column(decoder_2_out3), .data(out_6), .data_2(out_6), .read(datar), .write(dataw));
  RamCell8 ramcell8_64 (
    .row(decoder_1_out15), .column(decoder_2_out3), .data(out_6), .data_2(out_6), .read(datar), .write(dataw));
  RamCell8 ramcell8_65 (
    .row(decoder_1_out0), .column(decoder_2_out4), .data(out_6), .data_2(out_6), .read(datar), .write(dataw));
  RamCell8 ramcell8_66 (
    .row(decoder_1_out1), .column(decoder_2_out4), .data(out_6), .data_2(out_6), .read(datar), .write(dataw));
  RamCell8 ramcell8_67 (
    .row(decoder_1_out2), .column(decoder_2_out4), .data(out_6), .data_2(out_6), .read(datar), .write(dataw));
  RamCell8 ramcell8_68 (
    .row(decoder_1_out3), .column(decoder_2_out4), .data(out_6), .data_2(out_6), .read(datar), .write(dataw));
  RamCell8 ramcell8_69 (
    .row(decoder_1_out4), .column(decoder_2_out4), .data(out_6), .data_2(out_6), .read(datar), .write(dataw));
  RamCell8 ramcell8_70 (
    .row(decoder_1_out5), .column(decoder_2_out4), .data(out_6), .data_2(out_6), .read(datar), .write(dataw));
  RamCell8 ramcell8_71 (
    .row(decoder_1_out6), .column(decoder_2_out4), .data(out_6), .data_2(out_6), .read(datar), .write(dataw));
  RamCell8 ramcell8_72 (
    .row(decoder_1_out7), .column(decoder_2_out4), .data(out_6), .data_2(out_6), .read(datar), .write(dataw));
  RamCell8 ramcell8_73 (
    .row(decoder_1_out8), .column(decoder_2_out4), .data(out_6), .data_2(out_6), .read(datar), .write(dataw));
  RamCell8 ramcell8_74 (
    .row(decoder_1_out9), .column(decoder_2_out4), .data(out_6), .data_2(out_6), .read(datar), .write(dataw));
  RamCell8 ramcell8_75 (
    .row(decoder_1_out10), .column(decoder_2_out4), .data(out_6), .data_2(out_6), .read(datar), .write(dataw));
  RamCell8 ramcell8_76 (
    .row(decoder_1_out11), .column(decoder_2_out4), .data(out_6), .data_2(out_6), .read(datar), .write(dataw));
  RamCell8 ramcell8_77 (
    .row(decoder_1_out12), .column(decoder_2_out4), .data(out_6), .data_2(out_6), .read(datar), .write(dataw));
  RamCell8 ramcell8_78 (
    .row(decoder_1_out13), .column(decoder_2_out4), .data(out_6), .data_2(out_6), .read(datar), .write(dataw));
  RamCell8 ramcell8_79 (
    .row(decoder_1_out14), .column(decoder_2_out4), .data(out_6), .data_2(out_6), .read(datar), .write(dataw));
  RamCell8 ramcell8_80 (
    .row(decoder_1_out15), .column(decoder_2_out4), .data(out_6), .data_2(out_6), .read(datar), .write(dataw));
  RamCell8 ramcell8_81 (
    .row(decoder_1_out0), .column(decoder_2_out5), .data(out_6), .data_2(out_6), .read(datar), .write(dataw));
  RamCell8 ramcell8_82 (
    .row(decoder_1_out1), .column(decoder_2_out5), .data(out_6), .data_2(out_6), .read(datar), .write(dataw));
  RamCell8 ramcell8_83 (
    .row(decoder_1_out2), .column(decoder_2_out5), .data(out_6), .data_2(out_6), .read(datar), .write(dataw));
  RamCell8 ramcell8_84 (
    .row(decoder_1_out3), .column(decoder_2_out5), .data(out_6), .data_2(out_6), .read(datar), .write(dataw));
  RamCell8 ramcell8_85 (
    .row(decoder_1_out4), .column(decoder_2_out5), .data(out_6), .data_2(out_6), .read(datar), .write(dataw));
  RamCell8 ramcell8_86 (
    .row(decoder_1_out5), .column(decoder_2_out5), .data(out_6), .data_2(out_6), .read(datar), .write(dataw));
  RamCell8 ramcell8_87 (
    .row(decoder_1_out6), .column(decoder_2_out5), .data(out_6), .data_2(out_6), .read(datar), .write(dataw));
  RamCell8 ramcell8_88 (
    .row(decoder_1_out7), .column(decoder_2_out5), .data(out_6), .data_2(out_6), .read(datar), .write(dataw));
  RamCell8 ramcell8_89 (
    .row(decoder_1_out8), .column(decoder_2_out5), .data(out_6), .data_2(out_6), .read(datar), .write(dataw));
  RamCell8 ramcell8_90 (
    .row(decoder_1_out9), .column(decoder_2_out5), .data(out_6), .data_2(out_6), .read(datar), .write(dataw));
  RamCell8 ramcell8_91 (
    .row(decoder_1_out10), .column(decoder_2_out5), .data(out_6), .data_2(out_6), .read(datar), .write(dataw));
  RamCell8 ramcell8_92 (
    .row(decoder_1_out11), .column(decoder_2_out5), .data(out_6), .data_2(out_6), .read(datar), .write(dataw));
  RamCell8 ramcell8_93 (
    .row(decoder_1_out12), .column(decoder_2_out5), .data(out_6), .data_2(out_6), .read(datar), .write(dataw));
  RamCell8 ramcell8_94 (
    .row(decoder_1_out13), .column(decoder_2_out5), .data(out_6), .data_2(out_6), .read(datar), .write(dataw));
  RamCell8 ramcell8_95 (
    .row(decoder_1_out14), .column(decoder_2_out5), .data(out_6), .data_2(out_6), .read(datar), .write(dataw));
  RamCell8 ramcell8_96 (
    .row(decoder_1_out15), .column(decoder_2_out5), .data(out_6), .data_2(out_6), .read(datar), .write(dataw));
  RamCell8 ramcell8_97 (
    .row(decoder_1_out0), .column(decoder_2_out6), .data(out_6), .data_2(out_6), .read(datar), .write(dataw));
  RamCell8 ramcell8_98 (
    .row(decoder_1_out1), .column(decoder_2_out6), .data(out_6), .data_2(out_6), .read(datar), .write(dataw));
  RamCell8 ramcell8_99 (
    .row(decoder_1_out2), .column(decoder_2_out6), .data(out_6), .data_2(out_6), .read(datar), .write(dataw));
  RamCell8 ramcell8_100 (
    .row(decoder_1_out3), .column(decoder_2_out6), .data(out_6), .data_2(out_6), .read(datar), .write(dataw));
  RamCell8 ramcell8_101 (
    .row(decoder_1_out4), .column(decoder_2_out6), .data(out_6), .data_2(out_6), .read(datar), .write(dataw));
  RamCell8 ramcell8_102 (
    .row(decoder_1_out5), .column(decoder_2_out6), .data(out_6), .data_2(out_6), .read(datar), .write(dataw));
  RamCell8 ramcell8_103 (
    .row(decoder_1_out6), .column(decoder_2_out6), .data(out_6), .data_2(out_6), .read(datar), .write(dataw));
  RamCell8 ramcell8_104 (
    .row(decoder_1_out7), .column(decoder_2_out6), .data(out_6), .data_2(out_6), .read(datar), .write(dataw));
  RamCell8 ramcell8_105 (
    .row(decoder_1_out8), .column(decoder_2_out6), .data(out_6), .data_2(out_6), .read(datar), .write(dataw));
  RamCell8 ramcell8_106 (
    .row(decoder_1_out9), .column(decoder_2_out6), .data(out_6), .data_2(out_6), .read(datar), .write(dataw));
  RamCell8 ramcell8_107 (
    .row(decoder_1_out10), .column(decoder_2_out6), .data(out_6), .data_2(out_6), .read(datar), .write(dataw));
  RamCell8 ramcell8_108 (
    .row(decoder_1_out11), .column(decoder_2_out6), .data(out_6), .data_2(out_6), .read(datar), .write(dataw));
  RamCell8 ramcell8_109 (
    .row(decoder_1_out12), .column(decoder_2_out6), .data(out_6), .data_2(out_6), .read(datar), .write(dataw));
  RamCell8 ramcell8_110 (
    .row(decoder_1_out13), .column(decoder_2_out6), .data(out_6), .data_2(out_6), .read(datar), .write(dataw));
  RamCell8 ramcell8_111 (
    .row(decoder_1_out14), .column(decoder_2_out6), .data(out_6), .data_2(out_6), .read(datar), .write(dataw));
  RamCell8 ramcell8_112 (
    .row(decoder_1_out15), .column(decoder_2_out6), .data(out_6), .data_2(out_6), .read(datar), .write(dataw));
  Decoder #(.select(4)) decoder_2 (
    .out0(decoder_2_out0), .out1(decoder_2_out1), .out2(decoder_2_out2), .out3(decoder_2_out3),
    .out4(decoder_2_out4), .out5(decoder_2_out5), .out6(decoder_2_out6), .out7(decoder_2_out7),
    .out8(decoder_2_out8), .out9(decoder_2_out9), .out10(decoder_2_out10), .out11(decoder_2_out11),
    .out12(decoder_2_out12), .out13(decoder_2_out13), .out14(decoder_2_out14), .out15(decoder_2_out15),
    .sel(reg8_1_out[3:0]), .en(1'b1));
  RamCell8 ramcell8_113 (
    .row(decoder_1_out0), .column(decoder_2_out7), .data(out_6), .data_2(out_6), .read(datar), .write(dataw));
  RamCell8 ramcell8_114 (
    .row(decoder_1_out1), .column(decoder_2_out7), .data(out_6), .data_2(out_6), .read(datar), .write(dataw));
  RamCell8 ramcell8_115 (
    .row(decoder_1_out2), .column(decoder_2_out7), .data(out_6), .data_2(out_6), .read(datar), .write(dataw));
  RamCell8 ramcell8_116 (
    .row(decoder_1_out3), .column(decoder_2_out7), .data(out_6), .data_2(out_6), .read(datar), .write(dataw));
  RamCell8 ramcell8_117 (
    .row(decoder_1_out4), .column(decoder_2_out7), .data(out_6), .data_2(out_6), .read(datar), .write(dataw));
  RamCell8 ramcell8_118 (
    .row(decoder_1_out5), .column(decoder_2_out7), .data(out_6), .data_2(out_6), .read(datar), .write(dataw));
  RamCell8 ramcell8_119 (
    .row(decoder_1_out6), .column(decoder_2_out7), .data(out_6), .data_2(out_6), .read(datar), .write(dataw));
  RamCell8 ramcell8_120 (
    .row(decoder_1_out7), .column(decoder_2_out7), .data(out_6), .data_2(out_6), .read(datar), .write(dataw));
  RamCell8 ramcell8_121 (
    .row(decoder_1_out8), .column(decoder_2_out7), .data(out_6), .data_2(out_6), .read(datar), .write(dataw));
  RamCell8 ramcell8_122 (
    .row(decoder_1_out9), .column(decoder_2_out7), .data(out_6), .data_2(out_6), .read(datar), .write(dataw));
  RamCell8 ramcell8_123 (
    .row(decoder_1_out10), .column(decoder_2_out7), .data(out_6), .data_2(out_6), .read(datar), .write(dataw));
  RamCell8 ramcell8_124 (
    .row(decoder_1_out11), .column(decoder_2_out7), .data(out_6), .data_2(out_6), .read(datar), .write(dataw));
  RamCell8 ramcell8_125 (
    .row(decoder_1_out12), .column(decoder_2_out7), .data(out_6), .data_2(out_6), .read(datar), .write(dataw));
  RamCell8 ramcell8_126 (
    .row(decoder_1_out13), .column(decoder_2_out7), .data(out_6), .data_2(out_6), .read(datar), .write(dataw));
  RamCell8 ramcell8_127 (
    .row(decoder_1_out14), .column(decoder_2_out7), .data(out_6), .data_2(out_6), .read(datar), .write(dataw));
  RamCell8 ramcell8_128 (
    .row(decoder_1_out15), .column(decoder_2_out7), .data(out_6), .data_2(out_6), .read(datar), .write(dataw));
  RamCell8 ramcell8_129 (
    .row(decoder_1_out0), .column(decoder_2_out8), .data(out_6), .data_2(out_6), .read(datar), .write(dataw));
  RamCell8 ramcell8_130 (
    .row(decoder_1_out1), .column(decoder_2_out8), .data(out_6), .data_2(out_6), .read(datar), .write(dataw));
  RamCell8 ramcell8_131 (
    .row(decoder_1_out2), .column(decoder_2_out8), .data(out_6), .data_2(out_6), .read(datar), .write(dataw));
  RamCell8 ramcell8_132 (
    .row(decoder_1_out3), .column(decoder_2_out8), .data(out_6), .data_2(out_6), .read(datar), .write(dataw));
  RamCell8 ramcell8_133 (
    .row(decoder_1_out4), .column(decoder_2_out8), .data(out_6), .data_2(out_6), .read(datar), .write(dataw));
  RamCell8 ramcell8_134 (
    .row(decoder_1_out5), .column(decoder_2_out8), .data(out_6), .data_2(out_6), .read(datar), .write(dataw));
  RamCell8 ramcell8_135 (
    .row(decoder_1_out6), .column(decoder_2_out8), .data(out_6), .data_2(out_6), .read(datar), .write(dataw));
  RamCell8 ramcell8_136 (
    .row(decoder_1_out7), .column(decoder_2_out8), .data(out_6), .data_2(out_6), .read(datar), .write(dataw));
  RamCell8 ramcell8_137 (
    .row(decoder_1_out8), .column(decoder_2_out8), .data(out_6), .data_2(out_6), .read(datar), .write(dataw));
  RamCell8 ramcell8_138 (
    .row(decoder_1_out9), .column(decoder_2_out8), .data(out_6), .data_2(out_6), .read(datar), .write(dataw));
  RamCell8 ramcell8_139 (
    .row(decoder_1_out10), .column(decoder_2_out8), .data(out_6), .data_2(out_6), .read(datar), .write(dataw));
  RamCell8 ramcell8_140 (
    .row(decoder_1_out11), .column(decoder_2_out8), .data(out_6), .data_2(out_6), .read(datar), .write(dataw));
  RamCell8 ramcell8_141 (
    .row(decoder_1_out12), .column(decoder_2_out8), .data(out_6), .data_2(out_6), .read(datar), .write(dataw));
  RamCell8 ramcell8_142 (
    .row(decoder_1_out13), .column(decoder_2_out8), .data(out_6), .data_2(out_6), .read(datar), .write(dataw));
  RamCell8 ramcell8_143 (
    .row(decoder_1_out14), .column(decoder_2_out8), .data(out_6), .data_2(out_6), .read(datar), .write(dataw));
  RamCell8 ramcell8_144 (
    .row(decoder_1_out15), .column(decoder_2_out8), .data(out_6), .data_2(out_6), .read(datar), .write(dataw));
  RamCell8 ramcell8_145 (
    .row(decoder_1_out0), .column(decoder_2_out9), .data(out_6), .data_2(out_6), .read(datar), .write(dataw));
  RamCell8 ramcell8_146 (
    .row(decoder_1_out1), .column(decoder_2_out9), .data(out_6), .data_2(out_6), .read(datar), .write(dataw));
  RamCell8 ramcell8_147 (
    .row(decoder_1_out2), .column(decoder_2_out9), .data(out_6), .data_2(out_6), .read(datar), .write(dataw));
  RamCell8 ramcell8_148 (
    .row(decoder_1_out3), .column(decoder_2_out9), .data(out_6), .data_2(out_6), .read(datar), .write(dataw));
  RamCell8 ramcell8_149 (
    .row(decoder_1_out4), .column(decoder_2_out9), .data(out_6), .data_2(out_6), .read(datar), .write(dataw));
  RamCell8 ramcell8_150 (
    .row(decoder_1_out5), .column(decoder_2_out9), .data(out_6), .data_2(out_6), .read(datar), .write(dataw));
  RamCell8 ramcell8_151 (
    .row(decoder_1_out6), .column(decoder_2_out9), .data(out_6), .data_2(out_6), .read(datar), .write(dataw));
  RamCell8 ramcell8_152 (
    .row(decoder_1_out7), .column(decoder_2_out9), .data(out_6), .data_2(out_6), .read(datar), .write(dataw));
  RamCell8 ramcell8_153 (
    .row(decoder_1_out8), .column(decoder_2_out9), .data(out_6), .data_2(out_6), .read(datar), .write(dataw));
  RamCell8 ramcell8_154 (
    .row(decoder_1_out9), .column(decoder_2_out9), .data(out_6), .data_2(out_6), .read(datar), .write(dataw));
  RamCell8 ramcell8_155 (
    .row(decoder_1_out10), .column(decoder_2_out9), .data(out_6), .data_2(out_6), .read(datar), .write(dataw));
  RamCell8 ramcell8_156 (
    .row(decoder_1_out11), .column(decoder_2_out9), .data(out_6), .data_2(out_6), .read(datar), .write(dataw));
  RamCell8 ramcell8_157 (
    .row(decoder_1_out12), .column(decoder_2_out9), .data(out_6), .data_2(out_6), .read(datar), .write(dataw));
  RamCell8 ramcell8_158 (
    .row(decoder_1_out13), .column(decoder_2_out9), .data(out_6), .data_2(out_6), .read(datar), .write(dataw));
  RamCell8 ramcell8_159 (
    .row(decoder_1_out14), .column(decoder_2_out9), .data(out_6), .data_2(out_6), .read(datar), .write(dataw));
  RamCell8 ramcell8_160 (
    .row(decoder_1_out15), .column(decoder_2_out9), .data(out_6), .data_2(out_6), .read(datar), .write(dataw));
  RamCell8 ramcell8_161 (
    .row(decoder_1_out0), .column(decoder_2_out10), .data(out_6), .data_2(out_6), .read(datar), .write(dataw));
  RamCell8 ramcell8_162 (
    .row(decoder_1_out1), .column(decoder_2_out10), .data(out_6), .data_2(out_6), .read(datar), .write(dataw));
  RamCell8 ramcell8_163 (
    .row(decoder_1_out2), .column(decoder_2_out10), .data(out_6), .data_2(out_6), .read(datar), .write(dataw));
  RamCell8 ramcell8_164 (
    .row(decoder_1_out3), .column(decoder_2_out10), .data(out_6), .data_2(out_6), .read(datar), .write(dataw));
  RamCell8 ramcell8_165 (
    .row(decoder_1_out4), .column(decoder_2_out10), .data(out_6), .data_2(out_6), .read(datar), .write(dataw));
  RamCell8 ramcell8_166 (
    .row(decoder_1_out5), .column(decoder_2_out10), .data(out_6), .data_2(out_6), .read(datar), .write(dataw));
  RamCell8 ramcell8_167 (
    .row(decoder_1_out6), .column(decoder_2_out10), .data(out_6), .data_2(out_6), .read(datar), .write(dataw));
  RamCell8 ramcell8_168 (
    .row(decoder_1_out7), .column(decoder_2_out10), .data(out_6), .data_2(out_6), .read(datar), .write(dataw));
  RamCell8 ramcell8_169 (
    .row(decoder_1_out8), .column(decoder_2_out10), .data(out_6), .data_2(out_6), .read(datar), .write(dataw));
  RamCell8 ramcell8_170 (
    .row(decoder_1_out9), .column(decoder_2_out10), .data(out_6), .data_2(out_6), .read(datar), .write(dataw));
  RamCell8 ramcell8_171 (
    .row(decoder_1_out10), .column(decoder_2_out10), .data(out_6), .data_2(out_6), .read(datar), .write(dataw));
  RamCell8 ramcell8_172 (
    .row(decoder_1_out11), .column(decoder_2_out10), .data(out_6), .data_2(out_6), .read(datar), .write(dataw));
  RamCell8 ramcell8_173 (
    .row(decoder_1_out12), .column(decoder_2_out10), .data(out_6), .data_2(out_6), .read(datar), .write(dataw));
  RamCell8 ramcell8_174 (
    .row(decoder_1_out13), .column(decoder_2_out10), .data(out_6), .data_2(out_6), .read(datar), .write(dataw));
  RamCell8 ramcell8_175 (
    .row(decoder_1_out14), .column(decoder_2_out10), .data(out_6), .data_2(out_6), .read(datar), .write(dataw));
  RamCell8 ramcell8_176 (
    .row(decoder_1_out15), .column(decoder_2_out10), .data(out_6), .data_2(out_6), .read(datar), .write(dataw));
  RamCell8 ramcell8_177 (
    .row(decoder_1_out0), .column(decoder_2_out11), .data(out_6), .data_2(out_6), .read(datar), .write(dataw));
  RamCell8 ramcell8_178 (
    .row(decoder_1_out1), .column(decoder_2_out11), .data(out_6), .data_2(out_6), .read(datar), .write(dataw));
  RamCell8 ramcell8_179 (
    .row(decoder_1_out2), .column(decoder_2_out11), .data(out_6), .data_2(out_6), .read(datar), .write(dataw));
  RamCell8 ramcell8_180 (
    .row(decoder_1_out3), .column(decoder_2_out11), .data(out_6), .data_2(out_6), .read(datar), .write(dataw));
  RamCell8 ramcell8_181 (
    .row(decoder_1_out4), .column(decoder_2_out11), .data(out_6), .data_2(out_6), .read(datar), .write(dataw));
  RamCell8 ramcell8_182 (
    .row(decoder_1_out5), .column(decoder_2_out11), .data(out_6), .data_2(out_6), .read(datar), .write(dataw));
  RamCell8 ramcell8_183 (
    .row(decoder_1_out6), .column(decoder_2_out11), .data(out_6), .data_2(out_6), .read(datar), .write(dataw));
  RamCell8 ramcell8_184 (
    .row(decoder_1_out7), .column(decoder_2_out11), .data(out_6), .data_2(out_6), .read(datar), .write(dataw));
  RamCell8 ramcell8_185 (
    .row(decoder_1_out8), .column(decoder_2_out11), .data(out_6), .data_2(out_6), .read(datar), .write(dataw));
  RamCell8 ramcell8_186 (
    .row(decoder_1_out9), .column(decoder_2_out11), .data(out_6), .data_2(out_6), .read(datar), .write(dataw));
  RamCell8 ramcell8_187 (
    .row(decoder_1_out10), .column(decoder_2_out11), .data(out_6), .data_2(out_6), .read(datar), .write(dataw));
  RamCell8 ramcell8_188 (
    .row(decoder_1_out11), .column(decoder_2_out11), .data(out_6), .data_2(out_6), .read(datar), .write(dataw));
  RamCell8 ramcell8_189 (
    .row(decoder_1_out12), .column(decoder_2_out11), .data(out_6), .data_2(out_6), .read(datar), .write(dataw));
  RamCell8 ramcell8_190 (
    .row(decoder_1_out13), .column(decoder_2_out11), .data(out_6), .data_2(out_6), .read(datar), .write(dataw));
  RamCell8 ramcell8_191 (
    .row(decoder_1_out14), .column(decoder_2_out11), .data(out_6), .data_2(out_6), .read(datar), .write(dataw));
  RamCell8 ramcell8_192 (
    .row(decoder_1_out15), .column(decoder_2_out11), .data(out_6), .data_2(out_6), .read(datar), .write(dataw));
  RamCell8 ramcell8_193 (
    .row(decoder_1_out0), .column(decoder_2_out12), .data(out_6), .data_2(out_6), .read(datar), .write(dataw));
  RamCell8 ramcell8_194 (
    .row(decoder_1_out1), .column(decoder_2_out12), .data(out_6), .data_2(out_6), .read(datar), .write(dataw));
  RamCell8 ramcell8_195 (
    .row(decoder_1_out2), .column(decoder_2_out12), .data(out_6), .data_2(out_6), .read(datar), .write(dataw));
  RamCell8 ramcell8_196 (
    .row(decoder_1_out3), .column(decoder_2_out12), .data(out_6), .data_2(out_6), .read(datar), .write(dataw));
  RamCell8 ramcell8_197 (
    .row(decoder_1_out4), .column(decoder_2_out12), .data(out_6), .data_2(out_6), .read(datar), .write(dataw));
  RamCell8 ramcell8_198 (
    .row(decoder_1_out5), .column(decoder_2_out12), .data(out_6), .data_2(out_6), .read(datar), .write(dataw));
  RamCell8 ramcell8_199 (
    .row(decoder_1_out6), .column(decoder_2_out12), .data(out_6), .data_2(out_6), .read(datar), .write(dataw));
  RamCell8 ramcell8_200 (
    .row(decoder_1_out7), .column(decoder_2_out12), .data(out_6), .data_2(out_6), .read(datar), .write(dataw));
  RamCell8 ramcell8_201 (
    .row(decoder_1_out8), .column(decoder_2_out12), .data(out_6), .data_2(out_6), .read(datar), .write(dataw));
  RamCell8 ramcell8_202 (
    .row(decoder_1_out9), .column(decoder_2_out12), .data(out_6), .data_2(out_6), .read(datar), .write(dataw));
  RamCell8 ramcell8_203 (
    .row(decoder_1_out10), .column(decoder_2_out12), .data(out_6), .data_2(out_6), .read(datar), .write(dataw));
  RamCell8 ramcell8_204 (
    .row(decoder_1_out11), .column(decoder_2_out12), .data(out_6), .data_2(out_6), .read(datar), .write(dataw));
  RamCell8 ramcell8_205 (
    .row(decoder_1_out12), .column(decoder_2_out12), .data(out_6), .data_2(out_6), .read(datar), .write(dataw));
  RamCell8 ramcell8_206 (
    .row(decoder_1_out13), .column(decoder_2_out12), .data(out_6), .data_2(out_6), .read(datar), .write(dataw));
  RamCell8 ramcell8_207 (
    .row(decoder_1_out14), .column(decoder_2_out12), .data(out_6), .data_2(out_6), .read(datar), .write(dataw));
  RamCell8 ramcell8_208 (
    .row(decoder_1_out15), .column(decoder_2_out12), .data(out_6), .data_2(out_6), .read(datar), .write(dataw));
  RamCell8 ramcell8_209 (
    .row(decoder_1_out0), .column(decoder_2_out13), .data(out_6), .data_2(out_6), .read(datar), .write(dataw));
  RamCell8 ramcell8_210 (
    .row(decoder_1_out1), .column(decoder_2_out13), .data(out_6), .data_2(out_6), .read(datar), .write(dataw));
  RamCell8 ramcell8_211 (
    .row(decoder_1_out2), .column(decoder_2_out13), .data(out_6), .data_2(out_6), .read(datar), .write(dataw));
  RamCell8 ramcell8_212 (
    .row(decoder_1_out3), .column(decoder_2_out13), .data(out_6), .data_2(out_6), .read(datar), .write(dataw));
  RamCell8 ramcell8_213 (
    .row(decoder_1_out4), .column(decoder_2_out13), .data(out_6), .data_2(out_6), .read(datar), .write(dataw));
  RamCell8 ramcell8_214 (
    .row(decoder_1_out5), .column(decoder_2_out13), .data(out_6), .data_2(out_6), .read(datar), .write(dataw));
  RamCell8 ramcell8_215 (
    .row(decoder_1_out6), .column(decoder_2_out13), .data(out_6), .data_2(out_6), .read(datar), .write(dataw));
  RamCell8 ramcell8_216 (
    .row(decoder_1_out7), .column(decoder_2_out13), .data(out_6), .data_2(out_6), .read(datar), .write(dataw));
  RamCell8 ramcell8_217 (
    .row(decoder_1_out8), .column(decoder_2_out13), .data(out_6), .data_2(out_6), .read(datar), .write(dataw));
  RamCell8 ramcell8_218 (
    .row(decoder_1_out9), .column(decoder_2_out13), .data(out_6), .data_2(out_6), .read(datar), .write(dataw));
  RamCell8 ramcell8_219 (
    .row(decoder_1_out10), .column(decoder_2_out13), .data(out_6), .data_2(out_6), .read(datar), .write(dataw));
  RamCell8 ramcell8_220 (
    .row(decoder_1_out11), .column(decoder_2_out13), .data(out_6), .data_2(out_6), .read(datar), .write(dataw));
  RamCell8 ramcell8_221 (
    .row(decoder_1_out12), .column(decoder_2_out13), .data(out_6), .data_2(out_6), .read(datar), .write(dataw));
  RamCell8 ramcell8_222 (
    .row(decoder_1_out13), .column(decoder_2_out13), .data(out_6), .data_2(out_6), .read(datar), .write(dataw));
  RamCell8 ramcell8_223 (
    .row(decoder_1_out14), .column(decoder_2_out13), .data(out_6), .data_2(out_6), .read(datar), .write(dataw));
  RamCell8 ramcell8_224 (
    .row(decoder_1_out15), .column(decoder_2_out13), .data(out_6), .data_2(out_6), .read(datar), .write(dataw));
  RamCell8 ramcell8_225 (
    .row(decoder_1_out0), .column(decoder_2_out14), .data(out_6), .data_2(out_6), .read(datar), .write(dataw));
  RamCell8 ramcell8_226 (
    .row(decoder_1_out1), .column(decoder_2_out14), .data(out_6), .data_2(out_6), .read(datar), .write(dataw));
  RamCell8 ramcell8_227 (
    .row(decoder_1_out2), .column(decoder_2_out14), .data(out_6), .data_2(out_6), .read(datar), .write(dataw));
  RamCell8 ramcell8_228 (
    .row(decoder_1_out3), .column(decoder_2_out14), .data(out_6), .data_2(out_6), .read(datar), .write(dataw));
  RamCell8 ramcell8_229 (
    .row(decoder_1_out4), .column(decoder_2_out14), .data(out_6), .data_2(out_6), .read(datar), .write(dataw));
  RamCell8 ramcell8_230 (
    .row(decoder_1_out5), .column(decoder_2_out14), .data(out_6), .data_2(out_6), .read(datar), .write(dataw));
  RamCell8 ramcell8_231 (
    .row(decoder_1_out6), .column(decoder_2_out14), .data(out_6), .data_2(out_6), .read(datar), .write(dataw));
  RamCell8 ramcell8_232 (
    .row(decoder_1_out7), .column(decoder_2_out14), .data(out_6), .data_2(out_6), .read(datar), .write(dataw));
  RamCell8 ramcell8_233 (
    .row(decoder_1_out8), .column(decoder_2_out14), .data(out_6), .data_2(out_6), .read(datar), .write(dataw));
  RamCell8 ramcell8_234 (
    .row(decoder_1_out9), .column(decoder_2_out14), .data(out_6), .data_2(out_6), .read(datar), .write(dataw));
  RamCell8 ramcell8_235 (
    .row(decoder_1_out10), .column(decoder_2_out14), .data(out_6), .data_2(out_6), .read(datar), .write(dataw));
  RamCell8 ramcell8_236 (
    .row(decoder_1_out11), .column(decoder_2_out14), .data(out_6), .data_2(out_6), .read(datar), .write(dataw));
  RamCell8 ramcell8_237 (
    .row(decoder_1_out12), .column(decoder_2_out14), .data(out_6), .data_2(out_6), .read(datar), .write(dataw));
  RamCell8 ramcell8_238 (
    .row(decoder_1_out13), .column(decoder_2_out14), .data(out_6), .data_2(out_6), .read(datar), .write(dataw));
  RamCell8 ramcell8_239 (
    .row(decoder_1_out14), .column(decoder_2_out14), .data(out_6), .data_2(out_6), .read(datar), .write(dataw));
  RamCell8 ramcell8_240 (
    .row(decoder_1_out15), .column(decoder_2_out14), .data(out_6), .data_2(out_6), .read(datar), .write(dataw));
  RamCell8 ramcell8_241 (
    .row(decoder_1_out0), .column(decoder_2_out15), .data(out_6), .data_2(out_6), .read(datar), .write(dataw));
  RamCell8 ramcell8_242 (
    .row(decoder_1_out1), .column(decoder_2_out15), .data(out_6), .data_2(out_6), .read(datar), .write(dataw));
  RamCell8 ramcell8_243 (
    .row(decoder_1_out2), .column(decoder_2_out15), .data(out_6), .data_2(out_6), .read(datar), .write(dataw));
  RamCell8 ramcell8_244 (
    .row(decoder_1_out3), .column(decoder_2_out15), .data(out_6), .data_2(out_6), .read(datar), .write(dataw));
  RamCell8 ramcell8_245 (
    .row(decoder_1_out4), .column(decoder_2_out15), .data(out_6), .data_2(out_6), .read(datar), .write(dataw));
  RamCell8 ramcell8_246 (
    .row(decoder_1_out5), .column(decoder_2_out15), .data(out_6), .data_2(out_6), .read(datar), .write(dataw));
  RamCell8 ramcell8_247 (
    .row(decoder_1_out6), .column(decoder_2_out15), .data(out_6), .data_2(out_6), .read(datar), .write(dataw));
  RamCell8 ramcell8_248 (
    .row(decoder_1_out7), .column(decoder_2_out15), .data(out_6), .data_2(out_6), .read(datar), .write(dataw));
  RamCell8 ramcell8_249 (
    .row(decoder_1_out8), .column(decoder_2_out15), .data(out_6), .data_2(out_6), .read(datar), .write(dataw));
  RamCell8 ramcell8_250 (
    .row(decoder_1_out9), .column(decoder_2_out15), .data(out_6), .data_2(out_6), .read(datar), .write(dataw));
  RamCell8 ramcell8_251 (
    .row(decoder_1_out10), .column(decoder_2_out15), .data(out_6), .data_2(out_6), .read(datar), .write(dataw));
  RamCell8 ramcell8_252 (
    .row(decoder_1_out11), .column(decoder_2_out15), .data(out_6), .data_2(out_6), .read(datar), .write(dataw));
  RamCell8 ramcell8_253 (
    .row(decoder_1_out12), .column(decoder_2_out15), .data(out_6), .data_2(out_6), .read(datar), .write(dataw));
  RamCell8 ramcell8_254 (
    .row(decoder_1_out13), .column(decoder_2_out15), .data(out_6), .data_2(out_6), .read(datar), .write(dataw));
  RamCell8 ramcell8_255 (
    .row(decoder_1_out14), .column(decoder_2_out15), .data(out_6), .data_2(out_6), .read(datar), .write(dataw));
  RamCell8 ramcell8_256 (
    .row(decoder_1_out15), .column(decoder_2_out15), .data(out_6), .data_2(out_6), .read(datar), .write(dataw));
endmodule
