// Logisim project transistor.circ as structural Verilog
module DATAPATH (
  input  rx1,
  input  rx0,
  input  w,
  input  r,
  input  pc_w,
  input  ra_w,
  input  rst,
  input  pc_r,
  input  bus0,
  input  rb_w,
  input  cin,
  input  op2,
  input  op1,
  input  op0,
  input  fr_w,
  input  rd_r,
  input  mar,
  input  r_2,
  input  w_2,
  input  clk_r,
  input  clk_w,
  output _7,
  output _6,
  output _5,
  output _4,
  output _3,
  output _2,
  output _1,
  output _0,
  output v,
  output c,
  output s,
  output z
);

  wire transistor_1_out, transistor_2_out, transistor_4_out, transistor_6_out, transistor_8_out,
       transistor_10_out, transistor_12_out, transistor_14_out, transistor_16_out, transistor_18_out,
       transistor_20_out, transistor_22_out, transistor_24_out, transistor_27_out, transistor_31_out,
       transistor_35_out, transistor_39_out, transistor_43_out, transistor_47_out, transistor_51_out,
       transistor_55_out, transistor_59_out, transistor_65_out, transistor_66_out, transistor_67_out,
       transistor_69_out, transistor_71_out, transistor_73_out, transistor_75_out, transistor_77_out,
       transistor_79_out, transistor_81_out, transistor_83_out, transistor_85_out, transistor_88_out,
       transistor_89_out, transistor_91_out, transistor_93_out, transistor_97_out, transistor_101_out,
       transistor_105_out, transistor_109_out, transistor_113_out, transistor_117_out, transistor_121_out,
       transistor_125_out, transistor_129_out, transistor_133_out, transistor_134_out, transistor_135_out,
       transistor_137_out, transistor_139_out, transistor_141_out, transistor_143_out, transistor_145_out,
       transistor_147_out, transistor_149_out, transistor_151_out, transistor_153_out, transistor_155_out,
       transistor_157_out, transistor_159_out, transistor_161_out, transistor_163_out, transistor_165_out,
       transistor_167_out, transistor_169_out, transistor_170_out, transistor_172_out, transistor_174_out,
       transistor_176_out, transistor_178_out, transistor_180_out, transistor_182_out, transistor_184_out,
       transistor_186_out, transistor_188_out, transistor_190_out, transistor_194_out, transistor_199_out,
       transistor_200_out, transistor_201_out, transistor_205_out, transistor_209_out, transistor_213_out,
       transistor_217_out, transistor_221_out, transistor_225_out, transistor_229_out, transistor_233_out,
       transistor_237_out, transistor_238_out, transistor_240_out, transistor_242_out, transistor_244_out,
       transistor_246_out, transistor_248_out, transistor_250_out, transistor_252_out, transistor_254_out,
       transistor_258_out, transistor_259_out, transistor_261_out, transistor_263_out, transistor_268_out,
       transistor_273_out, transistor_278_out, transistor_283_out, transistor_288_out, transistor_293_out,
       transistor_298_out, transistor_303_out, transistor_307_out, transistor_311_out, transistor_312_out,
       transistor_313_out, transistor_316_out, transistor_319_out, transistor_322_out, transistor_325_out,
       transistor_328_out, transistor_331_out, transistor_334_out, transistor_337_out, transistor_339_out,
       transistor_340_out, transistor_342_out, transistor_344_out, transistor_346_out, transistor_348_out,
       transistor_350_out, transistor_352_out, transistor_354_out, transistor_356_out, transistor_358_out,
       transistor_362_out, transistor_367_out, transistor_368_out, transistor_369_out, transistor_373_out,
       transistor_377_out, transistor_381_out, transistor_385_out, transistor_389_out, transistor_393_out,
       transistor_397_out, transistor_401_out, transistor_403_out, transistor_407_out, transistor_408_out,
       transistor_409_out, transistor_411_out, transistor_413_out, transistor_417_out, transistor_419_out,
       transistor_423_out, transistor_425_out, transistor_429_out, transistor_431_out, transistor_435_out,
       transistor_437_out, transistor_441_out, transistor_443_out, transistor_447_out, transistor_449_out,
       transistor_453_out, transistor_455_out, transistor_459_out, transistor_461_out, transistor_465_out,
       transistor_467_out, transistor_471_out, transistor_475_out, transistor_479_out, transistor_483_out,
       transistor_487_out, transistor_491_out, transistor_495_out, transistor_499_out, transistor_505_out,
       transistor_506_out, transistor_507_out, transistor_509_out, transistor_511_out, transistor_513_out,
       transistor_515_out, transistor_519_out, transistor_521_out, transistor_525_out, transistor_527_out,
       transistor_531_out, transistor_533_out, transistor_537_out, transistor_539_out, transistor_543_out,
       transistor_545_out, transistor_549_out, transistor_551_out, transistor_555_out, transistor_557_out,
       transistor_561_out, transistor_567_out, transistor_568_out, transistor_569_out, transistor_571_out,
       transistor_573_out, transistor_575_out, transistor_577_out, transistor_579_out, transistor_581_out,
       transistor_583_out, transistor_585_out, transistor_587_out, transistor_591_out, transistor_592_out,
       transistor_593_out, transistor_595_out, transistor_599_out, transistor_603_out, transistor_607_out,
       transistor_611_out, transistor_615_out, transistor_619_out, transistor_623_out, transistor_627_out,
       transistor_629_out, transistor_633_out, transistor_637_out, transistor_638_out, transistor_639_out,
       transistor_643_out, transistor_647_out, transistor_651_out, transistor_655_out, transistor_659_out,
       transistor_663_out, transistor_667_out, transistor_671_out, transistor_675_out, transistor_676_out,
       transistor_678_out, transistor_680_out, transistor_682_out, transistor_684_out, transistor_686_out,
       transistor_688_out, transistor_690_out, transistor_692_out, transistor_694_out, transistor_698_out,
       transistor_699_out, transistor_703_out, transistor_707_out, transistor_711_out, transistor_715_out,
       transistor_719_out, transistor_723_out, transistor_727_out, transistor_731_out, transistor_735_out,
       transistor_736_out, transistor_738_out, transistor_740_out, transistor_742_out, transistor_744_out,
       transistor_746_out, transistor_748_out, transistor_750_out, transistor_752_out, transistor_754_out,
       transistor_756_out, transistor_762_out, transistor_763_out, transistor_767_out, transistor_771_out,
       transistor_775_out, transistor_779_out, transistor_783_out, transistor_787_out, transistor_791_out,
       transistor_795_out, transistor_797_out, transistor_801_out, transistor_805_out, transistor_809_out,
       transistor_813_out, transistor_817_out, transistor_821_out, transistor_825_out, transistor_829_out,
       transistor_833_out, transistor_835_out, transistor_837_out, transistor_839_out, transistor_841_out,
       transistor_843_out, transistor_845_out, transistor_847_out, transistor_849_out, transistor_851_out,
       transistor_855_out, transistor_859_out, transistor_863_out, transistor_867_out, transistor_871_out,
       transistor_875_out, transistor_879_out, transistor_883_out, transistor_887_out, transistor_888_out,
       transistor_890_out, transistor_892_out, transistor_894_out, transistor_896_out, transistor_898_out,
       transistor_900_out, transistor_902_out, transistor_904_out, transistor_906_out, transistor_908_out,
       transistor_914_out, transistor_915_out, transistor_919_out, transistor_923_out, transistor_927_out,
       transistor_931_out, transistor_935_out, transistor_939_out, transistor_943_out, transistor_947_out,
       transistor_949_out, transistor_953_out, transistor_955_out, transistor_959_out, transistor_961_out,
       transistor_965_out, transistor_967_out, transistor_971_out, transistor_973_out, transistor_977_out,
       transistor_979_out, transistor_983_out, transistor_985_out, transistor_989_out, transistor_991_out,
       transistor_995_out, transistor_998_out, transistor_999_out, transistor_1001_out, transistor_1003_out,
       transistor_1007_out, transistor_1009_out, transistor_1013_out, transistor_1015_out,
       transistor_1019_out, transistor_1021_out, transistor_1025_out, transistor_1027_out,
       transistor_1031_out, transistor_1033_out, transistor_1037_out, transistor_1039_out,
       transistor_1043_out, transistor_1045_out, transistor_1049_out, transistor_1051_out,
       transistor_1053_out, transistor_1055_out, transistor_1057_out, transistor_1059_out,
       transistor_1061_out, transistor_1063_out, transistor_1065_out, transistor_1069_out,
       transistor_1073_out, transistor_1077_out, transistor_1081_out, transistor_1085_out,
       transistor_1089_out, transistor_1093_out, transistor_1097_out, transistor_1098_out,
       transistor_1099_out, transistor_1100_out, transistor_1101_out, transistor_1102_out,
       transistor_1103_out, transistor_1104_out, transistor_1107_out, transistor_1110_out,
       transistor_1113_out, transistor_1116_out, transistor_1119_out, transistor_1122_out,
       transistor_1125_out, transistor_1128_out, transistor_1129_out, transistor_1131_out,
       transistor_1133_out, transistor_1135_out, transistor_1137_out, transistor_1139_out,
       transistor_1141_out, transistor_1143_out, transistor_1145_out, transistor_1146_out,
       transistor_1149_out, transistor_1150_out, transistor_1153_out, transistor_1154_out,
       transistor_1157_out, transistor_1158_out, transistor_1161_out, transistor_1162_out,
       transistor_1165_out, transistor_1166_out, transistor_1169_out, transistor_1170_out,
       transistor_1173_out, transistor_1174_out, transistor_1177_out, transistor_1179_out,
       transistor_1181_out, transistor_1183_out, transistor_1185_out, transistor_1187_out,
       transistor_1189_out, transistor_1191_out, transistor_1193_out, transistor_1194_out,
       transistor_1195_out, transistor_1196_out, transistor_1197_out, transistor_1198_out,
       transistor_1199_out, transistor_1200_out, transistor_1201_out, transistor_1206_out,
       transistor_1208_out, transistor_1209_out, transistor_1212_out, transistor_1214_out,
       transistor_1216_out, transistor_1217_out, transistor_1220_out, transistor_1222_out,
       transistor_1224_out, transistor_1226_out, transistor_1228_out, transistor_1229_out,
       transistor_1232_out, transistor_1234_out, transistor_1236_out, transistor_1237_out,
       transistor_1241_out, transistor_1244_out, transistor_1247_out, transistor_1250_out,
       transistor_1253_out, transistor_1256_out, transistor_1259_out, transistor_1262_out,
       transistor_1265_out, transistor_1268_out, transistor_1269_out, transistor_1272_out,
       transistor_1273_out, transistor_1276_out, transistor_1277_out, transistor_1280_out,
       transistor_1281_out, transistor_1284_out, transistor_1285_out, transistor_1288_out,
       transistor_1289_out, transistor_1292_out, transistor_1293_out, transistor_1296_out,
       transistor_1297_out, transistor_1301_out, transistor_1302_out, transistor_1303_out,
       transistor_1304_out, transistor_1305_out, transistor_1306_out, transistor_1307_out,
       transistor_1308_out, transistor_1311_out, transistor_1314_out, transistor_1317_out,
       transistor_1320_out, transistor_1323_out, transistor_1326_out, transistor_1329_out,
       transistor_1332_out, transistor_1333_out, transistor_1337_out, transistor_1340_out,
       transistor_1341_out, transistor_1344_out, transistor_1345_out, transistor_1348_out,
       transistor_1349_out, transistor_1352_out, transistor_1353_out, transistor_1356_out,
       transistor_1357_out, transistor_1360_out, transistor_1361_out, transistor_1364_out,
       transistor_1365_out, transistor_1368_out, transistor_1369_out, transistor_1372_out,
       transistor_1373_out, transistor_1374_out, transistor_1375_out, transistor_1376_out,
       transistor_1377_out, transistor_1378_out, transistor_1379_out, transistor_1383_out,
       transistor_1386_out, transistor_1389_out, transistor_1392_out, transistor_1395_out,
       transistor_1398_out, transistor_1401_out, transistor_1404_out, transistor_1405_out,
       transistor_1409_out, transistor_1412_out, transistor_1413_out, transistor_1416_out,
       transistor_1417_out, transistor_1420_out, transistor_1421_out, transistor_1424_out,
       transistor_1425_out, transistor_1428_out, transistor_1429_out, transistor_1432_out,
       transistor_1433_out, transistor_1436_out, transistor_1437_out, transistor_1440_out,
       transistor_1441_out, transistor_1444_out, transistor_1445_out, transistor_1448_out,
       transistor_1449_out, transistor_1452_out, transistor_1453_out, transistor_1456_out,
       transistor_1457_out, transistor_1460_out, transistor_1461_out, transistor_1464_out,
       transistor_1465_out, transistor_1468_out, transistor_1469_out, transistor_1472_out,
       transistor_1473_out, transistor_1477_out, transistor_1478_out, transistor_1479_out,
       transistor_1480_out, transistor_1481_out, transistor_1482_out, transistor_1483_out,
       transistor_1484_out, transistor_1485_out, transistor_1490_out, transistor_1493_out,
       transistor_1496_out, transistor_1499_out, transistor_1502_out, transistor_1505_out,
       transistor_1508_out, transistor_1511_out, transistor_1513_out, transistor_1515_out,
       transistor_1517_out, transistor_1519_out, transistor_1521_out, transistor_1523_out,
       transistor_1525_out, transistor_1527_out, transistor_1529_out, transistor_1530_out,
       transistor_1533_out, transistor_1534_out, transistor_1537_out, transistor_1538_out,
       transistor_1541_out, transistor_1542_out, transistor_1545_out, transistor_1546_out,
       transistor_1549_out, transistor_1550_out, transistor_1553_out, transistor_1554_out,
       transistor_1557_out, transistor_1558_out, transistor_1561_out, transistor_1563_out,
       transistor_1565_out, transistor_1566_out, transistor_1567_out, transistor_1568_out,
       transistor_1569_out, transistor_1570_out, transistor_1571_out, transistor_1572_out,
       transistor_1573_out, transistor_1576_out, transistor_1577_out, transistor_1580_out,
       transistor_1581_out, transistor_1584_out, transistor_1586_out, transistor_1588_out,
       transistor_1589_out, transistor_1592_out, transistor_1594_out, transistor_1596_out,
       transistor_1597_out, transistor_1600_out, transistor_1602_out, transistor_1604_out,
       transistor_1606_out, transistor_1608_out, transistor_1609_out, transistor_1610_out,
       transistor_1614_out, transistor_1617_out, transistor_1620_out, transistor_1623_out,
       transistor_1626_out, transistor_1629_out, transistor_1632_out, transistor_1635_out,
       transistor_1636_out, transistor_1639_out, transistor_1640_out, transistor_1644_out,
       transistor_1647_out, transistor_1648_out, transistor_1651_out, transistor_1652_out,
       transistor_1655_out, transistor_1656_out, transistor_1659_out, transistor_1660_out,
       transistor_1663_out, transistor_1664_out, transistor_1667_out, transistor_1668_out,
       transistor_1671_out, transistor_1672_out, transistor_1675_out, transistor_1678_out,
       transistor_1679_out, transistor_1681_out, transistor_1685_out, transistor_1686_out,
       transistor_1687_out, transistor_1688_out, transistor_1689_out, transistor_1690_out,
       transistor_1691_out, transistor_1692_out, transistor_1693_out, transistor_1695_out,
       transistor_1697_out, transistor_1700_out, transistor_1703_out, transistor_1706_out,
       transistor_1709_out, transistor_1712_out, transistor_1715_out, transistor_1718_out,
       transistor_1721_out, transistor_1724_out, transistor_1725_out, transistor_1729_out,
       transistor_1730_out, transistor_1732_out, transistor_1733_out, transistor_1735_out,
       transistor_1736_out, transistor_1738_out, transistor_1739_out, transistor_1741_out,
       transistor_1742_out, transistor_1744_out, transistor_1745_out, transistor_1747_out,
       transistor_1748_out, transistor_1750_out, transistor_1751_out, transistor_1753_out,
       transistor_1755_out, transistor_1758_out, transistor_1761_out, transistor_1762_out,
       transistor_1766_out, transistor_1768_out, transistor_1771_out, transistor_1773_out,
       transistor_1776_out, transistor_1777_out, transistor_1781_out, transistor_1783_out,
       transistor_1786_out, transistor_1788_out, transistor_1791_out, transistor_1792_out,
       transistor_1796_out, transistor_1797_out, transistor_1800_out, transistor_1801_out,
       transistor_1805_out, transistor_1806_out, transistor_1807_out, transistor_1808_out,
       transistor_1809_out, transistor_1810_out, transistor_1811_out, transistor_1812_out,
       transistor_1813_out, transistor_1814_out, transistor_1816_out, transistor_1820_out,
       transistor_1823_out, transistor_1826_out, transistor_1829_out, transistor_1832_out,
       transistor_1835_out, transistor_1838_out, transistor_1841_out, transistor_1844_out,
       transistor_1845_out, transistor_1846_out, transistor_1848_out, transistor_1852_out,
       transistor_1855_out, transistor_1856_out, transistor_1859_out, transistor_1860_out,
       transistor_1863_out, transistor_1864_out, transistor_1867_out, transistor_1868_out,
       transistor_1871_out, transistor_1872_out, transistor_1875_out, transistor_1876_out,
       transistor_1879_out, transistor_1880_out, transistor_1883_out, transistor_1884_out,
       transistor_1887_out, transistor_1888_out, transistor_1891_out, transistor_1892_out,
       transistor_1896_out, transistor_1897_out, transistor_1898_out, transistor_1899_out,
       transistor_1900_out, transistor_1901_out, transistor_1902_out, transistor_1903_out,
       transistor_1904_out, transistor_1907_out, transistor_1908_out, transistor_1911_out,
       transistor_1913_out, transistor_1915_out, transistor_1917_out, transistor_1918_out,
       transistor_1921_out, transistor_1923_out, transistor_1925_out, transistor_1927_out,
       transistor_1929_out, transistor_1931_out, transistor_1933_out, transistor_1935_out,
       transistor_1937_out, transistor_1938_out, transistor_1941_out, transistor_1942_out,
       transistor_1945_out, transistor_1946_out, transistor_1949_out, transistor_1950_out,
       transistor_1956_out, transistor_1959_out, transistor_1962_out, transistor_1965_out,
       transistor_1968_out, transistor_1971_out, transistor_1974_out, transistor_1977_out,
       transistor_1980_out, transistor_1981_out, transistor_1982_out, transistor_1986_out,
       transistor_1987_out, transistor_1991_out, transistor_1993_out, transistor_1995_out,
       transistor_1999_out, transistor_2003_out, transistor_2005_out, transistor_2007_out,
       transistor_2009_out, transistor_2011_out, transistor_2013_out, transistor_2015_out,
       transistor_2017_out, transistor_2019_out, transistor_2021_out, transistor_2023_out,
       transistor_2025_out, transistor_2027_out, transistor_2029_out, transistor_2031_out,
       transistor_2033_out, transistor_2035_out, transistor_2037_out, transistor_2057_out,
       transistor_2058_out, transistor_2060_out, transistor_2062_out, transistor_2064_out,
       transistor_2066_out, transistor_2068_out, transistor_2070_out, transistor_2072_out,
       transistor_2074_out, transistor_2076_out, transistor_2081_out, transistor_2085_out,
       transistor_2089_out, transistor_2093_out, transistor_2097_out, transistor_2101_out,
       transistor_2105_out, transistor_2109_out, transistor_2113_out, transistor_2117_out,
       transistor_2118_out, transistor_2120_out, transistor_2124_out, transistor_2128_out,
       transistor_2130_out, transistor_2132_out, transistor_2134_out, transistor_2136_out,
       transistor_2138_out, transistor_2140_out, transistor_2142_out, transistor_2144_out,
       transistor_2146_out, transistor_2148_out, transistor_2150_out, transistor_2152_out,
       transistor_2154_out, transistor_2156_out, transistor_2158_out, transistor_2160_out,
       transistor_2163_out, transistor_2183_out, transistor_2185_out, transistor_2187_out,
       transistor_2189_out, transistor_2191_out, transistor_2193_out, transistor_2195_out,
       transistor_2197_out, transistor_2199_out, transistor_2201_out, transistor_2203_out,
       transistor_2207_out, transistor_2211_out, transistor_2215_out, transistor_2219_out,
       transistor_2223_out, transistor_2227_out, transistor_2231_out, transistor_2235_out,
       transistor_2239_out, transistor_2243_out, transistor_2245_out, transistor_2247_out,
       transistor_2255_out, transistor_2257_out, transistor_2259_out, transistor_2261_out,
       transistor_2263_out, transistor_2265_out, transistor_2267_out, transistor_2269_out,
       transistor_2271_out, transistor_2273_out, transistor_2275_out, transistor_2277_out,
       transistor_2279_out, transistor_2281_out, transistor_2283_out, transistor_2285_out,
       transistor_2287_out, transistor_2289_out, transistor_2291_out, transistor_2311_out,
       transistor_2315_out, transistor_2317_out, transistor_2319_out, transistor_2321_out,
       transistor_2323_out, transistor_2325_out, transistor_2327_out, transistor_2329_out,
       transistor_2331_out, transistor_2333_out, transistor_2337_out, transistor_2341_out,
       transistor_2345_out, transistor_2349_out, transistor_2353_out, transistor_2357_out,
       transistor_2361_out, transistor_2369_out, transistor_2371_out, transistor_2373_out,
       transistor_2375_out, transistor_2377_out, transistor_2379_out, transistor_2381_out,
       transistor_2383_out, transistor_2385_out, transistor_2387_out, transistor_2391_out,
       transistor_2395_out, transistor_2399_out, transistor_2403_out, transistor_2407_out,
       transistor_2411_out, transistor_2415_out, transistor_2419_out, transistor_2425_out,
       transistor_2429_out, transistor_2431_out, transistor_2435_out, transistor_2437_out,
       transistor_2441_out, transistor_2443_out, transistor_2447_out, transistor_2449_out,
       transistor_2453_out, transistor_2455_out, transistor_2459_out, transistor_2461_out,
       transistor_2465_out, transistor_2467_out, transistor_2471_out, transistor_2473_out,
       transistor_2477_out, transistor_2478_out, transistor_2479_out, transistor_2480_out,
       transistor_2481_out, transistor_2482_out, transistor_2483_out, transistor_2484_out,
       transistor_2486_out, transistor_2490_out, transistor_2493_out, transistor_2496_out,
       transistor_2499_out, transistor_2502_out, transistor_2505_out, transistor_2508_out,
       transistor_2511_out, transistor_2513_out, transistor_2516_out, transistor_2517_out,
       transistor_2519_out, transistor_2521_out, transistor_2523_out, transistor_2525_out,
       transistor_2527_out, transistor_2529_out, transistor_2535_out, transistor_2536_out,
       transistor_2538_out, transistor_2541_out, transistor_2544_out, transistor_2547_out,
       transistor_2550_out, transistor_2553_out, transistor_2556_out, transistor_2559_out,
       transistor_2564_out, undriven, undriven_2, undriven_3, undriven_4, undriven_5, undriven_6, undriven_7,
       undriven_8;

  Transistor transistor_1 (.in(1'b1), .out(transistor_1_out), .gate(clk_w));
  Transistor transistor_2 (.in(1'b1), .out(transistor_2_out), .gate(transistor_1_out));
  Transistor #(.\type ("n")) transistor_3 (.in(1'b0), .out(transistor_2_out), .gate(transistor_1_out));
  Transistor transistor_4 (.in(1'b1), .out(transistor_4_out), .gate(transistor_2_out));
  Transistor #(.\type ("n")) transistor_5 (.in(1'b0), .out(transistor_4_out), .gate(transistor_2_out));
  Transistor transistor_6 (.in(1'b1), .out(transistor_6_out), .gate(transistor_2_out));
  Transistor #(.\type ("n")) transistor_7 (.in(1'b0), .out(transistor_6_out), .gate(transistor_2_out));
  Transistor transistor_8 (.in(1'b1), .out(transistor_8_out), .gate(transistor_2_out));
  Transistor #(.\type ("n")) transistor_9 (.in(1'b0), .out(transistor_8_out), .gate(transistor_2_out));
  Transistor transistor_10 (.in(1'b1), .out(transistor_10_out), .gate(transistor_2_out));
  Transistor #(.\type ("n")) transistor_11 (.in(1'b0), .out(transistor_10_out), .gate(transistor_2_out));
  Transistor transistor_12 (.in(1'b1), .out(transistor_12_out), .gate(transistor_2_out));
  Transistor #(.\type ("n")) transistor_13 (.in(1'b0), .out(transistor_12_out), .gate(transistor_2_out));
  Transistor transistor_14 (.in(1'b1), .out(transistor_14_out), .gate(transistor_2_out));
  Transistor #(.\type ("n")) transistor_15 (.in(1'b0), .out(transistor_14_out), .gate(transistor_2_out));
  Transistor transistor_16 (.in(1'b1), .out(transistor_16_out), .gate(transistor_2_out));
  Transistor #(.\type ("n")) transistor_17 (.in(1'b0), .out(transistor_16_out), .gate(transistor_2_out));
  Transistor transistor_18 (.in(1'b1), .out(transistor_18_out), .gate(transistor_2_out));
  Transistor #(.\type ("n")) transistor_19 (.in(1'b0), .out(transistor_18_out), .gate(transistor_2_out));
  Transistor transistor_20 (.in(1'b1), .out(transistor_20_out), .gate(mar));
  Transistor #(.\type ("n")) transistor_21 (.in(1'b0), .out(transistor_20_out), .gate(mar));
  Transistor transistor_22 (.in(1'b1), .out(transistor_22_out), .gate(rx0));
  Transistor #(.\type ("n")) transistor_23 (.in(1'b0), .out(transistor_22_out), .gate(rx0));
  Transistor transistor_24 (.in(1'b1), .out(transistor_24_out), .gate(rx1));
  Transistor #(.\type ("n")) transistor_25 (.in(1'b0), .out(transistor_24_out), .gate(rx1));
  Transistor transistor_26 (.in(1'b1), .out(transistor_1_out), .gate(w));
  Transistor #(.\type ("n")) transistor_27 (.in(_0), .out(transistor_27_out), .gate(transistor_2_out));
  Transistor #(.gate("br")) transistor_28 (.in(_0), .out(transistor_27_out), .gate(transistor_4_out));
  Transistor #(.\type ("n")) transistor_29 (.in(transistor_93_out), .out(transistor_27_out), .gate(transistor_4_out));
  Transistor #(.gate("br")) transistor_30 (.in(transistor_93_out), .out(transistor_27_out), .gate(transistor_2_out));
  Transistor #(.\type ("n")) transistor_31 (.in(_1), .out(transistor_31_out), .gate(transistor_2_out));
  Transistor #(.gate("br")) transistor_32 (.in(_1), .out(transistor_31_out), .gate(transistor_6_out));
  Transistor #(.\type ("n")) transistor_33 (.in(transistor_97_out), .out(transistor_31_out), .gate(transistor_6_out));
  Transistor #(.gate("br")) transistor_34 (.in(transistor_97_out), .out(transistor_31_out), .gate(transistor_2_out));
  Transistor #(.\type ("n")) transistor_35 (.in(_2), .out(transistor_35_out), .gate(transistor_2_out));
  Transistor #(.gate("br")) transistor_36 (.in(_2), .out(transistor_35_out), .gate(transistor_8_out));
  Transistor #(.\type ("n")) transistor_37 (.in(transistor_101_out), .out(transistor_35_out), .gate(transistor_8_out));
  Transistor #(.gate("br")) transistor_38 (.in(transistor_101_out), .out(transistor_35_out), .gate(transistor_2_out));
  Transistor #(.\type ("n")) transistor_39 (.in(_3), .out(transistor_39_out), .gate(transistor_2_out));
  Transistor #(.gate("br")) transistor_40 (.in(_3), .out(transistor_39_out), .gate(transistor_10_out));
  Transistor #(.\type ("n")) transistor_41 (.in(transistor_105_out), .out(transistor_39_out), .gate(transistor_10_out));
  Transistor #(.gate("br")) transistor_42 (.in(transistor_105_out), .out(transistor_39_out), .gate(transistor_2_out));
  Transistor #(.\type ("n")) transistor_43 (.in(_4), .out(transistor_43_out), .gate(transistor_2_out));
  Transistor #(.gate("br")) transistor_44 (.in(_4), .out(transistor_43_out), .gate(transistor_12_out));
  Transistor #(.\type ("n")) transistor_45 (.in(transistor_109_out), .out(transistor_43_out), .gate(transistor_12_out));
  Transistor #(.gate("br")) transistor_46 (.in(transistor_109_out), .out(transistor_43_out), .gate(transistor_2_out));
  Transistor #(.\type ("n")) transistor_47 (.in(_5), .out(transistor_47_out), .gate(transistor_2_out));
  Transistor #(.gate("br")) transistor_48 (.in(_5), .out(transistor_47_out), .gate(transistor_14_out));
  Transistor #(.\type ("n")) transistor_49 (.in(transistor_113_out), .out(transistor_47_out), .gate(transistor_14_out));
  Transistor #(.gate("br")) transistor_50 (.in(transistor_113_out), .out(transistor_47_out), .gate(transistor_2_out));
  Transistor #(.\type ("n")) transistor_51 (.in(_6), .out(transistor_51_out), .gate(transistor_2_out));
  Transistor #(.gate("br")) transistor_52 (.in(_6), .out(transistor_51_out), .gate(transistor_16_out));
  Transistor #(.\type ("n")) transistor_53 (.in(transistor_117_out), .out(transistor_51_out), .gate(transistor_16_out));
  Transistor #(.gate("br")) transistor_54 (.in(transistor_117_out), .out(transistor_51_out), .gate(transistor_2_out));
  Transistor #(.\type ("n")) transistor_55 (.in(_7), .out(transistor_55_out), .gate(transistor_2_out));
  Transistor #(.gate("br")) transistor_56 (.in(_7), .out(transistor_55_out), .gate(transistor_18_out));
  Transistor #(.\type ("n")) transistor_57 (.in(transistor_121_out), .out(transistor_55_out), .gate(transistor_18_out));
  Transistor #(.gate("br")) transistor_58 (.in(transistor_121_out), .out(transistor_55_out), .gate(transistor_2_out));
  Transistor #(.\type ("n")) transistor_59 (.in(_7), .out(transistor_59_out), .gate(mar));
  Transistor #(.gate("br")) transistor_60 (.in(_7), .out(transistor_59_out), .gate(transistor_20_out));
  Transistor #(.\type ("n")) transistor_61 (.in(transistor_125_out), .out(transistor_59_out), .gate(transistor_20_out));
  Transistor #(.gate("br")) transistor_62 (.in(transistor_125_out), .out(transistor_59_out), .gate(mar));
  Transistor transistor_63 (.in(1'b1), .out(transistor_1_out), .gate(transistor_129_out));
  Transistor #(.\type ("n")) transistor_64 (.in(transistor_65_out), .out(transistor_1_out), .gate(clk_w));
  Transistor #(.\type ("n")) transistor_65 (.in(transistor_66_out), .out(transistor_65_out), .gate(w));
  Transistor #(.\type ("n")) transistor_66 (.in(1'b0), .out(transistor_66_out), .gate(transistor_129_out));
  Transistor transistor_67 (.in(1'b1), .out(transistor_67_out), .gate(rst));
  Transistor #(.\type ("n")) transistor_68 (.in(1'b0), .out(transistor_67_out), .gate(rst));
  Transistor transistor_69 (.in(1'b1), .out(transistor_69_out), .gate(rst));
  Transistor #(.\type ("n")) transistor_70 (.in(1'b0), .out(transistor_69_out), .gate(rst));
  Transistor transistor_71 (.in(1'b1), .out(transistor_71_out), .gate(rst));
  Transistor #(.\type ("n")) transistor_72 (.in(1'b0), .out(transistor_71_out), .gate(rst));
  Transistor transistor_73 (.in(1'b1), .out(transistor_73_out), .gate(rst));
  Transistor #(.\type ("n")) transistor_74 (.in(1'b0), .out(transistor_73_out), .gate(rst));
  Transistor transistor_75 (.in(1'b1), .out(transistor_75_out), .gate(rst));
  Transistor #(.\type ("n")) transistor_76 (.in(1'b0), .out(transistor_75_out), .gate(rst));
  Transistor transistor_77 (.in(1'b1), .out(transistor_77_out), .gate(rst));
  Transistor #(.\type ("n")) transistor_78 (.in(1'b0), .out(transistor_77_out), .gate(rst));
  Transistor transistor_79 (.in(1'b1), .out(transistor_79_out), .gate(rst));
  Transistor #(.\type ("n")) transistor_80 (.in(1'b0), .out(transistor_79_out), .gate(rst));
  Transistor transistor_81 (.in(1'b1), .out(transistor_81_out), .gate(rst));
  Transistor #(.\type ("n")) transistor_82 (.in(1'b0), .out(transistor_81_out), .gate(rst));
  Transistor transistor_83 (.in(1'b1), .out(transistor_83_out), .gate(rst));
  Transistor #(.\type ("n")) transistor_84 (.in(1'b0), .out(transistor_83_out), .gate(rst));
  LED led_1 (.in(transistor_125_out));
  Transistor transistor_85 (.in(1'b1), .out(transistor_85_out), .gate(transistor_22_out));
  Transistor transistor_86 (.in(1'b1), .out(transistor_85_out), .gate(transistor_24_out));
  Transistor #(.\type ("n")) transistor_87 (.in(transistor_88_out), .out(transistor_85_out), .gate(transistor_22_out));
  Transistor #(.\type ("n")) transistor_88 (.in(1'b0), .out(transistor_88_out), .gate(transistor_24_out));
  Transistor transistor_89 (.in(1'b1), .out(transistor_89_out), .gate(r));
  Transistor transistor_90 (.in(1'b1), .out(transistor_89_out), .gate(clk_r));
  Transistor transistor_91 (.in(1'b1), .out(transistor_91_out), .gate(transistor_89_out));
  Transistor #(.\type ("n")) transistor_92 (.in(1'b0), .out(transistor_91_out), .gate(transistor_89_out));
  Transistor #(.\type ("n")) transistor_93 (.in(1'b0), .out(transistor_93_out), .gate(rst));
  Transistor #(.gate("br")) transistor_94 (.in(1'b0), .out(transistor_93_out), .gate(transistor_67_out));
  Transistor #(.\type ("n")) transistor_95 (.in(transistor_27_out), .out(transistor_93_out), .gate(transistor_67_out));
  Transistor #(.gate("br")) transistor_96 (.in(transistor_27_out), .out(transistor_93_out), .gate(rst));
  Transistor #(.\type ("n")) transistor_97 (.in(1'b0), .out(transistor_97_out), .gate(rst));
  Transistor #(.gate("br")) transistor_98 (.in(1'b0), .out(transistor_97_out), .gate(transistor_69_out));
  Transistor #(.\type ("n")) transistor_99 (.in(transistor_31_out), .out(transistor_97_out), .gate(transistor_69_out));
  Transistor #(.gate("br")) transistor_100 (.in(transistor_31_out), .out(transistor_97_out), .gate(rst));
  Transistor #(.\type ("n")) transistor_101 (.in(1'b0), .out(transistor_101_out), .gate(rst));
  Transistor #(.gate("br")) transistor_102 (.in(1'b0), .out(transistor_101_out), .gate(transistor_71_out));
  Transistor #(.\type ("n")) transistor_103 (
    .in(transistor_35_out), .out(transistor_101_out), .gate(transistor_71_out));
  Transistor #(.gate("br")) transistor_104 (.in(transistor_35_out), .out(transistor_101_out), .gate(rst));
  Transistor #(.\type ("n")) transistor_105 (.in(1'b0), .out(transistor_105_out), .gate(rst));
  Transistor #(.gate("br")) transistor_106 (.in(1'b0), .out(transistor_105_out), .gate(transistor_73_out));
  Transistor #(.\type ("n")) transistor_107 (
    .in(transistor_39_out), .out(transistor_105_out), .gate(transistor_73_out));
  Transistor #(.gate("br")) transistor_108 (.in(transistor_39_out), .out(transistor_105_out), .gate(rst));
  Transistor #(.\type ("n")) transistor_109 (.in(1'b0), .out(transistor_109_out), .gate(rst));
  Transistor #(.gate("br")) transistor_110 (.in(1'b0), .out(transistor_109_out), .gate(transistor_75_out));
  Transistor #(.\type ("n")) transistor_111 (
    .in(transistor_43_out), .out(transistor_109_out), .gate(transistor_75_out));
  Transistor #(.gate("br")) transistor_112 (.in(transistor_43_out), .out(transistor_109_out), .gate(rst));
  Transistor #(.\type ("n")) transistor_113 (.in(1'b0), .out(transistor_113_out), .gate(rst));
  Transistor #(.gate("br")) transistor_114 (.in(1'b0), .out(transistor_113_out), .gate(transistor_77_out));
  Transistor #(.\type ("n")) transistor_115 (
    .in(transistor_47_out), .out(transistor_113_out), .gate(transistor_77_out));
  Transistor #(.gate("br")) transistor_116 (.in(transistor_47_out), .out(transistor_113_out), .gate(rst));
  Transistor #(.\type ("n")) transistor_117 (.in(1'b0), .out(transistor_117_out), .gate(rst));
  Transistor #(.gate("br")) transistor_118 (.in(1'b0), .out(transistor_117_out), .gate(transistor_79_out));
  Transistor #(.\type ("n")) transistor_119 (
    .in(transistor_51_out), .out(transistor_117_out), .gate(transistor_79_out));
  Transistor #(.gate("br")) transistor_120 (.in(transistor_51_out), .out(transistor_117_out), .gate(rst));
  Transistor #(.\type ("n")) transistor_121 (.in(1'b0), .out(transistor_121_out), .gate(rst));
  Transistor #(.gate("br")) transistor_122 (.in(1'b0), .out(transistor_121_out), .gate(transistor_81_out));
  Transistor #(.\type ("n")) transistor_123 (
    .in(transistor_55_out), .out(transistor_121_out), .gate(transistor_81_out));
  Transistor #(.gate("br")) transistor_124 (.in(transistor_55_out), .out(transistor_121_out), .gate(rst));
  Transistor #(.\type ("n")) transistor_125 (.in(1'b0), .out(transistor_125_out), .gate(rst));
  Transistor #(.gate("br")) transistor_126 (.in(1'b0), .out(transistor_125_out), .gate(transistor_83_out));
  Transistor #(.\type ("n")) transistor_127 (
    .in(transistor_59_out), .out(transistor_125_out), .gate(transistor_83_out));
  Transistor #(.gate("br")) transistor_128 (.in(transistor_59_out), .out(transistor_125_out), .gate(rst));
  Transistor transistor_129 (.in(1'b1), .out(transistor_129_out), .gate(transistor_85_out));
  Transistor #(.\type ("n")) transistor_130 (.in(1'b0), .out(transistor_129_out), .gate(transistor_85_out));
  Transistor transistor_131 (.in(1'b1), .out(transistor_89_out), .gate(transistor_129_out));
  Transistor #(.\type ("n")) transistor_132 (.in(transistor_133_out), .out(transistor_89_out), .gate(clk_r));
  Transistor #(.\type ("n")) transistor_133 (.in(transistor_134_out), .out(transistor_133_out), .gate(r));
  Transistor #(.\type ("n")) transistor_134 (.in(1'b0), .out(transistor_134_out), .gate(transistor_129_out));
  Transistor transistor_135 (.in(1'b1), .out(transistor_135_out), .gate(transistor_91_out));
  Transistor #(.\type ("n")) transistor_136 (.in(1'b0), .out(transistor_135_out), .gate(transistor_91_out));
  Transistor #(.\type ("n")) transistor_137 (
    .in(transistor_93_out), .out(transistor_137_out), .gate(transistor_91_out));
  Transistor #(.gate("br")) transistor_138 (
    .in(transistor_93_out), .out(transistor_137_out), .gate(transistor_135_out));
  Transistor transistor_139 (.in(1'b1), .out(transistor_139_out), .gate(transistor_91_out));
  Transistor #(.\type ("n")) transistor_140 (.in(1'b0), .out(transistor_139_out), .gate(transistor_91_out));
  Transistor #(.\type ("n")) transistor_141 (
    .in(transistor_97_out), .out(transistor_141_out), .gate(transistor_91_out));
  Transistor #(.gate("br")) transistor_142 (
    .in(transistor_97_out), .out(transistor_141_out), .gate(transistor_139_out));
  Transistor transistor_143 (.in(1'b1), .out(transistor_143_out), .gate(transistor_91_out));
  Transistor #(.\type ("n")) transistor_144 (.in(1'b0), .out(transistor_143_out), .gate(transistor_91_out));
  Transistor #(.\type ("n")) transistor_145 (
    .in(transistor_101_out), .out(transistor_145_out), .gate(transistor_91_out));
  Transistor #(.gate("br")) transistor_146 (
    .in(transistor_101_out), .out(transistor_145_out), .gate(transistor_143_out));
  Transistor transistor_147 (.in(1'b1), .out(transistor_147_out), .gate(transistor_91_out));
  Transistor #(.\type ("n")) transistor_148 (.in(1'b0), .out(transistor_147_out), .gate(transistor_91_out));
  Transistor #(.gate("br")) transistor_149 (
    .in(transistor_105_out), .out(transistor_149_out), .gate(transistor_147_out));
  Transistor #(.\type ("n")) transistor_150 (
    .in(transistor_105_out), .out(transistor_149_out), .gate(transistor_91_out));
  Transistor transistor_151 (.in(1'b1), .out(transistor_151_out), .gate(transistor_91_out));
  Transistor #(.\type ("n")) transistor_152 (.in(1'b0), .out(transistor_151_out), .gate(transistor_91_out));
  Transistor #(.\type ("n")) transistor_153 (
    .in(transistor_109_out), .out(transistor_153_out), .gate(transistor_91_out));
  Transistor #(.gate("br")) transistor_154 (
    .in(transistor_109_out), .out(transistor_153_out), .gate(transistor_151_out));
  Transistor transistor_155 (.in(1'b1), .out(transistor_155_out), .gate(transistor_91_out));
  Transistor #(.\type ("n")) transistor_156 (.in(1'b0), .out(transistor_155_out), .gate(transistor_91_out));
  Transistor #(.gate("br")) transistor_157 (
    .in(transistor_113_out), .out(transistor_157_out), .gate(transistor_155_out));
  Transistor #(.\type ("n")) transistor_158 (
    .in(transistor_113_out), .out(transistor_157_out), .gate(transistor_91_out));
  Transistor transistor_159 (.in(1'b1), .out(transistor_159_out), .gate(transistor_91_out));
  Transistor #(.\type ("n")) transistor_160 (.in(1'b0), .out(transistor_159_out), .gate(transistor_91_out));
  Transistor #(.\type ("n")) transistor_161 (
    .in(transistor_117_out), .out(transistor_161_out), .gate(transistor_91_out));
  Transistor #(.gate("br")) transistor_162 (
    .in(transistor_117_out), .out(transistor_161_out), .gate(transistor_159_out));
  Transistor transistor_163 (.in(1'b1), .out(transistor_163_out), .gate(transistor_91_out));
  Transistor #(.\type ("n")) transistor_164 (.in(1'b0), .out(transistor_163_out), .gate(transistor_91_out));
  Transistor #(.gate("br")) transistor_165 (
    .in(transistor_121_out), .out(transistor_165_out), .gate(transistor_163_out));
  Transistor #(.\type ("n")) transistor_166 (
    .in(transistor_121_out), .out(transistor_165_out), .gate(transistor_91_out));
  Transistor transistor_167 (.in(1'b1), .out(transistor_167_out), .gate(mar));
  Transistor #(.\type ("n")) transistor_168 (.in(1'b0), .out(transistor_167_out), .gate(mar));
  Transistor transistor_169 (.in(1'b1), .out(transistor_169_out), .gate(clk_w));
  Transistor transistor_170 (.in(1'b1), .out(transistor_170_out), .gate(transistor_169_out));
  Transistor #(.\type ("n")) transistor_171 (.in(1'b0), .out(transistor_170_out), .gate(transistor_169_out));
  Transistor transistor_172 (.in(1'b1), .out(transistor_172_out), .gate(transistor_170_out));
  Transistor #(.\type ("n")) transistor_173 (.in(1'b0), .out(transistor_172_out), .gate(transistor_170_out));
  Transistor transistor_174 (.in(1'b1), .out(transistor_174_out), .gate(transistor_170_out));
  Transistor #(.\type ("n")) transistor_175 (.in(1'b0), .out(transistor_174_out), .gate(transistor_170_out));
  Transistor transistor_176 (.in(1'b1), .out(transistor_176_out), .gate(transistor_170_out));
  Transistor #(.\type ("n")) transistor_177 (.in(1'b0), .out(transistor_176_out), .gate(transistor_170_out));
  Transistor transistor_178 (.in(1'b1), .out(transistor_178_out), .gate(transistor_170_out));
  Transistor #(.\type ("n")) transistor_179 (.in(1'b0), .out(transistor_178_out), .gate(transistor_170_out));
  Transistor transistor_180 (.in(1'b1), .out(transistor_180_out), .gate(transistor_170_out));
  Transistor #(.\type ("n")) transistor_181 (.in(1'b0), .out(transistor_180_out), .gate(transistor_170_out));
  Transistor transistor_182 (.in(1'b1), .out(transistor_182_out), .gate(transistor_170_out));
  Transistor #(.\type ("n")) transistor_183 (.in(1'b0), .out(transistor_182_out), .gate(transistor_170_out));
  Transistor transistor_184 (.in(1'b1), .out(transistor_184_out), .gate(transistor_170_out));
  Transistor #(.\type ("n")) transistor_185 (.in(1'b0), .out(transistor_184_out), .gate(transistor_170_out));
  Transistor transistor_186 (.in(1'b1), .out(transistor_186_out), .gate(transistor_170_out));
  Transistor #(.\type ("n")) transistor_187 (.in(1'b0), .out(transistor_186_out), .gate(transistor_170_out));
  Transistor #(.\type ("n")) transistor_188 (.in(_6), .out(transistor_188_out), .gate(mar));
  Transistor #(.gate("br")) transistor_189 (.in(_6), .out(transistor_188_out), .gate(transistor_167_out));
  Transistor transistor_190 (.in(1'b1), .out(transistor_190_out), .gate(rst));
  Transistor #(.\type ("n")) transistor_191 (.in(1'b0), .out(transistor_190_out), .gate(rst));
  Transistor #(.\type ("n")) transistor_192 (
    .in(transistor_233_out), .out(transistor_188_out), .gate(transistor_167_out));
  Transistor #(.gate("br")) transistor_193 (.in(transistor_233_out), .out(transistor_188_out), .gate(mar));
  LED led_2 (.in(transistor_233_out));
  Transistor transistor_194 (.in(1'b1), .out(transistor_194_out), .gate(rx1));
  Transistor #(.\type ("n")) transistor_195 (.in(1'b0), .out(transistor_194_out), .gate(rx1));
  Transistor transistor_196 (.in(1'b1), .out(transistor_169_out), .gate(w));
  Transistor transistor_197 (.in(1'b1), .out(transistor_169_out), .gate(transistor_307_out));
  Transistor #(.\type ("n")) transistor_198 (.in(transistor_199_out), .out(transistor_169_out), .gate(clk_w));
  Transistor #(.\type ("n")) transistor_199 (.in(transistor_200_out), .out(transistor_199_out), .gate(w));
  Transistor #(.\type ("n")) transistor_200 (.in(1'b0), .out(transistor_200_out), .gate(transistor_307_out));
  Transistor #(.\type ("n")) transistor_201 (.in(_0), .out(transistor_201_out), .gate(transistor_170_out));
  Transistor #(.gate("br")) transistor_202 (.in(_0), .out(transistor_201_out), .gate(transistor_172_out));
  Transistor #(.\type ("n")) transistor_203 (
    .in(transistor_263_out), .out(transistor_201_out), .gate(transistor_172_out));
  Transistor #(.gate("br")) transistor_204 (
    .in(transistor_263_out), .out(transistor_201_out), .gate(transistor_170_out));
  Transistor #(.\type ("n")) transistor_205 (.in(_1), .out(transistor_205_out), .gate(transistor_170_out));
  Transistor #(.gate("br")) transistor_206 (.in(_1), .out(transistor_205_out), .gate(transistor_174_out));
  Transistor #(.\type ("n")) transistor_207 (
    .in(transistor_268_out), .out(transistor_205_out), .gate(transistor_174_out));
  Transistor #(.gate("br")) transistor_208 (
    .in(transistor_268_out), .out(transistor_205_out), .gate(transistor_170_out));
  Transistor #(.\type ("n")) transistor_209 (.in(_2), .out(transistor_209_out), .gate(transistor_170_out));
  Transistor #(.gate("br")) transistor_210 (.in(_2), .out(transistor_209_out), .gate(transistor_176_out));
  Transistor #(.\type ("n")) transistor_211 (
    .in(transistor_273_out), .out(transistor_209_out), .gate(transistor_176_out));
  Transistor #(.gate("br")) transistor_212 (
    .in(transistor_273_out), .out(transistor_209_out), .gate(transistor_170_out));
  Transistor #(.\type ("n")) transistor_213 (.in(_3), .out(transistor_213_out), .gate(transistor_170_out));
  Transistor #(.gate("br")) transistor_214 (.in(_3), .out(transistor_213_out), .gate(transistor_178_out));
  Transistor #(.\type ("n")) transistor_215 (
    .in(transistor_278_out), .out(transistor_213_out), .gate(transistor_178_out));
  Transistor #(.gate("br")) transistor_216 (
    .in(transistor_278_out), .out(transistor_213_out), .gate(transistor_170_out));
  Transistor #(.\type ("n")) transistor_217 (.in(_4), .out(transistor_217_out), .gate(transistor_170_out));
  Transistor #(.gate("br")) transistor_218 (.in(_4), .out(transistor_217_out), .gate(transistor_180_out));
  Transistor #(.\type ("n")) transistor_219 (
    .in(transistor_283_out), .out(transistor_217_out), .gate(transistor_180_out));
  Transistor #(.gate("br")) transistor_220 (
    .in(transistor_283_out), .out(transistor_217_out), .gate(transistor_170_out));
  Transistor #(.\type ("n")) transistor_221 (.in(_5), .out(transistor_221_out), .gate(transistor_170_out));
  Transistor #(.gate("br")) transistor_222 (.in(_5), .out(transistor_221_out), .gate(transistor_182_out));
  Transistor #(.\type ("n")) transistor_223 (
    .in(transistor_288_out), .out(transistor_221_out), .gate(transistor_182_out));
  Transistor #(.gate("br")) transistor_224 (
    .in(transistor_288_out), .out(transistor_221_out), .gate(transistor_170_out));
  Transistor #(.\type ("n")) transistor_225 (.in(_6), .out(transistor_225_out), .gate(transistor_170_out));
  Transistor #(.gate("br")) transistor_226 (.in(_6), .out(transistor_225_out), .gate(transistor_184_out));
  Transistor #(.\type ("n")) transistor_227 (
    .in(transistor_293_out), .out(transistor_225_out), .gate(transistor_184_out));
  Transistor #(.gate("br")) transistor_228 (
    .in(transistor_293_out), .out(transistor_225_out), .gate(transistor_170_out));
  Transistor #(.\type ("n")) transistor_229 (.in(_7), .out(transistor_229_out), .gate(transistor_170_out));
  Transistor #(.gate("br")) transistor_230 (.in(_7), .out(transistor_229_out), .gate(transistor_186_out));
  Transistor #(.\type ("n")) transistor_231 (
    .in(transistor_298_out), .out(transistor_229_out), .gate(transistor_186_out));
  Transistor #(.gate("br")) transistor_232 (
    .in(transistor_298_out), .out(transistor_229_out), .gate(transistor_170_out));
  Transistor #(.\type ("n")) transistor_233 (.in(1'b0), .out(transistor_233_out), .gate(rst));
  Transistor #(.gate("br")) transistor_234 (.in(1'b0), .out(transistor_233_out), .gate(transistor_190_out));
  Transistor #(.\type ("n")) transistor_235 (
    .in(transistor_188_out), .out(transistor_233_out), .gate(transistor_190_out));
  Transistor #(.gate("br")) transistor_236 (.in(transistor_188_out), .out(transistor_233_out), .gate(rst));
  Transistor transistor_237 (.in(1'b1), .out(transistor_237_out), .gate(rx0));
  Transistor transistor_238 (.in(1'b1), .out(transistor_238_out), .gate(rst));
  Transistor #(.\type ("n")) transistor_239 (.in(1'b0), .out(transistor_238_out), .gate(rst));
  Transistor transistor_240 (.in(1'b1), .out(transistor_240_out), .gate(rst));
  Transistor #(.\type ("n")) transistor_241 (.in(1'b0), .out(transistor_240_out), .gate(rst));
  Transistor transistor_242 (.in(1'b1), .out(transistor_242_out), .gate(rst));
  Transistor #(.\type ("n")) transistor_243 (.in(1'b0), .out(transistor_242_out), .gate(rst));
  Transistor transistor_244 (.in(1'b1), .out(transistor_244_out), .gate(rst));
  Transistor #(.\type ("n")) transistor_245 (.in(1'b0), .out(transistor_244_out), .gate(rst));
  Transistor transistor_246 (.in(1'b1), .out(transistor_246_out), .gate(rst));
  Transistor #(.\type ("n")) transistor_247 (.in(1'b0), .out(transistor_246_out), .gate(rst));
  Transistor transistor_248 (.in(1'b1), .out(transistor_248_out), .gate(rst));
  Transistor #(.\type ("n")) transistor_249 (.in(1'b0), .out(transistor_248_out), .gate(rst));
  Transistor transistor_250 (.in(1'b1), .out(transistor_250_out), .gate(rst));
  Transistor #(.\type ("n")) transistor_251 (.in(1'b0), .out(transistor_250_out), .gate(rst));
  Transistor transistor_252 (.in(1'b1), .out(transistor_252_out), .gate(rst));
  Transistor #(.\type ("n")) transistor_253 (.in(1'b0), .out(transistor_252_out), .gate(rst));
  Transistor transistor_254 (.in(1'b1), .out(transistor_254_out), .gate(mar));
  Transistor #(.\type ("n")) transistor_255 (.in(1'b0), .out(transistor_254_out), .gate(mar));
  Transistor transistor_256 (.in(1'b1), .out(transistor_237_out), .gate(transistor_194_out));
  Transistor #(.\type ("n")) transistor_257 (.in(transistor_258_out), .out(transistor_237_out), .gate(rx0));
  Transistor #(.\type ("n")) transistor_258 (.in(1'b0), .out(transistor_258_out), .gate(transistor_194_out));
  Transistor transistor_259 (.in(1'b1), .out(transistor_259_out), .gate(r));
  Transistor transistor_260 (.in(1'b1), .out(transistor_259_out), .gate(clk_r));
  Transistor transistor_261 (.in(1'b1), .out(transistor_261_out), .gate(transistor_259_out));
  Transistor #(.\type ("n")) transistor_262 (.in(1'b0), .out(transistor_261_out), .gate(transistor_259_out));
  Transistor #(.\type ("n")) transistor_263 (.in(1'b0), .out(transistor_263_out), .gate(rst));
  Transistor #(.gate("br")) transistor_264 (.in(1'b0), .out(transistor_263_out), .gate(transistor_238_out));
  Transistor #(.\type ("n")) transistor_265 (
    .in(transistor_201_out), .out(transistor_263_out), .gate(transistor_238_out));
  Transistor #(.gate("br")) transistor_266 (.in(transistor_201_out), .out(transistor_263_out), .gate(rst));
  Transistor #(.\type ("n")) transistor_267 (
    .in(transistor_263_out), .out(transistor_137_out), .gate(transistor_261_out));
  Transistor #(.\type ("n")) transistor_268 (.in(1'b0), .out(transistor_268_out), .gate(rst));
  Transistor #(.gate("br")) transistor_269 (.in(1'b0), .out(transistor_268_out), .gate(transistor_240_out));
  Transistor #(.\type ("n")) transistor_270 (
    .in(transistor_205_out), .out(transistor_268_out), .gate(transistor_240_out));
  Transistor #(.gate("br")) transistor_271 (.in(transistor_205_out), .out(transistor_268_out), .gate(rst));
  Transistor #(.\type ("n")) transistor_272 (
    .in(transistor_268_out), .out(transistor_141_out), .gate(transistor_261_out));
  Transistor #(.\type ("n")) transistor_273 (.in(1'b0), .out(transistor_273_out), .gate(rst));
  Transistor #(.gate("br")) transistor_274 (.in(1'b0), .out(transistor_273_out), .gate(transistor_242_out));
  Transistor #(.\type ("n")) transistor_275 (
    .in(transistor_209_out), .out(transistor_273_out), .gate(transistor_242_out));
  Transistor #(.gate("br")) transistor_276 (.in(transistor_209_out), .out(transistor_273_out), .gate(rst));
  Transistor #(.\type ("n")) transistor_277 (
    .in(transistor_273_out), .out(transistor_145_out), .gate(transistor_261_out));
  Transistor #(.\type ("n")) transistor_278 (.in(1'b0), .out(transistor_278_out), .gate(rst));
  Transistor #(.gate("br")) transistor_279 (.in(1'b0), .out(transistor_278_out), .gate(transistor_244_out));
  Transistor #(.\type ("n")) transistor_280 (
    .in(transistor_213_out), .out(transistor_278_out), .gate(transistor_244_out));
  Transistor #(.gate("br")) transistor_281 (.in(transistor_213_out), .out(transistor_278_out), .gate(rst));
  Transistor #(.\type ("n")) transistor_282 (
    .in(transistor_278_out), .out(transistor_149_out), .gate(transistor_261_out));
  Transistor #(.\type ("n")) transistor_283 (.in(1'b0), .out(transistor_283_out), .gate(rst));
  Transistor #(.gate("br")) transistor_284 (.in(1'b0), .out(transistor_283_out), .gate(transistor_246_out));
  Transistor #(.\type ("n")) transistor_285 (
    .in(transistor_217_out), .out(transistor_283_out), .gate(transistor_246_out));
  Transistor #(.gate("br")) transistor_286 (.in(transistor_217_out), .out(transistor_283_out), .gate(rst));
  Transistor #(.\type ("n")) transistor_287 (
    .in(transistor_283_out), .out(transistor_153_out), .gate(transistor_261_out));
  Transistor #(.\type ("n")) transistor_288 (.in(1'b0), .out(transistor_288_out), .gate(rst));
  Transistor #(.gate("br")) transistor_289 (.in(1'b0), .out(transistor_288_out), .gate(transistor_248_out));
  Transistor #(.\type ("n")) transistor_290 (
    .in(transistor_221_out), .out(transistor_288_out), .gate(transistor_248_out));
  Transistor #(.gate("br")) transistor_291 (.in(transistor_221_out), .out(transistor_288_out), .gate(rst));
  Transistor #(.\type ("n")) transistor_292 (
    .in(transistor_288_out), .out(transistor_157_out), .gate(transistor_261_out));
  Transistor #(.\type ("n")) transistor_293 (.in(1'b0), .out(transistor_293_out), .gate(rst));
  Transistor #(.gate("br")) transistor_294 (.in(1'b0), .out(transistor_293_out), .gate(transistor_250_out));
  Transistor #(.\type ("n")) transistor_295 (
    .in(transistor_225_out), .out(transistor_293_out), .gate(transistor_250_out));
  Transistor #(.gate("br")) transistor_296 (.in(transistor_225_out), .out(transistor_293_out), .gate(rst));
  Transistor #(.\type ("n")) transistor_297 (
    .in(transistor_293_out), .out(transistor_161_out), .gate(transistor_261_out));
  Transistor #(.\type ("n")) transistor_298 (.in(1'b0), .out(transistor_298_out), .gate(rst));
  Transistor #(.gate("br")) transistor_299 (.in(1'b0), .out(transistor_298_out), .gate(transistor_252_out));
  Transistor #(.\type ("n")) transistor_300 (
    .in(transistor_229_out), .out(transistor_298_out), .gate(transistor_252_out));
  Transistor #(.gate("br")) transistor_301 (.in(transistor_229_out), .out(transistor_298_out), .gate(rst));
  Transistor #(.\type ("n")) transistor_302 (
    .in(transistor_298_out), .out(transistor_165_out), .gate(transistor_261_out));
  Transistor #(.\type ("n")) transistor_303 (.in(_5), .out(transistor_303_out), .gate(mar));
  Transistor #(.gate("br")) transistor_304 (.in(_5), .out(transistor_303_out), .gate(transistor_254_out));
  Transistor #(.\type ("n")) transistor_305 (
    .in(transistor_358_out), .out(transistor_303_out), .gate(transistor_254_out));
  Transistor #(.gate("br")) transistor_306 (.in(transistor_358_out), .out(transistor_303_out), .gate(mar));
  LED led_3 (.in(transistor_358_out));
  Transistor transistor_307 (.in(1'b1), .out(transistor_307_out), .gate(transistor_237_out));
  Transistor #(.\type ("n")) transistor_308 (.in(1'b0), .out(transistor_307_out), .gate(transistor_237_out));
  Transistor transistor_309 (.in(1'b1), .out(transistor_259_out), .gate(transistor_307_out));
  Transistor #(.\type ("n")) transistor_310 (.in(transistor_311_out), .out(transistor_259_out), .gate(clk_r));
  Transistor #(.\type ("n")) transistor_311 (.in(transistor_312_out), .out(transistor_311_out), .gate(r));
  Transistor #(.\type ("n")) transistor_312 (.in(1'b0), .out(transistor_312_out), .gate(transistor_307_out));
  Transistor transistor_313 (.in(1'b1), .out(transistor_313_out), .gate(transistor_261_out));
  Transistor #(.\type ("n")) transistor_314 (.in(1'b0), .out(transistor_313_out), .gate(transistor_261_out));
  Transistor #(.gate("br")) transistor_315 (
    .in(transistor_263_out), .out(transistor_137_out), .gate(transistor_313_out));
  Transistor transistor_316 (.in(1'b1), .out(transistor_316_out), .gate(transistor_261_out));
  Transistor #(.\type ("n")) transistor_317 (.in(1'b0), .out(transistor_316_out), .gate(transistor_261_out));
  Transistor #(.gate("br")) transistor_318 (
    .in(transistor_268_out), .out(transistor_141_out), .gate(transistor_316_out));
  Transistor transistor_319 (.in(1'b1), .out(transistor_319_out), .gate(transistor_261_out));
  Transistor #(.\type ("n")) transistor_320 (.in(1'b0), .out(transistor_319_out), .gate(transistor_261_out));
  Transistor #(.gate("br")) transistor_321 (
    .in(transistor_273_out), .out(transistor_145_out), .gate(transistor_319_out));
  Transistor transistor_322 (.in(1'b1), .out(transistor_322_out), .gate(transistor_261_out));
  Transistor #(.\type ("n")) transistor_323 (.in(1'b0), .out(transistor_322_out), .gate(transistor_261_out));
  Transistor #(.gate("br")) transistor_324 (
    .in(transistor_278_out), .out(transistor_149_out), .gate(transistor_322_out));
  Transistor transistor_325 (.in(1'b1), .out(transistor_325_out), .gate(transistor_261_out));
  Transistor #(.\type ("n")) transistor_326 (.in(1'b0), .out(transistor_325_out), .gate(transistor_261_out));
  Transistor #(.gate("br")) transistor_327 (
    .in(transistor_283_out), .out(transistor_153_out), .gate(transistor_325_out));
  Transistor transistor_328 (.in(1'b1), .out(transistor_328_out), .gate(transistor_261_out));
  Transistor #(.\type ("n")) transistor_329 (.in(1'b0), .out(transistor_328_out), .gate(transistor_261_out));
  Transistor #(.gate("br")) transistor_330 (
    .in(transistor_288_out), .out(transistor_157_out), .gate(transistor_328_out));
  Transistor transistor_331 (.in(1'b1), .out(transistor_331_out), .gate(transistor_261_out));
  Transistor #(.\type ("n")) transistor_332 (.in(1'b0), .out(transistor_331_out), .gate(transistor_261_out));
  Transistor #(.gate("br")) transistor_333 (
    .in(transistor_293_out), .out(transistor_161_out), .gate(transistor_331_out));
  Transistor transistor_334 (.in(1'b1), .out(transistor_334_out), .gate(transistor_261_out));
  Transistor #(.\type ("n")) transistor_335 (.in(1'b0), .out(transistor_334_out), .gate(transistor_261_out));
  Transistor #(.gate("br")) transistor_336 (
    .in(transistor_298_out), .out(transistor_165_out), .gate(transistor_334_out));
  Transistor transistor_337 (.in(1'b1), .out(transistor_337_out), .gate(rst));
  Transistor #(.\type ("n")) transistor_338 (.in(1'b0), .out(transistor_337_out), .gate(rst));
  Transistor transistor_339 (.in(1'b1), .out(transistor_339_out), .gate(clk_w));
  Transistor transistor_340 (.in(1'b1), .out(transistor_340_out), .gate(transistor_339_out));
  Transistor #(.\type ("n")) transistor_341 (.in(1'b0), .out(transistor_340_out), .gate(transistor_339_out));
  Transistor transistor_342 (.in(1'b1), .out(transistor_342_out), .gate(transistor_340_out));
  Transistor #(.\type ("n")) transistor_343 (.in(1'b0), .out(transistor_342_out), .gate(transistor_340_out));
  Transistor transistor_344 (.in(1'b1), .out(transistor_344_out), .gate(transistor_340_out));
  Transistor #(.\type ("n")) transistor_345 (.in(1'b0), .out(transistor_344_out), .gate(transistor_340_out));
  Transistor transistor_346 (.in(1'b1), .out(transistor_346_out), .gate(transistor_340_out));
  Transistor #(.\type ("n")) transistor_347 (.in(1'b0), .out(transistor_346_out), .gate(transistor_340_out));
  Transistor transistor_348 (.in(1'b1), .out(transistor_348_out), .gate(transistor_340_out));
  Transistor #(.\type ("n")) transistor_349 (.in(1'b0), .out(transistor_348_out), .gate(transistor_340_out));
  Transistor transistor_350 (.in(1'b1), .out(transistor_350_out), .gate(transistor_340_out));
  Transistor #(.\type ("n")) transistor_351 (.in(1'b0), .out(transistor_350_out), .gate(transistor_340_out));
  Transistor transistor_352 (.in(1'b1), .out(transistor_352_out), .gate(transistor_340_out));
  Transistor #(.\type ("n")) transistor_353 (.in(1'b0), .out(transistor_352_out), .gate(transistor_340_out));
  Transistor transistor_354 (.in(1'b1), .out(transistor_354_out), .gate(transistor_340_out));
  Transistor #(.\type ("n")) transistor_355 (.in(1'b0), .out(transistor_354_out), .gate(transistor_340_out));
  Transistor transistor_356 (.in(1'b1), .out(transistor_356_out), .gate(transistor_340_out));
  Transistor #(.\type ("n")) transistor_357 (.in(1'b0), .out(transistor_356_out), .gate(transistor_340_out));
  Transistor #(.\type ("n")) transistor_358 (.in(1'b0), .out(transistor_358_out), .gate(rst));
  Transistor #(.gate("br")) transistor_359 (.in(1'b0), .out(transistor_358_out), .gate(transistor_337_out));
  Transistor #(.\type ("n")) transistor_360 (
    .in(transistor_303_out), .out(transistor_358_out), .gate(transistor_337_out));
  Transistor #(.gate("br")) transistor_361 (.in(transistor_303_out), .out(transistor_358_out), .gate(rst));
  Transistor #(.\type ("n")) transistor_362 (.in(1'b0), .out(transistor_362_out), .gate(rx0));
  Transistor transistor_363 (.in(1'b1), .out(transistor_362_out), .gate(rx0));
  Transistor transistor_364 (.in(1'b1), .out(transistor_339_out), .gate(w));
  Transistor transistor_365 (.in(1'b1), .out(transistor_339_out), .gate(transistor_461_out));
  Transistor #(.\type ("n")) transistor_366 (.in(transistor_367_out), .out(transistor_339_out), .gate(clk_w));
  Transistor #(.\type ("n")) transistor_367 (.in(transistor_368_out), .out(transistor_367_out), .gate(w));
  Transistor #(.\type ("n")) transistor_368 (.in(1'b0), .out(transistor_368_out), .gate(transistor_461_out));
  Transistor #(.\type ("n")) transistor_369 (.in(_0), .out(transistor_369_out), .gate(transistor_340_out));
  Transistor #(.gate("br")) transistor_370 (.in(_0), .out(transistor_369_out), .gate(transistor_342_out));
  Transistor #(.\type ("n")) transistor_371 (
    .in(transistor_411_out), .out(transistor_369_out), .gate(transistor_342_out));
  Transistor #(.gate("br")) transistor_372 (
    .in(transistor_411_out), .out(transistor_369_out), .gate(transistor_340_out));
  Transistor #(.\type ("n")) transistor_373 (.in(_1), .out(transistor_373_out), .gate(transistor_340_out));
  Transistor #(.gate("br")) transistor_374 (.in(_1), .out(transistor_373_out), .gate(transistor_344_out));
  Transistor #(.\type ("n")) transistor_375 (
    .in(transistor_417_out), .out(transistor_373_out), .gate(transistor_344_out));
  Transistor #(.gate("br")) transistor_376 (
    .in(transistor_417_out), .out(transistor_373_out), .gate(transistor_340_out));
  Transistor #(.\type ("n")) transistor_377 (.in(_2), .out(transistor_377_out), .gate(transistor_340_out));
  Transistor #(.gate("br")) transistor_378 (.in(_2), .out(transistor_377_out), .gate(transistor_346_out));
  Transistor #(.\type ("n")) transistor_379 (
    .in(transistor_423_out), .out(transistor_377_out), .gate(transistor_346_out));
  Transistor #(.gate("br")) transistor_380 (
    .in(transistor_423_out), .out(transistor_377_out), .gate(transistor_340_out));
  Transistor #(.\type ("n")) transistor_381 (.in(_3), .out(transistor_381_out), .gate(transistor_340_out));
  Transistor #(.gate("br")) transistor_382 (.in(_3), .out(transistor_381_out), .gate(transistor_348_out));
  Transistor #(.\type ("n")) transistor_383 (
    .in(transistor_429_out), .out(transistor_381_out), .gate(transistor_348_out));
  Transistor #(.gate("br")) transistor_384 (
    .in(transistor_429_out), .out(transistor_381_out), .gate(transistor_340_out));
  Transistor #(.\type ("n")) transistor_385 (.in(_4), .out(transistor_385_out), .gate(transistor_340_out));
  Transistor #(.gate("br")) transistor_386 (.in(_4), .out(transistor_385_out), .gate(transistor_350_out));
  Transistor #(.\type ("n")) transistor_387 (
    .in(transistor_435_out), .out(transistor_385_out), .gate(transistor_350_out));
  Transistor #(.gate("br")) transistor_388 (
    .in(transistor_435_out), .out(transistor_385_out), .gate(transistor_340_out));
  Transistor #(.\type ("n")) transistor_389 (.in(_5), .out(transistor_389_out), .gate(transistor_340_out));
  Transistor #(.gate("br")) transistor_390 (.in(_5), .out(transistor_389_out), .gate(transistor_352_out));
  Transistor #(.\type ("n")) transistor_391 (
    .in(transistor_441_out), .out(transistor_389_out), .gate(transistor_352_out));
  Transistor #(.gate("br")) transistor_392 (
    .in(transistor_441_out), .out(transistor_389_out), .gate(transistor_340_out));
  Transistor #(.\type ("n")) transistor_393 (.in(_6), .out(transistor_393_out), .gate(transistor_340_out));
  Transistor #(.gate("br")) transistor_394 (.in(_6), .out(transistor_393_out), .gate(transistor_354_out));
  Transistor #(.\type ("n")) transistor_395 (
    .in(transistor_447_out), .out(transistor_393_out), .gate(transistor_354_out));
  Transistor #(.gate("br")) transistor_396 (
    .in(transistor_447_out), .out(transistor_393_out), .gate(transistor_340_out));
  Transistor #(.\type ("n")) transistor_397 (.in(_7), .out(transistor_397_out), .gate(transistor_340_out));
  Transistor #(.gate("br")) transistor_398 (.in(_7), .out(transistor_397_out), .gate(transistor_356_out));
  Transistor #(.\type ("n")) transistor_399 (
    .in(transistor_453_out), .out(transistor_397_out), .gate(transistor_356_out));
  Transistor #(.gate("br")) transistor_400 (
    .in(transistor_453_out), .out(transistor_397_out), .gate(transistor_340_out));
  Transistor #(.\type ("n")) transistor_401 (.in(_4), .out(transistor_401_out), .gate(mar));
  Transistor #(.gate("br")) transistor_402 (.in(_4), .out(transistor_401_out), .gate(transistor_403_out));
  Transistor transistor_403 (.in(1'b1), .out(transistor_403_out), .gate(mar));
  Transistor #(.\type ("n")) transistor_404 (.in(1'b0), .out(transistor_403_out), .gate(mar));
  Transistor #(.\type ("n")) transistor_405 (
    .in(transistor_499_out), .out(transistor_401_out), .gate(transistor_403_out));
  Transistor #(.gate("br")) transistor_406 (.in(transistor_499_out), .out(transistor_401_out), .gate(mar));
  Transistor transistor_407 (.in(1'b1), .out(transistor_407_out), .gate(transistor_362_out));
  Transistor transistor_408 (.in(1'b1), .out(transistor_408_out), .gate(clk_r));
  Transistor transistor_409 (.in(1'b1), .out(transistor_409_out), .gate(transistor_408_out));
  Transistor #(.\type ("n")) transistor_410 (.in(1'b0), .out(transistor_409_out), .gate(transistor_408_out));
  Transistor #(.\type ("n")) transistor_411 (.in(1'b0), .out(transistor_411_out), .gate(rst));
  Transistor #(.gate("br")) transistor_412 (.in(1'b0), .out(transistor_411_out), .gate(transistor_413_out));
  Transistor transistor_413 (.in(1'b1), .out(transistor_413_out), .gate(rst));
  Transistor #(.\type ("n")) transistor_414 (.in(1'b0), .out(transistor_413_out), .gate(rst));
  Transistor #(.\type ("n")) transistor_415 (
    .in(transistor_369_out), .out(transistor_411_out), .gate(transistor_413_out));
  Transistor #(.gate("br")) transistor_416 (.in(transistor_369_out), .out(transistor_411_out), .gate(rst));
  Transistor #(.\type ("n")) transistor_417 (.in(1'b0), .out(transistor_417_out), .gate(rst));
  Transistor #(.gate("br")) transistor_418 (.in(1'b0), .out(transistor_417_out), .gate(transistor_419_out));
  Transistor transistor_419 (.in(1'b1), .out(transistor_419_out), .gate(rst));
  Transistor #(.\type ("n")) transistor_420 (.in(1'b0), .out(transistor_419_out), .gate(rst));
  Transistor #(.\type ("n")) transistor_421 (
    .in(transistor_373_out), .out(transistor_417_out), .gate(transistor_419_out));
  Transistor #(.gate("br")) transistor_422 (.in(transistor_373_out), .out(transistor_417_out), .gate(rst));
  Transistor #(.\type ("n")) transistor_423 (.in(1'b0), .out(transistor_423_out), .gate(rst));
  Transistor #(.gate("br")) transistor_424 (.in(1'b0), .out(transistor_423_out), .gate(transistor_425_out));
  Transistor transistor_425 (.in(1'b1), .out(transistor_425_out), .gate(rst));
  Transistor #(.\type ("n")) transistor_426 (.in(1'b0), .out(transistor_425_out), .gate(rst));
  Transistor #(.\type ("n")) transistor_427 (
    .in(transistor_377_out), .out(transistor_423_out), .gate(transistor_425_out));
  Transistor #(.gate("br")) transistor_428 (.in(transistor_377_out), .out(transistor_423_out), .gate(rst));
  Transistor #(.\type ("n")) transistor_429 (.in(1'b0), .out(transistor_429_out), .gate(rst));
  Transistor #(.gate("br")) transistor_430 (.in(1'b0), .out(transistor_429_out), .gate(transistor_431_out));
  Transistor transistor_431 (.in(1'b1), .out(transistor_431_out), .gate(rst));
  Transistor #(.\type ("n")) transistor_432 (.in(1'b0), .out(transistor_431_out), .gate(rst));
  Transistor #(.\type ("n")) transistor_433 (
    .in(transistor_381_out), .out(transistor_429_out), .gate(transistor_431_out));
  Transistor #(.gate("br")) transistor_434 (.in(transistor_381_out), .out(transistor_429_out), .gate(rst));
  Transistor #(.\type ("n")) transistor_435 (.in(1'b0), .out(transistor_435_out), .gate(rst));
  Transistor #(.gate("br")) transistor_436 (.in(1'b0), .out(transistor_435_out), .gate(transistor_437_out));
  Transistor transistor_437 (.in(1'b1), .out(transistor_437_out), .gate(rst));
  Transistor #(.\type ("n")) transistor_438 (.in(1'b0), .out(transistor_437_out), .gate(rst));
  Transistor #(.\type ("n")) transistor_439 (
    .in(transistor_385_out), .out(transistor_435_out), .gate(transistor_437_out));
  Transistor #(.gate("br")) transistor_440 (.in(transistor_385_out), .out(transistor_435_out), .gate(rst));
  Transistor #(.\type ("n")) transistor_441 (.in(1'b0), .out(transistor_441_out), .gate(rst));
  Transistor #(.gate("br")) transistor_442 (.in(1'b0), .out(transistor_441_out), .gate(transistor_443_out));
  Transistor transistor_443 (.in(1'b1), .out(transistor_443_out), .gate(rst));
  Transistor #(.\type ("n")) transistor_444 (.in(1'b0), .out(transistor_443_out), .gate(rst));
  Transistor #(.\type ("n")) transistor_445 (
    .in(transistor_389_out), .out(transistor_441_out), .gate(transistor_443_out));
  Transistor #(.gate("br")) transistor_446 (.in(transistor_389_out), .out(transistor_441_out), .gate(rst));
  Transistor #(.\type ("n")) transistor_447 (.in(1'b0), .out(transistor_447_out), .gate(rst));
  Transistor #(.gate("br")) transistor_448 (.in(1'b0), .out(transistor_447_out), .gate(transistor_449_out));
  Transistor transistor_449 (.in(1'b1), .out(transistor_449_out), .gate(rst));
  Transistor #(.\type ("n")) transistor_450 (.in(1'b0), .out(transistor_449_out), .gate(rst));
  Transistor #(.\type ("n")) transistor_451 (
    .in(transistor_393_out), .out(transistor_447_out), .gate(transistor_449_out));
  Transistor #(.gate("br")) transistor_452 (.in(transistor_393_out), .out(transistor_447_out), .gate(rst));
  Transistor #(.\type ("n")) transistor_453 (.in(1'b0), .out(transistor_453_out), .gate(rst));
  Transistor #(.gate("br")) transistor_454 (.in(1'b0), .out(transistor_453_out), .gate(transistor_455_out));
  Transistor transistor_455 (.in(1'b1), .out(transistor_455_out), .gate(rst));
  Transistor #(.\type ("n")) transistor_456 (.in(1'b0), .out(transistor_455_out), .gate(rst));
  Transistor #(.\type ("n")) transistor_457 (
    .in(transistor_397_out), .out(transistor_453_out), .gate(transistor_455_out));
  Transistor #(.gate("br")) transistor_458 (.in(transistor_397_out), .out(transistor_453_out), .gate(rst));
  Transistor transistor_459 (.in(1'b1), .out(transistor_459_out), .gate(rst));
  Transistor #(.\type ("n")) transistor_460 (.in(1'b0), .out(transistor_459_out), .gate(rst));
  LED led_4 (.in(transistor_499_out));
  Transistor transistor_461 (.in(1'b1), .out(transistor_461_out), .gate(transistor_407_out));
  Transistor transistor_462 (.in(1'b1), .out(transistor_407_out), .gate(rx1));
  Transistor #(.\type ("n")) transistor_463 (
    .in(transistor_465_out), .out(transistor_407_out), .gate(transistor_362_out));
  Transistor #(.\type ("n")) transistor_464 (.in(1'b0), .out(transistor_461_out), .gate(transistor_407_out));
  Transistor #(.\type ("n")) transistor_465 (.in(1'b0), .out(transistor_465_out), .gate(rx1));
  Transistor transistor_466 (.in(1'b1), .out(transistor_408_out), .gate(r));
  Transistor transistor_467 (.in(1'b1), .out(transistor_467_out), .gate(transistor_409_out));
  Transistor #(.\type ("n")) transistor_468 (.in(1'b0), .out(transistor_467_out), .gate(transistor_409_out));
  Transistor #(.gate("br")) transistor_469 (
    .in(transistor_411_out), .out(transistor_137_out), .gate(transistor_467_out));
  Transistor #(.\type ("n")) transistor_470 (
    .in(transistor_411_out), .out(transistor_137_out), .gate(transistor_409_out));
  Transistor transistor_471 (.in(1'b1), .out(transistor_471_out), .gate(transistor_409_out));
  Transistor #(.\type ("n")) transistor_472 (.in(1'b0), .out(transistor_471_out), .gate(transistor_409_out));
  Transistor #(.gate("br")) transistor_473 (
    .in(transistor_417_out), .out(transistor_141_out), .gate(transistor_471_out));
  Transistor #(.\type ("n")) transistor_474 (
    .in(transistor_417_out), .out(transistor_141_out), .gate(transistor_409_out));
  Transistor transistor_475 (.in(1'b1), .out(transistor_475_out), .gate(transistor_409_out));
  Transistor #(.\type ("n")) transistor_476 (.in(1'b0), .out(transistor_475_out), .gate(transistor_409_out));
  Transistor #(.\type ("n")) transistor_477 (
    .in(transistor_423_out), .out(transistor_145_out), .gate(transistor_409_out));
  Transistor #(.gate("br")) transistor_478 (
    .in(transistor_423_out), .out(transistor_145_out), .gate(transistor_475_out));
  Transistor transistor_479 (.in(1'b1), .out(transistor_479_out), .gate(transistor_409_out));
  Transistor #(.\type ("n")) transistor_480 (.in(1'b0), .out(transistor_479_out), .gate(transistor_409_out));
  Transistor #(.gate("br")) transistor_481 (
    .in(transistor_429_out), .out(transistor_149_out), .gate(transistor_479_out));
  Transistor #(.\type ("n")) transistor_482 (
    .in(transistor_429_out), .out(transistor_149_out), .gate(transistor_409_out));
  Transistor transistor_483 (.in(1'b1), .out(transistor_483_out), .gate(transistor_409_out));
  Transistor #(.\type ("n")) transistor_484 (.in(1'b0), .out(transistor_483_out), .gate(transistor_409_out));
  Transistor #(.\type ("n")) transistor_485 (
    .in(transistor_435_out), .out(transistor_153_out), .gate(transistor_409_out));
  Transistor #(.gate("br")) transistor_486 (
    .in(transistor_435_out), .out(transistor_153_out), .gate(transistor_483_out));
  Transistor transistor_487 (.in(1'b1), .out(transistor_487_out), .gate(transistor_409_out));
  Transistor #(.\type ("n")) transistor_488 (.in(1'b0), .out(transistor_487_out), .gate(transistor_409_out));
  Transistor #(.gate("br")) transistor_489 (
    .in(transistor_441_out), .out(transistor_157_out), .gate(transistor_487_out));
  Transistor #(.\type ("n")) transistor_490 (
    .in(transistor_441_out), .out(transistor_157_out), .gate(transistor_409_out));
  Transistor transistor_491 (.in(1'b1), .out(transistor_491_out), .gate(transistor_409_out));
  Transistor #(.\type ("n")) transistor_492 (.in(1'b0), .out(transistor_491_out), .gate(transistor_409_out));
  Transistor #(.\type ("n")) transistor_493 (
    .in(transistor_447_out), .out(transistor_161_out), .gate(transistor_409_out));
  Transistor #(.gate("br")) transistor_494 (
    .in(transistor_447_out), .out(transistor_161_out), .gate(transistor_491_out));
  Transistor transistor_495 (.in(1'b1), .out(transistor_495_out), .gate(transistor_409_out));
  Transistor #(.\type ("n")) transistor_496 (.in(1'b0), .out(transistor_495_out), .gate(transistor_409_out));
  Transistor #(.gate("br")) transistor_497 (
    .in(transistor_453_out), .out(transistor_165_out), .gate(transistor_495_out));
  Transistor #(.\type ("n")) transistor_498 (
    .in(transistor_453_out), .out(transistor_165_out), .gate(transistor_409_out));
  Transistor #(.\type ("n")) transistor_499 (.in(1'b0), .out(transistor_499_out), .gate(rst));
  Transistor #(.gate("br")) transistor_500 (.in(1'b0), .out(transistor_499_out), .gate(transistor_459_out));
  Transistor #(.\type ("n")) transistor_501 (
    .in(transistor_401_out), .out(transistor_499_out), .gate(transistor_459_out));
  Transistor #(.gate("br")) transistor_502 (.in(transistor_401_out), .out(transistor_499_out), .gate(rst));
  Transistor transistor_503 (.in(1'b1), .out(transistor_408_out), .gate(transistor_461_out));
  Transistor #(.\type ("n")) transistor_504 (.in(transistor_505_out), .out(transistor_408_out), .gate(clk_r));
  Transistor #(.\type ("n")) transistor_505 (.in(transistor_506_out), .out(transistor_505_out), .gate(r));
  Transistor #(.\type ("n")) transistor_506 (.in(1'b0), .out(transistor_506_out), .gate(transistor_461_out));
  Transistor transistor_507 (.in(1'b1), .out(transistor_507_out), .gate(mar));
  Transistor #(.\type ("n")) transistor_508 (.in(1'b0), .out(transistor_507_out), .gate(mar));
  Transistor transistor_509 (.in(1'b1), .out(transistor_509_out), .gate(w));
  Transistor transistor_510 (.in(1'b1), .out(transistor_509_out), .gate(clk_w));
  Transistor transistor_511 (.in(1'b1), .out(transistor_511_out), .gate(transistor_509_out));
  Transistor #(.\type ("n")) transistor_512 (.in(1'b0), .out(transistor_511_out), .gate(transistor_509_out));
  Transistor #(.\type ("n")) transistor_513 (.in(_0), .out(transistor_513_out), .gate(transistor_511_out));
  Transistor #(.gate("br")) transistor_514 (.in(_0), .out(transistor_513_out), .gate(transistor_515_out));
  Transistor transistor_515 (.in(1'b1), .out(transistor_515_out), .gate(transistor_511_out));
  Transistor #(.\type ("n")) transistor_516 (.in(1'b0), .out(transistor_515_out), .gate(transistor_511_out));
  Transistor #(.\type ("n")) transistor_517 (
    .in(transistor_595_out), .out(transistor_513_out), .gate(transistor_515_out));
  Transistor #(.gate("br")) transistor_518 (
    .in(transistor_595_out), .out(transistor_513_out), .gate(transistor_511_out));
  Transistor #(.\type ("n")) transistor_519 (.in(_1), .out(transistor_519_out), .gate(transistor_511_out));
  Transistor #(.gate("br")) transistor_520 (.in(_1), .out(transistor_519_out), .gate(transistor_521_out));
  Transistor transistor_521 (.in(1'b1), .out(transistor_521_out), .gate(transistor_511_out));
  Transistor #(.\type ("n")) transistor_522 (.in(1'b0), .out(transistor_521_out), .gate(transistor_511_out));
  Transistor #(.\type ("n")) transistor_523 (
    .in(transistor_599_out), .out(transistor_519_out), .gate(transistor_521_out));
  Transistor #(.gate("br")) transistor_524 (
    .in(transistor_599_out), .out(transistor_519_out), .gate(transistor_511_out));
  Transistor #(.\type ("n")) transistor_525 (.in(_2), .out(transistor_525_out), .gate(transistor_511_out));
  Transistor #(.gate("br")) transistor_526 (.in(_2), .out(transistor_525_out), .gate(transistor_527_out));
  Transistor transistor_527 (.in(1'b1), .out(transistor_527_out), .gate(transistor_511_out));
  Transistor #(.\type ("n")) transistor_528 (.in(1'b0), .out(transistor_527_out), .gate(transistor_511_out));
  Transistor #(.\type ("n")) transistor_529 (
    .in(transistor_603_out), .out(transistor_525_out), .gate(transistor_527_out));
  Transistor #(.gate("br")) transistor_530 (
    .in(transistor_603_out), .out(transistor_525_out), .gate(transistor_511_out));
  Transistor #(.\type ("n")) transistor_531 (.in(_3), .out(transistor_531_out), .gate(transistor_511_out));
  Transistor #(.gate("br")) transistor_532 (.in(_3), .out(transistor_531_out), .gate(transistor_533_out));
  Transistor transistor_533 (.in(1'b1), .out(transistor_533_out), .gate(transistor_511_out));
  Transistor #(.\type ("n")) transistor_534 (.in(1'b0), .out(transistor_533_out), .gate(transistor_511_out));
  Transistor #(.\type ("n")) transistor_535 (
    .in(transistor_607_out), .out(transistor_531_out), .gate(transistor_533_out));
  Transistor #(.gate("br")) transistor_536 (
    .in(transistor_607_out), .out(transistor_531_out), .gate(transistor_511_out));
  Transistor #(.\type ("n")) transistor_537 (.in(_4), .out(transistor_537_out), .gate(transistor_511_out));
  Transistor #(.gate("br")) transistor_538 (.in(_4), .out(transistor_537_out), .gate(transistor_539_out));
  Transistor transistor_539 (.in(1'b1), .out(transistor_539_out), .gate(transistor_511_out));
  Transistor #(.\type ("n")) transistor_540 (.in(1'b0), .out(transistor_539_out), .gate(transistor_511_out));
  Transistor #(.\type ("n")) transistor_541 (
    .in(transistor_611_out), .out(transistor_537_out), .gate(transistor_539_out));
  Transistor #(.gate("br")) transistor_542 (
    .in(transistor_611_out), .out(transistor_537_out), .gate(transistor_511_out));
  Transistor #(.\type ("n")) transistor_543 (.in(_5), .out(transistor_543_out), .gate(transistor_511_out));
  Transistor #(.gate("br")) transistor_544 (.in(_5), .out(transistor_543_out), .gate(transistor_545_out));
  Transistor transistor_545 (.in(1'b1), .out(transistor_545_out), .gate(transistor_511_out));
  Transistor #(.\type ("n")) transistor_546 (.in(1'b0), .out(transistor_545_out), .gate(transistor_511_out));
  Transistor #(.\type ("n")) transistor_547 (
    .in(transistor_615_out), .out(transistor_543_out), .gate(transistor_545_out));
  Transistor #(.gate("br")) transistor_548 (
    .in(transistor_615_out), .out(transistor_543_out), .gate(transistor_511_out));
  Transistor #(.\type ("n")) transistor_549 (.in(_6), .out(transistor_549_out), .gate(transistor_511_out));
  Transistor #(.gate("br")) transistor_550 (.in(_6), .out(transistor_549_out), .gate(transistor_551_out));
  Transistor transistor_551 (.in(1'b1), .out(transistor_551_out), .gate(transistor_511_out));
  Transistor #(.\type ("n")) transistor_552 (.in(1'b0), .out(transistor_551_out), .gate(transistor_511_out));
  Transistor #(.\type ("n")) transistor_553 (
    .in(transistor_619_out), .out(transistor_549_out), .gate(transistor_551_out));
  Transistor #(.gate("br")) transistor_554 (
    .in(transistor_619_out), .out(transistor_549_out), .gate(transistor_511_out));
  Transistor #(.\type ("n")) transistor_555 (.in(_7), .out(transistor_555_out), .gate(transistor_511_out));
  Transistor #(.gate("br")) transistor_556 (.in(_7), .out(transistor_555_out), .gate(transistor_557_out));
  Transistor transistor_557 (.in(1'b1), .out(transistor_557_out), .gate(transistor_511_out));
  Transistor #(.\type ("n")) transistor_558 (.in(1'b0), .out(transistor_557_out), .gate(transistor_511_out));
  Transistor #(.\type ("n")) transistor_559 (
    .in(transistor_623_out), .out(transistor_555_out), .gate(transistor_557_out));
  Transistor #(.gate("br")) transistor_560 (
    .in(transistor_623_out), .out(transistor_555_out), .gate(transistor_511_out));
  Transistor #(.\type ("n")) transistor_561 (.in(_3), .out(transistor_561_out), .gate(mar));
  Transistor #(.gate("br")) transistor_562 (.in(_3), .out(transistor_561_out), .gate(transistor_507_out));
  Transistor #(.\type ("n")) transistor_563 (
    .in(transistor_585_out), .out(transistor_561_out), .gate(transistor_507_out));
  Transistor #(.gate("br")) transistor_564 (.in(transistor_585_out), .out(transistor_561_out), .gate(mar));
  LED led_5 (.in(transistor_585_out));
  Transistor transistor_565 (.in(1'b1), .out(transistor_509_out), .gate(transistor_629_out));
  Transistor #(.\type ("n")) transistor_566 (.in(transistor_567_out), .out(transistor_509_out), .gate(clk_w));
  Transistor #(.\type ("n")) transistor_567 (.in(transistor_568_out), .out(transistor_567_out), .gate(w));
  Transistor #(.\type ("n")) transistor_568 (.in(1'b0), .out(transistor_568_out), .gate(transistor_629_out));
  Transistor transistor_569 (.in(1'b1), .out(transistor_569_out), .gate(rst));
  Transistor #(.\type ("n")) transistor_570 (.in(1'b0), .out(transistor_569_out), .gate(rst));
  Transistor transistor_571 (.in(1'b1), .out(transistor_571_out), .gate(rst));
  Transistor #(.\type ("n")) transistor_572 (.in(1'b0), .out(transistor_571_out), .gate(rst));
  Transistor transistor_573 (.in(1'b1), .out(transistor_573_out), .gate(rst));
  Transistor #(.\type ("n")) transistor_574 (.in(1'b0), .out(transistor_573_out), .gate(rst));
  Transistor transistor_575 (.in(1'b1), .out(transistor_575_out), .gate(rst));
  Transistor #(.\type ("n")) transistor_576 (.in(1'b0), .out(transistor_575_out), .gate(rst));
  Transistor transistor_577 (.in(1'b1), .out(transistor_577_out), .gate(rst));
  Transistor #(.\type ("n")) transistor_578 (.in(1'b0), .out(transistor_577_out), .gate(rst));
  Transistor transistor_579 (.in(1'b1), .out(transistor_579_out), .gate(rst));
  Transistor #(.\type ("n")) transistor_580 (.in(1'b0), .out(transistor_579_out), .gate(rst));
  Transistor transistor_581 (.in(1'b1), .out(transistor_581_out), .gate(rst));
  Transistor #(.\type ("n")) transistor_582 (.in(1'b0), .out(transistor_581_out), .gate(rst));
  Transistor transistor_583 (.in(1'b1), .out(transistor_583_out), .gate(rst));
  Transistor #(.\type ("n")) transistor_584 (.in(1'b0), .out(transistor_583_out), .gate(rst));
  Transistor #(.\type ("n")) transistor_585 (.in(1'b0), .out(transistor_585_out), .gate(rst));
  Transistor #(.gate("br")) transistor_586 (.in(1'b0), .out(transistor_585_out), .gate(transistor_587_out));
  Transistor transistor_587 (.in(1'b1), .out(transistor_587_out), .gate(rst));
  Transistor #(.\type ("n")) transistor_588 (.in(1'b0), .out(transistor_587_out), .gate(rst));
  Transistor #(.\type ("n")) transistor_589 (
    .in(transistor_561_out), .out(transistor_585_out), .gate(transistor_587_out));
  Transistor #(.gate("br")) transistor_590 (.in(transistor_561_out), .out(transistor_585_out), .gate(rst));
  Transistor transistor_591 (.in(1'b1), .out(transistor_591_out), .gate(rx0));
  Transistor transistor_592 (.in(1'b1), .out(transistor_592_out), .gate(clk_r));
  Transistor transistor_593 (.in(1'b1), .out(transistor_593_out), .gate(transistor_592_out));
  Transistor #(.\type ("n")) transistor_594 (.in(1'b0), .out(transistor_593_out), .gate(transistor_592_out));
  Transistor #(.\type ("n")) transistor_595 (.in(1'b0), .out(transistor_595_out), .gate(rst));
  Transistor #(.gate("br")) transistor_596 (.in(1'b0), .out(transistor_595_out), .gate(transistor_569_out));
  Transistor #(.\type ("n")) transistor_597 (
    .in(transistor_513_out), .out(transistor_595_out), .gate(transistor_569_out));
  Transistor #(.gate("br")) transistor_598 (.in(transistor_513_out), .out(transistor_595_out), .gate(rst));
  Transistor #(.\type ("n")) transistor_599 (.in(1'b0), .out(transistor_599_out), .gate(rst));
  Transistor #(.gate("br")) transistor_600 (.in(1'b0), .out(transistor_599_out), .gate(transistor_571_out));
  Transistor #(.\type ("n")) transistor_601 (
    .in(transistor_519_out), .out(transistor_599_out), .gate(transistor_571_out));
  Transistor #(.gate("br")) transistor_602 (.in(transistor_519_out), .out(transistor_599_out), .gate(rst));
  Transistor #(.\type ("n")) transistor_603 (.in(1'b0), .out(transistor_603_out), .gate(rst));
  Transistor #(.gate("br")) transistor_604 (.in(1'b0), .out(transistor_603_out), .gate(transistor_573_out));
  Transistor #(.\type ("n")) transistor_605 (
    .in(transistor_525_out), .out(transistor_603_out), .gate(transistor_573_out));
  Transistor #(.gate("br")) transistor_606 (.in(transistor_525_out), .out(transistor_603_out), .gate(rst));
  Transistor #(.\type ("n")) transistor_607 (.in(1'b0), .out(transistor_607_out), .gate(rst));
  Transistor #(.gate("br")) transistor_608 (.in(1'b0), .out(transistor_607_out), .gate(transistor_575_out));
  Transistor #(.\type ("n")) transistor_609 (
    .in(transistor_531_out), .out(transistor_607_out), .gate(transistor_575_out));
  Transistor #(.gate("br")) transistor_610 (.in(transistor_531_out), .out(transistor_607_out), .gate(rst));
  Transistor #(.\type ("n")) transistor_611 (.in(1'b0), .out(transistor_611_out), .gate(rst));
  Transistor #(.gate("br")) transistor_612 (.in(1'b0), .out(transistor_611_out), .gate(transistor_577_out));
  Transistor #(.\type ("n")) transistor_613 (
    .in(transistor_537_out), .out(transistor_611_out), .gate(transistor_577_out));
  Transistor #(.gate("br")) transistor_614 (.in(transistor_537_out), .out(transistor_611_out), .gate(rst));
  Transistor #(.\type ("n")) transistor_615 (.in(1'b0), .out(transistor_615_out), .gate(rst));
  Transistor #(.gate("br")) transistor_616 (.in(1'b0), .out(transistor_615_out), .gate(transistor_579_out));
  Transistor #(.\type ("n")) transistor_617 (
    .in(transistor_543_out), .out(transistor_615_out), .gate(transistor_579_out));
  Transistor #(.gate("br")) transistor_618 (.in(transistor_543_out), .out(transistor_615_out), .gate(rst));
  Transistor #(.\type ("n")) transistor_619 (.in(1'b0), .out(transistor_619_out), .gate(rst));
  Transistor #(.gate("br")) transistor_620 (.in(1'b0), .out(transistor_619_out), .gate(transistor_581_out));
  Transistor #(.\type ("n")) transistor_621 (
    .in(transistor_549_out), .out(transistor_619_out), .gate(transistor_581_out));
  Transistor #(.gate("br")) transistor_622 (.in(transistor_549_out), .out(transistor_619_out), .gate(rst));
  Transistor #(.\type ("n")) transistor_623 (.in(1'b0), .out(transistor_623_out), .gate(rst));
  Transistor #(.gate("br")) transistor_624 (.in(1'b0), .out(transistor_623_out), .gate(transistor_583_out));
  Transistor #(.\type ("n")) transistor_625 (
    .in(transistor_555_out), .out(transistor_623_out), .gate(transistor_583_out));
  Transistor #(.gate("br")) transistor_626 (.in(transistor_555_out), .out(transistor_623_out), .gate(rst));
  Transistor transistor_627 (.in(1'b1), .out(transistor_627_out), .gate(mar));
  Transistor #(.\type ("n")) transistor_628 (.in(1'b0), .out(transistor_627_out), .gate(mar));
  Transistor transistor_629 (.in(1'b1), .out(transistor_629_out), .gate(transistor_591_out));
  Transistor transistor_630 (.in(1'b1), .out(transistor_591_out), .gate(rx1));
  Transistor #(.\type ("n")) transistor_631 (.in(transistor_633_out), .out(transistor_591_out), .gate(rx0));
  Transistor #(.\type ("n")) transistor_632 (.in(1'b0), .out(transistor_629_out), .gate(transistor_591_out));
  Transistor #(.\type ("n")) transistor_633 (.in(1'b0), .out(transistor_633_out), .gate(rx1));
  Transistor transistor_634 (.in(1'b1), .out(transistor_592_out), .gate(transistor_629_out));
  Transistor transistor_635 (.in(1'b1), .out(transistor_592_out), .gate(r));
  Transistor #(.\type ("n")) transistor_636 (.in(transistor_637_out), .out(transistor_592_out), .gate(clk_r));
  Transistor #(.\type ("n")) transistor_637 (.in(transistor_638_out), .out(transistor_637_out), .gate(r));
  Transistor #(.\type ("n")) transistor_638 (.in(1'b0), .out(transistor_638_out), .gate(transistor_629_out));
  Transistor transistor_639 (.in(1'b1), .out(transistor_639_out), .gate(transistor_593_out));
  Transistor #(.\type ("n")) transistor_640 (.in(1'b0), .out(transistor_639_out), .gate(transistor_593_out));
  Transistor #(.\type ("n")) transistor_641 (
    .in(transistor_595_out), .out(transistor_137_out), .gate(transistor_593_out));
  Transistor #(.gate("br")) transistor_642 (
    .in(transistor_595_out), .out(transistor_137_out), .gate(transistor_639_out));
  Transistor transistor_643 (.in(1'b1), .out(transistor_643_out), .gate(transistor_593_out));
  Transistor #(.\type ("n")) transistor_644 (.in(1'b0), .out(transistor_643_out), .gate(transistor_593_out));
  Transistor #(.\type ("n")) transistor_645 (
    .in(transistor_599_out), .out(transistor_141_out), .gate(transistor_593_out));
  Transistor #(.gate("br")) transistor_646 (
    .in(transistor_599_out), .out(transistor_141_out), .gate(transistor_643_out));
  Transistor transistor_647 (.in(1'b1), .out(transistor_647_out), .gate(transistor_593_out));
  Transistor #(.\type ("n")) transistor_648 (.in(1'b0), .out(transistor_647_out), .gate(transistor_593_out));
  Transistor #(.gate("br")) transistor_649 (
    .in(transistor_603_out), .out(transistor_145_out), .gate(transistor_647_out));
  Transistor #(.\type ("n")) transistor_650 (
    .in(transistor_603_out), .out(transistor_145_out), .gate(transistor_593_out));
  Transistor transistor_651 (.in(1'b1), .out(transistor_651_out), .gate(transistor_593_out));
  Transistor #(.\type ("n")) transistor_652 (.in(1'b0), .out(transistor_651_out), .gate(transistor_593_out));
  Transistor #(.gate("br")) transistor_653 (
    .in(transistor_607_out), .out(transistor_149_out), .gate(transistor_651_out));
  Transistor #(.\type ("n")) transistor_654 (
    .in(transistor_607_out), .out(transistor_149_out), .gate(transistor_593_out));
  Transistor transistor_655 (.in(1'b1), .out(transistor_655_out), .gate(transistor_593_out));
  Transistor #(.\type ("n")) transistor_656 (.in(1'b0), .out(transistor_655_out), .gate(transistor_593_out));
  Transistor #(.\type ("n")) transistor_657 (
    .in(transistor_611_out), .out(transistor_153_out), .gate(transistor_593_out));
  Transistor #(.gate("br")) transistor_658 (
    .in(transistor_611_out), .out(transistor_153_out), .gate(transistor_655_out));
  Transistor transistor_659 (.in(1'b1), .out(transistor_659_out), .gate(transistor_593_out));
  Transistor #(.\type ("n")) transistor_660 (.in(1'b0), .out(transistor_659_out), .gate(transistor_593_out));
  Transistor #(.gate("br")) transistor_661 (
    .in(transistor_615_out), .out(transistor_157_out), .gate(transistor_659_out));
  Transistor #(.\type ("n")) transistor_662 (
    .in(transistor_615_out), .out(transistor_157_out), .gate(transistor_593_out));
  Transistor transistor_663 (.in(1'b1), .out(transistor_663_out), .gate(transistor_593_out));
  Transistor #(.\type ("n")) transistor_664 (.in(1'b0), .out(transistor_663_out), .gate(transistor_593_out));
  Transistor #(.gate("br")) transistor_665 (
    .in(transistor_619_out), .out(transistor_161_out), .gate(transistor_663_out));
  Transistor #(.\type ("n")) transistor_666 (
    .in(transistor_619_out), .out(transistor_161_out), .gate(transistor_593_out));
  Transistor transistor_667 (.in(1'b1), .out(transistor_667_out), .gate(transistor_593_out));
  Transistor #(.\type ("n")) transistor_668 (.in(1'b0), .out(transistor_667_out), .gate(transistor_593_out));
  Transistor #(.\type ("n")) transistor_669 (
    .in(transistor_623_out), .out(transistor_165_out), .gate(transistor_593_out));
  Transistor #(.gate("br")) transistor_670 (
    .in(transistor_623_out), .out(transistor_165_out), .gate(transistor_667_out));
  Transistor #(.\type ("n")) transistor_671 (.in(_2), .out(transistor_671_out), .gate(mar));
  Transistor #(.gate("br")) transistor_672 (.in(_2), .out(transistor_671_out), .gate(transistor_627_out));
  Transistor #(.\type ("n")) transistor_673 (
    .in(transistor_731_out), .out(transistor_671_out), .gate(transistor_627_out));
  Transistor #(.gate("br")) transistor_674 (.in(transistor_731_out), .out(transistor_671_out), .gate(mar));
  Transistor transistor_675 (.in(1'b1), .out(transistor_675_out), .gate(clk_w));
  Transistor transistor_676 (.in(1'b1), .out(transistor_676_out), .gate(transistor_675_out));
  Transistor #(.\type ("n")) transistor_677 (.in(1'b0), .out(transistor_676_out), .gate(transistor_675_out));
  Transistor transistor_678 (.in(1'b1), .out(transistor_678_out), .gate(transistor_676_out));
  Transistor #(.\type ("n")) transistor_679 (.in(1'b0), .out(transistor_678_out), .gate(transistor_676_out));
  Transistor transistor_680 (.in(1'b1), .out(transistor_680_out), .gate(transistor_676_out));
  Transistor #(.\type ("n")) transistor_681 (.in(1'b0), .out(transistor_680_out), .gate(transistor_676_out));
  Transistor transistor_682 (.in(1'b1), .out(transistor_682_out), .gate(transistor_676_out));
  Transistor #(.\type ("n")) transistor_683 (.in(1'b0), .out(transistor_682_out), .gate(transistor_676_out));
  Transistor transistor_684 (.in(1'b1), .out(transistor_684_out), .gate(transistor_676_out));
  Transistor #(.\type ("n")) transistor_685 (.in(1'b0), .out(transistor_684_out), .gate(transistor_676_out));
  Transistor transistor_686 (.in(1'b1), .out(transistor_686_out), .gate(transistor_676_out));
  Transistor #(.\type ("n")) transistor_687 (.in(1'b0), .out(transistor_686_out), .gate(transistor_676_out));
  Transistor transistor_688 (.in(1'b1), .out(transistor_688_out), .gate(transistor_676_out));
  Transistor #(.\type ("n")) transistor_689 (.in(1'b0), .out(transistor_688_out), .gate(transistor_676_out));
  Transistor transistor_690 (.in(1'b1), .out(transistor_690_out), .gate(transistor_676_out));
  Transistor #(.\type ("n")) transistor_691 (.in(1'b0), .out(transistor_690_out), .gate(transistor_676_out));
  Transistor transistor_692 (.in(1'b1), .out(transistor_692_out), .gate(transistor_676_out));
  Transistor #(.\type ("n")) transistor_693 (.in(1'b0), .out(transistor_692_out), .gate(transistor_676_out));
  Transistor transistor_694 (.in(1'b1), .out(transistor_694_out), .gate(rst));
  Transistor #(.\type ("n")) transistor_695 (.in(1'b0), .out(transistor_694_out), .gate(rst));
  LED led_6 (.in(transistor_731_out));
  Transistor transistor_696 (.in(1'b1), .out(transistor_675_out), .gate(pc_w));
  Transistor #(.\type ("n")) transistor_697 (.in(transistor_698_out), .out(transistor_675_out), .gate(clk_w));
  Transistor #(.\type ("n")) transistor_698 (.in(1'b0), .out(transistor_698_out), .gate(pc_w));
  Transistor #(.\type ("n")) transistor_699 (.in(_0), .out(transistor_699_out), .gate(transistor_676_out));
  Transistor #(.gate("br")) transistor_700 (.in(_0), .out(transistor_699_out), .gate(transistor_678_out));
  Transistor #(.\type ("n")) transistor_701 (
    .in(transistor_763_out), .out(transistor_699_out), .gate(transistor_678_out));
  Transistor #(.gate("br")) transistor_702 (
    .in(transistor_763_out), .out(transistor_699_out), .gate(transistor_676_out));
  Transistor #(.\type ("n")) transistor_703 (.in(_1), .out(transistor_703_out), .gate(transistor_676_out));
  Transistor #(.gate("br")) transistor_704 (.in(_1), .out(transistor_703_out), .gate(transistor_680_out));
  Transistor #(.\type ("n")) transistor_705 (
    .in(transistor_767_out), .out(transistor_703_out), .gate(transistor_680_out));
  Transistor #(.gate("br")) transistor_706 (
    .in(transistor_767_out), .out(transistor_703_out), .gate(transistor_676_out));
  Transistor #(.\type ("n")) transistor_707 (.in(_2), .out(transistor_707_out), .gate(transistor_676_out));
  Transistor #(.gate("br")) transistor_708 (.in(_2), .out(transistor_707_out), .gate(transistor_682_out));
  Transistor #(.\type ("n")) transistor_709 (
    .in(transistor_771_out), .out(transistor_707_out), .gate(transistor_682_out));
  Transistor #(.gate("br")) transistor_710 (
    .in(transistor_771_out), .out(transistor_707_out), .gate(transistor_676_out));
  Transistor #(.\type ("n")) transistor_711 (.in(_3), .out(transistor_711_out), .gate(transistor_676_out));
  Transistor #(.gate("br")) transistor_712 (.in(_3), .out(transistor_711_out), .gate(transistor_684_out));
  Transistor #(.\type ("n")) transistor_713 (
    .in(transistor_775_out), .out(transistor_711_out), .gate(transistor_684_out));
  Transistor #(.gate("br")) transistor_714 (
    .in(transistor_775_out), .out(transistor_711_out), .gate(transistor_676_out));
  Transistor #(.\type ("n")) transistor_715 (.in(_4), .out(transistor_715_out), .gate(transistor_676_out));
  Transistor #(.gate("br")) transistor_716 (.in(_4), .out(transistor_715_out), .gate(transistor_686_out));
  Transistor #(.\type ("n")) transistor_717 (
    .in(transistor_779_out), .out(transistor_715_out), .gate(transistor_686_out));
  Transistor #(.gate("br")) transistor_718 (
    .in(transistor_779_out), .out(transistor_715_out), .gate(transistor_676_out));
  Transistor #(.\type ("n")) transistor_719 (.in(_5), .out(transistor_719_out), .gate(transistor_676_out));
  Transistor #(.gate("br")) transistor_720 (.in(_5), .out(transistor_719_out), .gate(transistor_688_out));
  Transistor #(.\type ("n")) transistor_721 (
    .in(transistor_783_out), .out(transistor_719_out), .gate(transistor_688_out));
  Transistor #(.gate("br")) transistor_722 (
    .in(transistor_783_out), .out(transistor_719_out), .gate(transistor_676_out));
  Transistor #(.\type ("n")) transistor_723 (.in(_6), .out(transistor_723_out), .gate(transistor_676_out));
  Transistor #(.gate("br")) transistor_724 (.in(_6), .out(transistor_723_out), .gate(transistor_690_out));
  Transistor #(.\type ("n")) transistor_725 (
    .in(transistor_787_out), .out(transistor_723_out), .gate(transistor_690_out));
  Transistor #(.gate("br")) transistor_726 (
    .in(transistor_787_out), .out(transistor_723_out), .gate(transistor_676_out));
  Transistor #(.\type ("n")) transistor_727 (.in(_7), .out(transistor_727_out), .gate(transistor_676_out));
  Transistor #(.gate("br")) transistor_728 (.in(_7), .out(transistor_727_out), .gate(transistor_692_out));
  Transistor #(.\type ("n")) transistor_729 (
    .in(transistor_791_out), .out(transistor_727_out), .gate(transistor_692_out));
  Transistor #(.gate("br")) transistor_730 (
    .in(transistor_791_out), .out(transistor_727_out), .gate(transistor_676_out));
  Transistor #(.\type ("n")) transistor_731 (.in(1'b0), .out(transistor_731_out), .gate(rst));
  Transistor #(.gate("br")) transistor_732 (.in(1'b0), .out(transistor_731_out), .gate(transistor_694_out));
  Transistor #(.\type ("n")) transistor_733 (
    .in(transistor_671_out), .out(transistor_731_out), .gate(transistor_694_out));
  Transistor #(.gate("br")) transistor_734 (.in(transistor_671_out), .out(transistor_731_out), .gate(rst));
  Transistor transistor_735 (.in(1'b1), .out(transistor_735_out), .gate(clk_r));
  Transistor transistor_736 (.in(1'b1), .out(transistor_736_out), .gate(transistor_735_out));
  Transistor #(.\type ("n")) transistor_737 (.in(1'b0), .out(transistor_736_out), .gate(transistor_735_out));
  Transistor transistor_738 (.in(1'b1), .out(transistor_738_out), .gate(rst));
  Transistor #(.\type ("n")) transistor_739 (.in(1'b0), .out(transistor_738_out), .gate(rst));
  Transistor transistor_740 (.in(1'b1), .out(transistor_740_out), .gate(rst));
  Transistor #(.\type ("n")) transistor_741 (.in(1'b0), .out(transistor_740_out), .gate(rst));
  Transistor transistor_742 (.in(1'b1), .out(transistor_742_out), .gate(rst));
  Transistor #(.\type ("n")) transistor_743 (.in(1'b0), .out(transistor_742_out), .gate(rst));
  Transistor transistor_744 (.in(1'b1), .out(transistor_744_out), .gate(rst));
  Transistor #(.\type ("n")) transistor_745 (.in(1'b0), .out(transistor_744_out), .gate(rst));
  Transistor transistor_746 (.in(1'b1), .out(transistor_746_out), .gate(rst));
  Transistor #(.\type ("n")) transistor_747 (.in(1'b0), .out(transistor_746_out), .gate(rst));
  Transistor transistor_748 (.in(1'b1), .out(transistor_748_out), .gate(rst));
  Transistor #(.\type ("n")) transistor_749 (.in(1'b0), .out(transistor_748_out), .gate(rst));
  Transistor transistor_750 (.in(1'b1), .out(transistor_750_out), .gate(rst));
  Transistor #(.\type ("n")) transistor_751 (.in(1'b0), .out(transistor_750_out), .gate(rst));
  Transistor transistor_752 (.in(1'b1), .out(transistor_752_out), .gate(rst));
  Transistor #(.\type ("n")) transistor_753 (.in(1'b0), .out(transistor_752_out), .gate(rst));
  Transistor #(.\type ("n")) transistor_754 (.in(_1), .out(transistor_754_out), .gate(mar));
  Transistor #(.gate("br")) transistor_755 (.in(_1), .out(transistor_754_out), .gate(transistor_756_out));
  Transistor transistor_756 (.in(1'b1), .out(transistor_756_out), .gate(mar));
  Transistor #(.\type ("n")) transistor_757 (.in(1'b0), .out(transistor_756_out), .gate(mar));
  Transistor #(.\type ("n")) transistor_758 (
    .in(transistor_829_out), .out(transistor_754_out), .gate(transistor_756_out));
  Transistor #(.gate("br")) transistor_759 (.in(transistor_829_out), .out(transistor_754_out), .gate(mar));
  Transistor transistor_760 (.in(1'b1), .out(transistor_735_out), .gate(pc_r));
  Transistor #(.\type ("n")) transistor_761 (.in(transistor_762_out), .out(transistor_735_out), .gate(clk_r));
  Transistor #(.\type ("n")) transistor_762 (.in(1'b0), .out(transistor_762_out), .gate(pc_r));
  Transistor #(.\type ("n")) transistor_763 (.in(1'b0), .out(transistor_763_out), .gate(rst));
  Transistor #(.gate("br")) transistor_764 (.in(1'b0), .out(transistor_763_out), .gate(transistor_738_out));
  Transistor #(.\type ("n")) transistor_765 (
    .in(transistor_699_out), .out(transistor_763_out), .gate(transistor_738_out));
  Transistor #(.gate("br")) transistor_766 (.in(transistor_699_out), .out(transistor_763_out), .gate(rst));
  Transistor #(.\type ("n")) transistor_767 (.in(1'b0), .out(transistor_767_out), .gate(rst));
  Transistor #(.gate("br")) transistor_768 (.in(1'b0), .out(transistor_767_out), .gate(transistor_740_out));
  Transistor #(.\type ("n")) transistor_769 (
    .in(transistor_703_out), .out(transistor_767_out), .gate(transistor_740_out));
  Transistor #(.gate("br")) transistor_770 (.in(transistor_703_out), .out(transistor_767_out), .gate(rst));
  Transistor #(.\type ("n")) transistor_771 (.in(1'b0), .out(transistor_771_out), .gate(rst));
  Transistor #(.gate("br")) transistor_772 (.in(1'b0), .out(transistor_771_out), .gate(transistor_742_out));
  Transistor #(.\type ("n")) transistor_773 (
    .in(transistor_707_out), .out(transistor_771_out), .gate(transistor_742_out));
  Transistor #(.gate("br")) transistor_774 (.in(transistor_707_out), .out(transistor_771_out), .gate(rst));
  Transistor #(.\type ("n")) transistor_775 (.in(1'b0), .out(transistor_775_out), .gate(rst));
  Transistor #(.gate("br")) transistor_776 (.in(1'b0), .out(transistor_775_out), .gate(transistor_744_out));
  Transistor #(.\type ("n")) transistor_777 (
    .in(transistor_711_out), .out(transistor_775_out), .gate(transistor_744_out));
  Transistor #(.gate("br")) transistor_778 (.in(transistor_711_out), .out(transistor_775_out), .gate(rst));
  Transistor #(.\type ("n")) transistor_779 (.in(1'b0), .out(transistor_779_out), .gate(rst));
  Transistor #(.gate("br")) transistor_780 (.in(1'b0), .out(transistor_779_out), .gate(transistor_746_out));
  Transistor #(.\type ("n")) transistor_781 (
    .in(transistor_715_out), .out(transistor_779_out), .gate(transistor_746_out));
  Transistor #(.gate("br")) transistor_782 (.in(transistor_715_out), .out(transistor_779_out), .gate(rst));
  Transistor #(.\type ("n")) transistor_783 (.in(1'b0), .out(transistor_783_out), .gate(rst));
  Transistor #(.gate("br")) transistor_784 (.in(1'b0), .out(transistor_783_out), .gate(transistor_748_out));
  Transistor #(.\type ("n")) transistor_785 (
    .in(transistor_719_out), .out(transistor_783_out), .gate(transistor_748_out));
  Transistor #(.gate("br")) transistor_786 (.in(transistor_719_out), .out(transistor_783_out), .gate(rst));
  Transistor #(.\type ("n")) transistor_787 (.in(1'b0), .out(transistor_787_out), .gate(rst));
  Transistor #(.gate("br")) transistor_788 (.in(1'b0), .out(transistor_787_out), .gate(transistor_750_out));
  Transistor #(.\type ("n")) transistor_789 (
    .in(transistor_723_out), .out(transistor_787_out), .gate(transistor_750_out));
  Transistor #(.gate("br")) transistor_790 (.in(transistor_723_out), .out(transistor_787_out), .gate(rst));
  Transistor #(.\type ("n")) transistor_791 (.in(1'b0), .out(transistor_791_out), .gate(rst));
  Transistor #(.gate("br")) transistor_792 (.in(1'b0), .out(transistor_791_out), .gate(transistor_752_out));
  Transistor #(.\type ("n")) transistor_793 (
    .in(transistor_727_out), .out(transistor_791_out), .gate(transistor_752_out));
  Transistor #(.gate("br")) transistor_794 (.in(transistor_727_out), .out(transistor_791_out), .gate(rst));
  Transistor transistor_795 (.in(1'b1), .out(transistor_795_out), .gate(rst));
  Transistor #(.\type ("n")) transistor_796 (.in(1'b0), .out(transistor_795_out), .gate(rst));
  LED led_7 (.in(transistor_829_out));
  Transistor transistor_797 (.in(1'b1), .out(transistor_797_out), .gate(transistor_736_out));
  Transistor #(.\type ("n")) transistor_798 (.in(1'b0), .out(transistor_797_out), .gate(transistor_736_out));
  Transistor #(.\type ("n")) transistor_799 (
    .in(transistor_763_out), .out(transistor_137_out), .gate(transistor_736_out));
  Transistor #(.gate("br")) transistor_800 (
    .in(transistor_763_out), .out(transistor_137_out), .gate(transistor_797_out));
  Transistor transistor_801 (.in(1'b1), .out(transistor_801_out), .gate(transistor_736_out));
  Transistor #(.\type ("n")) transistor_802 (.in(1'b0), .out(transistor_801_out), .gate(transistor_736_out));
  Transistor #(.gate("br")) transistor_803 (
    .in(transistor_767_out), .out(transistor_141_out), .gate(transistor_801_out));
  Transistor #(.\type ("n")) transistor_804 (
    .in(transistor_767_out), .out(transistor_141_out), .gate(transistor_736_out));
  Transistor transistor_805 (.in(1'b1), .out(transistor_805_out), .gate(transistor_736_out));
  Transistor #(.\type ("n")) transistor_806 (.in(1'b0), .out(transistor_805_out), .gate(transistor_736_out));
  Transistor #(.gate("br")) transistor_807 (
    .in(transistor_771_out), .out(transistor_145_out), .gate(transistor_805_out));
  Transistor #(.\type ("n")) transistor_808 (
    .in(transistor_771_out), .out(transistor_145_out), .gate(transistor_736_out));
  Transistor transistor_809 (.in(1'b1), .out(transistor_809_out), .gate(transistor_736_out));
  Transistor #(.\type ("n")) transistor_810 (.in(1'b0), .out(transistor_809_out), .gate(transistor_736_out));
  Transistor #(.\type ("n")) transistor_811 (
    .in(transistor_775_out), .out(transistor_149_out), .gate(transistor_736_out));
  Transistor #(.gate("br")) transistor_812 (
    .in(transistor_775_out), .out(transistor_149_out), .gate(transistor_809_out));
  Transistor transistor_813 (.in(1'b1), .out(transistor_813_out), .gate(transistor_736_out));
  Transistor #(.\type ("n")) transistor_814 (.in(1'b0), .out(transistor_813_out), .gate(transistor_736_out));
  Transistor #(.\type ("n")) transistor_815 (
    .in(transistor_779_out), .out(transistor_153_out), .gate(transistor_736_out));
  Transistor #(.gate("br")) transistor_816 (
    .in(transistor_779_out), .out(transistor_153_out), .gate(transistor_813_out));
  Transistor transistor_817 (.in(1'b1), .out(transistor_817_out), .gate(transistor_736_out));
  Transistor #(.\type ("n")) transistor_818 (.in(1'b0), .out(transistor_817_out), .gate(transistor_736_out));
  Transistor #(.gate("br")) transistor_819 (
    .in(transistor_783_out), .out(transistor_157_out), .gate(transistor_817_out));
  Transistor #(.\type ("n")) transistor_820 (
    .in(transistor_783_out), .out(transistor_157_out), .gate(transistor_736_out));
  Transistor transistor_821 (.in(1'b1), .out(transistor_821_out), .gate(transistor_736_out));
  Transistor #(.\type ("n")) transistor_822 (.in(1'b0), .out(transistor_821_out), .gate(transistor_736_out));
  Transistor #(.gate("br")) transistor_823 (
    .in(transistor_787_out), .out(transistor_161_out), .gate(transistor_821_out));
  Transistor #(.\type ("n")) transistor_824 (
    .in(transistor_787_out), .out(transistor_161_out), .gate(transistor_736_out));
  Transistor transistor_825 (.in(1'b1), .out(transistor_825_out), .gate(transistor_736_out));
  Transistor #(.\type ("n")) transistor_826 (.in(1'b0), .out(transistor_825_out), .gate(transistor_736_out));
  Transistor #(.gate("br")) transistor_827 (
    .in(transistor_791_out), .out(transistor_165_out), .gate(transistor_825_out));
  Transistor #(.\type ("n")) transistor_828 (
    .in(transistor_791_out), .out(transistor_165_out), .gate(transistor_736_out));
  Transistor #(.\type ("n")) transistor_829 (.in(1'b0), .out(transistor_829_out), .gate(rst));
  Transistor #(.gate("br")) transistor_830 (.in(1'b0), .out(transistor_829_out), .gate(transistor_795_out));
  Transistor #(.\type ("n")) transistor_831 (
    .in(transistor_754_out), .out(transistor_829_out), .gate(transistor_795_out));
  Transistor #(.gate("br")) transistor_832 (.in(transistor_754_out), .out(transistor_829_out), .gate(rst));
  Transistor transistor_833 (.in(1'b1), .out(transistor_833_out), .gate(bus0));
  Transistor #(.\type ("n")) transistor_834 (.in(1'b0), .out(transistor_833_out), .gate(bus0));
  Transistor transistor_835 (.in(1'b1), .out(transistor_835_out), .gate(bus0));
  Transistor #(.\type ("n")) transistor_836 (.in(1'b0), .out(transistor_835_out), .gate(bus0));
  Transistor transistor_837 (.in(1'b1), .out(transistor_837_out), .gate(bus0));
  Transistor #(.\type ("n")) transistor_838 (.in(1'b0), .out(transistor_837_out), .gate(bus0));
  Transistor transistor_839 (.in(1'b1), .out(transistor_839_out), .gate(bus0));
  Transistor #(.\type ("n")) transistor_840 (.in(1'b0), .out(transistor_839_out), .gate(bus0));
  Transistor transistor_841 (.in(1'b1), .out(transistor_841_out), .gate(bus0));
  Transistor #(.\type ("n")) transistor_842 (.in(1'b0), .out(transistor_841_out), .gate(bus0));
  Transistor transistor_843 (.in(1'b1), .out(transistor_843_out), .gate(bus0));
  Transistor #(.\type ("n")) transistor_844 (.in(1'b0), .out(transistor_843_out), .gate(bus0));
  Transistor transistor_845 (.in(1'b1), .out(transistor_845_out), .gate(bus0));
  Transistor #(.\type ("n")) transistor_846 (.in(1'b0), .out(transistor_845_out), .gate(bus0));
  Transistor transistor_847 (.in(1'b1), .out(transistor_847_out), .gate(bus0));
  Transistor #(.\type ("n")) transistor_848 (.in(1'b0), .out(transistor_847_out), .gate(bus0));
  Transistor transistor_849 (.in(1'b1), .out(transistor_849_out), .gate(mar));
  Transistor #(.\type ("n")) transistor_850 (.in(1'b0), .out(transistor_849_out), .gate(mar));
  Transistor transistor_851 (.in(1'b0), .out(transistor_851_out), .gate(bus0));
  Transistor #(.\type ("n"), .gate("br")) transistor_852 (
    .in(1'b0), .out(transistor_851_out), .gate(transistor_833_out));
  Transistor transistor_853 (.in(transistor_137_out), .out(transistor_851_out), .gate(transistor_833_out));
  Pull_Resistor pull_resistor_1 (.node(transistor_851_out));
  Transistor #(.\type ("n"), .gate("br")) transistor_854 (
    .in(transistor_137_out), .out(transistor_851_out), .gate(bus0));
  Transistor transistor_855 (.in(1'b0), .out(transistor_855_out), .gate(bus0));
  Transistor #(.\type ("n"), .gate("br")) transistor_856 (
    .in(1'b0), .out(transistor_855_out), .gate(transistor_835_out));
  Transistor transistor_857 (.in(transistor_141_out), .out(transistor_855_out), .gate(transistor_835_out));
  Pull_Resistor pull_resistor_2 (.node(transistor_855_out));
  Transistor #(.\type ("n"), .gate("br")) transistor_858 (
    .in(transistor_141_out), .out(transistor_855_out), .gate(bus0));
  Transistor transistor_859 (.in(1'b0), .out(transistor_859_out), .gate(bus0));
  Transistor #(.\type ("n"), .gate("br")) transistor_860 (
    .in(1'b0), .out(transistor_859_out), .gate(transistor_837_out));
  Transistor transistor_861 (.in(transistor_145_out), .out(transistor_859_out), .gate(transistor_837_out));
  Transistor #(.\type ("n"), .gate("br")) transistor_862 (
    .in(transistor_145_out), .out(transistor_859_out), .gate(bus0));
  Pull_Resistor pull_resistor_3 (.node(transistor_859_out));
  Transistor transistor_863 (.in(1'b0), .out(transistor_863_out), .gate(bus0));
  Transistor #(.\type ("n"), .gate("br")) transistor_864 (
    .in(1'b0), .out(transistor_863_out), .gate(transistor_839_out));
  Transistor transistor_865 (.in(transistor_149_out), .out(transistor_863_out), .gate(transistor_839_out));
  Transistor #(.\type ("n"), .gate("br")) transistor_866 (
    .in(transistor_149_out), .out(transistor_863_out), .gate(bus0));
  Pull_Resistor pull_resistor_4 (.node(transistor_863_out));
  Transistor transistor_867 (.in(1'b0), .out(transistor_867_out), .gate(bus0));
  Transistor #(.\type ("n"), .gate("br")) transistor_868 (
    .in(1'b0), .out(transistor_867_out), .gate(transistor_841_out));
  Transistor transistor_869 (.in(transistor_153_out), .out(transistor_867_out), .gate(transistor_841_out));
  Transistor #(.\type ("n"), .gate("br")) transistor_870 (
    .in(transistor_153_out), .out(transistor_867_out), .gate(bus0));
  Pull_Resistor pull_resistor_5 (.node(transistor_867_out));
  Transistor transistor_871 (.in(1'b0), .out(transistor_871_out), .gate(bus0));
  Transistor #(.\type ("n"), .gate("br")) transistor_872 (
    .in(1'b0), .out(transistor_871_out), .gate(transistor_843_out));
  Transistor transistor_873 (.in(transistor_157_out), .out(transistor_871_out), .gate(transistor_843_out));
  Transistor #(.\type ("n"), .gate("br")) transistor_874 (
    .in(transistor_157_out), .out(transistor_871_out), .gate(bus0));
  Pull_Resistor pull_resistor_6 (.node(transistor_871_out));
  Transistor transistor_875 (.in(1'b0), .out(transistor_875_out), .gate(bus0));
  Transistor #(.\type ("n"), .gate("br")) transistor_876 (
    .in(1'b0), .out(transistor_875_out), .gate(transistor_845_out));
  Transistor transistor_877 (.in(transistor_161_out), .out(transistor_875_out), .gate(transistor_845_out));
  Transistor #(.\type ("n"), .gate("br")) transistor_878 (
    .in(transistor_161_out), .out(transistor_875_out), .gate(bus0));
  Pull_Resistor pull_resistor_7 (.node(transistor_875_out));
  Transistor transistor_879 (.in(1'b0), .out(transistor_879_out), .gate(bus0));
  Transistor #(.\type ("n"), .gate("br")) transistor_880 (
    .in(1'b0), .out(transistor_879_out), .gate(transistor_847_out));
  Transistor transistor_881 (.in(transistor_165_out), .out(transistor_879_out), .gate(transistor_847_out));
  Pull_Resistor pull_resistor_8 (.node(transistor_879_out));
  Transistor #(.\type ("n"), .gate("br")) transistor_882 (
    .in(transistor_165_out), .out(transistor_879_out), .gate(bus0));
  Transistor #(.\type ("n")) transistor_883 (.in(_0), .out(transistor_883_out), .gate(mar));
  Transistor #(.gate("br")) transistor_884 (.in(_0), .out(transistor_883_out), .gate(transistor_849_out));
  Transistor #(.\type ("n")) transistor_885 (
    .in(transistor_906_out), .out(transistor_883_out), .gate(transistor_849_out));
  Transistor #(.gate("br")) transistor_886 (.in(transistor_906_out), .out(transistor_883_out), .gate(mar));
  LED led_8 (.in(transistor_906_out));
  Transistor transistor_887 (.in(1'b1), .out(transistor_887_out), .gate(clk_w));
  Transistor transistor_888 (.in(1'b1), .out(transistor_888_out), .gate(transistor_887_out));
  Transistor #(.\type ("n")) transistor_889 (.in(1'b0), .out(transistor_888_out), .gate(transistor_887_out));
  Transistor transistor_890 (.in(1'b1), .out(transistor_890_out), .gate(transistor_888_out));
  Transistor #(.\type ("n")) transistor_891 (.in(1'b0), .out(transistor_890_out), .gate(transistor_888_out));
  Transistor transistor_892 (.in(1'b1), .out(transistor_892_out), .gate(transistor_888_out));
  Transistor #(.\type ("n")) transistor_893 (.in(1'b0), .out(transistor_892_out), .gate(transistor_888_out));
  Transistor transistor_894 (.in(1'b1), .out(transistor_894_out), .gate(transistor_888_out));
  Transistor #(.\type ("n")) transistor_895 (.in(1'b0), .out(transistor_894_out), .gate(transistor_888_out));
  Transistor transistor_896 (.in(1'b1), .out(transistor_896_out), .gate(transistor_888_out));
  Transistor #(.\type ("n")) transistor_897 (.in(1'b0), .out(transistor_896_out), .gate(transistor_888_out));
  Transistor transistor_898 (.in(1'b1), .out(transistor_898_out), .gate(transistor_888_out));
  Transistor #(.\type ("n")) transistor_899 (.in(1'b0), .out(transistor_898_out), .gate(transistor_888_out));
  Transistor transistor_900 (.in(1'b1), .out(transistor_900_out), .gate(transistor_888_out));
  Transistor #(.\type ("n")) transistor_901 (.in(1'b0), .out(transistor_900_out), .gate(transistor_888_out));
  Transistor transistor_902 (.in(1'b1), .out(transistor_902_out), .gate(transistor_888_out));
  Transistor #(.\type ("n")) transistor_903 (.in(1'b0), .out(transistor_902_out), .gate(transistor_888_out));
  Transistor transistor_904 (.in(1'b1), .out(transistor_904_out), .gate(transistor_888_out));
  Transistor #(.\type ("n")) transistor_905 (.in(1'b0), .out(transistor_904_out), .gate(transistor_888_out));
  Transistor #(.\type ("n")) transistor_906 (.in(1'b0), .out(transistor_906_out), .gate(rst));
  Transistor #(.gate("br")) transistor_907 (.in(1'b0), .out(transistor_906_out), .gate(transistor_908_out));
  Transistor transistor_908 (.in(1'b1), .out(transistor_908_out), .gate(rst));
  Transistor #(.\type ("n")) transistor_909 (.in(1'b0), .out(transistor_908_out), .gate(rst));
  Transistor #(.\type ("n")) transistor_910 (
    .in(transistor_883_out), .out(transistor_906_out), .gate(transistor_908_out));
  Transistor #(.gate("br")) transistor_911 (.in(transistor_883_out), .out(transistor_906_out), .gate(rst));
  Transistor transistor_912 (.in(1'b1), .out(transistor_887_out), .gate(ra_w));
  Transistor #(.\type ("n")) transistor_913 (.in(transistor_914_out), .out(transistor_887_out), .gate(clk_w));
  Transistor #(.\type ("n")) transistor_914 (.in(1'b0), .out(transistor_914_out), .gate(ra_w));
  Transistor #(.\type ("n")) transistor_915 (
    .in(transistor_851_out), .out(transistor_915_out), .gate(transistor_888_out));
  Transistor #(.gate("br")) transistor_916 (
    .in(transistor_851_out), .out(transistor_915_out), .gate(transistor_890_out));
  Transistor #(.\type ("n")) transistor_917 (
    .in(transistor_947_out), .out(transistor_915_out), .gate(transistor_890_out));
  Transistor #(.gate("br")) transistor_918 (
    .in(transistor_947_out), .out(transistor_915_out), .gate(transistor_888_out));
  Transistor #(.\type ("n")) transistor_919 (
    .in(transistor_855_out), .out(transistor_919_out), .gate(transistor_888_out));
  Transistor #(.gate("br")) transistor_920 (
    .in(transistor_855_out), .out(transistor_919_out), .gate(transistor_892_out));
  Transistor #(.\type ("n")) transistor_921 (
    .in(transistor_953_out), .out(transistor_919_out), .gate(transistor_892_out));
  Transistor #(.gate("br")) transistor_922 (
    .in(transistor_953_out), .out(transistor_919_out), .gate(transistor_888_out));
  Transistor #(.\type ("n")) transistor_923 (
    .in(transistor_859_out), .out(transistor_923_out), .gate(transistor_888_out));
  Transistor #(.gate("br")) transistor_924 (
    .in(transistor_859_out), .out(transistor_923_out), .gate(transistor_894_out));
  Transistor #(.\type ("n")) transistor_925 (
    .in(transistor_959_out), .out(transistor_923_out), .gate(transistor_894_out));
  Transistor #(.gate("br")) transistor_926 (
    .in(transistor_959_out), .out(transistor_923_out), .gate(transistor_888_out));
  Transistor #(.\type ("n")) transistor_927 (
    .in(transistor_863_out), .out(transistor_927_out), .gate(transistor_888_out));
  Transistor #(.gate("br")) transistor_928 (
    .in(transistor_863_out), .out(transistor_927_out), .gate(transistor_896_out));
  Transistor #(.\type ("n")) transistor_929 (
    .in(transistor_965_out), .out(transistor_927_out), .gate(transistor_896_out));
  Transistor #(.gate("br")) transistor_930 (
    .in(transistor_965_out), .out(transistor_927_out), .gate(transistor_888_out));
  Transistor #(.\type ("n")) transistor_931 (
    .in(transistor_867_out), .out(transistor_931_out), .gate(transistor_888_out));
  Transistor #(.gate("br")) transistor_932 (
    .in(transistor_867_out), .out(transistor_931_out), .gate(transistor_898_out));
  Transistor #(.\type ("n")) transistor_933 (
    .in(transistor_971_out), .out(transistor_931_out), .gate(transistor_898_out));
  Transistor #(.gate("br")) transistor_934 (
    .in(transistor_971_out), .out(transistor_931_out), .gate(transistor_888_out));
  Transistor #(.\type ("n")) transistor_935 (
    .in(transistor_871_out), .out(transistor_935_out), .gate(transistor_888_out));
  Transistor #(.gate("br")) transistor_936 (
    .in(transistor_871_out), .out(transistor_935_out), .gate(transistor_900_out));
  Transistor #(.\type ("n")) transistor_937 (
    .in(transistor_977_out), .out(transistor_935_out), .gate(transistor_900_out));
  Transistor #(.gate("br")) transistor_938 (
    .in(transistor_977_out), .out(transistor_935_out), .gate(transistor_888_out));
  Transistor #(.\type ("n")) transistor_939 (
    .in(transistor_875_out), .out(transistor_939_out), .gate(transistor_888_out));
  Transistor #(.gate("br")) transistor_940 (
    .in(transistor_875_out), .out(transistor_939_out), .gate(transistor_902_out));
  Transistor #(.\type ("n")) transistor_941 (
    .in(transistor_983_out), .out(transistor_939_out), .gate(transistor_902_out));
  Transistor #(.gate("br")) transistor_942 (
    .in(transistor_983_out), .out(transistor_939_out), .gate(transistor_888_out));
  Transistor #(.\type ("n")) transistor_943 (
    .in(transistor_879_out), .out(transistor_943_out), .gate(transistor_888_out));
  Transistor #(.gate("br")) transistor_944 (
    .in(transistor_879_out), .out(transistor_943_out), .gate(transistor_904_out));
  Transistor #(.\type ("n")) transistor_945 (
    .in(transistor_989_out), .out(transistor_943_out), .gate(transistor_904_out));
  Transistor #(.gate("br")) transistor_946 (
    .in(transistor_989_out), .out(transistor_943_out), .gate(transistor_888_out));
  Transistor #(.\type ("n")) transistor_947 (.in(1'b0), .out(transistor_947_out), .gate(rst));
  Transistor #(.gate("br")) transistor_948 (.in(1'b0), .out(transistor_947_out), .gate(transistor_949_out));
  Transistor transistor_949 (.in(1'b1), .out(transistor_949_out), .gate(rst));
  Transistor #(.\type ("n")) transistor_950 (.in(1'b0), .out(transistor_949_out), .gate(rst));
  Transistor #(.\type ("n")) transistor_951 (
    .in(transistor_915_out), .out(transistor_947_out), .gate(transistor_949_out));
  Transistor #(.gate("br")) transistor_952 (.in(transistor_915_out), .out(transistor_947_out), .gate(rst));
  Transistor #(.\type ("n")) transistor_953 (.in(1'b0), .out(transistor_953_out), .gate(rst));
  Transistor #(.gate("br")) transistor_954 (.in(1'b0), .out(transistor_953_out), .gate(transistor_955_out));
  Transistor transistor_955 (.in(1'b1), .out(transistor_955_out), .gate(rst));
  Transistor #(.\type ("n")) transistor_956 (.in(1'b0), .out(transistor_955_out), .gate(rst));
  Transistor #(.\type ("n")) transistor_957 (
    .in(transistor_919_out), .out(transistor_953_out), .gate(transistor_955_out));
  Transistor #(.gate("br")) transistor_958 (.in(transistor_919_out), .out(transistor_953_out), .gate(rst));
  Transistor #(.\type ("n")) transistor_959 (.in(1'b0), .out(transistor_959_out), .gate(rst));
  Transistor #(.gate("br")) transistor_960 (.in(1'b0), .out(transistor_959_out), .gate(transistor_961_out));
  Transistor transistor_961 (.in(1'b1), .out(transistor_961_out), .gate(rst));
  Transistor #(.\type ("n")) transistor_962 (.in(1'b0), .out(transistor_961_out), .gate(rst));
  Transistor #(.\type ("n")) transistor_963 (
    .in(transistor_923_out), .out(transistor_959_out), .gate(transistor_961_out));
  Transistor #(.gate("br")) transistor_964 (.in(transistor_923_out), .out(transistor_959_out), .gate(rst));
  Transistor #(.\type ("n")) transistor_965 (.in(1'b0), .out(transistor_965_out), .gate(rst));
  Transistor #(.gate("br")) transistor_966 (.in(1'b0), .out(transistor_965_out), .gate(transistor_967_out));
  Transistor transistor_967 (.in(1'b1), .out(transistor_967_out), .gate(rst));
  Transistor #(.\type ("n")) transistor_968 (.in(1'b0), .out(transistor_967_out), .gate(rst));
  Transistor #(.\type ("n")) transistor_969 (
    .in(transistor_927_out), .out(transistor_965_out), .gate(transistor_967_out));
  Transistor #(.gate("br")) transistor_970 (.in(transistor_927_out), .out(transistor_965_out), .gate(rst));
  Transistor #(.\type ("n")) transistor_971 (.in(1'b0), .out(transistor_971_out), .gate(rst));
  Transistor #(.gate("br")) transistor_972 (.in(1'b0), .out(transistor_971_out), .gate(transistor_973_out));
  Transistor transistor_973 (.in(1'b1), .out(transistor_973_out), .gate(rst));
  Transistor #(.\type ("n")) transistor_974 (.in(1'b0), .out(transistor_973_out), .gate(rst));
  Transistor #(.\type ("n")) transistor_975 (
    .in(transistor_931_out), .out(transistor_971_out), .gate(transistor_973_out));
  Transistor #(.gate("br")) transistor_976 (.in(transistor_931_out), .out(transistor_971_out), .gate(rst));
  Transistor #(.\type ("n")) transistor_977 (.in(1'b0), .out(transistor_977_out), .gate(rst));
  Transistor #(.gate("br")) transistor_978 (.in(1'b0), .out(transistor_977_out), .gate(transistor_979_out));
  Transistor transistor_979 (.in(1'b1), .out(transistor_979_out), .gate(rst));
  Transistor #(.\type ("n")) transistor_980 (.in(1'b0), .out(transistor_979_out), .gate(rst));
  Transistor #(.\type ("n")) transistor_981 (
    .in(transistor_935_out), .out(transistor_977_out), .gate(transistor_979_out));
  Transistor #(.gate("br")) transistor_982 (.in(transistor_935_out), .out(transistor_977_out), .gate(rst));
  Transistor #(.\type ("n")) transistor_983 (.in(1'b0), .out(transistor_983_out), .gate(rst));
  Transistor #(.gate("br")) transistor_984 (.in(1'b0), .out(transistor_983_out), .gate(transistor_985_out));
  Transistor transistor_985 (.in(1'b1), .out(transistor_985_out), .gate(rst));
  Transistor #(.\type ("n")) transistor_986 (.in(1'b0), .out(transistor_985_out), .gate(rst));
  Transistor #(.\type ("n")) transistor_987 (
    .in(transistor_939_out), .out(transistor_983_out), .gate(transistor_985_out));
  Transistor #(.gate("br")) transistor_988 (.in(transistor_939_out), .out(transistor_983_out), .gate(rst));
  Transistor #(.\type ("n")) transistor_989 (.in(1'b0), .out(transistor_989_out), .gate(rst));
  Transistor #(.gate("br")) transistor_990 (.in(1'b0), .out(transistor_989_out), .gate(transistor_991_out));
  Transistor transistor_991 (.in(1'b1), .out(transistor_991_out), .gate(rst));
  Transistor #(.\type ("n")) transistor_992 (.in(1'b0), .out(transistor_991_out), .gate(rst));
  Transistor #(.\type ("n")) transistor_993 (
    .in(transistor_943_out), .out(transistor_989_out), .gate(transistor_991_out));
  Transistor #(.gate("br")) transistor_994 (.in(transistor_943_out), .out(transistor_989_out), .gate(rst));
  Transistor transistor_995 (.in(1'b1), .out(transistor_995_out), .gate(rb_w));
  Transistor transistor_996 (.in(1'b1), .out(transistor_995_out), .gate(clk_w));
  Transistor #(.\type ("n")) transistor_997 (.in(transistor_998_out), .out(transistor_995_out), .gate(clk_w));
  Transistor #(.\type ("n")) transistor_998 (.in(1'b0), .out(transistor_998_out), .gate(rb_w));
  Transistor transistor_999 (.in(1'b1), .out(transistor_999_out), .gate(transistor_995_out));
  Transistor #(.\type ("n")) transistor_1000 (.in(1'b0), .out(transistor_999_out), .gate(transistor_995_out));
  Transistor #(.\type ("n")) transistor_1001 (
    .in(transistor_851_out), .out(transistor_1001_out), .gate(transistor_999_out));
  Transistor #(.gate("br")) transistor_1002 (
    .in(transistor_851_out), .out(transistor_1001_out), .gate(transistor_1003_out));
  Transistor transistor_1003 (.in(1'b1), .out(transistor_1003_out), .gate(transistor_999_out));
  Transistor #(.\type ("n")) transistor_1004 (.in(1'b0), .out(transistor_1003_out), .gate(transistor_999_out));
  Transistor #(.\type ("n")) transistor_1005 (
    .in(transistor_1065_out), .out(transistor_1001_out), .gate(transistor_1003_out));
  Transistor #(.gate("br")) transistor_1006 (
    .in(transistor_1065_out), .out(transistor_1001_out), .gate(transistor_999_out));
  Transistor #(.\type ("n")) transistor_1007 (
    .in(transistor_855_out), .out(transistor_1007_out), .gate(transistor_999_out));
  Transistor #(.gate("br")) transistor_1008 (
    .in(transistor_855_out), .out(transistor_1007_out), .gate(transistor_1009_out));
  Transistor transistor_1009 (.in(1'b1), .out(transistor_1009_out), .gate(transistor_999_out));
  Transistor #(.\type ("n")) transistor_1010 (.in(1'b0), .out(transistor_1009_out), .gate(transistor_999_out));
  Transistor #(.\type ("n")) transistor_1011 (
    .in(transistor_1069_out), .out(transistor_1007_out), .gate(transistor_1009_out));
  Transistor #(.gate("br")) transistor_1012 (
    .in(transistor_1069_out), .out(transistor_1007_out), .gate(transistor_999_out));
  Transistor #(.\type ("n")) transistor_1013 (
    .in(transistor_859_out), .out(transistor_1013_out), .gate(transistor_999_out));
  Transistor #(.gate("br")) transistor_1014 (
    .in(transistor_859_out), .out(transistor_1013_out), .gate(transistor_1015_out));
  Transistor transistor_1015 (.in(1'b1), .out(transistor_1015_out), .gate(transistor_999_out));
  Transistor #(.\type ("n")) transistor_1016 (.in(1'b0), .out(transistor_1015_out), .gate(transistor_999_out));
  Transistor #(.\type ("n")) transistor_1017 (
    .in(transistor_1073_out), .out(transistor_1013_out), .gate(transistor_1015_out));
  Transistor #(.gate("br")) transistor_1018 (
    .in(transistor_1073_out), .out(transistor_1013_out), .gate(transistor_999_out));
  Transistor #(.\type ("n")) transistor_1019 (
    .in(transistor_863_out), .out(transistor_1019_out), .gate(transistor_999_out));
  Transistor #(.gate("br")) transistor_1020 (
    .in(transistor_863_out), .out(transistor_1019_out), .gate(transistor_1021_out));
  Transistor transistor_1021 (.in(1'b1), .out(transistor_1021_out), .gate(transistor_999_out));
  Transistor #(.\type ("n")) transistor_1022 (.in(1'b0), .out(transistor_1021_out), .gate(transistor_999_out));
  Transistor #(.\type ("n")) transistor_1023 (
    .in(transistor_1077_out), .out(transistor_1019_out), .gate(transistor_1021_out));
  Transistor #(.gate("br")) transistor_1024 (
    .in(transistor_1077_out), .out(transistor_1019_out), .gate(transistor_999_out));
  Transistor #(.\type ("n")) transistor_1025 (
    .in(transistor_867_out), .out(transistor_1025_out), .gate(transistor_999_out));
  Transistor #(.gate("br")) transistor_1026 (
    .in(transistor_867_out), .out(transistor_1025_out), .gate(transistor_1027_out));
  Transistor transistor_1027 (.in(1'b1), .out(transistor_1027_out), .gate(transistor_999_out));
  Transistor #(.\type ("n")) transistor_1028 (.in(1'b0), .out(transistor_1027_out), .gate(transistor_999_out));
  Transistor #(.\type ("n")) transistor_1029 (
    .in(transistor_1081_out), .out(transistor_1025_out), .gate(transistor_1027_out));
  Transistor #(.gate("br")) transistor_1030 (
    .in(transistor_1081_out), .out(transistor_1025_out), .gate(transistor_999_out));
  Transistor #(.\type ("n")) transistor_1031 (
    .in(transistor_871_out), .out(transistor_1031_out), .gate(transistor_999_out));
  Transistor #(.gate("br")) transistor_1032 (
    .in(transistor_871_out), .out(transistor_1031_out), .gate(transistor_1033_out));
  Transistor transistor_1033 (.in(1'b1), .out(transistor_1033_out), .gate(transistor_999_out));
  Transistor #(.\type ("n")) transistor_1034 (.in(1'b0), .out(transistor_1033_out), .gate(transistor_999_out));
  Transistor #(.\type ("n")) transistor_1035 (
    .in(transistor_1085_out), .out(transistor_1031_out), .gate(transistor_1033_out));
  Transistor #(.gate("br")) transistor_1036 (
    .in(transistor_1085_out), .out(transistor_1031_out), .gate(transistor_999_out));
  Transistor #(.\type ("n")) transistor_1037 (
    .in(transistor_875_out), .out(transistor_1037_out), .gate(transistor_999_out));
  Transistor #(.gate("br")) transistor_1038 (
    .in(transistor_875_out), .out(transistor_1037_out), .gate(transistor_1039_out));
  Transistor transistor_1039 (.in(1'b1), .out(transistor_1039_out), .gate(transistor_999_out));
  Transistor #(.\type ("n")) transistor_1040 (.in(1'b0), .out(transistor_1039_out), .gate(transistor_999_out));
  Transistor #(.\type ("n")) transistor_1041 (
    .in(transistor_1089_out), .out(transistor_1037_out), .gate(transistor_1039_out));
  Transistor #(.gate("br")) transistor_1042 (
    .in(transistor_1089_out), .out(transistor_1037_out), .gate(transistor_999_out));
  Transistor #(.\type ("n")) transistor_1043 (
    .in(transistor_879_out), .out(transistor_1043_out), .gate(transistor_999_out));
  Transistor #(.gate("br")) transistor_1044 (
    .in(transistor_879_out), .out(transistor_1043_out), .gate(transistor_1045_out));
  Transistor transistor_1045 (.in(1'b1), .out(transistor_1045_out), .gate(transistor_999_out));
  Transistor #(.\type ("n")) transistor_1046 (.in(1'b0), .out(transistor_1045_out), .gate(transistor_999_out));
  Transistor #(.\type ("n")) transistor_1047 (
    .in(transistor_1093_out), .out(transistor_1043_out), .gate(transistor_1045_out));
  Transistor #(.gate("br")) transistor_1048 (
    .in(transistor_1093_out), .out(transistor_1043_out), .gate(transistor_999_out));
  Transistor transistor_1049 (.in(1'b1), .out(transistor_1049_out), .gate(rst));
  Transistor #(.\type ("n")) transistor_1050 (.in(1'b0), .out(transistor_1049_out), .gate(rst));
  Transistor transistor_1051 (.in(1'b1), .out(transistor_1051_out), .gate(rst));
  Transistor #(.\type ("n")) transistor_1052 (.in(1'b0), .out(transistor_1051_out), .gate(rst));
  Transistor transistor_1053 (.in(1'b1), .out(transistor_1053_out), .gate(rst));
  Transistor #(.\type ("n")) transistor_1054 (.in(1'b0), .out(transistor_1053_out), .gate(rst));
  Transistor transistor_1055 (.in(1'b1), .out(transistor_1055_out), .gate(rst));
  Transistor #(.\type ("n")) transistor_1056 (.in(1'b0), .out(transistor_1055_out), .gate(rst));
  Transistor transistor_1057 (.in(1'b1), .out(transistor_1057_out), .gate(rst));
  Transistor #(.\type ("n")) transistor_1058 (.in(1'b0), .out(transistor_1057_out), .gate(rst));
  Transistor transistor_1059 (.in(1'b1), .out(transistor_1059_out), .gate(rst));
  Transistor #(.\type ("n")) transistor_1060 (.in(1'b0), .out(transistor_1059_out), .gate(rst));
  Transistor transistor_1061 (.in(1'b1), .out(transistor_1061_out), .gate(rst));
  Transistor #(.\type ("n")) transistor_1062 (.in(1'b0), .out(transistor_1061_out), .gate(rst));
  Transistor transistor_1063 (.in(1'b1), .out(transistor_1063_out), .gate(rst));
  Transistor #(.\type ("n")) transistor_1064 (.in(1'b0), .out(transistor_1063_out), .gate(rst));
  Transistor #(.\type ("n")) transistor_1065 (.in(1'b0), .out(transistor_1065_out), .gate(rst));
  Transistor #(.gate("br")) transistor_1066 (.in(1'b0), .out(transistor_1065_out), .gate(transistor_1049_out));
  Transistor #(.\type ("n")) transistor_1067 (
    .in(transistor_1001_out), .out(transistor_1065_out), .gate(transistor_1049_out));
  Transistor #(.gate("br")) transistor_1068 (.in(transistor_1001_out), .out(transistor_1065_out), .gate(rst));
  Transistor #(.\type ("n")) transistor_1069 (.in(1'b0), .out(transistor_1069_out), .gate(rst));
  Transistor #(.gate("br")) transistor_1070 (.in(1'b0), .out(transistor_1069_out), .gate(transistor_1051_out));
  Transistor #(.\type ("n")) transistor_1071 (
    .in(transistor_1007_out), .out(transistor_1069_out), .gate(transistor_1051_out));
  Transistor #(.gate("br")) transistor_1072 (.in(transistor_1007_out), .out(transistor_1069_out), .gate(rst));
  Transistor #(.\type ("n")) transistor_1073 (.in(1'b0), .out(transistor_1073_out), .gate(rst));
  Transistor #(.gate("br")) transistor_1074 (.in(1'b0), .out(transistor_1073_out), .gate(transistor_1053_out));
  Transistor #(.\type ("n")) transistor_1075 (
    .in(transistor_1013_out), .out(transistor_1073_out), .gate(transistor_1053_out));
  Transistor #(.gate("br")) transistor_1076 (.in(transistor_1013_out), .out(transistor_1073_out), .gate(rst));
  Transistor #(.\type ("n")) transistor_1077 (.in(1'b0), .out(transistor_1077_out), .gate(rst));
  Transistor #(.gate("br")) transistor_1078 (.in(1'b0), .out(transistor_1077_out), .gate(transistor_1055_out));
  Transistor #(.\type ("n")) transistor_1079 (
    .in(transistor_1019_out), .out(transistor_1077_out), .gate(transistor_1055_out));
  Transistor #(.gate("br")) transistor_1080 (.in(transistor_1019_out), .out(transistor_1077_out), .gate(rst));
  Transistor #(.\type ("n")) transistor_1081 (.in(1'b0), .out(transistor_1081_out), .gate(rst));
  Transistor #(.gate("br")) transistor_1082 (.in(1'b0), .out(transistor_1081_out), .gate(transistor_1057_out));
  Transistor #(.\type ("n")) transistor_1083 (
    .in(transistor_1025_out), .out(transistor_1081_out), .gate(transistor_1057_out));
  Transistor #(.gate("br")) transistor_1084 (.in(transistor_1025_out), .out(transistor_1081_out), .gate(rst));
  Transistor #(.\type ("n")) transistor_1085 (.in(1'b0), .out(transistor_1085_out), .gate(rst));
  Transistor #(.gate("br")) transistor_1086 (.in(1'b0), .out(transistor_1085_out), .gate(transistor_1059_out));
  Transistor #(.\type ("n")) transistor_1087 (
    .in(transistor_1031_out), .out(transistor_1085_out), .gate(transistor_1059_out));
  Transistor #(.gate("br")) transistor_1088 (.in(transistor_1031_out), .out(transistor_1085_out), .gate(rst));
  Transistor #(.\type ("n")) transistor_1089 (.in(1'b0), .out(transistor_1089_out), .gate(rst));
  Transistor #(.gate("br")) transistor_1090 (.in(1'b0), .out(transistor_1089_out), .gate(transistor_1061_out));
  Transistor #(.\type ("n")) transistor_1091 (
    .in(transistor_1037_out), .out(transistor_1089_out), .gate(transistor_1061_out));
  Transistor #(.gate("br")) transistor_1092 (.in(transistor_1037_out), .out(transistor_1089_out), .gate(rst));
  Transistor #(.\type ("n")) transistor_1093 (.in(1'b0), .out(transistor_1093_out), .gate(rst));
  Transistor #(.gate("br")) transistor_1094 (.in(1'b0), .out(transistor_1093_out), .gate(transistor_1063_out));
  Transistor #(.\type ("n")) transistor_1095 (
    .in(transistor_1043_out), .out(transistor_1093_out), .gate(transistor_1063_out));
  Transistor #(.gate("br")) transistor_1096 (.in(transistor_1043_out), .out(transistor_1093_out), .gate(rst));
  Transistor transistor_1097 (.in(1'b1), .out(transistor_1097_out), .gate(transistor_947_out));
  Transistor transistor_1098 (.in(1'b1), .out(transistor_1098_out), .gate(transistor_953_out));
  Transistor transistor_1099 (.in(1'b1), .out(transistor_1099_out), .gate(transistor_959_out));
  Transistor transistor_1100 (.in(1'b1), .out(transistor_1100_out), .gate(transistor_965_out));
  Transistor transistor_1101 (.in(1'b1), .out(transistor_1101_out), .gate(transistor_971_out));
  Transistor transistor_1102 (.in(1'b1), .out(transistor_1102_out), .gate(transistor_977_out));
  Transistor transistor_1103 (.in(1'b1), .out(transistor_1103_out), .gate(transistor_983_out));
  Transistor transistor_1104 (.in(1'b1), .out(transistor_1104_out), .gate(transistor_989_out));
  Transistor transistor_1105 (.in(1'b1), .out(transistor_1097_out), .gate(transistor_1065_out));
  Transistor #(.\type ("n")) transistor_1106 (
    .in(transistor_1107_out), .out(transistor_1097_out), .gate(transistor_1065_out));
  Transistor #(.\type ("n")) transistor_1107 (.in(1'b0), .out(transistor_1107_out), .gate(transistor_947_out));
  Transistor transistor_1108 (.in(1'b1), .out(transistor_1098_out), .gate(transistor_1069_out));
  Transistor #(.\type ("n")) transistor_1109 (
    .in(transistor_1110_out), .out(transistor_1098_out), .gate(transistor_1069_out));
  Transistor #(.\type ("n")) transistor_1110 (.in(1'b0), .out(transistor_1110_out), .gate(transistor_953_out));
  Transistor transistor_1111 (.in(1'b1), .out(transistor_1099_out), .gate(transistor_1073_out));
  Transistor #(.\type ("n")) transistor_1112 (
    .in(transistor_1113_out), .out(transistor_1099_out), .gate(transistor_1073_out));
  Transistor #(.\type ("n")) transistor_1113 (.in(1'b0), .out(transistor_1113_out), .gate(transistor_959_out));
  Transistor transistor_1114 (.in(1'b1), .out(transistor_1100_out), .gate(transistor_1077_out));
  Transistor #(.\type ("n")) transistor_1115 (
    .in(transistor_1116_out), .out(transistor_1100_out), .gate(transistor_1077_out));
  Transistor #(.\type ("n")) transistor_1116 (.in(1'b0), .out(transistor_1116_out), .gate(transistor_965_out));
  Transistor transistor_1117 (.in(1'b1), .out(transistor_1101_out), .gate(transistor_1081_out));
  Transistor #(.\type ("n")) transistor_1118 (
    .in(transistor_1119_out), .out(transistor_1101_out), .gate(transistor_1081_out));
  Transistor #(.\type ("n")) transistor_1119 (.in(1'b0), .out(transistor_1119_out), .gate(transistor_971_out));
  Transistor transistor_1120 (.in(1'b1), .out(transistor_1102_out), .gate(transistor_1085_out));
  Transistor #(.\type ("n")) transistor_1121 (
    .in(transistor_1122_out), .out(transistor_1102_out), .gate(transistor_1085_out));
  Transistor #(.\type ("n")) transistor_1122 (.in(1'b0), .out(transistor_1122_out), .gate(transistor_977_out));
  Transistor transistor_1123 (.in(1'b1), .out(transistor_1103_out), .gate(transistor_1089_out));
  Transistor #(.\type ("n")) transistor_1124 (
    .in(transistor_1125_out), .out(transistor_1103_out), .gate(transistor_1089_out));
  Transistor #(.\type ("n")) transistor_1125 (.in(1'b0), .out(transistor_1125_out), .gate(transistor_983_out));
  Transistor transistor_1126 (.in(1'b1), .out(transistor_1104_out), .gate(transistor_1093_out));
  Transistor #(.\type ("n")) transistor_1127 (
    .in(transistor_1128_out), .out(transistor_1104_out), .gate(transistor_1093_out));
  Transistor #(.\type ("n")) transistor_1128 (.in(1'b0), .out(transistor_1128_out), .gate(transistor_989_out));
  Transistor transistor_1129 (.in(1'b1), .out(transistor_1129_out), .gate(transistor_1097_out));
  Transistor #(.\type ("n")) transistor_1130 (.in(1'b0), .out(transistor_1129_out), .gate(transistor_1097_out));
  Transistor transistor_1131 (.in(1'b1), .out(transistor_1131_out), .gate(transistor_1098_out));
  Transistor #(.\type ("n")) transistor_1132 (.in(1'b0), .out(transistor_1131_out), .gate(transistor_1098_out));
  Transistor transistor_1133 (.in(1'b1), .out(transistor_1133_out), .gate(transistor_1099_out));
  Transistor #(.\type ("n")) transistor_1134 (.in(1'b0), .out(transistor_1133_out), .gate(transistor_1099_out));
  Transistor transistor_1135 (.in(1'b1), .out(transistor_1135_out), .gate(transistor_1100_out));
  Transistor #(.\type ("n")) transistor_1136 (.in(1'b0), .out(transistor_1135_out), .gate(transistor_1100_out));
  Transistor transistor_1137 (.in(1'b1), .out(transistor_1137_out), .gate(transistor_1101_out));
  Transistor #(.\type ("n")) transistor_1138 (.in(1'b0), .out(transistor_1137_out), .gate(transistor_1101_out));
  Transistor transistor_1139 (.in(1'b1), .out(transistor_1139_out), .gate(transistor_1102_out));
  Transistor #(.\type ("n")) transistor_1140 (.in(1'b0), .out(transistor_1139_out), .gate(transistor_1102_out));
  Transistor transistor_1141 (.in(1'b1), .out(transistor_1141_out), .gate(transistor_1103_out));
  Transistor #(.\type ("n")) transistor_1142 (.in(1'b0), .out(transistor_1141_out), .gate(transistor_1103_out));
  Transistor transistor_1143 (.in(1'b1), .out(transistor_1143_out), .gate(transistor_1104_out));
  Transistor #(.\type ("n")) transistor_1144 (.in(1'b0), .out(transistor_1143_out), .gate(transistor_1104_out));
  Transistor transistor_1145 (.in(1'b1), .out(transistor_1145_out), .gate(transistor_947_out));
  Transistor transistor_1146 (.in(transistor_1145_out), .out(transistor_1146_out), .gate(transistor_1065_out));
  Transistor #(.\type ("n")) transistor_1147 (.in(1'b0), .out(transistor_1146_out), .gate(transistor_1065_out));
  Transistor #(.\type ("n")) transistor_1148 (.in(1'b0), .out(transistor_1146_out), .gate(transistor_947_out));
  Transistor transistor_1149 (.in(1'b1), .out(transistor_1149_out), .gate(transistor_953_out));
  Transistor transistor_1150 (.in(transistor_1149_out), .out(transistor_1150_out), .gate(transistor_1069_out));
  Transistor #(.\type ("n")) transistor_1151 (.in(1'b0), .out(transistor_1150_out), .gate(transistor_1069_out));
  Transistor #(.\type ("n")) transistor_1152 (.in(1'b0), .out(transistor_1150_out), .gate(transistor_953_out));
  Transistor transistor_1153 (.in(1'b1), .out(transistor_1153_out), .gate(transistor_959_out));
  Transistor transistor_1154 (.in(transistor_1153_out), .out(transistor_1154_out), .gate(transistor_1073_out));
  Transistor #(.\type ("n")) transistor_1155 (.in(1'b0), .out(transistor_1154_out), .gate(transistor_959_out));
  Transistor #(.\type ("n")) transistor_1156 (.in(1'b0), .out(transistor_1154_out), .gate(transistor_1073_out));
  Transistor transistor_1157 (.in(1'b1), .out(transistor_1157_out), .gate(transistor_965_out));
  Transistor transistor_1158 (.in(transistor_1157_out), .out(transistor_1158_out), .gate(transistor_1077_out));
  Transistor #(.\type ("n")) transistor_1159 (.in(1'b0), .out(transistor_1158_out), .gate(transistor_1077_out));
  Transistor #(.\type ("n")) transistor_1160 (.in(1'b0), .out(transistor_1158_out), .gate(transistor_965_out));
  Transistor transistor_1161 (.in(1'b1), .out(transistor_1161_out), .gate(transistor_971_out));
  Transistor transistor_1162 (.in(transistor_1161_out), .out(transistor_1162_out), .gate(transistor_1081_out));
  Transistor #(.\type ("n")) transistor_1163 (.in(1'b0), .out(transistor_1162_out), .gate(transistor_1081_out));
  Transistor #(.\type ("n")) transistor_1164 (.in(1'b0), .out(transistor_1162_out), .gate(transistor_971_out));
  Transistor transistor_1165 (.in(1'b1), .out(transistor_1165_out), .gate(transistor_977_out));
  Transistor transistor_1166 (.in(transistor_1165_out), .out(transistor_1166_out), .gate(transistor_1085_out));
  Transistor #(.\type ("n")) transistor_1167 (.in(1'b0), .out(transistor_1166_out), .gate(transistor_1085_out));
  Transistor #(.\type ("n")) transistor_1168 (.in(1'b0), .out(transistor_1166_out), .gate(transistor_977_out));
  Transistor transistor_1169 (.in(1'b1), .out(transistor_1169_out), .gate(transistor_983_out));
  Transistor transistor_1170 (.in(transistor_1169_out), .out(transistor_1170_out), .gate(transistor_1089_out));
  Transistor #(.\type ("n")) transistor_1171 (.in(1'b0), .out(transistor_1170_out), .gate(transistor_1089_out));
  Transistor #(.\type ("n")) transistor_1172 (.in(1'b0), .out(transistor_1170_out), .gate(transistor_983_out));
  Transistor transistor_1173 (.in(1'b1), .out(transistor_1173_out), .gate(transistor_989_out));
  Transistor transistor_1174 (.in(transistor_1173_out), .out(transistor_1174_out), .gate(transistor_1093_out));
  Transistor #(.\type ("n")) transistor_1175 (.in(1'b0), .out(transistor_1174_out), .gate(transistor_1093_out));
  Transistor #(.\type ("n")) transistor_1176 (.in(1'b0), .out(transistor_1174_out), .gate(transistor_989_out));
  Transistor transistor_1177 (.in(1'b1), .out(transistor_1177_out), .gate(transistor_1146_out));
  Transistor #(.\type ("n")) transistor_1178 (.in(1'b0), .out(transistor_1177_out), .gate(transistor_1146_out));
  Transistor transistor_1179 (.in(1'b1), .out(transistor_1179_out), .gate(transistor_1150_out));
  Transistor #(.\type ("n")) transistor_1180 (.in(1'b0), .out(transistor_1179_out), .gate(transistor_1150_out));
  Transistor transistor_1181 (.in(1'b1), .out(transistor_1181_out), .gate(transistor_1154_out));
  Transistor #(.\type ("n")) transistor_1182 (.in(1'b0), .out(transistor_1181_out), .gate(transistor_1154_out));
  Transistor transistor_1183 (.in(1'b1), .out(transistor_1183_out), .gate(transistor_1158_out));
  Transistor #(.\type ("n")) transistor_1184 (.in(1'b0), .out(transistor_1183_out), .gate(transistor_1158_out));
  Transistor transistor_1185 (.in(1'b1), .out(transistor_1185_out), .gate(transistor_1162_out));
  Transistor #(.\type ("n")) transistor_1186 (.in(1'b0), .out(transistor_1185_out), .gate(transistor_1162_out));
  Transistor transistor_1187 (.in(1'b1), .out(transistor_1187_out), .gate(transistor_1166_out));
  Transistor #(.\type ("n")) transistor_1188 (.in(1'b0), .out(transistor_1187_out), .gate(transistor_1166_out));
  Transistor transistor_1189 (.in(1'b1), .out(transistor_1189_out), .gate(transistor_1170_out));
  Transistor #(.\type ("n")) transistor_1190 (.in(1'b0), .out(transistor_1189_out), .gate(transistor_1170_out));
  Transistor transistor_1191 (.in(1'b1), .out(transistor_1191_out), .gate(transistor_1174_out));
  Transistor #(.\type ("n")) transistor_1192 (.in(1'b0), .out(transistor_1191_out), .gate(transistor_1174_out));
  Transistor transistor_1193 (.in(1'b1), .out(transistor_1193_out), .gate(transistor_947_out));
  Transistor transistor_1194 (.in(1'b1), .out(transistor_1194_out), .gate(transistor_953_out));
  Transistor transistor_1195 (.in(1'b1), .out(transistor_1195_out), .gate(transistor_959_out));
  Transistor transistor_1196 (.in(1'b1), .out(transistor_1196_out), .gate(transistor_965_out));
  Transistor transistor_1197 (.in(1'b1), .out(transistor_1197_out), .gate(transistor_971_out));
  Transistor transistor_1198 (.in(1'b1), .out(transistor_1198_out), .gate(transistor_977_out));
  Transistor transistor_1199 (.in(1'b1), .out(transistor_1199_out), .gate(transistor_983_out));
  Transistor transistor_1200 (.in(1'b1), .out(transistor_1200_out), .gate(transistor_989_out));
  Transistor transistor_1201 (.in(1'b1), .out(transistor_1201_out), .gate(r_2));
  Transistor #(.\type ("n")) transistor_1202 (.in(1'b0), .out(transistor_1201_out), .gate(r_2));
  Transistor #(.gate("br")) transistor_1203 (.in(undriven), .out(_7), .gate(transistor_1201_out));
  Transistor #(.\type ("n")) transistor_1204 (.in(undriven), .out(_7), .gate(r_2));
  LED led_9 (.in(undriven));
  Transistor transistor_1205 (.in(1'b1), .out(transistor_1193_out), .gate(transistor_1065_out));
  Transistor transistor_1206 (.in(1'b1), .out(transistor_1206_out), .gate(transistor_1193_out));
  Transistor #(.\type ("n")) transistor_1207 (
    .in(transistor_1208_out), .out(transistor_1193_out), .gate(transistor_947_out));
  Transistor #(.\type ("n")) transistor_1208 (.in(1'b0), .out(transistor_1208_out), .gate(transistor_1065_out));
  Transistor transistor_1209 (.in(1'b1), .out(transistor_1209_out), .gate(transistor_1194_out));
  Transistor transistor_1210 (.in(1'b1), .out(transistor_1194_out), .gate(transistor_1069_out));
  Transistor #(.\type ("n")) transistor_1211 (
    .in(transistor_1212_out), .out(transistor_1194_out), .gate(transistor_953_out));
  Transistor #(.\type ("n")) transistor_1212 (.in(1'b0), .out(transistor_1212_out), .gate(transistor_1069_out));
  Transistor transistor_1213 (.in(1'b1), .out(transistor_1195_out), .gate(transistor_1073_out));
  Transistor transistor_1214 (.in(1'b1), .out(transistor_1214_out), .gate(transistor_1195_out));
  Transistor #(.\type ("n")) transistor_1215 (
    .in(transistor_1216_out), .out(transistor_1195_out), .gate(transistor_959_out));
  Transistor #(.\type ("n")) transistor_1216 (.in(1'b0), .out(transistor_1216_out), .gate(transistor_1073_out));
  Transistor transistor_1217 (.in(1'b1), .out(transistor_1217_out), .gate(transistor_1196_out));
  Transistor transistor_1218 (.in(1'b1), .out(transistor_1196_out), .gate(transistor_1077_out));
  Transistor #(.\type ("n")) transistor_1219 (
    .in(transistor_1220_out), .out(transistor_1196_out), .gate(transistor_965_out));
  Transistor #(.\type ("n")) transistor_1220 (.in(1'b0), .out(transistor_1220_out), .gate(transistor_1077_out));
  Transistor transistor_1221 (.in(1'b1), .out(transistor_1197_out), .gate(transistor_1081_out));
  Transistor transistor_1222 (.in(1'b1), .out(transistor_1222_out), .gate(transistor_1197_out));
  Transistor #(.\type ("n")) transistor_1223 (
    .in(transistor_1224_out), .out(transistor_1197_out), .gate(transistor_971_out));
  Transistor #(.\type ("n")) transistor_1224 (.in(1'b0), .out(transistor_1224_out), .gate(transistor_1081_out));
  Transistor transistor_1225 (.in(1'b1), .out(transistor_1198_out), .gate(transistor_1085_out));
  Transistor transistor_1226 (.in(1'b1), .out(transistor_1226_out), .gate(transistor_1198_out));
  Transistor #(.\type ("n")) transistor_1227 (
    .in(transistor_1228_out), .out(transistor_1198_out), .gate(transistor_977_out));
  Transistor #(.\type ("n")) transistor_1228 (.in(1'b0), .out(transistor_1228_out), .gate(transistor_1085_out));
  Transistor transistor_1229 (.in(1'b1), .out(transistor_1229_out), .gate(transistor_1199_out));
  Transistor transistor_1230 (.in(1'b1), .out(transistor_1199_out), .gate(transistor_1089_out));
  Transistor #(.\type ("n")) transistor_1231 (
    .in(transistor_1232_out), .out(transistor_1199_out), .gate(transistor_983_out));
  Transistor #(.\type ("n")) transistor_1232 (.in(1'b0), .out(transistor_1232_out), .gate(transistor_1089_out));
  Transistor transistor_1233 (.in(1'b1), .out(transistor_1200_out), .gate(transistor_1093_out));
  Transistor transistor_1234 (.in(1'b1), .out(transistor_1234_out), .gate(transistor_1200_out));
  Transistor #(.\type ("n")) transistor_1235 (
    .in(transistor_1236_out), .out(transistor_1200_out), .gate(transistor_989_out));
  Transistor #(.\type ("n")) transistor_1236 (.in(1'b0), .out(transistor_1236_out), .gate(transistor_1093_out));
  Transistor transistor_1237 (.in(1'b1), .out(transistor_1237_out), .gate(r_2));
  Transistor #(.\type ("n")) transistor_1238 (.in(1'b0), .out(transistor_1237_out), .gate(r_2));
  Transistor transistor_1239 (.in(1'b1), .out(transistor_1206_out), .gate(transistor_1065_out));
  Transistor #(.\type ("n")) transistor_1240 (
    .in(transistor_1241_out), .out(transistor_1206_out), .gate(transistor_1193_out));
  Transistor #(.\type ("n")) transistor_1241 (.in(1'b0), .out(transistor_1241_out), .gate(transistor_1065_out));
  Transistor transistor_1242 (.in(1'b1), .out(transistor_1209_out), .gate(transistor_1069_out));
  Transistor #(.\type ("n")) transistor_1243 (
    .in(transistor_1244_out), .out(transistor_1209_out), .gate(transistor_1194_out));
  Transistor #(.\type ("n")) transistor_1244 (.in(1'b0), .out(transistor_1244_out), .gate(transistor_1069_out));
  Transistor transistor_1245 (.in(1'b1), .out(transistor_1214_out), .gate(transistor_1073_out));
  Transistor #(.\type ("n")) transistor_1246 (
    .in(transistor_1247_out), .out(transistor_1214_out), .gate(transistor_1195_out));
  Transistor #(.\type ("n")) transistor_1247 (.in(1'b0), .out(transistor_1247_out), .gate(transistor_1073_out));
  Transistor transistor_1248 (.in(1'b1), .out(transistor_1217_out), .gate(transistor_1077_out));
  Transistor #(.\type ("n")) transistor_1249 (
    .in(transistor_1250_out), .out(transistor_1217_out), .gate(transistor_1196_out));
  Transistor #(.\type ("n")) transistor_1250 (.in(1'b0), .out(transistor_1250_out), .gate(transistor_1077_out));
  Transistor transistor_1251 (.in(1'b1), .out(transistor_1222_out), .gate(transistor_1081_out));
  Transistor #(.\type ("n")) transistor_1252 (
    .in(transistor_1253_out), .out(transistor_1222_out), .gate(transistor_1197_out));
  Transistor #(.\type ("n")) transistor_1253 (.in(1'b0), .out(transistor_1253_out), .gate(transistor_1081_out));
  Transistor transistor_1254 (.in(1'b1), .out(transistor_1226_out), .gate(transistor_1085_out));
  Transistor #(.\type ("n")) transistor_1255 (
    .in(transistor_1256_out), .out(transistor_1226_out), .gate(transistor_1198_out));
  Transistor #(.\type ("n")) transistor_1256 (.in(1'b0), .out(transistor_1256_out), .gate(transistor_1085_out));
  Transistor transistor_1257 (.in(1'b1), .out(transistor_1229_out), .gate(transistor_1089_out));
  Transistor #(.\type ("n")) transistor_1258 (
    .in(transistor_1259_out), .out(transistor_1229_out), .gate(transistor_1199_out));
  Transistor #(.\type ("n")) transistor_1259 (.in(1'b0), .out(transistor_1259_out), .gate(transistor_1089_out));
  Transistor transistor_1260 (.in(1'b1), .out(transistor_1234_out), .gate(transistor_1093_out));
  Transistor #(.\type ("n")) transistor_1261 (
    .in(transistor_1262_out), .out(transistor_1234_out), .gate(transistor_1200_out));
  Transistor #(.\type ("n")) transistor_1262 (.in(1'b0), .out(transistor_1262_out), .gate(transistor_1093_out));
  Transistor #(.gate("br")) transistor_1263 (.in(undriven_2), .out(_6), .gate(transistor_1237_out));
  Transistor #(.\type ("n")) transistor_1264 (.in(undriven_2), .out(_6), .gate(r_2));
  LED led_10 (.in(undriven_2));
  Transistor transistor_1265 (.in(1'b1), .out(transistor_1265_out), .gate(transistor_1193_out));
  Transistor transistor_1266 (.in(1'b1), .out(transistor_1265_out), .gate(transistor_947_out));
  Transistor #(.\type ("n")) transistor_1267 (
    .in(transistor_1268_out), .out(transistor_1265_out), .gate(transistor_1193_out));
  Transistor #(.\type ("n")) transistor_1268 (.in(1'b0), .out(transistor_1268_out), .gate(transistor_947_out));
  Transistor transistor_1269 (.in(1'b1), .out(transistor_1269_out), .gate(transistor_1194_out));
  Transistor transistor_1270 (.in(1'b1), .out(transistor_1269_out), .gate(transistor_953_out));
  Transistor #(.\type ("n")) transistor_1271 (
    .in(transistor_1272_out), .out(transistor_1269_out), .gate(transistor_1194_out));
  Transistor #(.\type ("n")) transistor_1272 (.in(1'b0), .out(transistor_1272_out), .gate(transistor_953_out));
  Transistor transistor_1273 (.in(1'b1), .out(transistor_1273_out), .gate(transistor_959_out));
  Transistor transistor_1274 (.in(1'b1), .out(transistor_1273_out), .gate(transistor_1195_out));
  Transistor #(.\type ("n")) transistor_1275 (
    .in(transistor_1276_out), .out(transistor_1273_out), .gate(transistor_1195_out));
  Transistor #(.\type ("n")) transistor_1276 (.in(1'b0), .out(transistor_1276_out), .gate(transistor_959_out));
  Transistor transistor_1277 (.in(1'b1), .out(transistor_1277_out), .gate(transistor_1196_out));
  Transistor transistor_1278 (.in(1'b1), .out(transistor_1277_out), .gate(transistor_965_out));
  Transistor #(.\type ("n")) transistor_1279 (
    .in(transistor_1280_out), .out(transistor_1277_out), .gate(transistor_1196_out));
  Transistor #(.\type ("n")) transistor_1280 (.in(1'b0), .out(transistor_1280_out), .gate(transistor_965_out));
  Transistor transistor_1281 (.in(1'b1), .out(transistor_1281_out), .gate(transistor_1197_out));
  Transistor transistor_1282 (.in(1'b1), .out(transistor_1281_out), .gate(transistor_971_out));
  Transistor #(.\type ("n")) transistor_1283 (
    .in(transistor_1284_out), .out(transistor_1281_out), .gate(transistor_1197_out));
  Transistor #(.\type ("n")) transistor_1284 (.in(1'b0), .out(transistor_1284_out), .gate(transistor_971_out));
  Transistor transistor_1285 (.in(1'b1), .out(transistor_1285_out), .gate(transistor_1198_out));
  Transistor transistor_1286 (.in(1'b1), .out(transistor_1285_out), .gate(transistor_977_out));
  Transistor #(.\type ("n")) transistor_1287 (
    .in(transistor_1288_out), .out(transistor_1285_out), .gate(transistor_1198_out));
  Transistor #(.\type ("n")) transistor_1288 (.in(1'b0), .out(transistor_1288_out), .gate(transistor_977_out));
  Transistor transistor_1289 (.in(1'b1), .out(transistor_1289_out), .gate(transistor_1199_out));
  Transistor transistor_1290 (.in(1'b1), .out(transistor_1289_out), .gate(transistor_983_out));
  Transistor #(.\type ("n")) transistor_1291 (
    .in(transistor_1292_out), .out(transistor_1289_out), .gate(transistor_1199_out));
  Transistor #(.\type ("n")) transistor_1292 (.in(1'b0), .out(transistor_1292_out), .gate(transistor_983_out));
  Transistor transistor_1293 (.in(1'b1), .out(transistor_1293_out), .gate(transistor_1200_out));
  Transistor transistor_1294 (.in(1'b1), .out(transistor_1293_out), .gate(transistor_989_out));
  Transistor #(.\type ("n")) transistor_1295 (
    .in(transistor_1296_out), .out(transistor_1293_out), .gate(transistor_1200_out));
  Transistor #(.\type ("n")) transistor_1296 (.in(1'b0), .out(transistor_1296_out), .gate(transistor_989_out));
  Transistor transistor_1297 (.in(1'b1), .out(transistor_1297_out), .gate(r_2));
  Transistor #(.\type ("n")) transistor_1298 (.in(1'b0), .out(transistor_1297_out), .gate(r_2));
  Transistor #(.\type ("n")) transistor_1299 (.in(undriven_3), .out(_5), .gate(r_2));
  Transistor #(.gate("br")) transistor_1300 (.in(undriven_3), .out(_5), .gate(transistor_1297_out));
  LED led_11 (.in(undriven_3));
  Transistor transistor_1301 (.in(1'b1), .out(transistor_1301_out), .gate(transistor_1265_out));
  Transistor transistor_1302 (.in(1'b1), .out(transistor_1302_out), .gate(transistor_1269_out));
  Transistor transistor_1303 (.in(1'b1), .out(transistor_1303_out), .gate(transistor_1273_out));
  Transistor transistor_1304 (.in(1'b1), .out(transistor_1304_out), .gate(transistor_1277_out));
  Transistor transistor_1305 (.in(1'b1), .out(transistor_1305_out), .gate(transistor_1281_out));
  Transistor transistor_1306 (.in(1'b1), .out(transistor_1306_out), .gate(transistor_1285_out));
  Transistor transistor_1307 (.in(1'b1), .out(transistor_1307_out), .gate(transistor_1289_out));
  Transistor transistor_1308 (.in(1'b1), .out(transistor_1308_out), .gate(transistor_1293_out));
  Transistor transistor_1309 (.in(1'b1), .out(transistor_1301_out), .gate(transistor_1206_out));
  Transistor #(.\type ("n")) transistor_1310 (
    .in(transistor_1311_out), .out(transistor_1301_out), .gate(transistor_1265_out));
  Transistor #(.\type ("n")) transistor_1311 (.in(1'b0), .out(transistor_1311_out), .gate(transistor_1206_out));
  Transistor transistor_1312 (.in(1'b1), .out(transistor_1302_out), .gate(transistor_1209_out));
  Transistor #(.\type ("n")) transistor_1313 (
    .in(transistor_1314_out), .out(transistor_1302_out), .gate(transistor_1269_out));
  Transistor #(.\type ("n")) transistor_1314 (.in(1'b0), .out(transistor_1314_out), .gate(transistor_1209_out));
  Transistor transistor_1315 (.in(1'b1), .out(transistor_1303_out), .gate(transistor_1214_out));
  Transistor #(.\type ("n")) transistor_1316 (
    .in(transistor_1317_out), .out(transistor_1303_out), .gate(transistor_1273_out));
  Transistor #(.\type ("n")) transistor_1317 (.in(1'b0), .out(transistor_1317_out), .gate(transistor_1214_out));
  Transistor transistor_1318 (.in(1'b1), .out(transistor_1304_out), .gate(transistor_1217_out));
  Transistor #(.\type ("n")) transistor_1319 (
    .in(transistor_1320_out), .out(transistor_1304_out), .gate(transistor_1277_out));
  Transistor #(.\type ("n")) transistor_1320 (.in(1'b0), .out(transistor_1320_out), .gate(transistor_1217_out));
  Transistor transistor_1321 (.in(1'b1), .out(transistor_1305_out), .gate(transistor_1222_out));
  Transistor #(.\type ("n")) transistor_1322 (
    .in(transistor_1323_out), .out(transistor_1305_out), .gate(transistor_1281_out));
  Transistor #(.\type ("n")) transistor_1323 (.in(1'b0), .out(transistor_1323_out), .gate(transistor_1222_out));
  Transistor transistor_1324 (.in(1'b1), .out(transistor_1306_out), .gate(transistor_1226_out));
  Transistor #(.\type ("n")) transistor_1325 (
    .in(transistor_1326_out), .out(transistor_1306_out), .gate(transistor_1285_out));
  Transistor #(.\type ("n")) transistor_1326 (.in(1'b0), .out(transistor_1326_out), .gate(transistor_1226_out));
  Transistor transistor_1327 (.in(1'b1), .out(transistor_1307_out), .gate(transistor_1229_out));
  Transistor #(.\type ("n")) transistor_1328 (
    .in(transistor_1329_out), .out(transistor_1307_out), .gate(transistor_1289_out));
  Transistor #(.\type ("n")) transistor_1329 (.in(1'b0), .out(transistor_1329_out), .gate(transistor_1229_out));
  Transistor transistor_1330 (.in(1'b1), .out(transistor_1308_out), .gate(transistor_1234_out));
  Transistor #(.\type ("n")) transistor_1331 (
    .in(transistor_1332_out), .out(transistor_1308_out), .gate(transistor_1293_out));
  Transistor #(.\type ("n")) transistor_1332 (.in(1'b0), .out(transistor_1332_out), .gate(transistor_1234_out));
  Transistor transistor_1333 (.in(1'b1), .out(transistor_1333_out), .gate(r_2));
  Transistor #(.\type ("n")) transistor_1334 (.in(1'b0), .out(transistor_1333_out), .gate(r_2));
  Transistor #(.\type ("n")) transistor_1335 (.in(undriven_4), .out(_4), .gate(r_2));
  Transistor #(.gate("br")) transistor_1336 (.in(undriven_4), .out(_4), .gate(transistor_1333_out));
  LED led_12 (.in(undriven_4));
  Transistor transistor_1337 (.in(1'b1), .out(transistor_1337_out), .gate(transistor_1065_out));
  Transistor transistor_1338 (.in(1'b1), .out(transistor_1337_out), .gate(op0));
  Transistor #(.\type ("n")) transistor_1339 (.in(transistor_1340_out), .out(transistor_1337_out), .gate(op0));
  Transistor #(.\type ("n")) transistor_1340 (.in(1'b0), .out(transistor_1340_out), .gate(transistor_1065_out));
  Transistor transistor_1341 (.in(1'b1), .out(transistor_1341_out), .gate(transistor_1069_out));
  Transistor transistor_1342 (.in(1'b1), .out(transistor_1341_out), .gate(op0));
  Transistor #(.\type ("n")) transistor_1343 (.in(transistor_1344_out), .out(transistor_1341_out), .gate(op0));
  Transistor #(.\type ("n")) transistor_1344 (.in(1'b0), .out(transistor_1344_out), .gate(transistor_1069_out));
  Transistor transistor_1345 (.in(1'b1), .out(transistor_1345_out), .gate(transistor_1073_out));
  Transistor transistor_1346 (.in(1'b1), .out(transistor_1345_out), .gate(op0));
  Transistor #(.\type ("n")) transistor_1347 (.in(transistor_1348_out), .out(transistor_1345_out), .gate(op0));
  Transistor #(.\type ("n")) transistor_1348 (.in(1'b0), .out(transistor_1348_out), .gate(transistor_1073_out));
  Transistor transistor_1349 (.in(1'b1), .out(transistor_1349_out), .gate(transistor_1077_out));
  Transistor transistor_1350 (.in(1'b1), .out(transistor_1349_out), .gate(op0));
  Transistor #(.\type ("n")) transistor_1351 (.in(transistor_1352_out), .out(transistor_1349_out), .gate(op0));
  Transistor #(.\type ("n")) transistor_1352 (.in(1'b0), .out(transistor_1352_out), .gate(transistor_1077_out));
  Transistor transistor_1353 (.in(1'b1), .out(transistor_1353_out), .gate(transistor_1081_out));
  Transistor transistor_1354 (.in(1'b1), .out(transistor_1353_out), .gate(op0));
  Transistor #(.\type ("n")) transistor_1355 (.in(transistor_1356_out), .out(transistor_1353_out), .gate(op0));
  Transistor #(.\type ("n")) transistor_1356 (.in(1'b0), .out(transistor_1356_out), .gate(transistor_1081_out));
  Transistor transistor_1357 (.in(1'b1), .out(transistor_1357_out), .gate(op0));
  Transistor transistor_1358 (.in(1'b1), .out(transistor_1357_out), .gate(transistor_1085_out));
  Transistor #(.\type ("n")) transistor_1359 (.in(transistor_1360_out), .out(transistor_1357_out), .gate(op0));
  Transistor #(.\type ("n")) transistor_1360 (.in(1'b0), .out(transistor_1360_out), .gate(transistor_1085_out));
  Transistor transistor_1361 (.in(1'b1), .out(transistor_1361_out), .gate(op0));
  Transistor transistor_1362 (.in(1'b1), .out(transistor_1361_out), .gate(transistor_1089_out));
  Transistor #(.\type ("n")) transistor_1363 (.in(transistor_1364_out), .out(transistor_1361_out), .gate(op0));
  Transistor #(.\type ("n")) transistor_1364 (.in(1'b0), .out(transistor_1364_out), .gate(transistor_1089_out));
  Transistor transistor_1365 (.in(1'b1), .out(transistor_1365_out), .gate(op0));
  Transistor transistor_1366 (.in(1'b1), .out(transistor_1365_out), .gate(transistor_1093_out));
  Transistor #(.\type ("n")) transistor_1367 (.in(transistor_1368_out), .out(transistor_1365_out), .gate(op0));
  Transistor #(.\type ("n")) transistor_1368 (.in(1'b0), .out(transistor_1368_out), .gate(transistor_1093_out));
  Transistor transistor_1369 (.in(1'b1), .out(transistor_1369_out), .gate(r_2));
  Transistor #(.\type ("n")) transistor_1370 (.in(1'b0), .out(transistor_1369_out), .gate(r_2));
  Transistor #(.\type ("n")) transistor_1371 (.in(undriven_5), .out(_3), .gate(r_2));
  Transistor transistor_1372 (.in(1'b1), .out(transistor_1372_out), .gate(transistor_1337_out));
  Transistor transistor_1373 (.in(1'b1), .out(transistor_1373_out), .gate(transistor_1341_out));
  Transistor transistor_1374 (.in(1'b1), .out(transistor_1374_out), .gate(transistor_1345_out));
  Transistor transistor_1375 (.in(1'b1), .out(transistor_1375_out), .gate(transistor_1349_out));
  Transistor transistor_1376 (.in(1'b1), .out(transistor_1376_out), .gate(transistor_1353_out));
  Transistor transistor_1377 (.in(1'b1), .out(transistor_1377_out), .gate(transistor_1357_out));
  Transistor transistor_1378 (.in(1'b1), .out(transistor_1378_out), .gate(transistor_1361_out));
  Transistor transistor_1379 (.in(1'b1), .out(transistor_1379_out), .gate(transistor_1365_out));
  Transistor #(.gate("br")) transistor_1380 (.in(undriven_5), .out(_3), .gate(transistor_1369_out));
  LED led_13 (.in(undriven_5));
  Transistor transistor_1381 (.in(1'b1), .out(transistor_1372_out), .gate(transistor_1065_out));
  Transistor #(.\type ("n")) transistor_1382 (
    .in(transistor_1383_out), .out(transistor_1372_out), .gate(transistor_1337_out));
  Transistor #(.\type ("n")) transistor_1383 (.in(1'b0), .out(transistor_1383_out), .gate(transistor_1065_out));
  Transistor transistor_1384 (.in(1'b1), .out(transistor_1373_out), .gate(transistor_1069_out));
  Transistor #(.\type ("n")) transistor_1385 (
    .in(transistor_1386_out), .out(transistor_1373_out), .gate(transistor_1341_out));
  Transistor #(.\type ("n")) transistor_1386 (.in(1'b0), .out(transistor_1386_out), .gate(transistor_1069_out));
  Transistor transistor_1387 (.in(1'b1), .out(transistor_1374_out), .gate(transistor_1073_out));
  Transistor #(.\type ("n")) transistor_1388 (
    .in(transistor_1389_out), .out(transistor_1374_out), .gate(transistor_1345_out));
  Transistor #(.\type ("n")) transistor_1389 (.in(1'b0), .out(transistor_1389_out), .gate(transistor_1073_out));
  Transistor transistor_1390 (.in(1'b1), .out(transistor_1375_out), .gate(transistor_1077_out));
  Transistor #(.\type ("n")) transistor_1391 (
    .in(transistor_1392_out), .out(transistor_1375_out), .gate(transistor_1349_out));
  Transistor #(.\type ("n")) transistor_1392 (.in(1'b0), .out(transistor_1392_out), .gate(transistor_1077_out));
  Transistor transistor_1393 (.in(1'b1), .out(transistor_1376_out), .gate(transistor_1081_out));
  Transistor #(.\type ("n")) transistor_1394 (
    .in(transistor_1395_out), .out(transistor_1376_out), .gate(transistor_1353_out));
  Transistor #(.\type ("n")) transistor_1395 (.in(1'b0), .out(transistor_1395_out), .gate(transistor_1081_out));
  Transistor transistor_1396 (.in(1'b1), .out(transistor_1377_out), .gate(transistor_1085_out));
  Transistor #(.\type ("n")) transistor_1397 (
    .in(transistor_1398_out), .out(transistor_1377_out), .gate(transistor_1357_out));
  Transistor #(.\type ("n")) transistor_1398 (.in(1'b0), .out(transistor_1398_out), .gate(transistor_1085_out));
  Transistor transistor_1399 (.in(1'b1), .out(transistor_1378_out), .gate(transistor_1089_out));
  Transistor #(.\type ("n")) transistor_1400 (
    .in(transistor_1401_out), .out(transistor_1378_out), .gate(transistor_1361_out));
  Transistor #(.\type ("n")) transistor_1401 (.in(1'b0), .out(transistor_1401_out), .gate(transistor_1089_out));
  Transistor transistor_1402 (.in(1'b1), .out(transistor_1379_out), .gate(transistor_1093_out));
  Transistor #(.\type ("n")) transistor_1403 (
    .in(transistor_1404_out), .out(transistor_1379_out), .gate(transistor_1365_out));
  Transistor #(.\type ("n")) transistor_1404 (.in(1'b0), .out(transistor_1404_out), .gate(transistor_1093_out));
  Transistor transistor_1405 (.in(1'b1), .out(transistor_1405_out), .gate(r_2));
  Transistor #(.\type ("n")) transistor_1406 (.in(1'b0), .out(transistor_1405_out), .gate(r_2));
  Transistor #(.\type ("n")) transistor_1407 (.in(undriven_6), .out(_2), .gate(r_2));
  Transistor #(.gate("br")) transistor_1408 (.in(undriven_6), .out(_2), .gate(transistor_1405_out));
  LED led_14 (.in(undriven_6));
  Transistor transistor_1409 (.in(1'b1), .out(transistor_1409_out), .gate(transistor_1337_out));
  Transistor transistor_1410 (.in(1'b1), .out(transistor_1409_out), .gate(op0));
  Transistor #(.\type ("n")) transistor_1411 (
    .in(transistor_1412_out), .out(transistor_1409_out), .gate(transistor_1337_out));
  Transistor #(.\type ("n")) transistor_1412 (.in(1'b0), .out(transistor_1412_out), .gate(op0));
  Transistor transistor_1413 (.in(1'b1), .out(transistor_1413_out), .gate(transistor_1341_out));
  Transistor transistor_1414 (.in(1'b1), .out(transistor_1413_out), .gate(op0));
  Transistor #(.\type ("n")) transistor_1415 (
    .in(transistor_1416_out), .out(transistor_1413_out), .gate(transistor_1341_out));
  Transistor #(.\type ("n")) transistor_1416 (.in(1'b0), .out(transistor_1416_out), .gate(op0));
  Transistor transistor_1417 (.in(1'b1), .out(transistor_1417_out), .gate(op0));
  Transistor transistor_1418 (.in(1'b1), .out(transistor_1417_out), .gate(transistor_1345_out));
  Transistor #(.\type ("n")) transistor_1419 (
    .in(transistor_1420_out), .out(transistor_1417_out), .gate(transistor_1345_out));
  Transistor #(.\type ("n")) transistor_1420 (.in(1'b0), .out(transistor_1420_out), .gate(op0));
  Transistor transistor_1421 (.in(1'b1), .out(transistor_1421_out), .gate(op0));
  Transistor transistor_1422 (.in(1'b1), .out(transistor_1421_out), .gate(transistor_1349_out));
  Transistor #(.\type ("n")) transistor_1423 (
    .in(transistor_1424_out), .out(transistor_1421_out), .gate(transistor_1349_out));
  Transistor #(.\type ("n")) transistor_1424 (.in(1'b0), .out(transistor_1424_out), .gate(op0));
  Transistor transistor_1425 (.in(1'b1), .out(transistor_1425_out), .gate(transistor_1353_out));
  Transistor transistor_1426 (.in(1'b1), .out(transistor_1425_out), .gate(op0));
  Transistor #(.\type ("n")) transistor_1427 (
    .in(transistor_1428_out), .out(transistor_1425_out), .gate(transistor_1353_out));
  Transistor #(.\type ("n")) transistor_1428 (.in(1'b0), .out(transistor_1428_out), .gate(op0));
  Transistor transistor_1429 (.in(1'b1), .out(transistor_1429_out), .gate(op0));
  Transistor transistor_1430 (.in(1'b1), .out(transistor_1429_out), .gate(transistor_1357_out));
  Transistor #(.\type ("n")) transistor_1431 (
    .in(transistor_1432_out), .out(transistor_1429_out), .gate(transistor_1357_out));
  Transistor #(.\type ("n")) transistor_1432 (.in(1'b0), .out(transistor_1432_out), .gate(op0));
  Transistor transistor_1433 (.in(1'b1), .out(transistor_1433_out), .gate(op0));
  Transistor transistor_1434 (.in(1'b1), .out(transistor_1433_out), .gate(transistor_1361_out));
  Transistor #(.\type ("n")) transistor_1435 (
    .in(transistor_1436_out), .out(transistor_1433_out), .gate(transistor_1361_out));
  Transistor #(.\type ("n")) transistor_1436 (.in(1'b0), .out(transistor_1436_out), .gate(op0));
  Transistor transistor_1437 (.in(1'b1), .out(transistor_1437_out), .gate(op0));
  Transistor transistor_1438 (.in(1'b1), .out(transistor_1437_out), .gate(transistor_1365_out));
  Transistor #(.\type ("n")) transistor_1439 (
    .in(transistor_1440_out), .out(transistor_1437_out), .gate(transistor_1365_out));
  Transistor #(.\type ("n")) transistor_1440 (.in(1'b0), .out(transistor_1440_out), .gate(op0));
  Transistor transistor_1441 (.in(1'b1), .out(transistor_1441_out), .gate(transistor_1409_out));
  Transistor transistor_1442 (.in(1'b1), .out(transistor_1441_out), .gate(transistor_1372_out));
  Transistor #(.\type ("n")) transistor_1443 (
    .in(transistor_1444_out), .out(transistor_1441_out), .gate(transistor_1409_out));
  Transistor #(.\type ("n")) transistor_1444 (.in(1'b0), .out(transistor_1444_out), .gate(transistor_1372_out));
  Transistor transistor_1445 (.in(1'b1), .out(transistor_1445_out), .gate(transistor_1373_out));
  Transistor transistor_1446 (.in(1'b1), .out(transistor_1445_out), .gate(transistor_1413_out));
  Transistor #(.\type ("n")) transistor_1447 (
    .in(transistor_1448_out), .out(transistor_1445_out), .gate(transistor_1413_out));
  Transistor #(.\type ("n")) transistor_1448 (.in(1'b0), .out(transistor_1448_out), .gate(transistor_1373_out));
  Transistor transistor_1449 (.in(1'b1), .out(transistor_1449_out), .gate(transistor_1374_out));
  Transistor transistor_1450 (.in(1'b1), .out(transistor_1449_out), .gate(transistor_1417_out));
  Transistor #(.\type ("n")) transistor_1451 (
    .in(transistor_1452_out), .out(transistor_1449_out), .gate(transistor_1417_out));
  Transistor #(.\type ("n")) transistor_1452 (.in(1'b0), .out(transistor_1452_out), .gate(transistor_1374_out));
  Transistor transistor_1453 (.in(1'b1), .out(transistor_1453_out), .gate(transistor_1375_out));
  Transistor transistor_1454 (.in(1'b1), .out(transistor_1453_out), .gate(transistor_1421_out));
  Transistor #(.\type ("n")) transistor_1455 (
    .in(transistor_1456_out), .out(transistor_1453_out), .gate(transistor_1421_out));
  Transistor #(.\type ("n")) transistor_1456 (.in(1'b0), .out(transistor_1456_out), .gate(transistor_1375_out));
  Transistor transistor_1457 (.in(1'b1), .out(transistor_1457_out), .gate(transistor_1376_out));
  Transistor transistor_1458 (.in(1'b1), .out(transistor_1457_out), .gate(transistor_1425_out));
  Transistor #(.\type ("n")) transistor_1459 (
    .in(transistor_1460_out), .out(transistor_1457_out), .gate(transistor_1425_out));
  Transistor #(.\type ("n")) transistor_1460 (.in(1'b0), .out(transistor_1460_out), .gate(transistor_1376_out));
  Transistor transistor_1461 (.in(1'b1), .out(transistor_1461_out), .gate(transistor_1429_out));
  Transistor transistor_1462 (.in(1'b1), .out(transistor_1461_out), .gate(transistor_1377_out));
  Transistor #(.\type ("n")) transistor_1463 (
    .in(transistor_1464_out), .out(transistor_1461_out), .gate(transistor_1429_out));
  Transistor #(.\type ("n")) transistor_1464 (.in(1'b0), .out(transistor_1464_out), .gate(transistor_1377_out));
  Transistor transistor_1465 (.in(1'b1), .out(transistor_1465_out), .gate(transistor_1433_out));
  Transistor transistor_1466 (.in(1'b1), .out(transistor_1465_out), .gate(transistor_1378_out));
  Transistor #(.\type ("n")) transistor_1467 (
    .in(transistor_1468_out), .out(transistor_1465_out), .gate(transistor_1433_out));
  Transistor #(.\type ("n")) transistor_1468 (.in(1'b0), .out(transistor_1468_out), .gate(transistor_1378_out));
  Transistor transistor_1469 (.in(1'b1), .out(transistor_1469_out), .gate(transistor_1379_out));
  Transistor transistor_1470 (.in(1'b1), .out(transistor_1469_out), .gate(transistor_1437_out));
  Transistor #(.\type ("n")) transistor_1471 (
    .in(transistor_1472_out), .out(transistor_1469_out), .gate(transistor_1437_out));
  Transistor #(.\type ("n")) transistor_1472 (.in(1'b0), .out(transistor_1472_out), .gate(transistor_1379_out));
  Transistor transistor_1473 (.in(1'b1), .out(transistor_1473_out), .gate(r_2));
  Transistor #(.\type ("n")) transistor_1474 (.in(1'b0), .out(transistor_1473_out), .gate(r_2));
  Transistor #(.gate("br")) transistor_1475 (.in(undriven_7), .out(_1), .gate(transistor_1473_out));
  Transistor #(.\type ("n")) transistor_1476 (.in(undriven_7), .out(_1), .gate(r_2));
  LED led_15 (.in(undriven_7));
  Transistor transistor_1477 (.in(1'b1), .out(transistor_1477_out), .gate(transistor_947_out));
  Transistor transistor_1478 (.in(1'b1), .out(transistor_1478_out), .gate(transistor_953_out));
  Transistor transistor_1479 (.in(1'b1), .out(transistor_1479_out), .gate(transistor_959_out));
  Transistor transistor_1480 (.in(1'b1), .out(transistor_1480_out), .gate(transistor_965_out));
  Transistor transistor_1481 (.in(1'b1), .out(transistor_1481_out), .gate(transistor_971_out));
  Transistor transistor_1482 (.in(1'b1), .out(transistor_1482_out), .gate(transistor_977_out));
  Transistor transistor_1483 (.in(1'b1), .out(transistor_1483_out), .gate(transistor_983_out));
  Transistor transistor_1484 (.in(1'b1), .out(transistor_1484_out), .gate(transistor_989_out));
  Transistor transistor_1485 (.in(1'b1), .out(transistor_1485_out), .gate(r_2));
  Transistor #(.\type ("n")) transistor_1486 (.in(1'b0), .out(transistor_1485_out), .gate(r_2));
  Transistor #(.\type ("n")) transistor_1487 (.in(undriven_8), .out(_0), .gate(r_2));
  LED led_16 (.in(undriven_8));
  Transistor transistor_1488 (.in(1'b1), .out(transistor_1477_out), .gate(transistor_1441_out));
  Transistor #(.\type ("n")) transistor_1489 (
    .in(transistor_1490_out), .out(transistor_1477_out), .gate(transistor_947_out));
  Transistor #(.\type ("n")) transistor_1490 (.in(1'b0), .out(transistor_1490_out), .gate(transistor_1441_out));
  Transistor transistor_1491 (.in(1'b1), .out(transistor_1478_out), .gate(transistor_1445_out));
  Transistor #(.\type ("n")) transistor_1492 (
    .in(transistor_1493_out), .out(transistor_1478_out), .gate(transistor_953_out));
  Transistor #(.\type ("n")) transistor_1493 (.in(1'b0), .out(transistor_1493_out), .gate(transistor_1445_out));
  Transistor transistor_1494 (.in(1'b1), .out(transistor_1479_out), .gate(transistor_1449_out));
  Transistor #(.\type ("n")) transistor_1495 (
    .in(transistor_1496_out), .out(transistor_1479_out), .gate(transistor_959_out));
  Transistor #(.\type ("n")) transistor_1496 (.in(1'b0), .out(transistor_1496_out), .gate(transistor_1449_out));
  Transistor transistor_1497 (.in(1'b1), .out(transistor_1480_out), .gate(transistor_1453_out));
  Transistor #(.\type ("n")) transistor_1498 (
    .in(transistor_1499_out), .out(transistor_1480_out), .gate(transistor_965_out));
  Transistor #(.\type ("n")) transistor_1499 (.in(1'b0), .out(transistor_1499_out), .gate(transistor_1453_out));
  Transistor transistor_1500 (.in(1'b1), .out(transistor_1481_out), .gate(transistor_1457_out));
  Transistor #(.\type ("n")) transistor_1501 (
    .in(transistor_1502_out), .out(transistor_1481_out), .gate(transistor_971_out));
  Transistor #(.\type ("n")) transistor_1502 (.in(1'b0), .out(transistor_1502_out), .gate(transistor_1457_out));
  Transistor transistor_1503 (.in(1'b1), .out(transistor_1482_out), .gate(transistor_1461_out));
  Transistor #(.\type ("n")) transistor_1504 (
    .in(transistor_1505_out), .out(transistor_1482_out), .gate(transistor_977_out));
  Transistor #(.\type ("n")) transistor_1505 (.in(1'b0), .out(transistor_1505_out), .gate(transistor_1461_out));
  Transistor transistor_1506 (.in(1'b1), .out(transistor_1483_out), .gate(transistor_1465_out));
  Transistor #(.\type ("n")) transistor_1507 (
    .in(transistor_1508_out), .out(transistor_1483_out), .gate(transistor_983_out));
  Transistor #(.\type ("n")) transistor_1508 (.in(1'b0), .out(transistor_1508_out), .gate(transistor_1465_out));
  Transistor transistor_1509 (.in(1'b1), .out(transistor_1484_out), .gate(transistor_1469_out));
  Transistor #(.\type ("n")) transistor_1510 (
    .in(transistor_1511_out), .out(transistor_1484_out), .gate(transistor_989_out));
  Transistor #(.\type ("n")) transistor_1511 (.in(1'b0), .out(transistor_1511_out), .gate(transistor_1469_out));
  Transistor #(.gate("br")) transistor_1512 (.in(undriven_8), .out(_0), .gate(transistor_1485_out));
  Transistor transistor_1513 (.in(1'b1), .out(transistor_1513_out), .gate(transistor_1477_out));
  Transistor #(.\type ("n")) transistor_1514 (.in(1'b0), .out(transistor_1513_out), .gate(transistor_1477_out));
  Transistor transistor_1515 (.in(1'b1), .out(transistor_1515_out), .gate(transistor_1478_out));
  Transistor #(.\type ("n")) transistor_1516 (.in(1'b0), .out(transistor_1515_out), .gate(transistor_1478_out));
  Transistor transistor_1517 (.in(1'b1), .out(transistor_1517_out), .gate(transistor_1479_out));
  Transistor #(.\type ("n")) transistor_1518 (.in(1'b0), .out(transistor_1517_out), .gate(transistor_1479_out));
  Transistor transistor_1519 (.in(1'b1), .out(transistor_1519_out), .gate(transistor_1480_out));
  Transistor #(.\type ("n")) transistor_1520 (.in(1'b0), .out(transistor_1519_out), .gate(transistor_1480_out));
  Transistor transistor_1521 (.in(1'b1), .out(transistor_1521_out), .gate(transistor_1481_out));
  Transistor #(.\type ("n")) transistor_1522 (.in(1'b0), .out(transistor_1521_out), .gate(transistor_1481_out));
  Transistor transistor_1523 (.in(1'b1), .out(transistor_1523_out), .gate(transistor_1482_out));
  Transistor #(.\type ("n")) transistor_1524 (.in(1'b0), .out(transistor_1523_out), .gate(transistor_1482_out));
  Transistor transistor_1525 (.in(1'b1), .out(transistor_1525_out), .gate(transistor_1483_out));
  Transistor #(.\type ("n")) transistor_1526 (.in(1'b0), .out(transistor_1525_out), .gate(transistor_1483_out));
  Transistor transistor_1527 (.in(1'b1), .out(transistor_1527_out), .gate(transistor_1484_out));
  Transistor #(.\type ("n")) transistor_1528 (.in(1'b0), .out(transistor_1527_out), .gate(transistor_1484_out));
  Transistor transistor_1529 (.in(1'b1), .out(transistor_1529_out), .gate(transistor_1748_out));
  Transistor transistor_1530 (.in(1'b1), .out(transistor_1530_out), .gate(transistor_947_out));
  Transistor transistor_1531 (.in(1'b1), .out(transistor_1530_out), .gate(transistor_1441_out));
  Transistor #(.\type ("n")) transistor_1532 (
    .in(transistor_1533_out), .out(transistor_1530_out), .gate(transistor_947_out));
  Transistor #(.\type ("n")) transistor_1533 (.in(1'b0), .out(transistor_1533_out), .gate(transistor_1441_out));
  Transistor transistor_1534 (.in(1'b1), .out(transistor_1534_out), .gate(transistor_1445_out));
  Transistor transistor_1535 (.in(1'b1), .out(transistor_1534_out), .gate(transistor_953_out));
  Transistor #(.\type ("n")) transistor_1536 (
    .in(transistor_1537_out), .out(transistor_1534_out), .gate(transistor_953_out));
  Transistor #(.\type ("n")) transistor_1537 (.in(1'b0), .out(transistor_1537_out), .gate(transistor_1445_out));
  Transistor transistor_1538 (.in(1'b1), .out(transistor_1538_out), .gate(transistor_959_out));
  Transistor transistor_1539 (.in(1'b1), .out(transistor_1538_out), .gate(transistor_1449_out));
  Transistor #(.\type ("n")) transistor_1540 (
    .in(transistor_1541_out), .out(transistor_1538_out), .gate(transistor_959_out));
  Transistor #(.\type ("n")) transistor_1541 (.in(1'b0), .out(transistor_1541_out), .gate(transistor_1449_out));
  Transistor transistor_1542 (.in(1'b1), .out(transistor_1542_out), .gate(transistor_965_out));
  Transistor transistor_1543 (.in(1'b1), .out(transistor_1542_out), .gate(transistor_1453_out));
  Transistor #(.\type ("n")) transistor_1544 (
    .in(transistor_1545_out), .out(transistor_1542_out), .gate(transistor_965_out));
  Transistor #(.\type ("n")) transistor_1545 (.in(1'b0), .out(transistor_1545_out), .gate(transistor_1453_out));
  Transistor transistor_1546 (.in(1'b1), .out(transistor_1546_out), .gate(transistor_1457_out));
  Transistor transistor_1547 (.in(1'b1), .out(transistor_1546_out), .gate(transistor_971_out));
  Transistor #(.\type ("n")) transistor_1548 (
    .in(transistor_1549_out), .out(transistor_1546_out), .gate(transistor_971_out));
  Transistor #(.\type ("n")) transistor_1549 (.in(1'b0), .out(transistor_1549_out), .gate(transistor_1457_out));
  Transistor transistor_1550 (.in(1'b1), .out(transistor_1550_out), .gate(transistor_1461_out));
  Transistor transistor_1551 (.in(1'b1), .out(transistor_1550_out), .gate(transistor_977_out));
  Transistor #(.\type ("n")) transistor_1552 (
    .in(transistor_1553_out), .out(transistor_1550_out), .gate(transistor_977_out));
  Transistor #(.\type ("n")) transistor_1553 (.in(1'b0), .out(transistor_1553_out), .gate(transistor_1461_out));
  Transistor transistor_1554 (.in(1'b1), .out(transistor_1554_out), .gate(transistor_1465_out));
  Transistor transistor_1555 (.in(1'b1), .out(transistor_1554_out), .gate(transistor_983_out));
  Transistor #(.\type ("n")) transistor_1556 (
    .in(transistor_1557_out), .out(transistor_1554_out), .gate(transistor_983_out));
  Transistor #(.\type ("n")) transistor_1557 (.in(1'b0), .out(transistor_1557_out), .gate(transistor_1465_out));
  Transistor transistor_1558 (.in(1'b1), .out(transistor_1558_out), .gate(transistor_989_out));
  Transistor transistor_1559 (.in(1'b1), .out(transistor_1558_out), .gate(transistor_1469_out));
  Transistor #(.\type ("n")) transistor_1560 (
    .in(transistor_1561_out), .out(transistor_1558_out), .gate(transistor_989_out));
  Transistor #(.\type ("n")) transistor_1561 (.in(1'b0), .out(transistor_1561_out), .gate(transistor_1469_out));
  Transistor transistor_1562 (.in(1'b1), .out(transistor_1529_out), .gate(transistor_1751_out));
  Transistor transistor_1563 (.in(1'b1), .out(transistor_1563_out), .gate(transistor_1529_out));
  Transistor #(.\type ("n")) transistor_1564 (
    .in(transistor_1565_out), .out(transistor_1529_out), .gate(transistor_1748_out));
  Transistor #(.\type ("n")) transistor_1565 (.in(1'b0), .out(transistor_1565_out), .gate(transistor_1751_out));
  Transistor transistor_1566 (.in(1'b1), .out(transistor_1566_out), .gate(transistor_1530_out));
  Transistor transistor_1567 (.in(1'b1), .out(transistor_1567_out), .gate(transistor_1534_out));
  Transistor transistor_1568 (.in(1'b1), .out(transistor_1568_out), .gate(transistor_1538_out));
  Transistor transistor_1569 (.in(1'b1), .out(transistor_1569_out), .gate(transistor_1542_out));
  Transistor transistor_1570 (.in(1'b1), .out(transistor_1570_out), .gate(transistor_1546_out));
  Transistor transistor_1571 (.in(1'b1), .out(transistor_1571_out), .gate(transistor_1550_out));
  Transistor transistor_1572 (.in(1'b1), .out(transistor_1572_out), .gate(transistor_1554_out));
  Transistor transistor_1573 (.in(1'b1), .out(transistor_1573_out), .gate(transistor_1558_out));
  Transistor transistor_1574 (.in(1'b1), .out(transistor_1563_out), .gate(transistor_1751_out));
  Transistor #(.\type ("n")) transistor_1575 (
    .in(transistor_1576_out), .out(transistor_1563_out), .gate(transistor_1529_out));
  Transistor #(.\type ("n")) transistor_1576 (.in(1'b0), .out(transistor_1576_out), .gate(transistor_1751_out));
  Transistor transistor_1577 (.in(1'b1), .out(transistor_1577_out), .gate(transistor_947_out));
  Transistor transistor_1578 (.in(1'b1), .out(transistor_1566_out), .gate(transistor_1441_out));
  Transistor #(.\type ("n")) transistor_1579 (
    .in(transistor_1580_out), .out(transistor_1566_out), .gate(transistor_1530_out));
  Transistor #(.\type ("n")) transistor_1580 (.in(1'b0), .out(transistor_1580_out), .gate(transistor_1441_out));
  Transistor transistor_1581 (.in(1'b1), .out(transistor_1581_out), .gate(transistor_953_out));
  Transistor transistor_1582 (.in(1'b1), .out(transistor_1567_out), .gate(transistor_1445_out));
  Transistor #(.\type ("n")) transistor_1583 (
    .in(transistor_1584_out), .out(transistor_1567_out), .gate(transistor_1534_out));
  Transistor #(.\type ("n")) transistor_1584 (.in(1'b0), .out(transistor_1584_out), .gate(transistor_1445_out));
  Transistor transistor_1585 (.in(1'b1), .out(transistor_1568_out), .gate(transistor_1449_out));
  Transistor transistor_1586 (.in(1'b1), .out(transistor_1586_out), .gate(transistor_959_out));
  Transistor #(.\type ("n")) transistor_1587 (
    .in(transistor_1588_out), .out(transistor_1568_out), .gate(transistor_1538_out));
  Transistor #(.\type ("n")) transistor_1588 (.in(1'b0), .out(transistor_1588_out), .gate(transistor_1449_out));
  Transistor transistor_1589 (.in(1'b1), .out(transistor_1589_out), .gate(transistor_965_out));
  Transistor transistor_1590 (.in(1'b1), .out(transistor_1569_out), .gate(transistor_1453_out));
  Transistor #(.\type ("n")) transistor_1591 (
    .in(transistor_1592_out), .out(transistor_1569_out), .gate(transistor_1542_out));
  Transistor #(.\type ("n")) transistor_1592 (.in(1'b0), .out(transistor_1592_out), .gate(transistor_1453_out));
  Transistor transistor_1593 (.in(1'b1), .out(transistor_1570_out), .gate(transistor_1457_out));
  Transistor transistor_1594 (.in(1'b1), .out(transistor_1594_out), .gate(transistor_971_out));
  Transistor #(.\type ("n")) transistor_1595 (
    .in(transistor_1596_out), .out(transistor_1570_out), .gate(transistor_1546_out));
  Transistor #(.\type ("n")) transistor_1596 (.in(1'b0), .out(transistor_1596_out), .gate(transistor_1457_out));
  Transistor transistor_1597 (.in(1'b1), .out(transistor_1597_out), .gate(transistor_977_out));
  Transistor transistor_1598 (.in(1'b1), .out(transistor_1571_out), .gate(transistor_1461_out));
  Transistor #(.\type ("n")) transistor_1599 (
    .in(transistor_1600_out), .out(transistor_1571_out), .gate(transistor_1550_out));
  Transistor #(.\type ("n")) transistor_1600 (.in(1'b0), .out(transistor_1600_out), .gate(transistor_1461_out));
  Transistor transistor_1601 (.in(1'b1), .out(transistor_1572_out), .gate(transistor_1465_out));
  Transistor transistor_1602 (.in(1'b1), .out(transistor_1602_out), .gate(transistor_983_out));
  Transistor #(.\type ("n")) transistor_1603 (
    .in(transistor_1604_out), .out(transistor_1572_out), .gate(transistor_1554_out));
  Transistor #(.\type ("n")) transistor_1604 (.in(1'b0), .out(transistor_1604_out), .gate(transistor_1465_out));
  Transistor transistor_1605 (.in(1'b1), .out(transistor_1573_out), .gate(transistor_1469_out));
  Transistor transistor_1606 (.in(1'b1), .out(transistor_1606_out), .gate(transistor_989_out));
  Transistor #(.\type ("n")) transistor_1607 (
    .in(transistor_1608_out), .out(transistor_1573_out), .gate(transistor_1558_out));
  Transistor #(.\type ("n")) transistor_1608 (.in(1'b0), .out(transistor_1608_out), .gate(transistor_1469_out));
  Transistor transistor_1609 (.in(1'b1), .out(transistor_1609_out), .gate(transistor_1748_out));
  Transistor transistor_1610 (.in(1'b1), .out(transistor_1610_out), .gate(w_2));
  Transistor #(.\type ("n")) transistor_1611 (.in(1'b0), .out(transistor_1610_out), .gate(w_2));
  Transistor transistor_1612 (.in(1'b1), .out(transistor_1577_out), .gate(transistor_1530_out));
  Transistor #(.\type ("n")) transistor_1613 (
    .in(transistor_1614_out), .out(transistor_1577_out), .gate(transistor_1530_out));
  Transistor #(.\type ("n")) transistor_1614 (.in(1'b0), .out(transistor_1614_out), .gate(transistor_947_out));
  Transistor transistor_1615 (.in(1'b1), .out(transistor_1581_out), .gate(transistor_1534_out));
  Transistor #(.\type ("n")) transistor_1616 (
    .in(transistor_1617_out), .out(transistor_1581_out), .gate(transistor_1534_out));
  Transistor #(.\type ("n")) transistor_1617 (.in(1'b0), .out(transistor_1617_out), .gate(transistor_953_out));
  Transistor transistor_1618 (.in(1'b1), .out(transistor_1586_out), .gate(transistor_1538_out));
  Transistor #(.\type ("n")) transistor_1619 (
    .in(transistor_1620_out), .out(transistor_1586_out), .gate(transistor_1538_out));
  Transistor #(.\type ("n")) transistor_1620 (.in(1'b0), .out(transistor_1620_out), .gate(transistor_959_out));
  Transistor transistor_1621 (.in(1'b1), .out(transistor_1589_out), .gate(transistor_1542_out));
  Transistor #(.\type ("n")) transistor_1622 (
    .in(transistor_1623_out), .out(transistor_1589_out), .gate(transistor_1542_out));
  Transistor #(.\type ("n")) transistor_1623 (.in(1'b0), .out(transistor_1623_out), .gate(transistor_965_out));
  Transistor transistor_1624 (.in(1'b1), .out(transistor_1594_out), .gate(transistor_1546_out));
  Transistor #(.\type ("n")) transistor_1625 (
    .in(transistor_1626_out), .out(transistor_1594_out), .gate(transistor_1546_out));
  Transistor #(.\type ("n")) transistor_1626 (.in(1'b0), .out(transistor_1626_out), .gate(transistor_971_out));
  Transistor transistor_1627 (.in(1'b1), .out(transistor_1597_out), .gate(transistor_1550_out));
  Transistor #(.\type ("n")) transistor_1628 (
    .in(transistor_1629_out), .out(transistor_1597_out), .gate(transistor_1550_out));
  Transistor #(.\type ("n")) transistor_1629 (.in(1'b0), .out(transistor_1629_out), .gate(transistor_977_out));
  Transistor transistor_1630 (.in(1'b1), .out(transistor_1602_out), .gate(transistor_1554_out));
  Transistor #(.\type ("n")) transistor_1631 (
    .in(transistor_1632_out), .out(transistor_1602_out), .gate(transistor_1554_out));
  Transistor #(.\type ("n")) transistor_1632 (.in(1'b0), .out(transistor_1632_out), .gate(transistor_983_out));
  Transistor transistor_1633 (.in(1'b1), .out(transistor_1606_out), .gate(transistor_1558_out));
  Transistor #(.\type ("n")) transistor_1634 (
    .in(transistor_1635_out), .out(transistor_1606_out), .gate(transistor_1558_out));
  Transistor #(.\type ("n")) transistor_1635 (.in(1'b0), .out(transistor_1635_out), .gate(transistor_989_out));
  Transistor transistor_1636 (.in(1'b1), .out(transistor_1636_out), .gate(transistor_1609_out));
  Transistor transistor_1637 (.in(1'b1), .out(transistor_1609_out), .gate(transistor_1529_out));
  Transistor #(.\type ("n")) transistor_1638 (
    .in(transistor_1639_out), .out(transistor_1609_out), .gate(transistor_1529_out));
  Transistor #(.\type ("n")) transistor_1639 (.in(1'b0), .out(transistor_1639_out), .gate(transistor_1748_out));
  Transistor #(.\type ("n")) transistor_1640 (.in(_7), .out(transistor_1640_out), .gate(w_2));
  Transistor #(.gate("br")) transistor_1641 (.in(_7), .out(transistor_1640_out), .gate(transistor_1610_out));
  Transistor #(.\type ("n")) transistor_1642 (
    .in(transistor_1679_out), .out(transistor_1640_out), .gate(transistor_1610_out));
  Transistor #(.gate("br")) transistor_1643 (.in(transistor_1679_out), .out(transistor_1640_out), .gate(w_2));
  LED led_17 (.in(transistor_1679_out));
  Transistor transistor_1644 (.in(1'b1), .out(transistor_1644_out), .gate(transistor_1566_out));
  Transistor transistor_1645 (.in(1'b1), .out(transistor_1644_out), .gate(transistor_1577_out));
  Transistor #(.\type ("n")) transistor_1646 (
    .in(transistor_1647_out), .out(transistor_1644_out), .gate(transistor_1577_out));
  Transistor #(.\type ("n")) transistor_1647 (.in(1'b0), .out(transistor_1647_out), .gate(transistor_1566_out));
  Transistor transistor_1648 (.in(1'b1), .out(transistor_1648_out), .gate(transistor_1581_out));
  Transistor transistor_1649 (.in(1'b1), .out(transistor_1648_out), .gate(transistor_1567_out));
  Transistor #(.\type ("n")) transistor_1650 (
    .in(transistor_1651_out), .out(transistor_1648_out), .gate(transistor_1581_out));
  Transistor #(.\type ("n")) transistor_1651 (.in(1'b0), .out(transistor_1651_out), .gate(transistor_1567_out));
  Transistor transistor_1652 (.in(1'b1), .out(transistor_1652_out), .gate(transistor_1568_out));
  Transistor transistor_1653 (.in(1'b1), .out(transistor_1652_out), .gate(transistor_1586_out));
  Transistor #(.\type ("n")) transistor_1654 (
    .in(transistor_1655_out), .out(transistor_1652_out), .gate(transistor_1586_out));
  Transistor #(.\type ("n")) transistor_1655 (.in(1'b0), .out(transistor_1655_out), .gate(transistor_1568_out));
  Transistor transistor_1656 (.in(1'b1), .out(transistor_1656_out), .gate(transistor_1569_out));
  Transistor transistor_1657 (.in(1'b1), .out(transistor_1656_out), .gate(transistor_1589_out));
  Transistor #(.\type ("n")) transistor_1658 (
    .in(transistor_1659_out), .out(transistor_1656_out), .gate(transistor_1589_out));
  Transistor #(.\type ("n")) transistor_1659 (.in(1'b0), .out(transistor_1659_out), .gate(transistor_1569_out));
  Transistor transistor_1660 (.in(1'b1), .out(transistor_1660_out), .gate(transistor_1594_out));
  Transistor transistor_1661 (.in(1'b1), .out(transistor_1660_out), .gate(transistor_1570_out));
  Transistor #(.\type ("n")) transistor_1662 (
    .in(transistor_1663_out), .out(transistor_1660_out), .gate(transistor_1594_out));
  Transistor #(.\type ("n")) transistor_1663 (.in(1'b0), .out(transistor_1663_out), .gate(transistor_1570_out));
  Transistor transistor_1664 (.in(1'b1), .out(transistor_1664_out), .gate(transistor_1597_out));
  Transistor transistor_1665 (.in(1'b1), .out(transistor_1664_out), .gate(transistor_1571_out));
  Transistor #(.\type ("n")) transistor_1666 (
    .in(transistor_1667_out), .out(transistor_1664_out), .gate(transistor_1597_out));
  Transistor #(.\type ("n")) transistor_1667 (.in(1'b0), .out(transistor_1667_out), .gate(transistor_1571_out));
  Transistor transistor_1668 (.in(1'b1), .out(transistor_1668_out), .gate(transistor_1602_out));
  Transistor transistor_1669 (.in(1'b1), .out(transistor_1668_out), .gate(transistor_1572_out));
  Transistor #(.\type ("n")) transistor_1670 (
    .in(transistor_1671_out), .out(transistor_1668_out), .gate(transistor_1602_out));
  Transistor #(.\type ("n")) transistor_1671 (.in(1'b0), .out(transistor_1671_out), .gate(transistor_1572_out));
  Transistor transistor_1672 (.in(1'b1), .out(transistor_1672_out), .gate(transistor_1573_out));
  Transistor transistor_1673 (.in(1'b1), .out(transistor_1672_out), .gate(transistor_1606_out));
  Transistor #(.\type ("n")) transistor_1674 (
    .in(transistor_1675_out), .out(transistor_1672_out), .gate(transistor_1606_out));
  Transistor #(.\type ("n")) transistor_1675 (.in(1'b0), .out(transistor_1675_out), .gate(transistor_1573_out));
  Transistor transistor_1676 (.in(1'b1), .out(transistor_1636_out), .gate(transistor_1563_out));
  Transistor #(.\type ("n")) transistor_1677 (
    .in(transistor_1678_out), .out(transistor_1636_out), .gate(transistor_1609_out));
  Transistor #(.\type ("n")) transistor_1678 (.in(1'b0), .out(transistor_1678_out), .gate(transistor_1563_out));
  Transistor #(.\type ("n")) transistor_1679 (.in(1'b0), .out(transistor_1679_out), .gate(rst));
  Transistor #(.gate("br")) transistor_1680 (.in(1'b0), .out(transistor_1679_out), .gate(transistor_1681_out));
  Transistor transistor_1681 (.in(1'b1), .out(transistor_1681_out), .gate(rst));
  Transistor #(.\type ("n")) transistor_1682 (.in(1'b0), .out(transistor_1681_out), .gate(rst));
  Transistor #(.\type ("n")) transistor_1683 (
    .in(transistor_1640_out), .out(transistor_1679_out), .gate(transistor_1681_out));
  Transistor #(.gate("br")) transistor_1684 (.in(transistor_1640_out), .out(transistor_1679_out), .gate(rst));
  Transistor #(.\type ("n")) transistor_1685 (.in(1'b0), .out(transistor_1685_out), .gate(transistor_1513_out));
  Transistor #(.\type ("n")) transistor_1686 (.in(1'b0), .out(transistor_1686_out), .gate(transistor_1515_out));
  Transistor #(.\type ("n")) transistor_1687 (.in(1'b0), .out(transistor_1687_out), .gate(transistor_1517_out));
  Transistor #(.\type ("n")) transistor_1688 (.in(1'b0), .out(transistor_1688_out), .gate(transistor_1519_out));
  Transistor #(.\type ("n")) transistor_1689 (.in(1'b0), .out(transistor_1689_out), .gate(transistor_1521_out));
  Transistor #(.\type ("n")) transistor_1690 (.in(1'b0), .out(transistor_1690_out), .gate(transistor_1523_out));
  Transistor #(.\type ("n")) transistor_1691 (.in(1'b0), .out(transistor_1691_out), .gate(transistor_1525_out));
  Transistor #(.\type ("n")) transistor_1692 (.in(1'b0), .out(transistor_1692_out), .gate(transistor_1527_out));
  Transistor transistor_1693 (.in(1'b1), .out(transistor_1693_out), .gate(op1));
  Transistor #(.\type ("n")) transistor_1694 (.in(1'b0), .out(transistor_1693_out), .gate(op1));
  Transistor transistor_1695 (.in(1'b1), .out(transistor_1695_out), .gate(w_2));
  Transistor #(.\type ("n")) transistor_1696 (.in(1'b0), .out(transistor_1695_out), .gate(w_2));
  Transistor transistor_1697 (.in(1'b1), .out(transistor_1697_out), .gate(transistor_1513_out));
  Transistor transistor_1698 (.in(transistor_1697_out), .out(transistor_1685_out), .gate(transistor_1758_out));
  Transistor #(.\type ("n")) transistor_1699 (.in(1'b0), .out(transistor_1685_out), .gate(transistor_1758_out));
  Transistor transistor_1700 (.in(1'b1), .out(transistor_1700_out), .gate(transistor_1515_out));
  Transistor transistor_1701 (.in(transistor_1700_out), .out(transistor_1686_out), .gate(transistor_1762_out));
  Transistor #(.\type ("n")) transistor_1702 (.in(1'b0), .out(transistor_1686_out), .gate(transistor_1762_out));
  Transistor transistor_1703 (.in(1'b1), .out(transistor_1703_out), .gate(transistor_1517_out));
  Transistor transistor_1704 (.in(transistor_1703_out), .out(transistor_1687_out), .gate(transistor_1768_out));
  Transistor #(.\type ("n")) transistor_1705 (.in(1'b0), .out(transistor_1687_out), .gate(transistor_1768_out));
  Transistor transistor_1706 (.in(1'b1), .out(transistor_1706_out), .gate(transistor_1519_out));
  Transistor transistor_1707 (.in(transistor_1706_out), .out(transistor_1688_out), .gate(transistor_1773_out));
  Transistor #(.\type ("n")) transistor_1708 (.in(1'b0), .out(transistor_1688_out), .gate(transistor_1773_out));
  Transistor transistor_1709 (.in(1'b1), .out(transistor_1709_out), .gate(transistor_1521_out));
  Transistor transistor_1710 (.in(transistor_1709_out), .out(transistor_1689_out), .gate(transistor_1777_out));
  Transistor #(.\type ("n")) transistor_1711 (.in(1'b0), .out(transistor_1689_out), .gate(transistor_1777_out));
  Transistor transistor_1712 (.in(1'b1), .out(transistor_1712_out), .gate(transistor_1523_out));
  Transistor transistor_1713 (.in(transistor_1712_out), .out(transistor_1690_out), .gate(transistor_1783_out));
  Transistor #(.\type ("n")) transistor_1714 (.in(1'b0), .out(transistor_1690_out), .gate(transistor_1783_out));
  Transistor transistor_1715 (.in(1'b1), .out(transistor_1715_out), .gate(transistor_1525_out));
  Transistor transistor_1716 (.in(transistor_1715_out), .out(transistor_1691_out), .gate(transistor_1788_out));
  Transistor #(.\type ("n")) transistor_1717 (.in(1'b0), .out(transistor_1691_out), .gate(transistor_1788_out));
  Transistor transistor_1718 (.in(1'b1), .out(transistor_1718_out), .gate(transistor_1527_out));
  Transistor transistor_1719 (.in(transistor_1718_out), .out(transistor_1692_out), .gate(transistor_1792_out));
  Transistor #(.\type ("n")) transistor_1720 (.in(1'b0), .out(transistor_1692_out), .gate(transistor_1792_out));
  Transistor transistor_1721 (.in(1'b1), .out(transistor_1721_out), .gate(op2));
  Transistor transistor_1722 (.in(1'b1), .out(transistor_1721_out), .gate(transistor_1693_out));
  Transistor #(.\type ("n")) transistor_1723 (
    .in(transistor_1724_out), .out(transistor_1721_out), .gate(transistor_1693_out));
  Transistor #(.\type ("n")) transistor_1724 (.in(1'b0), .out(transistor_1724_out), .gate(op2));
  Transistor #(.\type ("n")) transistor_1725 (.in(_6), .out(transistor_1725_out), .gate(w_2));
  Transistor #(.gate("br")) transistor_1726 (.in(_6), .out(transistor_1725_out), .gate(transistor_1695_out));
  Transistor #(.\type ("n")) transistor_1727 (
    .in(transistor_1801_out), .out(transistor_1725_out), .gate(transistor_1695_out));
  Transistor #(.gate("br")) transistor_1728 (.in(transistor_1801_out), .out(transistor_1725_out), .gate(w_2));
  Transistor transistor_1729 (.in(1'b1), .out(transistor_1729_out), .gate(transistor_1911_out));
  Transistor transistor_1730 (.in(1'b1), .out(transistor_1730_out), .gate(transistor_1685_out));
  Transistor #(.\type ("n")) transistor_1731 (.in(1'b0), .out(transistor_1730_out), .gate(transistor_1685_out));
  Transistor transistor_1732 (.in(1'b1), .out(transistor_1732_out), .gate(transistor_1730_out));
  Transistor transistor_1733 (.in(1'b1), .out(transistor_1733_out), .gate(transistor_1686_out));
  Transistor #(.\type ("n")) transistor_1734 (.in(1'b0), .out(transistor_1733_out), .gate(transistor_1686_out));
  Transistor transistor_1735 (.in(1'b1), .out(transistor_1735_out), .gate(transistor_1733_out));
  Transistor transistor_1736 (.in(1'b1), .out(transistor_1736_out), .gate(transistor_1687_out));
  Transistor #(.\type ("n")) transistor_1737 (.in(1'b0), .out(transistor_1736_out), .gate(transistor_1687_out));
  Transistor transistor_1738 (.in(1'b1), .out(transistor_1738_out), .gate(transistor_1736_out));
  Transistor transistor_1739 (.in(1'b1), .out(transistor_1739_out), .gate(transistor_1688_out));
  Transistor #(.\type ("n")) transistor_1740 (.in(1'b0), .out(transistor_1739_out), .gate(transistor_1688_out));
  Transistor transistor_1741 (.in(1'b1), .out(transistor_1741_out), .gate(transistor_1739_out));
  Transistor transistor_1742 (.in(1'b1), .out(transistor_1742_out), .gate(transistor_1689_out));
  Transistor #(.\type ("n")) transistor_1743 (.in(1'b0), .out(transistor_1742_out), .gate(transistor_1689_out));
  Transistor transistor_1744 (.in(1'b1), .out(transistor_1744_out), .gate(transistor_1742_out));
  Transistor transistor_1745 (.in(1'b1), .out(transistor_1745_out), .gate(transistor_1690_out));
  Transistor #(.\type ("n")) transistor_1746 (.in(1'b0), .out(transistor_1745_out), .gate(transistor_1690_out));
  Transistor transistor_1747 (.in(1'b1), .out(transistor_1747_out), .gate(transistor_1745_out));
  Transistor transistor_1748 (.in(1'b1), .out(transistor_1748_out), .gate(transistor_1691_out));
  Transistor #(.\type ("n")) transistor_1749 (.in(1'b0), .out(transistor_1748_out), .gate(transistor_1691_out));
  Transistor transistor_1750 (.in(1'b1), .out(transistor_1750_out), .gate(transistor_1748_out));
  Transistor transistor_1751 (.in(1'b1), .out(transistor_1751_out), .gate(transistor_1692_out));
  Transistor #(.\type ("n")) transistor_1752 (.in(1'b0), .out(transistor_1751_out), .gate(transistor_1692_out));
  Transistor transistor_1753 (.in(1'b1), .out(transistor_1753_out), .gate(transistor_1721_out));
  Transistor #(.\type ("n")) transistor_1754 (.in(1'b0), .out(transistor_1753_out), .gate(transistor_1721_out));
  Transistor transistor_1755 (.in(1'b1), .out(transistor_1755_out), .gate(rst));
  Transistor #(.\type ("n")) transistor_1756 (.in(1'b0), .out(transistor_1755_out), .gate(rst));
  LED led_18 (.in(transistor_1801_out));
  Transistor transistor_1757 (.in(1'b1), .out(transistor_1729_out), .gate(transistor_1644_out));
  Transistor transistor_1758 (.in(1'b1), .out(transistor_1758_out), .gate(transistor_1729_out));
  Transistor #(.\type ("n")) transistor_1759 (
    .in(transistor_1761_out), .out(transistor_1729_out), .gate(transistor_1911_out));
  Transistor #(.\type ("n")) transistor_1760 (.in(1'b0), .out(transistor_1758_out), .gate(transistor_1729_out));
  Transistor #(.\type ("n")) transistor_1761 (.in(1'b0), .out(transistor_1761_out), .gate(transistor_1644_out));
  Transistor transistor_1762 (.in(1'b1), .out(transistor_1762_out), .gate(transistor_1732_out));
  Transistor transistor_1763 (.in(1'b1), .out(transistor_1732_out), .gate(transistor_1648_out));
  Transistor #(.\type ("n")) transistor_1764 (.in(1'b0), .out(transistor_1762_out), .gate(transistor_1732_out));
  Transistor #(.\type ("n")) transistor_1765 (
    .in(transistor_1766_out), .out(transistor_1732_out), .gate(transistor_1730_out));
  Transistor #(.\type ("n")) transistor_1766 (.in(1'b0), .out(transistor_1766_out), .gate(transistor_1648_out));
  Transistor transistor_1767 (.in(1'b1), .out(transistor_1735_out), .gate(transistor_1652_out));
  Transistor transistor_1768 (.in(1'b1), .out(transistor_1768_out), .gate(transistor_1735_out));
  Transistor #(.\type ("n")) transistor_1769 (
    .in(transistor_1771_out), .out(transistor_1735_out), .gate(transistor_1733_out));
  Transistor #(.\type ("n")) transistor_1770 (.in(1'b0), .out(transistor_1768_out), .gate(transistor_1735_out));
  Transistor #(.\type ("n")) transistor_1771 (.in(1'b0), .out(transistor_1771_out), .gate(transistor_1652_out));
  Transistor transistor_1772 (.in(1'b1), .out(transistor_1738_out), .gate(transistor_1656_out));
  Transistor transistor_1773 (.in(1'b1), .out(transistor_1773_out), .gate(transistor_1738_out));
  Transistor #(.\type ("n")) transistor_1774 (.in(1'b0), .out(transistor_1773_out), .gate(transistor_1738_out));
  Transistor #(.\type ("n")) transistor_1775 (
    .in(transistor_1776_out), .out(transistor_1738_out), .gate(transistor_1736_out));
  Transistor #(.\type ("n")) transistor_1776 (.in(1'b0), .out(transistor_1776_out), .gate(transistor_1656_out));
  Transistor transistor_1777 (.in(1'b1), .out(transistor_1777_out), .gate(transistor_1741_out));
  Transistor transistor_1778 (.in(1'b1), .out(transistor_1741_out), .gate(transistor_1660_out));
  Transistor #(.\type ("n")) transistor_1779 (
    .in(transistor_1781_out), .out(transistor_1741_out), .gate(transistor_1739_out));
  Transistor #(.\type ("n")) transistor_1780 (.in(1'b0), .out(transistor_1777_out), .gate(transistor_1741_out));
  Transistor #(.\type ("n")) transistor_1781 (.in(1'b0), .out(transistor_1781_out), .gate(transistor_1660_out));
  Transistor transistor_1782 (.in(1'b1), .out(transistor_1744_out), .gate(transistor_1664_out));
  Transistor transistor_1783 (.in(1'b1), .out(transistor_1783_out), .gate(transistor_1744_out));
  Transistor #(.\type ("n")) transistor_1784 (.in(1'b0), .out(transistor_1783_out), .gate(transistor_1744_out));
  Transistor #(.\type ("n")) transistor_1785 (
    .in(transistor_1786_out), .out(transistor_1744_out), .gate(transistor_1742_out));
  Transistor #(.\type ("n")) transistor_1786 (.in(1'b0), .out(transistor_1786_out), .gate(transistor_1664_out));
  Transistor transistor_1787 (.in(1'b1), .out(transistor_1747_out), .gate(transistor_1668_out));
  Transistor transistor_1788 (.in(1'b1), .out(transistor_1788_out), .gate(transistor_1747_out));
  Transistor #(.\type ("n")) transistor_1789 (.in(1'b0), .out(transistor_1788_out), .gate(transistor_1747_out));
  Transistor #(.\type ("n")) transistor_1790 (
    .in(transistor_1791_out), .out(transistor_1747_out), .gate(transistor_1745_out));
  Transistor #(.\type ("n")) transistor_1791 (.in(1'b0), .out(transistor_1791_out), .gate(transistor_1668_out));
  Transistor transistor_1792 (.in(1'b1), .out(transistor_1792_out), .gate(transistor_1750_out));
  Transistor transistor_1793 (.in(1'b1), .out(transistor_1750_out), .gate(transistor_1672_out));
  Transistor #(.\type ("n")) transistor_1794 (.in(1'b0), .out(transistor_1792_out), .gate(transistor_1750_out));
  Transistor #(.\type ("n")) transistor_1795 (
    .in(transistor_1796_out), .out(transistor_1750_out), .gate(transistor_1748_out));
  Transistor #(.\type ("n")) transistor_1796 (.in(1'b0), .out(transistor_1796_out), .gate(transistor_1672_out));
  Transistor transistor_1797 (.in(1'b1), .out(transistor_1797_out), .gate(transistor_1753_out));
  Transistor transistor_1798 (.in(1'b1), .out(transistor_1797_out), .gate(transistor_1636_out));
  Transistor #(.\type ("n")) transistor_1799 (
    .in(transistor_1800_out), .out(transistor_1797_out), .gate(transistor_1753_out));
  Transistor #(.\type ("n")) transistor_1800 (.in(1'b0), .out(transistor_1800_out), .gate(transistor_1636_out));
  Transistor #(.\type ("n")) transistor_1801 (.in(1'b0), .out(transistor_1801_out), .gate(rst));
  Transistor #(.gate("br")) transistor_1802 (.in(1'b0), .out(transistor_1801_out), .gate(transistor_1755_out));
  Transistor #(.\type ("n")) transistor_1803 (
    .in(transistor_1725_out), .out(transistor_1801_out), .gate(transistor_1755_out));
  Transistor #(.gate("br")) transistor_1804 (.in(transistor_1725_out), .out(transistor_1801_out), .gate(rst));
  Transistor transistor_1805 (.in(1'b1), .out(transistor_1805_out), .gate(op0));
  Transistor transistor_1806 (.in(1'b1), .out(transistor_1806_out), .gate(transistor_1644_out));
  Transistor transistor_1807 (.in(1'b1), .out(transistor_1807_out), .gate(transistor_1648_out));
  Transistor transistor_1808 (.in(1'b1), .out(transistor_1808_out), .gate(transistor_1652_out));
  Transistor transistor_1809 (.in(1'b1), .out(transistor_1809_out), .gate(transistor_1656_out));
  Transistor transistor_1810 (.in(1'b1), .out(transistor_1810_out), .gate(transistor_1660_out));
  Transistor transistor_1811 (.in(1'b1), .out(transistor_1811_out), .gate(transistor_1664_out));
  Transistor transistor_1812 (.in(1'b1), .out(transistor_1812_out), .gate(transistor_1668_out));
  Transistor transistor_1813 (.in(1'b1), .out(transistor_1813_out), .gate(transistor_1672_out));
  Transistor transistor_1814 (.in(1'b1), .out(transistor_1814_out), .gate(transistor_1797_out));
  Transistor #(.\type ("n")) transistor_1815 (.in(1'b0), .out(transistor_1814_out), .gate(transistor_1797_out));
  Transistor transistor_1816 (.in(1'b1), .out(transistor_1816_out), .gate(w_2));
  Transistor #(.\type ("n")) transistor_1817 (.in(1'b0), .out(transistor_1816_out), .gate(w_2));
  Transistor transistor_1818 (.in(1'b1), .out(transistor_1805_out), .gate(cin));
  Transistor #(.\type ("n")) transistor_1819 (.in(transistor_1820_out), .out(transistor_1805_out), .gate(op0));
  Transistor #(.\type ("n")) transistor_1820 (.in(1'b0), .out(transistor_1820_out), .gate(cin));
  Transistor transistor_1821 (.in(1'b1), .out(transistor_1806_out), .gate(transistor_1911_out));
  Transistor #(.\type ("n")) transistor_1822 (
    .in(transistor_1823_out), .out(transistor_1806_out), .gate(transistor_1644_out));
  Transistor #(.\type ("n")) transistor_1823 (.in(1'b0), .out(transistor_1823_out), .gate(transistor_1911_out));
  Transistor transistor_1824 (.in(1'b1), .out(transistor_1807_out), .gate(transistor_1730_out));
  Transistor #(.\type ("n")) transistor_1825 (
    .in(transistor_1826_out), .out(transistor_1807_out), .gate(transistor_1648_out));
  Transistor #(.\type ("n")) transistor_1826 (.in(1'b0), .out(transistor_1826_out), .gate(transistor_1730_out));
  Transistor transistor_1827 (.in(1'b1), .out(transistor_1808_out), .gate(transistor_1733_out));
  Transistor #(.\type ("n")) transistor_1828 (
    .in(transistor_1829_out), .out(transistor_1808_out), .gate(transistor_1652_out));
  Transistor #(.\type ("n")) transistor_1829 (.in(1'b0), .out(transistor_1829_out), .gate(transistor_1733_out));
  Transistor transistor_1830 (.in(1'b1), .out(transistor_1809_out), .gate(transistor_1736_out));
  Transistor #(.\type ("n")) transistor_1831 (
    .in(transistor_1832_out), .out(transistor_1809_out), .gate(transistor_1656_out));
  Transistor #(.\type ("n")) transistor_1832 (.in(1'b0), .out(transistor_1832_out), .gate(transistor_1736_out));
  Transistor transistor_1833 (.in(1'b1), .out(transistor_1810_out), .gate(transistor_1739_out));
  Transistor #(.\type ("n")) transistor_1834 (
    .in(transistor_1835_out), .out(transistor_1810_out), .gate(transistor_1660_out));
  Transistor #(.\type ("n")) transistor_1835 (.in(1'b0), .out(transistor_1835_out), .gate(transistor_1739_out));
  Transistor transistor_1836 (.in(1'b1), .out(transistor_1811_out), .gate(transistor_1742_out));
  Transistor #(.\type ("n")) transistor_1837 (
    .in(transistor_1838_out), .out(transistor_1811_out), .gate(transistor_1664_out));
  Transistor #(.\type ("n")) transistor_1838 (.in(1'b0), .out(transistor_1838_out), .gate(transistor_1742_out));
  Transistor transistor_1839 (.in(1'b1), .out(transistor_1812_out), .gate(transistor_1745_out));
  Transistor #(.\type ("n")) transistor_1840 (
    .in(transistor_1841_out), .out(transistor_1812_out), .gate(transistor_1668_out));
  Transistor #(.\type ("n")) transistor_1841 (.in(1'b0), .out(transistor_1841_out), .gate(transistor_1745_out));
  Transistor transistor_1842 (.in(1'b1), .out(transistor_1813_out), .gate(transistor_1748_out));
  Transistor #(.\type ("n")) transistor_1843 (
    .in(transistor_1844_out), .out(transistor_1813_out), .gate(transistor_1672_out));
  Transistor #(.\type ("n")) transistor_1844 (.in(1'b0), .out(transistor_1844_out), .gate(transistor_1748_out));
  Transistor transistor_1845 (.in(1'b1), .out(transistor_1845_out), .gate(op0));
  Transistor #(.\type ("n")) transistor_1846 (.in(_5), .out(transistor_1846_out), .gate(w_2));
  Transistor #(.gate("br")) transistor_1847 (.in(_5), .out(transistor_1846_out), .gate(transistor_1816_out));
  Transistor transistor_1848 (.in(1'b1), .out(transistor_1848_out), .gate(rst));
  Transistor #(.\type ("n")) transistor_1849 (.in(1'b0), .out(transistor_1848_out), .gate(rst));
  Transistor #(.\type ("n")) transistor_1850 (
    .in(transistor_1892_out), .out(transistor_1846_out), .gate(transistor_1816_out));
  Transistor #(.gate("br")) transistor_1851 (.in(transistor_1892_out), .out(transistor_1846_out), .gate(w_2));
  LED led_19 (.in(transistor_1892_out));
  Transistor transistor_1852 (.in(1'b1), .out(transistor_1852_out), .gate(transistor_1805_out));
  Transistor transistor_1853 (.in(1'b1), .out(transistor_1852_out), .gate(cin));
  Transistor #(.\type ("n")) transistor_1854 (
    .in(transistor_1855_out), .out(transistor_1852_out), .gate(transistor_1805_out));
  Transistor #(.\type ("n")) transistor_1855 (.in(1'b0), .out(transistor_1855_out), .gate(cin));
  Transistor transistor_1856 (.in(1'b1), .out(transistor_1856_out), .gate(transistor_1911_out));
  Transistor transistor_1857 (.in(1'b1), .out(transistor_1856_out), .gate(transistor_1806_out));
  Transistor #(.\type ("n")) transistor_1858 (
    .in(transistor_1859_out), .out(transistor_1856_out), .gate(transistor_1806_out));
  Transistor #(.\type ("n")) transistor_1859 (.in(1'b0), .out(transistor_1859_out), .gate(transistor_1911_out));
  Transistor transistor_1860 (.in(1'b1), .out(transistor_1860_out), .gate(transistor_1807_out));
  Transistor transistor_1861 (.in(1'b1), .out(transistor_1860_out), .gate(transistor_1730_out));
  Transistor #(.\type ("n")) transistor_1862 (
    .in(transistor_1863_out), .out(transistor_1860_out), .gate(transistor_1807_out));
  Transistor #(.\type ("n")) transistor_1863 (.in(1'b0), .out(transistor_1863_out), .gate(transistor_1730_out));
  Transistor transistor_1864 (.in(1'b1), .out(transistor_1864_out), .gate(transistor_1733_out));
  Transistor transistor_1865 (.in(1'b1), .out(transistor_1864_out), .gate(transistor_1808_out));
  Transistor #(.\type ("n")) transistor_1866 (
    .in(transistor_1867_out), .out(transistor_1864_out), .gate(transistor_1808_out));
  Transistor #(.\type ("n")) transistor_1867 (.in(1'b0), .out(transistor_1867_out), .gate(transistor_1733_out));
  Transistor transistor_1868 (.in(1'b1), .out(transistor_1868_out), .gate(transistor_1809_out));
  Transistor transistor_1869 (.in(1'b1), .out(transistor_1868_out), .gate(transistor_1736_out));
  Transistor #(.\type ("n")) transistor_1870 (
    .in(transistor_1871_out), .out(transistor_1868_out), .gate(transistor_1809_out));
  Transistor #(.\type ("n")) transistor_1871 (.in(1'b0), .out(transistor_1871_out), .gate(transistor_1736_out));
  Transistor transistor_1872 (.in(1'b1), .out(transistor_1872_out), .gate(transistor_1810_out));
  Transistor transistor_1873 (.in(1'b1), .out(transistor_1872_out), .gate(transistor_1739_out));
  Transistor #(.\type ("n")) transistor_1874 (
    .in(transistor_1875_out), .out(transistor_1872_out), .gate(transistor_1810_out));
  Transistor #(.\type ("n")) transistor_1875 (.in(1'b0), .out(transistor_1875_out), .gate(transistor_1739_out));
  Transistor transistor_1876 (.in(1'b1), .out(transistor_1876_out), .gate(transistor_1742_out));
  Transistor transistor_1877 (.in(1'b1), .out(transistor_1876_out), .gate(transistor_1811_out));
  Transistor #(.\type ("n")) transistor_1878 (
    .in(transistor_1879_out), .out(transistor_1876_out), .gate(transistor_1811_out));
  Transistor #(.\type ("n")) transistor_1879 (.in(1'b0), .out(transistor_1879_out), .gate(transistor_1742_out));
  Transistor transistor_1880 (.in(1'b1), .out(transistor_1880_out), .gate(transistor_1812_out));
  Transistor transistor_1881 (.in(1'b1), .out(transistor_1880_out), .gate(transistor_1745_out));
  Transistor #(.\type ("n")) transistor_1882 (
    .in(transistor_1883_out), .out(transistor_1880_out), .gate(transistor_1812_out));
  Transistor #(.\type ("n")) transistor_1883 (.in(1'b0), .out(transistor_1883_out), .gate(transistor_1745_out));
  Transistor transistor_1884 (.in(1'b1), .out(transistor_1884_out), .gate(transistor_1748_out));
  Transistor transistor_1885 (.in(1'b1), .out(transistor_1884_out), .gate(transistor_1813_out));
  Transistor #(.\type ("n")) transistor_1886 (
    .in(transistor_1887_out), .out(transistor_1884_out), .gate(transistor_1813_out));
  Transistor #(.\type ("n")) transistor_1887 (.in(1'b0), .out(transistor_1887_out), .gate(transistor_1748_out));
  Transistor transistor_1888 (.in(1'b1), .out(transistor_1888_out), .gate(transistor_1845_out));
  Transistor transistor_1889 (.in(1'b1), .out(transistor_1845_out), .gate(transistor_1751_out));
  Transistor #(.\type ("n")) transistor_1890 (.in(transistor_1891_out), .out(transistor_1845_out), .gate(op0));
  Transistor #(.\type ("n")) transistor_1891 (.in(1'b0), .out(transistor_1891_out), .gate(transistor_1751_out));
  Transistor #(.\type ("n")) transistor_1892 (.in(1'b0), .out(transistor_1892_out), .gate(rst));
  Transistor #(.gate("br")) transistor_1893 (.in(1'b0), .out(transistor_1892_out), .gate(transistor_1848_out));
  Transistor #(.\type ("n")) transistor_1894 (
    .in(transistor_1846_out), .out(transistor_1892_out), .gate(transistor_1848_out));
  Transistor #(.gate("br")) transistor_1895 (.in(transistor_1846_out), .out(transistor_1892_out), .gate(rst));
  Transistor transistor_1896 (.in(1'b1), .out(transistor_1896_out), .gate(op0));
  Transistor transistor_1897 (.in(1'b1), .out(transistor_1897_out), .gate(transistor_1644_out));
  Transistor transistor_1898 (.in(1'b1), .out(transistor_1898_out), .gate(transistor_1648_out));
  Transistor transistor_1899 (.in(1'b1), .out(transistor_1899_out), .gate(transistor_1652_out));
  Transistor transistor_1900 (.in(1'b1), .out(transistor_1900_out), .gate(transistor_1656_out));
  Transistor transistor_1901 (.in(1'b1), .out(transistor_1901_out), .gate(transistor_1660_out));
  Transistor transistor_1902 (.in(1'b1), .out(transistor_1902_out), .gate(transistor_1664_out));
  Transistor transistor_1903 (.in(1'b1), .out(transistor_1903_out), .gate(transistor_1668_out));
  Transistor transistor_1904 (.in(1'b1), .out(transistor_1904_out), .gate(transistor_1672_out));
  Transistor transistor_1905 (.in(1'b1), .out(transistor_1888_out), .gate(transistor_1751_out));
  Transistor #(.\type ("n")) transistor_1906 (
    .in(transistor_1907_out), .out(transistor_1888_out), .gate(transistor_1845_out));
  Transistor #(.\type ("n")) transistor_1907 (.in(1'b0), .out(transistor_1907_out), .gate(transistor_1751_out));
  Transistor transistor_1908 (.in(1'b1), .out(transistor_1908_out), .gate(w_2));
  Transistor #(.\type ("n")) transistor_1909 (.in(1'b0), .out(transistor_1908_out), .gate(w_2));
  Transistor transistor_1910 (.in(1'b1), .out(transistor_1896_out), .gate(transistor_1805_out));
  Transistor transistor_1911 (.in(1'b1), .out(transistor_1911_out), .gate(transistor_1896_out));
  Transistor #(.\type ("n")) transistor_1912 (
    .in(transistor_1913_out), .out(transistor_1896_out), .gate(transistor_1805_out));
  Transistor #(.\type ("n")) transistor_1913 (.in(1'b0), .out(transistor_1913_out), .gate(op0));
  Transistor transistor_1914 (.in(1'b1), .out(transistor_1897_out), .gate(transistor_1806_out));
  Transistor transistor_1915 (.in(1'b1), .out(transistor_1915_out), .gate(transistor_1897_out));
  Transistor #(.\type ("n")) transistor_1916 (
    .in(transistor_1917_out), .out(transistor_1897_out), .gate(transistor_1806_out));
  Transistor #(.\type ("n")) transistor_1917 (.in(1'b0), .out(transistor_1917_out), .gate(transistor_1644_out));
  Transistor transistor_1918 (.in(1'b1), .out(transistor_1918_out), .gate(transistor_1898_out));
  Transistor transistor_1919 (.in(1'b1), .out(transistor_1898_out), .gate(transistor_1807_out));
  Transistor #(.\type ("n")) transistor_1920 (
    .in(transistor_1921_out), .out(transistor_1898_out), .gate(transistor_1807_out));
  Transistor #(.\type ("n")) transistor_1921 (.in(1'b0), .out(transistor_1921_out), .gate(transistor_1648_out));
  Transistor transistor_1922 (.in(1'b1), .out(transistor_1899_out), .gate(transistor_1808_out));
  Transistor transistor_1923 (.in(1'b1), .out(transistor_1923_out), .gate(transistor_1899_out));
  Transistor #(.\type ("n")) transistor_1924 (
    .in(transistor_1925_out), .out(transistor_1899_out), .gate(transistor_1808_out));
  Transistor #(.\type ("n")) transistor_1925 (.in(1'b0), .out(transistor_1925_out), .gate(transistor_1652_out));
  Transistor transistor_1926 (.in(1'b1), .out(transistor_1900_out), .gate(transistor_1809_out));
  Transistor transistor_1927 (.in(1'b1), .out(transistor_1927_out), .gate(transistor_1900_out));
  Transistor #(.\type ("n")) transistor_1928 (
    .in(transistor_1929_out), .out(transistor_1900_out), .gate(transistor_1809_out));
  Transistor #(.\type ("n")) transistor_1929 (.in(1'b0), .out(transistor_1929_out), .gate(transistor_1656_out));
  Transistor transistor_1930 (.in(1'b1), .out(transistor_1901_out), .gate(transistor_1810_out));
  Transistor transistor_1931 (.in(1'b1), .out(transistor_1931_out), .gate(transistor_1901_out));
  Transistor #(.\type ("n")) transistor_1932 (
    .in(transistor_1933_out), .out(transistor_1901_out), .gate(transistor_1810_out));
  Transistor #(.\type ("n")) transistor_1933 (.in(1'b0), .out(transistor_1933_out), .gate(transistor_1660_out));
  Transistor transistor_1934 (.in(1'b1), .out(transistor_1902_out), .gate(transistor_1811_out));
  Transistor transistor_1935 (.in(1'b1), .out(transistor_1935_out), .gate(transistor_1902_out));
  Transistor #(.\type ("n")) transistor_1936 (
    .in(transistor_1937_out), .out(transistor_1902_out), .gate(transistor_1811_out));
  Transistor #(.\type ("n")) transistor_1937 (.in(1'b0), .out(transistor_1937_out), .gate(transistor_1664_out));
  Transistor transistor_1938 (.in(1'b1), .out(transistor_1938_out), .gate(transistor_1903_out));
  Transistor transistor_1939 (.in(1'b1), .out(transistor_1903_out), .gate(transistor_1812_out));
  Transistor #(.\type ("n")) transistor_1940 (
    .in(transistor_1941_out), .out(transistor_1903_out), .gate(transistor_1812_out));
  Transistor #(.\type ("n")) transistor_1941 (.in(1'b0), .out(transistor_1941_out), .gate(transistor_1668_out));
  Transistor transistor_1942 (.in(1'b1), .out(transistor_1942_out), .gate(transistor_1904_out));
  Transistor transistor_1943 (.in(1'b1), .out(transistor_1904_out), .gate(transistor_1813_out));
  Transistor #(.\type ("n")) transistor_1944 (
    .in(transistor_1945_out), .out(transistor_1904_out), .gate(transistor_1813_out));
  Transistor #(.\type ("n")) transistor_1945 (.in(1'b0), .out(transistor_1945_out), .gate(transistor_1672_out));
  Transistor transistor_1946 (.in(1'b1), .out(transistor_1946_out), .gate(transistor_1845_out));
  Transistor transistor_1947 (.in(1'b1), .out(transistor_1946_out), .gate(op0));
  Transistor #(.\type ("n")) transistor_1948 (
    .in(transistor_1949_out), .out(transistor_1946_out), .gate(transistor_1845_out));
  Transistor #(.\type ("n")) transistor_1949 (.in(1'b0), .out(transistor_1949_out), .gate(op0));
  Transistor #(.\type ("n")) transistor_1950 (.in(_4), .out(transistor_1950_out), .gate(w_2));
  Transistor #(.gate("br")) transistor_1951 (.in(_4), .out(transistor_1950_out), .gate(transistor_1908_out));
  Transistor #(.\type ("n")) transistor_1952 (
    .in(transistor_1987_out), .out(transistor_1950_out), .gate(transistor_1908_out));
  Transistor #(.gate("br")) transistor_1953 (.in(transistor_1987_out), .out(transistor_1950_out), .gate(w_2));
  LED led_20 (.in(transistor_1987_out));
  Transistor transistor_1954 (.in(1'b1), .out(transistor_1911_out), .gate(transistor_1852_out));
  Transistor #(.\type ("n")) transistor_1955 (
    .in(transistor_1956_out), .out(transistor_1911_out), .gate(transistor_1896_out));
  Transistor #(.\type ("n")) transistor_1956 (.in(1'b0), .out(transistor_1956_out), .gate(transistor_1852_out));
  Transistor transistor_1957 (.in(1'b1), .out(transistor_1915_out), .gate(transistor_1856_out));
  Transistor #(.\type ("n")) transistor_1958 (
    .in(transistor_1959_out), .out(transistor_1915_out), .gate(transistor_1897_out));
  Transistor #(.\type ("n")) transistor_1959 (.in(1'b0), .out(transistor_1959_out), .gate(transistor_1856_out));
  Transistor transistor_1960 (.in(1'b1), .out(transistor_1918_out), .gate(transistor_1860_out));
  Transistor #(.\type ("n")) transistor_1961 (
    .in(transistor_1962_out), .out(transistor_1918_out), .gate(transistor_1898_out));
  Transistor #(.\type ("n")) transistor_1962 (.in(1'b0), .out(transistor_1962_out), .gate(transistor_1860_out));
  Transistor transistor_1963 (.in(1'b1), .out(transistor_1923_out), .gate(transistor_1864_out));
  Transistor #(.\type ("n")) transistor_1964 (
    .in(transistor_1965_out), .out(transistor_1923_out), .gate(transistor_1899_out));
  Transistor #(.\type ("n")) transistor_1965 (.in(1'b0), .out(transistor_1965_out), .gate(transistor_1864_out));
  Transistor transistor_1966 (.in(1'b1), .out(transistor_1927_out), .gate(transistor_1868_out));
  Transistor #(.\type ("n")) transistor_1967 (
    .in(transistor_1968_out), .out(transistor_1927_out), .gate(transistor_1900_out));
  Transistor #(.\type ("n")) transistor_1968 (.in(1'b0), .out(transistor_1968_out), .gate(transistor_1868_out));
  Transistor transistor_1969 (.in(1'b1), .out(transistor_1931_out), .gate(transistor_1872_out));
  Transistor #(.\type ("n")) transistor_1970 (
    .in(transistor_1971_out), .out(transistor_1931_out), .gate(transistor_1901_out));
  Transistor #(.\type ("n")) transistor_1971 (.in(1'b0), .out(transistor_1971_out), .gate(transistor_1872_out));
  Transistor transistor_1972 (.in(1'b1), .out(transistor_1935_out), .gate(transistor_1876_out));
  Transistor #(.\type ("n")) transistor_1973 (
    .in(transistor_1974_out), .out(transistor_1935_out), .gate(transistor_1902_out));
  Transistor #(.\type ("n")) transistor_1974 (.in(1'b0), .out(transistor_1974_out), .gate(transistor_1876_out));
  Transistor transistor_1975 (.in(1'b1), .out(transistor_1938_out), .gate(transistor_1880_out));
  Transistor #(.\type ("n")) transistor_1976 (
    .in(transistor_1977_out), .out(transistor_1938_out), .gate(transistor_1903_out));
  Transistor #(.\type ("n")) transistor_1977 (.in(1'b0), .out(transistor_1977_out), .gate(transistor_1880_out));
  Transistor transistor_1978 (.in(1'b1), .out(transistor_1942_out), .gate(transistor_1884_out));
  Transistor #(.\type ("n")) transistor_1979 (
    .in(transistor_1980_out), .out(transistor_1942_out), .gate(transistor_1904_out));
  Transistor #(.\type ("n")) transistor_1980 (.in(1'b0), .out(transistor_1980_out), .gate(transistor_1884_out));
  Transistor transistor_1981 (.in(1'b1), .out(transistor_1981_out), .gate(transistor_1946_out));
  Transistor transistor_1982 (.in(1'b1), .out(transistor_1982_out), .gate(rst));
  Transistor #(.\type ("n")) transistor_1983 (.in(1'b0), .out(transistor_1982_out), .gate(rst));
  Transistor transistor_1984 (.in(1'b1), .out(transistor_1981_out), .gate(transistor_1888_out));
  Transistor #(.\type ("n")) transistor_1985 (
    .in(transistor_1986_out), .out(transistor_1981_out), .gate(transistor_1946_out));
  Transistor #(.\type ("n")) transistor_1986 (.in(1'b0), .out(transistor_1986_out), .gate(transistor_1888_out));
  Transistor #(.\type ("n")) transistor_1987 (.in(1'b0), .out(transistor_1987_out), .gate(rst));
  Transistor #(.gate("br")) transistor_1988 (.in(1'b0), .out(transistor_1987_out), .gate(transistor_1982_out));
  Transistor #(.\type ("n")) transistor_1989 (
    .in(transistor_1950_out), .out(transistor_1987_out), .gate(transistor_1982_out));
  Transistor #(.gate("br")) transistor_1990 (.in(transistor_1950_out), .out(transistor_1987_out), .gate(rst));
  Transistor #(.gate("br")) transistor_1991 (
    .in(transistor_947_out), .out(transistor_1991_out), .gate(transistor_1999_out));
  Transistor #(.\type ("n")) transistor_1992 (.in(transistor_947_out), .out(transistor_1991_out), .gate(op0));
  Transistor #(.\type ("n")) transistor_1993 (.in(_3), .out(transistor_1993_out), .gate(w_2));
  Transistor #(.gate("br")) transistor_1994 (.in(_3), .out(transistor_1993_out), .gate(transistor_1995_out));
  Transistor transistor_1995 (.in(1'b1), .out(transistor_1995_out), .gate(w_2));
  Transistor #(.\type ("n")) transistor_1996 (.in(1'b0), .out(transistor_1995_out), .gate(w_2));
  Transistor #(.\type ("n")) transistor_1997 (
    .in(transistor_2037_out), .out(transistor_1993_out), .gate(transistor_1995_out));
  Transistor #(.gate("br")) transistor_1998 (.in(transistor_2037_out), .out(transistor_1993_out), .gate(w_2));
  Transistor transistor_1999 (.in(1'b1), .out(transistor_1999_out), .gate(op0));
  Transistor #(.\type ("n")) transistor_2000 (.in(1'b0), .out(transistor_1999_out), .gate(op0));
  Transistor #(.\type ("n")) transistor_2001 (
    .in(transistor_989_out), .out(transistor_1991_out), .gate(transistor_1999_out));
  Transistor #(.gate("br")) transistor_2002 (.in(transistor_989_out), .out(transistor_1991_out), .gate(op0));
  Transistor transistor_2003 (.in(1'b1), .out(transistor_2003_out), .gate(rst));
  Transistor #(.\type ("n")) transistor_2004 (.in(1'b0), .out(transistor_2003_out), .gate(rst));
  LED led_21 (.in(transistor_2037_out));
  Transistor transistor_2005 (.in(1'b1), .out(transistor_2005_out), .gate(op0));
  Transistor #(.\type ("n")) transistor_2006 (.in(1'b0), .out(transistor_2005_out), .gate(op0));
  Transistor #(.\type ("n")) transistor_2007 (.in(transistor_953_out), .out(transistor_2007_out), .gate(op0));
  Transistor #(.gate("br")) transistor_2008 (
    .in(transistor_953_out), .out(transistor_2007_out), .gate(transistor_2005_out));
  Transistor #(.\type ("n")) transistor_2009 (.in(1'b0), .out(transistor_2009_out), .gate(op0));
  Transistor transistor_2010 (.in(1'b1), .out(transistor_2009_out), .gate(op0));
  Transistor #(.gate("br")) transistor_2011 (
    .in(transistor_959_out), .out(transistor_2011_out), .gate(transistor_2009_out));
  Transistor #(.\type ("n")) transistor_2012 (.in(transistor_959_out), .out(transistor_2011_out), .gate(op0));
  Transistor transistor_2013 (.in(1'b1), .out(transistor_2013_out), .gate(op0));
  Transistor #(.\type ("n")) transistor_2014 (.in(1'b0), .out(transistor_2013_out), .gate(op0));
  Transistor #(.\type ("n")) transistor_2015 (.in(transistor_965_out), .out(transistor_2015_out), .gate(op0));
  Transistor #(.gate("br")) transistor_2016 (
    .in(transistor_965_out), .out(transistor_2015_out), .gate(transistor_2013_out));
  Transistor #(.\type ("n")) transistor_2017 (.in(1'b0), .out(transistor_2017_out), .gate(op0));
  Transistor transistor_2018 (.in(1'b1), .out(transistor_2017_out), .gate(op0));
  Transistor #(.\type ("n")) transistor_2019 (.in(transistor_971_out), .out(transistor_2019_out), .gate(op0));
  Transistor #(.gate("br")) transistor_2020 (
    .in(transistor_971_out), .out(transistor_2019_out), .gate(transistor_2017_out));
  Transistor transistor_2021 (.in(1'b1), .out(transistor_2021_out), .gate(op0));
  Transistor #(.\type ("n")) transistor_2022 (.in(1'b0), .out(transistor_2021_out), .gate(op0));
  Transistor #(.\type ("n")) transistor_2023 (.in(transistor_977_out), .out(transistor_2023_out), .gate(op0));
  Transistor #(.gate("br")) transistor_2024 (
    .in(transistor_977_out), .out(transistor_2023_out), .gate(transistor_2021_out));
  Transistor #(.\type ("n")) transistor_2025 (.in(1'b0), .out(transistor_2025_out), .gate(op0));
  Transistor transistor_2026 (.in(1'b1), .out(transistor_2025_out), .gate(op0));
  Transistor #(.gate("br")) transistor_2027 (
    .in(transistor_983_out), .out(transistor_2027_out), .gate(transistor_2025_out));
  Transistor #(.\type ("n")) transistor_2028 (.in(transistor_983_out), .out(transistor_2027_out), .gate(op0));
  Transistor transistor_2029 (.in(1'b1), .out(transistor_2029_out), .gate(op0));
  Transistor #(.\type ("n")) transistor_2030 (.in(1'b0), .out(transistor_2029_out), .gate(op0));
  Transistor #(.gate("br")) transistor_2031 (
    .in(transistor_989_out), .out(transistor_2031_out), .gate(transistor_2029_out));
  Transistor #(.\type ("n")) transistor_2032 (.in(transistor_989_out), .out(transistor_2031_out), .gate(op0));
  Transistor #(.\type ("n")) transistor_2033 (.in(1'b0), .out(transistor_2033_out), .gate(op0));
  Transistor transistor_2034 (.in(1'b1), .out(transistor_2033_out), .gate(op0));
  Transistor #(.\type ("n")) transistor_2035 (.in(cin), .out(transistor_2035_out), .gate(op0));
  Transistor #(.gate("br")) transistor_2036 (.in(cin), .out(transistor_2035_out), .gate(transistor_2033_out));
  Transistor #(.\type ("n")) transistor_2037 (.in(1'b0), .out(transistor_2037_out), .gate(rst));
  Transistor #(.gate("br")) transistor_2038 (.in(1'b0), .out(transistor_2037_out), .gate(transistor_2003_out));
  Transistor #(.\type ("n")) transistor_2039 (
    .in(transistor_1993_out), .out(transistor_2037_out), .gate(transistor_2003_out));
  Transistor #(.gate("br")) transistor_2040 (.in(transistor_1993_out), .out(transistor_2037_out), .gate(rst));
  Transistor #(.\type ("n")) transistor_2041 (.in(cin), .out(transistor_2007_out), .gate(transistor_2005_out));
  Transistor #(.gate("br")) transistor_2042 (.in(cin), .out(transistor_2007_out), .gate(op0));
  Transistor #(.\type ("n")) transistor_2043 (
    .in(transistor_947_out), .out(transistor_2011_out), .gate(transistor_2009_out));
  Transistor #(.gate("br")) transistor_2044 (.in(transistor_947_out), .out(transistor_2011_out), .gate(op0));
  Transistor #(.gate("br")) transistor_2045 (.in(transistor_953_out), .out(transistor_2015_out), .gate(op0));
  Transistor #(.\type ("n")) transistor_2046 (
    .in(transistor_953_out), .out(transistor_2015_out), .gate(transistor_2013_out));
  Transistor #(.gate("br")) transistor_2047 (.in(transistor_959_out), .out(transistor_2019_out), .gate(op0));
  Transistor #(.\type ("n")) transistor_2048 (
    .in(transistor_959_out), .out(transistor_2019_out), .gate(transistor_2017_out));
  Transistor #(.\type ("n")) transistor_2049 (
    .in(transistor_965_out), .out(transistor_2023_out), .gate(transistor_2021_out));
  Transistor #(.gate("br")) transistor_2050 (.in(transistor_965_out), .out(transistor_2023_out), .gate(op0));
  Transistor #(.gate("br")) transistor_2051 (.in(transistor_971_out), .out(transistor_2027_out), .gate(op0));
  Transistor #(.\type ("n")) transistor_2052 (
    .in(transistor_971_out), .out(transistor_2027_out), .gate(transistor_2025_out));
  Transistor #(.\type ("n")) transistor_2053 (
    .in(transistor_977_out), .out(transistor_2031_out), .gate(transistor_2029_out));
  Transistor #(.gate("br")) transistor_2054 (.in(transistor_977_out), .out(transistor_2031_out), .gate(op0));
  Transistor #(.gate("br")) transistor_2055 (.in(transistor_983_out), .out(transistor_2035_out), .gate(op0));
  Transistor #(.\type ("n")) transistor_2056 (
    .in(transistor_983_out), .out(transistor_2035_out), .gate(transistor_2033_out));
  Transistor transistor_2057 (.in(1'b1), .out(transistor_2057_out), .gate(op1));
  Transistor #(.gate("br")) transistor_2058 (
    .in(transistor_1991_out), .out(transistor_2058_out), .gate(transistor_2057_out));
  Transistor #(.\type ("n")) transistor_2059 (.in(transistor_1991_out), .out(transistor_2058_out), .gate(op1));
  Transistor transistor_2060 (.in(1'b1), .out(transistor_2060_out), .gate(w_2));
  Transistor #(.\type ("n")) transistor_2061 (.in(1'b0), .out(transistor_2060_out), .gate(w_2));
  Transistor #(.gate("br")) transistor_2062 (
    .in(transistor_1301_out), .out(transistor_2062_out), .gate(transistor_2085_out));
  Transistor #(.\type ("n")) transistor_2063 (.in(transistor_1301_out), .out(transistor_2062_out), .gate(op0));
  Transistor #(.gate("br")) transistor_2064 (
    .in(transistor_1302_out), .out(transistor_2064_out), .gate(transistor_2089_out));
  Transistor #(.\type ("n")) transistor_2065 (.in(transistor_1302_out), .out(transistor_2064_out), .gate(op0));
  Transistor #(.\type ("n")) transistor_2066 (.in(transistor_1303_out), .out(transistor_2066_out), .gate(op0));
  Transistor #(.gate("br")) transistor_2067 (
    .in(transistor_1303_out), .out(transistor_2066_out), .gate(transistor_2093_out));
  Transistor #(.\type ("n")) transistor_2068 (.in(transistor_1304_out), .out(transistor_2068_out), .gate(op0));
  Transistor #(.gate("br")) transistor_2069 (
    .in(transistor_1304_out), .out(transistor_2068_out), .gate(transistor_2097_out));
  Transistor #(.\type ("n")) transistor_2070 (.in(transistor_1305_out), .out(transistor_2070_out), .gate(op0));
  Transistor #(.gate("br")) transistor_2071 (
    .in(transistor_1305_out), .out(transistor_2070_out), .gate(transistor_2101_out));
  Transistor #(.\type ("n")) transistor_2072 (.in(transistor_1306_out), .out(transistor_2072_out), .gate(op0));
  Transistor #(.gate("br")) transistor_2073 (
    .in(transistor_1306_out), .out(transistor_2072_out), .gate(transistor_2105_out));
  Transistor #(.\type ("n")) transistor_2074 (.in(transistor_1307_out), .out(transistor_2074_out), .gate(op0));
  Transistor #(.gate("br")) transistor_2075 (
    .in(transistor_1307_out), .out(transistor_2074_out), .gate(transistor_2109_out));
  Transistor #(.\type ("n")) transistor_2076 (.in(transistor_1308_out), .out(transistor_2076_out), .gate(op0));
  Transistor #(.gate("br")) transistor_2077 (
    .in(transistor_1308_out), .out(transistor_2076_out), .gate(transistor_2113_out));
  Transistor #(.\type ("n")) transistor_2078 (.in(1'b0), .out(transistor_2057_out), .gate(op1));
  Transistor #(.gate("br")) transistor_2079 (.in(transistor_1981_out), .out(transistor_2058_out), .gate(op1));
  Transistor #(.\type ("n")) transistor_2080 (
    .in(transistor_1981_out), .out(transistor_2058_out), .gate(transistor_2057_out));
  Transistor #(.\type ("n")) transistor_2081 (.in(_2), .out(transistor_2081_out), .gate(w_2));
  Transistor #(.gate("br")) transistor_2082 (.in(_2), .out(transistor_2081_out), .gate(transistor_2060_out));
  Transistor #(.\type ("n")) transistor_2083 (
    .in(transistor_2118_out), .out(transistor_2081_out), .gate(transistor_2060_out));
  Transistor #(.gate("br")) transistor_2084 (.in(transistor_2118_out), .out(transistor_2081_out), .gate(w_2));
  LED led_22 (.in(transistor_2118_out));
  Transistor transistor_2085 (.in(1'b1), .out(transistor_2085_out), .gate(op0));
  Transistor #(.\type ("n")) transistor_2086 (.in(1'b0), .out(transistor_2085_out), .gate(op0));
  Transistor #(.gate("br")) transistor_2087 (.in(transistor_1177_out), .out(transistor_2062_out), .gate(op0));
  Transistor #(.\type ("n")) transistor_2088 (
    .in(transistor_1177_out), .out(transistor_2062_out), .gate(transistor_2085_out));
  Transistor #(.\type ("n")) transistor_2089 (.in(1'b0), .out(transistor_2089_out), .gate(op0));
  Transistor transistor_2090 (.in(1'b1), .out(transistor_2089_out), .gate(op0));
  Transistor #(.gate("br")) transistor_2091 (.in(transistor_1179_out), .out(transistor_2064_out), .gate(op0));
  Transistor #(.\type ("n")) transistor_2092 (
    .in(transistor_1179_out), .out(transistor_2064_out), .gate(transistor_2089_out));
  Transistor transistor_2093 (.in(1'b1), .out(transistor_2093_out), .gate(op0));
  Transistor #(.\type ("n")) transistor_2094 (.in(1'b0), .out(transistor_2093_out), .gate(op0));
  Transistor #(.\type ("n")) transistor_2095 (
    .in(transistor_1181_out), .out(transistor_2066_out), .gate(transistor_2093_out));
  Transistor #(.gate("br")) transistor_2096 (.in(transistor_1181_out), .out(transistor_2066_out), .gate(op0));
  Transistor transistor_2097 (.in(1'b1), .out(transistor_2097_out), .gate(op0));
  Transistor #(.\type ("n")) transistor_2098 (.in(1'b0), .out(transistor_2097_out), .gate(op0));
  Transistor #(.\type ("n")) transistor_2099 (
    .in(transistor_1183_out), .out(transistor_2068_out), .gate(transistor_2097_out));
  Transistor #(.gate("br")) transistor_2100 (.in(transistor_1183_out), .out(transistor_2068_out), .gate(op0));
  Transistor #(.\type ("n")) transistor_2101 (.in(1'b0), .out(transistor_2101_out), .gate(op0));
  Transistor transistor_2102 (.in(1'b1), .out(transistor_2101_out), .gate(op0));
  Transistor #(.\type ("n")) transistor_2103 (
    .in(transistor_1185_out), .out(transistor_2070_out), .gate(transistor_2101_out));
  Transistor #(.gate("br")) transistor_2104 (.in(transistor_1185_out), .out(transistor_2070_out), .gate(op0));
  Transistor transistor_2105 (.in(1'b1), .out(transistor_2105_out), .gate(op0));
  Transistor #(.\type ("n")) transistor_2106 (.in(1'b0), .out(transistor_2105_out), .gate(op0));
  Transistor #(.gate("br")) transistor_2107 (.in(transistor_1187_out), .out(transistor_2072_out), .gate(op0));
  Transistor #(.\type ("n")) transistor_2108 (
    .in(transistor_1187_out), .out(transistor_2072_out), .gate(transistor_2105_out));
  Transistor transistor_2109 (.in(1'b1), .out(transistor_2109_out), .gate(op0));
  Transistor #(.\type ("n")) transistor_2110 (.in(1'b0), .out(transistor_2109_out), .gate(op0));
  Transistor #(.\type ("n")) transistor_2111 (
    .in(transistor_1189_out), .out(transistor_2074_out), .gate(transistor_2109_out));
  Transistor #(.gate("br")) transistor_2112 (.in(transistor_1189_out), .out(transistor_2074_out), .gate(op0));
  Transistor transistor_2113 (.in(1'b1), .out(transistor_2113_out), .gate(op0));
  Transistor #(.\type ("n")) transistor_2114 (.in(1'b0), .out(transistor_2113_out), .gate(op0));
  Transistor #(.gate("br")) transistor_2115 (.in(transistor_1191_out), .out(transistor_2076_out), .gate(op0));
  Transistor #(.\type ("n")) transistor_2116 (
    .in(transistor_1191_out), .out(transistor_2076_out), .gate(transistor_2113_out));
  Transistor #(.\type ("n")) transistor_2117 (.in(transistor_2058_out), .out(transistor_2117_out), .gate(op2));
  Transistor #(.\type ("n")) transistor_2118 (.in(1'b0), .out(transistor_2118_out), .gate(rst));
  Transistor #(.gate("br")) transistor_2119 (.in(1'b0), .out(transistor_2118_out), .gate(transistor_2120_out));
  Transistor transistor_2120 (.in(1'b1), .out(transistor_2120_out), .gate(rst));
  Transistor #(.\type ("n")) transistor_2121 (.in(1'b0), .out(transistor_2120_out), .gate(rst));
  Transistor #(.\type ("n")) transistor_2122 (
    .in(transistor_2081_out), .out(transistor_2118_out), .gate(transistor_2120_out));
  Transistor #(.gate("br")) transistor_2123 (.in(transistor_2081_out), .out(transistor_2118_out), .gate(rst));
  Transistor #(.\type ("n")) transistor_2124 (.in(1'b0), .out(transistor_2124_out), .gate(op2));
  Transistor transistor_2125 (.in(1'b1), .out(transistor_2124_out), .gate(op2));
  Transistor #(.gate("br")) transistor_2126 (
    .in(transistor_2058_out), .out(transistor_2117_out), .gate(transistor_2124_out));
  Transistor #(.\type ("n")) transistor_2127 (.in(1'b0), .out(transistor_2117_out), .gate(transistor_2124_out));
  Transistor transistor_2128 (.in(1'b1), .out(transistor_2128_out), .gate(w_2));
  Transistor #(.\type ("n")) transistor_2129 (.in(1'b0), .out(transistor_2128_out), .gate(w_2));
  Transistor transistor_2130 (.in(1'b1), .out(transistor_2130_out), .gate(op0));
  Transistor #(.\type ("n")) transistor_2131 (.in(1'b0), .out(transistor_2130_out), .gate(op0));
  Transistor #(.gate("br")) transistor_2132 (
    .in(transistor_1129_out), .out(transistor_2132_out), .gate(transistor_2130_out));
  Transistor #(.\type ("n")) transistor_2133 (.in(transistor_1129_out), .out(transistor_2132_out), .gate(op0));
  Transistor transistor_2134 (.in(1'b1), .out(transistor_2134_out), .gate(op0));
  Transistor #(.\type ("n")) transistor_2135 (.in(1'b0), .out(transistor_2134_out), .gate(op0));
  Transistor #(.gate("br")) transistor_2136 (
    .in(transistor_1131_out), .out(transistor_2136_out), .gate(transistor_2134_out));
  Transistor #(.\type ("n")) transistor_2137 (.in(transistor_1131_out), .out(transistor_2136_out), .gate(op0));
  Transistor #(.\type ("n")) transistor_2138 (.in(1'b0), .out(transistor_2138_out), .gate(op0));
  Transistor transistor_2139 (.in(1'b1), .out(transistor_2138_out), .gate(op0));
  Transistor #(.\type ("n")) transistor_2140 (.in(transistor_1133_out), .out(transistor_2140_out), .gate(op0));
  Transistor #(.gate("br")) transistor_2141 (
    .in(transistor_1133_out), .out(transistor_2140_out), .gate(transistor_2138_out));
  Transistor #(.\type ("n")) transistor_2142 (.in(1'b0), .out(transistor_2142_out), .gate(op0));
  Transistor transistor_2143 (.in(1'b1), .out(transistor_2142_out), .gate(op0));
  Transistor #(.\type ("n")) transistor_2144 (.in(transistor_1135_out), .out(transistor_2144_out), .gate(op0));
  Transistor #(.gate("br")) transistor_2145 (
    .in(transistor_1135_out), .out(transistor_2144_out), .gate(transistor_2142_out));
  Transistor #(.\type ("n")) transistor_2146 (.in(1'b0), .out(transistor_2146_out), .gate(op0));
  Transistor transistor_2147 (.in(1'b1), .out(transistor_2146_out), .gate(op0));
  Transistor #(.\type ("n")) transistor_2148 (.in(transistor_1137_out), .out(transistor_2148_out), .gate(op0));
  Transistor #(.gate("br")) transistor_2149 (
    .in(transistor_1137_out), .out(transistor_2148_out), .gate(transistor_2146_out));
  Transistor #(.\type ("n")) transistor_2150 (.in(1'b0), .out(transistor_2150_out), .gate(op0));
  Transistor transistor_2151 (.in(1'b1), .out(transistor_2150_out), .gate(op0));
  Transistor #(.\type ("n")) transistor_2152 (.in(transistor_1139_out), .out(transistor_2152_out), .gate(op0));
  Transistor #(.gate("br")) transistor_2153 (
    .in(transistor_1139_out), .out(transistor_2152_out), .gate(transistor_2150_out));
  Transistor #(.\type ("n")) transistor_2154 (.in(1'b0), .out(transistor_2154_out), .gate(op0));
  Transistor transistor_2155 (.in(1'b1), .out(transistor_2154_out), .gate(op0));
  Transistor #(.gate("br")) transistor_2156 (
    .in(transistor_1141_out), .out(transistor_2156_out), .gate(transistor_2154_out));
  Transistor #(.\type ("n")) transistor_2157 (.in(transistor_1141_out), .out(transistor_2156_out), .gate(op0));
  Transistor #(.\type ("n")) transistor_2158 (.in(1'b0), .out(transistor_2158_out), .gate(op0));
  Transistor transistor_2159 (.in(1'b1), .out(transistor_2158_out), .gate(op0));
  Transistor #(.gate("br")) transistor_2160 (
    .in(transistor_1143_out), .out(transistor_2160_out), .gate(transistor_2158_out));
  Transistor #(.\type ("n")) transistor_2161 (.in(transistor_1143_out), .out(transistor_2160_out), .gate(op0));
  Transistor #(.gate("br")) transistor_2162 (.in(1'b0), .out(transistor_2117_out), .gate(op2));
  Transistor #(.\type ("n")) transistor_2163 (.in(_1), .out(transistor_2163_out), .gate(w_2));
  Transistor #(.gate("br")) transistor_2164 (.in(_1), .out(transistor_2163_out), .gate(transistor_2128_out));
  Transistor #(.\type ("n")) transistor_2165 (
    .in(transistor_2207_out), .out(transistor_2163_out), .gate(transistor_2128_out));
  Transistor #(.gate("br")) transistor_2166 (.in(transistor_2207_out), .out(transistor_2163_out), .gate(w_2));
  Transistor #(.\type ("n")) transistor_2167 (
    .in(transistor_947_out), .out(transistor_2132_out), .gate(transistor_2130_out));
  Transistor #(.gate("br")) transistor_2168 (.in(transistor_947_out), .out(transistor_2132_out), .gate(op0));
  Transistor #(.gate("br")) transistor_2169 (.in(transistor_953_out), .out(transistor_2136_out), .gate(op0));
  Transistor #(.\type ("n")) transistor_2170 (
    .in(transistor_953_out), .out(transistor_2136_out), .gate(transistor_2134_out));
  Transistor #(.gate("br")) transistor_2171 (.in(transistor_959_out), .out(transistor_2140_out), .gate(op0));
  Transistor #(.\type ("n")) transistor_2172 (
    .in(transistor_959_out), .out(transistor_2140_out), .gate(transistor_2138_out));
  Transistor #(.gate("br")) transistor_2173 (.in(transistor_965_out), .out(transistor_2144_out), .gate(op0));
  Transistor #(.\type ("n")) transistor_2174 (
    .in(transistor_965_out), .out(transistor_2144_out), .gate(transistor_2142_out));
  Transistor #(.gate("br")) transistor_2175 (.in(transistor_971_out), .out(transistor_2148_out), .gate(op0));
  Transistor #(.\type ("n")) transistor_2176 (
    .in(transistor_971_out), .out(transistor_2148_out), .gate(transistor_2146_out));
  Transistor #(.gate("br")) transistor_2177 (.in(transistor_977_out), .out(transistor_2152_out), .gate(op0));
  Transistor #(.\type ("n")) transistor_2178 (
    .in(transistor_977_out), .out(transistor_2152_out), .gate(transistor_2150_out));
  Transistor #(.\type ("n")) transistor_2179 (
    .in(transistor_983_out), .out(transistor_2156_out), .gate(transistor_2154_out));
  Transistor #(.gate("br")) transistor_2180 (.in(transistor_983_out), .out(transistor_2156_out), .gate(op0));
  Transistor #(.\type ("n")) transistor_2181 (
    .in(transistor_989_out), .out(transistor_2160_out), .gate(transistor_2158_out));
  Transistor #(.gate("br")) transistor_2182 (.in(transistor_989_out), .out(transistor_2160_out), .gate(op0));
  Transistor transistor_2183 (.in(1'b1), .out(transistor_2183_out), .gate(transistor_2517_out));
  Transistor #(.\type ("n")) transistor_2184 (.in(1'b0), .out(transistor_2183_out), .gate(transistor_2517_out));
  Transistor transistor_2185 (.in(1'b1), .out(transistor_2185_out), .gate(rst));
  Transistor #(.\type ("n")) transistor_2186 (.in(1'b0), .out(transistor_2185_out), .gate(rst));
  LED led_23 (.in(transistor_2207_out));
  Transistor #(.gate("br")) transistor_2187 (
    .in(transistor_2007_out), .out(transistor_2187_out), .gate(transistor_2211_out));
  Transistor #(.\type ("n")) transistor_2188 (.in(transistor_2007_out), .out(transistor_2187_out), .gate(op1));
  Transistor #(.\type ("n")) transistor_2189 (.in(transistor_2011_out), .out(transistor_2189_out), .gate(op1));
  Transistor #(.gate("br")) transistor_2190 (
    .in(transistor_2011_out), .out(transistor_2189_out), .gate(transistor_2215_out));
  Transistor #(.\type ("n")) transistor_2191 (.in(transistor_2015_out), .out(transistor_2191_out), .gate(op1));
  Transistor #(.gate("br")) transistor_2192 (
    .in(transistor_2015_out), .out(transistor_2191_out), .gate(transistor_2219_out));
  Transistor #(.gate("br")) transistor_2193 (
    .in(transistor_2019_out), .out(transistor_2193_out), .gate(transistor_2223_out));
  Transistor #(.\type ("n")) transistor_2194 (.in(transistor_2019_out), .out(transistor_2193_out), .gate(op1));
  Transistor #(.\type ("n")) transistor_2195 (.in(transistor_2023_out), .out(transistor_2195_out), .gate(op1));
  Transistor #(.gate("br")) transistor_2196 (
    .in(transistor_2023_out), .out(transistor_2195_out), .gate(transistor_2227_out));
  Transistor #(.\type ("n")) transistor_2197 (.in(transistor_2027_out), .out(transistor_2197_out), .gate(op1));
  Transistor #(.gate("br")) transistor_2198 (
    .in(transistor_2027_out), .out(transistor_2197_out), .gate(transistor_2231_out));
  Transistor #(.\type ("n")) transistor_2199 (.in(transistor_2031_out), .out(transistor_2199_out), .gate(op1));
  Transistor #(.gate("br")) transistor_2200 (
    .in(transistor_2031_out), .out(transistor_2199_out), .gate(transistor_2235_out));
  Transistor #(.\type ("n")) transistor_2201 (.in(transistor_2035_out), .out(transistor_2201_out), .gate(op1));
  Transistor #(.gate("br")) transistor_2202 (
    .in(transistor_2035_out), .out(transistor_2201_out), .gate(transistor_2239_out));
  Transistor #(.\type ("n")) transistor_2203 (
    .in(transistor_1814_out), .out(transistor_2203_out), .gate(transistor_2517_out));
  Transistor #(.gate("br")) transistor_2204 (
    .in(transistor_1814_out), .out(transistor_2203_out), .gate(transistor_2183_out));
  Transistor #(.\type ("n")) transistor_2205 (.in(v), .out(transistor_2203_out), .gate(transistor_2183_out));
  Transistor #(.gate("br")) transistor_2206 (.in(v), .out(transistor_2203_out), .gate(transistor_2517_out));
  Transistor #(.\type ("n")) transistor_2207 (.in(1'b0), .out(transistor_2207_out), .gate(rst));
  Transistor #(.gate("br")) transistor_2208 (.in(1'b0), .out(transistor_2207_out), .gate(transistor_2185_out));
  Transistor #(.\type ("n")) transistor_2209 (
    .in(transistor_2163_out), .out(transistor_2207_out), .gate(transistor_2185_out));
  Transistor #(.gate("br")) transistor_2210 (.in(transistor_2163_out), .out(transistor_2207_out), .gate(rst));
  Transistor #(.\type ("n")) transistor_2211 (.in(1'b0), .out(transistor_2211_out), .gate(op1));
  Transistor transistor_2212 (.in(1'b1), .out(transistor_2211_out), .gate(op1));
  Transistor #(.gate("br")) transistor_2213 (.in(transistor_1915_out), .out(transistor_2187_out), .gate(op1));
  Transistor #(.\type ("n")) transistor_2214 (
    .in(transistor_1915_out), .out(transistor_2187_out), .gate(transistor_2211_out));
  Transistor transistor_2215 (.in(1'b1), .out(transistor_2215_out), .gate(op1));
  Transistor #(.\type ("n")) transistor_2216 (.in(1'b0), .out(transistor_2215_out), .gate(op1));
  Transistor #(.gate("br")) transistor_2217 (.in(transistor_1918_out), .out(transistor_2189_out), .gate(op1));
  Transistor #(.\type ("n")) transistor_2218 (
    .in(transistor_1918_out), .out(transistor_2189_out), .gate(transistor_2215_out));
  Transistor transistor_2219 (.in(1'b1), .out(transistor_2219_out), .gate(op1));
  Transistor #(.\type ("n")) transistor_2220 (.in(1'b0), .out(transistor_2219_out), .gate(op1));
  Transistor #(.\type ("n")) transistor_2221 (
    .in(transistor_1923_out), .out(transistor_2191_out), .gate(transistor_2219_out));
  Transistor #(.gate("br")) transistor_2222 (.in(transistor_1923_out), .out(transistor_2191_out), .gate(op1));
  Transistor #(.\type ("n")) transistor_2223 (.in(1'b0), .out(transistor_2223_out), .gate(op1));
  Transistor transistor_2224 (.in(1'b1), .out(transistor_2223_out), .gate(op1));
  Transistor #(.\type ("n")) transistor_2225 (
    .in(transistor_1927_out), .out(transistor_2193_out), .gate(transistor_2223_out));
  Transistor #(.gate("br")) transistor_2226 (.in(transistor_1927_out), .out(transistor_2193_out), .gate(op1));
  Transistor #(.\type ("n")) transistor_2227 (.in(1'b0), .out(transistor_2227_out), .gate(op1));
  Transistor transistor_2228 (.in(1'b1), .out(transistor_2227_out), .gate(op1));
  Transistor #(.\type ("n")) transistor_2229 (
    .in(transistor_1931_out), .out(transistor_2195_out), .gate(transistor_2227_out));
  Transistor #(.gate("br")) transistor_2230 (.in(transistor_1931_out), .out(transistor_2195_out), .gate(op1));
  Transistor #(.\type ("n")) transistor_2231 (.in(1'b0), .out(transistor_2231_out), .gate(op1));
  Transistor transistor_2232 (.in(1'b1), .out(transistor_2231_out), .gate(op1));
  Transistor #(.\type ("n")) transistor_2233 (
    .in(transistor_1935_out), .out(transistor_2197_out), .gate(transistor_2231_out));
  Transistor #(.gate("br")) transistor_2234 (.in(transistor_1935_out), .out(transistor_2197_out), .gate(op1));
  Transistor transistor_2235 (.in(1'b1), .out(transistor_2235_out), .gate(op1));
  Transistor #(.\type ("n")) transistor_2236 (.in(1'b0), .out(transistor_2235_out), .gate(op1));
  Transistor #(.\type ("n")) transistor_2237 (
    .in(transistor_1938_out), .out(transistor_2199_out), .gate(transistor_2235_out));
  Transistor #(.gate("br")) transistor_2238 (.in(transistor_1938_out), .out(transistor_2199_out), .gate(op1));
  Transistor transistor_2239 (.in(1'b1), .out(transistor_2239_out), .gate(op1));
  Transistor #(.\type ("n")) transistor_2240 (.in(1'b0), .out(transistor_2239_out), .gate(op1));
  Transistor #(.\type ("n")) transistor_2241 (
    .in(transistor_1942_out), .out(transistor_2201_out), .gate(transistor_2239_out));
  Transistor #(.gate("br")) transistor_2242 (.in(transistor_1942_out), .out(transistor_2201_out), .gate(op1));
  Transistor transistor_2243 (.in(1'b1), .out(transistor_2243_out), .gate(rst));
  Transistor #(.\type ("n")) transistor_2244 (.in(1'b0), .out(transistor_2243_out), .gate(rst));
  Transistor #(.\type ("n")) transistor_2245 (.in(_0), .out(transistor_2245_out), .gate(w_2));
  Transistor #(.gate("br")) transistor_2246 (.in(_0), .out(transistor_2245_out), .gate(transistor_2247_out));
  Transistor transistor_2247 (.in(1'b1), .out(transistor_2247_out), .gate(w_2));
  Transistor #(.\type ("n")) transistor_2248 (.in(1'b0), .out(transistor_2247_out), .gate(w_2));
  Transistor #(.\type ("n")) transistor_2249 (
    .in(transistor_2291_out), .out(transistor_2245_out), .gate(transistor_2247_out));
  Transistor #(.gate("br")) transistor_2250 (.in(transistor_2291_out), .out(transistor_2245_out), .gate(w_2));
  Transistor #(.\type ("n")) transistor_2251 (.in(1'b0), .out(v), .gate(rst));
  Transistor #(.gate("br")) transistor_2252 (.in(1'b0), .out(v), .gate(transistor_2243_out));
  Pull_Resistor pull_resistor_9 (.node(v));
  Transistor #(.\type ("n")) transistor_2253 (.in(transistor_2203_out), .out(v), .gate(transistor_2243_out));
  Transistor #(.gate("br")) transistor_2254 (.in(transistor_2203_out), .out(v), .gate(rst));
  Transistor transistor_2255 (.in(1'b1), .out(transistor_2255_out), .gate(rst));
  Transistor #(.\type ("n")) transistor_2256 (.in(1'b0), .out(transistor_2255_out), .gate(rst));
  LED led_24 (.in(transistor_2291_out));
  Transistor #(.\type ("n")) transistor_2257 (.in(1'b0), .out(transistor_2257_out), .gate(op1));
  Transistor transistor_2258 (.in(1'b1), .out(transistor_2257_out), .gate(op1));
  Transistor #(.\type ("n")) transistor_2259 (.in(transistor_2062_out), .out(transistor_2259_out), .gate(op1));
  Transistor #(.gate("br")) transistor_2260 (
    .in(transistor_2062_out), .out(transistor_2259_out), .gate(transistor_2257_out));
  Transistor #(.\type ("n")) transistor_2261 (.in(1'b0), .out(transistor_2261_out), .gate(op1));
  Transistor transistor_2262 (.in(1'b1), .out(transistor_2261_out), .gate(op1));
  Transistor #(.gate("br")) transistor_2263 (
    .in(transistor_2064_out), .out(transistor_2263_out), .gate(transistor_2261_out));
  Transistor #(.\type ("n")) transistor_2264 (.in(transistor_2064_out), .out(transistor_2263_out), .gate(op1));
  Transistor transistor_2265 (.in(1'b1), .out(transistor_2265_out), .gate(op1));
  Transistor #(.\type ("n")) transistor_2266 (.in(1'b0), .out(transistor_2265_out), .gate(op1));
  Transistor #(.gate("br")) transistor_2267 (
    .in(transistor_2066_out), .out(transistor_2267_out), .gate(transistor_2265_out));
  Transistor #(.\type ("n")) transistor_2268 (.in(transistor_2066_out), .out(transistor_2267_out), .gate(op1));
  Transistor #(.\type ("n")) transistor_2269 (.in(1'b0), .out(transistor_2269_out), .gate(op1));
  Transistor transistor_2270 (.in(1'b1), .out(transistor_2269_out), .gate(op1));
  Transistor #(.\type ("n")) transistor_2271 (.in(transistor_2068_out), .out(transistor_2271_out), .gate(op1));
  Transistor #(.gate("br")) transistor_2272 (
    .in(transistor_2068_out), .out(transistor_2271_out), .gate(transistor_2269_out));
  Transistor #(.\type ("n")) transistor_2273 (.in(1'b0), .out(transistor_2273_out), .gate(op1));
  Transistor transistor_2274 (.in(1'b1), .out(transistor_2273_out), .gate(op1));
  Transistor #(.\type ("n")) transistor_2275 (.in(transistor_2070_out), .out(transistor_2275_out), .gate(op1));
  Transistor #(.gate("br")) transistor_2276 (
    .in(transistor_2070_out), .out(transistor_2275_out), .gate(transistor_2273_out));
  Transistor transistor_2277 (.in(1'b1), .out(transistor_2277_out), .gate(op1));
  Transistor #(.\type ("n")) transistor_2278 (.in(1'b0), .out(transistor_2277_out), .gate(op1));
  Transistor #(.gate("br")) transistor_2279 (
    .in(transistor_2072_out), .out(transistor_2279_out), .gate(transistor_2277_out));
  Transistor #(.\type ("n")) transistor_2280 (.in(transistor_2072_out), .out(transistor_2279_out), .gate(op1));
  Transistor transistor_2281 (.in(1'b1), .out(transistor_2281_out), .gate(op1));
  Transistor #(.\type ("n")) transistor_2282 (.in(1'b0), .out(transistor_2281_out), .gate(op1));
  Transistor #(.\type ("n")) transistor_2283 (.in(transistor_2074_out), .out(transistor_2283_out), .gate(op1));
  Transistor #(.gate("br")) transistor_2284 (
    .in(transistor_2074_out), .out(transistor_2283_out), .gate(transistor_2281_out));
  Transistor #(.\type ("n")) transistor_2285 (.in(1'b0), .out(transistor_2285_out), .gate(op1));
  Transistor transistor_2286 (.in(1'b1), .out(transistor_2285_out), .gate(op1));
  Transistor #(.gate("br")) transistor_2287 (
    .in(transistor_2076_out), .out(transistor_2287_out), .gate(transistor_2285_out));
  Transistor #(.\type ("n")) transistor_2288 (.in(transistor_2076_out), .out(transistor_2287_out), .gate(op1));
  Transistor transistor_2289 (.in(1'b1), .out(transistor_2289_out), .gate(transistor_2517_out));
  Transistor #(.\type ("n")) transistor_2290 (.in(1'b0), .out(transistor_2289_out), .gate(transistor_2517_out));
  Transistor #(.\type ("n")) transistor_2291 (.in(1'b0), .out(transistor_2291_out), .gate(rst));
  Transistor #(.gate("br")) transistor_2292 (.in(1'b0), .out(transistor_2291_out), .gate(transistor_2255_out));
  Transistor #(.\type ("n")) transistor_2293 (
    .in(transistor_2245_out), .out(transistor_2291_out), .gate(transistor_2255_out));
  Transistor #(.gate("br")) transistor_2294 (.in(transistor_2245_out), .out(transistor_2291_out), .gate(rst));
  Transistor #(.\type ("n")) transistor_2295 (
    .in(transistor_2132_out), .out(transistor_2259_out), .gate(transistor_2257_out));
  Transistor #(.gate("br")) transistor_2296 (.in(transistor_2132_out), .out(transistor_2259_out), .gate(op1));
  Transistor #(.\type ("n")) transistor_2297 (
    .in(transistor_2136_out), .out(transistor_2263_out), .gate(transistor_2261_out));
  Transistor #(.gate("br")) transistor_2298 (.in(transistor_2136_out), .out(transistor_2263_out), .gate(op1));
  Transistor #(.\type ("n")) transistor_2299 (
    .in(transistor_2140_out), .out(transistor_2267_out), .gate(transistor_2265_out));
  Transistor #(.gate("br")) transistor_2300 (.in(transistor_2140_out), .out(transistor_2267_out), .gate(op1));
  Transistor #(.gate("br")) transistor_2301 (.in(transistor_2144_out), .out(transistor_2271_out), .gate(op1));
  Transistor #(.\type ("n")) transistor_2302 (
    .in(transistor_2144_out), .out(transistor_2271_out), .gate(transistor_2269_out));
  Transistor #(.gate("br")) transistor_2303 (.in(transistor_2148_out), .out(transistor_2275_out), .gate(op1));
  Transistor #(.\type ("n")) transistor_2304 (
    .in(transistor_2148_out), .out(transistor_2275_out), .gate(transistor_2273_out));
  Transistor #(.gate("br")) transistor_2305 (.in(transistor_2152_out), .out(transistor_2279_out), .gate(op1));
  Transistor #(.\type ("n")) transistor_2306 (
    .in(transistor_2152_out), .out(transistor_2279_out), .gate(transistor_2277_out));
  Transistor #(.\type ("n")) transistor_2307 (
    .in(transistor_2156_out), .out(transistor_2283_out), .gate(transistor_2281_out));
  Transistor #(.gate("br")) transistor_2308 (.in(transistor_2156_out), .out(transistor_2283_out), .gate(op1));
  Transistor #(.gate("br")) transistor_2309 (.in(transistor_2160_out), .out(transistor_2287_out), .gate(op1));
  Transistor #(.\type ("n")) transistor_2310 (
    .in(transistor_2160_out), .out(transistor_2287_out), .gate(transistor_2285_out));
  Transistor #(.\type ("n")) transistor_2311 (
    .in(transistor_2117_out), .out(transistor_2311_out), .gate(transistor_2517_out));
  Transistor #(.gate("br")) transistor_2312 (
    .in(transistor_2117_out), .out(transistor_2311_out), .gate(transistor_2289_out));
  Transistor #(.\type ("n")) transistor_2313 (.in(c), .out(transistor_2311_out), .gate(transistor_2289_out));
  Transistor #(.gate("br")) transistor_2314 (.in(c), .out(transistor_2311_out), .gate(transistor_2517_out));
  Transistor #(.\type ("n")) transistor_2315 (.in(transistor_2187_out), .out(transistor_2315_out), .gate(op2));
  Transistor #(.gate("br")) transistor_2316 (
    .in(transistor_2187_out), .out(transistor_2315_out), .gate(transistor_2333_out));
  Transistor #(.\type ("n")) transistor_2317 (.in(transistor_2189_out), .out(transistor_2317_out), .gate(op2));
  Transistor #(.gate("br")) transistor_2318 (
    .in(transistor_2189_out), .out(transistor_2317_out), .gate(transistor_2337_out));
  Transistor #(.\type ("n")) transistor_2319 (.in(transistor_2191_out), .out(transistor_2319_out), .gate(op2));
  Transistor #(.gate("br")) transistor_2320 (
    .in(transistor_2191_out), .out(transistor_2319_out), .gate(transistor_2341_out));
  Transistor #(.\type ("n")) transistor_2321 (.in(transistor_2193_out), .out(transistor_2321_out), .gate(op2));
  Transistor #(.gate("br")) transistor_2322 (
    .in(transistor_2193_out), .out(transistor_2321_out), .gate(transistor_2345_out));
  Transistor #(.gate("br")) transistor_2323 (
    .in(transistor_2195_out), .out(transistor_2323_out), .gate(transistor_2349_out));
  Transistor #(.\type ("n")) transistor_2324 (.in(transistor_2195_out), .out(transistor_2323_out), .gate(op2));
  Transistor #(.gate("br")) transistor_2325 (
    .in(transistor_2197_out), .out(transistor_2325_out), .gate(transistor_2353_out));
  Transistor #(.\type ("n")) transistor_2326 (.in(transistor_2197_out), .out(transistor_2325_out), .gate(op2));
  Transistor #(.gate("br")) transistor_2327 (
    .in(transistor_2199_out), .out(transistor_2327_out), .gate(transistor_2357_out));
  Transistor #(.\type ("n")) transistor_2328 (.in(transistor_2199_out), .out(transistor_2327_out), .gate(op2));
  Transistor #(.gate("br")) transistor_2329 (
    .in(transistor_2201_out), .out(transistor_2329_out), .gate(transistor_2361_out));
  Transistor #(.\type ("n")) transistor_2330 (.in(transistor_2201_out), .out(transistor_2329_out), .gate(op2));
  Transistor transistor_2331 (.in(1'b1), .out(transistor_2331_out), .gate(rst));
  Transistor #(.\type ("n")) transistor_2332 (.in(1'b0), .out(transistor_2331_out), .gate(rst));
  Transistor transistor_2333 (.in(1'b1), .out(transistor_2333_out), .gate(op2));
  Transistor #(.\type ("n")) transistor_2334 (.in(1'b0), .out(transistor_2333_out), .gate(op2));
  Transistor #(.\type ("n")) transistor_2335 (
    .in(transistor_2259_out), .out(transistor_2315_out), .gate(transistor_2333_out));
  Transistor #(.gate("br")) transistor_2336 (.in(transistor_2259_out), .out(transistor_2315_out), .gate(op2));
  Transistor transistor_2337 (.in(1'b1), .out(transistor_2337_out), .gate(op2));
  Transistor #(.\type ("n")) transistor_2338 (.in(1'b0), .out(transistor_2337_out), .gate(op2));
  Transistor #(.\type ("n")) transistor_2339 (
    .in(transistor_2263_out), .out(transistor_2317_out), .gate(transistor_2337_out));
  Transistor #(.gate("br")) transistor_2340 (.in(transistor_2263_out), .out(transistor_2317_out), .gate(op2));
  Transistor transistor_2341 (.in(1'b1), .out(transistor_2341_out), .gate(op2));
  Transistor #(.\type ("n")) transistor_2342 (.in(1'b0), .out(transistor_2341_out), .gate(op2));
  Transistor #(.\type ("n")) transistor_2343 (
    .in(transistor_2267_out), .out(transistor_2319_out), .gate(transistor_2341_out));
  Transistor #(.gate("br")) transistor_2344 (.in(transistor_2267_out), .out(transistor_2319_out), .gate(op2));
  Transistor #(.\type ("n")) transistor_2345 (.in(1'b0), .out(transistor_2345_out), .gate(op2));
  Transistor transistor_2346 (.in(1'b1), .out(transistor_2345_out), .gate(op2));
  Transistor #(.\type ("n")) transistor_2347 (
    .in(transistor_2271_out), .out(transistor_2321_out), .gate(transistor_2345_out));
  Transistor #(.gate("br")) transistor_2348 (.in(transistor_2271_out), .out(transistor_2321_out), .gate(op2));
  Transistor #(.\type ("n")) transistor_2349 (.in(1'b0), .out(transistor_2349_out), .gate(op2));
  Transistor transistor_2350 (.in(1'b1), .out(transistor_2349_out), .gate(op2));
  Transistor #(.gate("br")) transistor_2351 (.in(transistor_2275_out), .out(transistor_2323_out), .gate(op2));
  Transistor #(.\type ("n")) transistor_2352 (
    .in(transistor_2275_out), .out(transistor_2323_out), .gate(transistor_2349_out));
  Transistor transistor_2353 (.in(1'b1), .out(transistor_2353_out), .gate(op2));
  Transistor #(.\type ("n")) transistor_2354 (.in(1'b0), .out(transistor_2353_out), .gate(op2));
  Transistor #(.\type ("n")) transistor_2355 (
    .in(transistor_2279_out), .out(transistor_2325_out), .gate(transistor_2353_out));
  Transistor #(.gate("br")) transistor_2356 (.in(transistor_2279_out), .out(transistor_2325_out), .gate(op2));
  Transistor transistor_2357 (.in(1'b1), .out(transistor_2357_out), .gate(op2));
  Transistor #(.\type ("n")) transistor_2358 (.in(1'b0), .out(transistor_2357_out), .gate(op2));
  Transistor #(.\type ("n")) transistor_2359 (
    .in(transistor_2283_out), .out(transistor_2327_out), .gate(transistor_2357_out));
  Transistor #(.gate("br")) transistor_2360 (.in(transistor_2283_out), .out(transistor_2327_out), .gate(op2));
  Transistor transistor_2361 (.in(1'b1), .out(transistor_2361_out), .gate(op2));
  Transistor #(.\type ("n")) transistor_2362 (.in(1'b0), .out(transistor_2361_out), .gate(op2));
  Transistor #(.\type ("n")) transistor_2363 (
    .in(transistor_2287_out), .out(transistor_2329_out), .gate(transistor_2361_out));
  Transistor #(.gate("br")) transistor_2364 (.in(transistor_2287_out), .out(transistor_2329_out), .gate(op2));
  Transistor #(.\type ("n")) transistor_2365 (.in(1'b0), .out(c), .gate(rst));
  Transistor #(.gate("br")) transistor_2366 (.in(1'b0), .out(c), .gate(transistor_2331_out));
  Pull_Resistor pull_resistor_10 (.node(c));
  Transistor #(.\type ("n")) transistor_2367 (.in(transistor_2311_out), .out(c), .gate(transistor_2331_out));
  Transistor #(.gate("br")) transistor_2368 (.in(transistor_2311_out), .out(c), .gate(rst));
  Pull_Resistor pull_resistor_11 (.node(transistor_2315_out));
  Pull_Resistor pull_resistor_12 (.node(transistor_2317_out));
  Pull_Resistor pull_resistor_13 (.node(transistor_2319_out));
  Pull_Resistor pull_resistor_14 (.node(transistor_2321_out));
  Pull_Resistor pull_resistor_15 (.node(transistor_2323_out));
  Pull_Resistor pull_resistor_16 (.node(transistor_2325_out));
  Pull_Resistor pull_resistor_17 (.node(transistor_2327_out));
  Pull_Resistor pull_resistor_18 (.node(transistor_2329_out));
  Transistor transistor_2369 (.in(1'b1), .out(transistor_2369_out), .gate(transistor_2517_out));
  Transistor #(.\type ("n")) transistor_2370 (.in(1'b0), .out(transistor_2369_out), .gate(transistor_2517_out));
  Transistor transistor_2371 (.in(1'b1), .out(transistor_2371_out), .gate(1'b1));
  Transistor #(.\type ("n")) transistor_2372 (.in(1'b0), .out(transistor_2371_out), .gate(1'b1));
  Transistor transistor_2373 (.in(1'b1), .out(transistor_2373_out), .gate(1'b1));
  Transistor #(.\type ("n")) transistor_2374 (.in(1'b0), .out(transistor_2373_out), .gate(1'b1));
  Transistor transistor_2375 (.in(1'b1), .out(transistor_2375_out), .gate(1'b1));
  Transistor #(.\type ("n")) transistor_2376 (.in(1'b0), .out(transistor_2375_out), .gate(1'b1));
  Transistor transistor_2377 (.in(1'b1), .out(transistor_2377_out), .gate(1'b1));
  Transistor #(.\type ("n")) transistor_2378 (.in(1'b0), .out(transistor_2377_out), .gate(1'b1));
  Transistor transistor_2379 (.in(1'b1), .out(transistor_2379_out), .gate(1'b1));
  Transistor #(.\type ("n")) transistor_2380 (.in(1'b0), .out(transistor_2379_out), .gate(1'b1));
  Transistor transistor_2381 (.in(1'b1), .out(transistor_2381_out), .gate(1'b1));
  Transistor #(.\type ("n")) transistor_2382 (.in(1'b0), .out(transistor_2381_out), .gate(1'b1));
  Transistor transistor_2383 (.in(1'b1), .out(transistor_2383_out), .gate(1'b1));
  Transistor #(.\type ("n")) transistor_2384 (.in(1'b0), .out(transistor_2383_out), .gate(1'b1));
  Transistor transistor_2385 (.in(1'b1), .out(transistor_2385_out), .gate(1'b1));
  Transistor #(.\type ("n")) transistor_2386 (.in(1'b0), .out(transistor_2385_out), .gate(1'b1));
  Transistor #(.\type ("n")) transistor_2387 (
    .in(transistor_2471_out), .out(transistor_2387_out), .gate(transistor_2517_out));
  Transistor #(.gate("br")) transistor_2388 (
    .in(transistor_2471_out), .out(transistor_2387_out), .gate(transistor_2369_out));
  Transistor #(.\type ("n")) transistor_2389 (.in(s), .out(transistor_2387_out), .gate(transistor_2369_out));
  Transistor #(.gate("br")) transistor_2390 (.in(s), .out(transistor_2387_out), .gate(transistor_2517_out));
  Transistor #(.\type ("n")) transistor_2391 (.in(transistor_2315_out), .out(transistor_2391_out), .gate(1'b1));
  Transistor #(.gate("br")) transistor_2392 (
    .in(transistor_2315_out), .out(transistor_2391_out), .gate(transistor_2371_out));
  Transistor #(.\type ("n")) transistor_2393 (
    .in(transistor_2429_out), .out(transistor_2391_out), .gate(transistor_2371_out));
  Transistor #(.gate("br")) transistor_2394 (.in(transistor_2429_out), .out(transistor_2391_out), .gate(1'b1));
  Transistor #(.\type ("n")) transistor_2395 (.in(transistor_2317_out), .out(transistor_2395_out), .gate(1'b1));
  Transistor #(.gate("br")) transistor_2396 (
    .in(transistor_2317_out), .out(transistor_2395_out), .gate(transistor_2373_out));
  Transistor #(.\type ("n")) transistor_2397 (
    .in(transistor_2435_out), .out(transistor_2395_out), .gate(transistor_2373_out));
  Transistor #(.gate("br")) transistor_2398 (.in(transistor_2435_out), .out(transistor_2395_out), .gate(1'b1));
  Transistor #(.\type ("n")) transistor_2399 (.in(transistor_2319_out), .out(transistor_2399_out), .gate(1'b1));
  Transistor #(.gate("br")) transistor_2400 (
    .in(transistor_2319_out), .out(transistor_2399_out), .gate(transistor_2375_out));
  Transistor #(.\type ("n")) transistor_2401 (
    .in(transistor_2441_out), .out(transistor_2399_out), .gate(transistor_2375_out));
  Transistor #(.gate("br")) transistor_2402 (.in(transistor_2441_out), .out(transistor_2399_out), .gate(1'b1));
  Transistor #(.\type ("n")) transistor_2403 (.in(transistor_2321_out), .out(transistor_2403_out), .gate(1'b1));
  Transistor #(.gate("br")) transistor_2404 (
    .in(transistor_2321_out), .out(transistor_2403_out), .gate(transistor_2377_out));
  Transistor #(.\type ("n")) transistor_2405 (
    .in(transistor_2447_out), .out(transistor_2403_out), .gate(transistor_2377_out));
  Transistor #(.gate("br")) transistor_2406 (.in(transistor_2447_out), .out(transistor_2403_out), .gate(1'b1));
  Transistor #(.\type ("n")) transistor_2407 (.in(transistor_2323_out), .out(transistor_2407_out), .gate(1'b1));
  Transistor #(.gate("br")) transistor_2408 (
    .in(transistor_2323_out), .out(transistor_2407_out), .gate(transistor_2379_out));
  Transistor #(.\type ("n")) transistor_2409 (
    .in(transistor_2453_out), .out(transistor_2407_out), .gate(transistor_2379_out));
  Transistor #(.gate("br")) transistor_2410 (.in(transistor_2453_out), .out(transistor_2407_out), .gate(1'b1));
  Transistor #(.\type ("n")) transistor_2411 (.in(transistor_2325_out), .out(transistor_2411_out), .gate(1'b1));
  Transistor #(.gate("br")) transistor_2412 (
    .in(transistor_2325_out), .out(transistor_2411_out), .gate(transistor_2381_out));
  Transistor #(.\type ("n")) transistor_2413 (
    .in(transistor_2459_out), .out(transistor_2411_out), .gate(transistor_2381_out));
  Transistor #(.gate("br")) transistor_2414 (.in(transistor_2459_out), .out(transistor_2411_out), .gate(1'b1));
  Transistor #(.\type ("n")) transistor_2415 (.in(transistor_2327_out), .out(transistor_2415_out), .gate(1'b1));
  Transistor #(.gate("br")) transistor_2416 (
    .in(transistor_2327_out), .out(transistor_2415_out), .gate(transistor_2383_out));
  Transistor #(.\type ("n")) transistor_2417 (
    .in(transistor_2465_out), .out(transistor_2415_out), .gate(transistor_2383_out));
  Transistor #(.gate("br")) transistor_2418 (.in(transistor_2465_out), .out(transistor_2415_out), .gate(1'b1));
  Transistor #(.\type ("n")) transistor_2419 (.in(transistor_2329_out), .out(transistor_2419_out), .gate(1'b1));
  Transistor #(.gate("br")) transistor_2420 (
    .in(transistor_2329_out), .out(transistor_2419_out), .gate(transistor_2385_out));
  Transistor #(.\type ("n")) transistor_2421 (
    .in(transistor_2471_out), .out(transistor_2419_out), .gate(transistor_2385_out));
  Transistor #(.gate("br")) transistor_2422 (.in(transistor_2471_out), .out(transistor_2419_out), .gate(1'b1));
  Transistor #(.\type ("n")) transistor_2423 (.in(1'b0), .out(s), .gate(rst));
  Transistor #(.gate("br")) transistor_2424 (.in(1'b0), .out(s), .gate(transistor_2425_out));
  Transistor transistor_2425 (.in(1'b1), .out(transistor_2425_out), .gate(rst));
  Transistor #(.\type ("n")) transistor_2426 (.in(1'b0), .out(transistor_2425_out), .gate(rst));
  Transistor #(.\type ("n")) transistor_2427 (.in(transistor_2387_out), .out(s), .gate(transistor_2425_out));
  Transistor #(.gate("br")) transistor_2428 (.in(transistor_2387_out), .out(s), .gate(rst));
  Transistor #(.\type ("n")) transistor_2429 (.in(1'b0), .out(transistor_2429_out), .gate(rst));
  Transistor #(.gate("br")) transistor_2430 (.in(1'b0), .out(transistor_2429_out), .gate(transistor_2431_out));
  Transistor transistor_2431 (.in(1'b1), .out(transistor_2431_out), .gate(rst));
  Transistor #(.\type ("n")) transistor_2432 (.in(1'b0), .out(transistor_2431_out), .gate(rst));
  Transistor #(.\type ("n")) transistor_2433 (
    .in(transistor_2391_out), .out(transistor_2429_out), .gate(transistor_2431_out));
  Transistor #(.gate("br")) transistor_2434 (.in(transistor_2391_out), .out(transistor_2429_out), .gate(rst));
  Transistor #(.\type ("n")) transistor_2435 (.in(1'b0), .out(transistor_2435_out), .gate(rst));
  Transistor #(.gate("br")) transistor_2436 (.in(1'b0), .out(transistor_2435_out), .gate(transistor_2437_out));
  Transistor transistor_2437 (.in(1'b1), .out(transistor_2437_out), .gate(rst));
  Transistor #(.\type ("n")) transistor_2438 (.in(1'b0), .out(transistor_2437_out), .gate(rst));
  Transistor #(.\type ("n")) transistor_2439 (
    .in(transistor_2395_out), .out(transistor_2435_out), .gate(transistor_2437_out));
  Transistor #(.gate("br")) transistor_2440 (.in(transistor_2395_out), .out(transistor_2435_out), .gate(rst));
  Transistor #(.\type ("n")) transistor_2441 (.in(1'b0), .out(transistor_2441_out), .gate(rst));
  Transistor #(.gate("br")) transistor_2442 (.in(1'b0), .out(transistor_2441_out), .gate(transistor_2443_out));
  Transistor transistor_2443 (.in(1'b1), .out(transistor_2443_out), .gate(rst));
  Transistor #(.\type ("n")) transistor_2444 (.in(1'b0), .out(transistor_2443_out), .gate(rst));
  Transistor #(.\type ("n")) transistor_2445 (
    .in(transistor_2399_out), .out(transistor_2441_out), .gate(transistor_2443_out));
  Transistor #(.gate("br")) transistor_2446 (.in(transistor_2399_out), .out(transistor_2441_out), .gate(rst));
  Transistor #(.\type ("n")) transistor_2447 (.in(1'b0), .out(transistor_2447_out), .gate(rst));
  Transistor #(.gate("br")) transistor_2448 (.in(1'b0), .out(transistor_2447_out), .gate(transistor_2449_out));
  Transistor transistor_2449 (.in(1'b1), .out(transistor_2449_out), .gate(rst));
  Transistor #(.\type ("n")) transistor_2450 (.in(1'b0), .out(transistor_2449_out), .gate(rst));
  Transistor #(.\type ("n")) transistor_2451 (
    .in(transistor_2403_out), .out(transistor_2447_out), .gate(transistor_2449_out));
  Transistor #(.gate("br")) transistor_2452 (.in(transistor_2403_out), .out(transistor_2447_out), .gate(rst));
  Transistor #(.\type ("n")) transistor_2453 (.in(1'b0), .out(transistor_2453_out), .gate(rst));
  Transistor #(.gate("br")) transistor_2454 (.in(1'b0), .out(transistor_2453_out), .gate(transistor_2455_out));
  Transistor transistor_2455 (.in(1'b1), .out(transistor_2455_out), .gate(rst));
  Transistor #(.\type ("n")) transistor_2456 (.in(1'b0), .out(transistor_2455_out), .gate(rst));
  Transistor #(.\type ("n")) transistor_2457 (
    .in(transistor_2407_out), .out(transistor_2453_out), .gate(transistor_2455_out));
  Transistor #(.gate("br")) transistor_2458 (.in(transistor_2407_out), .out(transistor_2453_out), .gate(rst));
  Transistor #(.\type ("n")) transistor_2459 (.in(1'b0), .out(transistor_2459_out), .gate(rst));
  Transistor #(.gate("br")) transistor_2460 (.in(1'b0), .out(transistor_2459_out), .gate(transistor_2461_out));
  Transistor transistor_2461 (.in(1'b1), .out(transistor_2461_out), .gate(rst));
  Transistor #(.\type ("n")) transistor_2462 (.in(1'b0), .out(transistor_2461_out), .gate(rst));
  Transistor #(.\type ("n")) transistor_2463 (
    .in(transistor_2411_out), .out(transistor_2459_out), .gate(transistor_2461_out));
  Transistor #(.gate("br")) transistor_2464 (.in(transistor_2411_out), .out(transistor_2459_out), .gate(rst));
  Transistor #(.\type ("n")) transistor_2465 (.in(1'b0), .out(transistor_2465_out), .gate(rst));
  Transistor #(.gate("br")) transistor_2466 (.in(1'b0), .out(transistor_2465_out), .gate(transistor_2467_out));
  Transistor transistor_2467 (.in(1'b1), .out(transistor_2467_out), .gate(rst));
  Transistor #(.\type ("n")) transistor_2468 (.in(1'b0), .out(transistor_2467_out), .gate(rst));
  Transistor #(.\type ("n")) transistor_2469 (
    .in(transistor_2415_out), .out(transistor_2465_out), .gate(transistor_2467_out));
  Transistor #(.gate("br")) transistor_2470 (.in(transistor_2415_out), .out(transistor_2465_out), .gate(rst));
  Transistor #(.\type ("n")) transistor_2471 (.in(1'b0), .out(transistor_2471_out), .gate(rst));
  Transistor #(.gate("br")) transistor_2472 (.in(1'b0), .out(transistor_2471_out), .gate(transistor_2473_out));
  Transistor transistor_2473 (.in(1'b1), .out(transistor_2473_out), .gate(rst));
  Transistor #(.\type ("n")) transistor_2474 (.in(1'b0), .out(transistor_2473_out), .gate(rst));
  Transistor #(.\type ("n")) transistor_2475 (
    .in(transistor_2419_out), .out(transistor_2471_out), .gate(transistor_2473_out));
  Transistor #(.gate("br")) transistor_2476 (.in(transistor_2419_out), .out(transistor_2471_out), .gate(rst));
  Pull_Resistor pull_resistor_19 (.node(s));
  Transistor #(.\type ("n")) transistor_2477 (.in(1'b0), .out(transistor_2477_out), .gate(transistor_2435_out));
  Transistor #(.\type ("n")) transistor_2478 (.in(1'b0), .out(transistor_2478_out), .gate(transistor_2441_out));
  Transistor #(.\type ("n")) transistor_2479 (.in(1'b0), .out(transistor_2479_out), .gate(transistor_2447_out));
  Transistor #(.\type ("n")) transistor_2480 (.in(1'b0), .out(transistor_2480_out), .gate(transistor_2453_out));
  Transistor #(.\type ("n")) transistor_2481 (.in(1'b0), .out(transistor_2481_out), .gate(transistor_2459_out));
  Transistor #(.\type ("n")) transistor_2482 (.in(1'b0), .out(transistor_2482_out), .gate(transistor_2465_out));
  Transistor #(.\type ("n")) transistor_2483 (.in(1'b0), .out(transistor_2483_out), .gate(transistor_2471_out));
  Transistor #(.\type ("n")) transistor_2484 (
    .in(transistor_2483_out), .out(transistor_2484_out), .gate(transistor_2517_out));
  Transistor #(.gate("br")) transistor_2485 (
    .in(transistor_2483_out), .out(transistor_2484_out), .gate(transistor_2486_out));
  Transistor transistor_2486 (.in(1'b1), .out(transistor_2486_out), .gate(transistor_2517_out));
  Transistor #(.\type ("n")) transistor_2487 (.in(1'b0), .out(transistor_2486_out), .gate(transistor_2517_out));
  Transistor #(.\type ("n")) transistor_2488 (.in(z), .out(transistor_2484_out), .gate(transistor_2486_out));
  Transistor #(.gate("br")) transistor_2489 (.in(z), .out(transistor_2484_out), .gate(transistor_2517_out));
  Transistor transistor_2490 (.in(1'b1), .out(transistor_2490_out), .gate(transistor_2435_out));
  Transistor transistor_2491 (.in(transistor_2490_out), .out(transistor_2477_out), .gate(transistor_2429_out));
  Transistor #(.\type ("n")) transistor_2492 (.in(1'b0), .out(transistor_2477_out), .gate(transistor_2429_out));
  Transistor transistor_2493 (.in(1'b1), .out(transistor_2493_out), .gate(transistor_2441_out));
  Transistor transistor_2494 (.in(transistor_2493_out), .out(transistor_2478_out), .gate(transistor_2519_out));
  Transistor #(.\type ("n")) transistor_2495 (.in(1'b0), .out(transistor_2478_out), .gate(transistor_2519_out));
  Transistor transistor_2496 (.in(1'b1), .out(transistor_2496_out), .gate(transistor_2447_out));
  Transistor transistor_2497 (.in(transistor_2496_out), .out(transistor_2479_out), .gate(transistor_2521_out));
  Transistor #(.\type ("n")) transistor_2498 (.in(1'b0), .out(transistor_2479_out), .gate(transistor_2521_out));
  Transistor transistor_2499 (.in(1'b1), .out(transistor_2499_out), .gate(transistor_2453_out));
  Transistor transistor_2500 (.in(transistor_2499_out), .out(transistor_2480_out), .gate(transistor_2523_out));
  Transistor #(.\type ("n")) transistor_2501 (.in(1'b0), .out(transistor_2480_out), .gate(transistor_2523_out));
  Transistor transistor_2502 (.in(1'b1), .out(transistor_2502_out), .gate(transistor_2459_out));
  Transistor transistor_2503 (.in(transistor_2502_out), .out(transistor_2481_out), .gate(transistor_2525_out));
  Transistor #(.\type ("n")) transistor_2504 (.in(1'b0), .out(transistor_2481_out), .gate(transistor_2525_out));
  Transistor transistor_2505 (.in(1'b1), .out(transistor_2505_out), .gate(transistor_2465_out));
  Transistor transistor_2506 (.in(transistor_2505_out), .out(transistor_2482_out), .gate(transistor_2527_out));
  Transistor #(.\type ("n")) transistor_2507 (.in(1'b0), .out(transistor_2482_out), .gate(transistor_2527_out));
  Transistor transistor_2508 (.in(1'b1), .out(transistor_2508_out), .gate(transistor_2471_out));
  Transistor transistor_2509 (.in(transistor_2508_out), .out(transistor_2483_out), .gate(transistor_2529_out));
  Transistor #(.\type ("n")) transistor_2510 (.in(1'b0), .out(transistor_2483_out), .gate(transistor_2529_out));
  Transistor transistor_2511 (.in(1'b1), .out(transistor_2511_out), .gate(rst));
  Transistor #(.\type ("n")) transistor_2512 (.in(1'b0), .out(transistor_2511_out), .gate(rst));
  Transistor transistor_2513 (.in(1'b1), .out(transistor_2513_out), .gate(clk_w));
  Transistor transistor_2514 (.in(1'b1), .out(transistor_2513_out), .gate(fr_w));
  Transistor #(.\type ("n")) transistor_2515 (.in(transistor_2516_out), .out(transistor_2513_out), .gate(clk_w));
  Transistor #(.\type ("n")) transistor_2516 (.in(1'b0), .out(transistor_2516_out), .gate(fr_w));
  Transistor transistor_2517 (.in(1'b1), .out(transistor_2517_out), .gate(transistor_2513_out));
  Transistor #(.\type ("n")) transistor_2518 (.in(1'b0), .out(transistor_2517_out), .gate(transistor_2513_out));
  Transistor transistor_2519 (.in(1'b1), .out(transistor_2519_out), .gate(transistor_2477_out));
  Transistor #(.\type ("n")) transistor_2520 (.in(1'b0), .out(transistor_2519_out), .gate(transistor_2477_out));
  Transistor transistor_2521 (.in(1'b1), .out(transistor_2521_out), .gate(transistor_2478_out));
  Transistor #(.\type ("n")) transistor_2522 (.in(1'b0), .out(transistor_2521_out), .gate(transistor_2478_out));
  Transistor transistor_2523 (.in(1'b1), .out(transistor_2523_out), .gate(transistor_2479_out));
  Transistor #(.\type ("n")) transistor_2524 (.in(1'b0), .out(transistor_2523_out), .gate(transistor_2479_out));
  Transistor transistor_2525 (.in(1'b1), .out(transistor_2525_out), .gate(transistor_2480_out));
  Transistor #(.\type ("n")) transistor_2526 (.in(1'b0), .out(transistor_2525_out), .gate(transistor_2480_out));
  Transistor transistor_2527 (.in(1'b1), .out(transistor_2527_out), .gate(transistor_2481_out));
  Transistor #(.\type ("n")) transistor_2528 (.in(1'b0), .out(transistor_2527_out), .gate(transistor_2481_out));
  Transistor transistor_2529 (.in(1'b1), .out(transistor_2529_out), .gate(transistor_2482_out));
  Transistor #(.\type ("n")) transistor_2530 (.in(1'b0), .out(transistor_2529_out), .gate(transistor_2482_out));
  Transistor #(.\type ("n")) transistor_2531 (.in(1'b0), .out(z), .gate(rst));
  Transistor #(.gate("br")) transistor_2532 (.in(1'b0), .out(z), .gate(transistor_2511_out));
  Pull_Resistor pull_resistor_20 (.node(z));
  Transistor #(.\type ("n")) transistor_2533 (.in(transistor_2484_out), .out(z), .gate(transistor_2511_out));
  Transistor #(.gate("br")) transistor_2534 (.in(transistor_2484_out), .out(z), .gate(rst));
  Transistor transistor_2535 (.in(1'b1), .out(transistor_2535_out), .gate(clk_r));
  Transistor transistor_2536 (.in(1'b1), .out(transistor_2536_out), .gate(transistor_2535_out));
  Transistor #(.\type ("n")) transistor_2537 (.in(1'b0), .out(transistor_2536_out), .gate(transistor_2535_out));
  Transistor transistor_2538 (.in(1'b1), .out(transistor_2538_out), .gate(transistor_2536_out));
  Transistor #(.\type ("n")) transistor_2539 (.in(1'b0), .out(transistor_2538_out), .gate(transistor_2536_out));
  Transistor #(.\type ("n")) transistor_2540 (.in(transistor_2429_out), .out(_0), .gate(transistor_2536_out));
  Transistor transistor_2541 (.in(1'b1), .out(transistor_2541_out), .gate(transistor_2536_out));
  Transistor #(.\type ("n")) transistor_2542 (.in(1'b0), .out(transistor_2541_out), .gate(transistor_2536_out));
  Transistor #(.\type ("n")) transistor_2543 (.in(transistor_2435_out), .out(_1), .gate(transistor_2536_out));
  Transistor transistor_2544 (.in(1'b1), .out(transistor_2544_out), .gate(transistor_2536_out));
  Transistor #(.\type ("n")) transistor_2545 (.in(1'b0), .out(transistor_2544_out), .gate(transistor_2536_out));
  Transistor #(.\type ("n")) transistor_2546 (.in(transistor_2441_out), .out(_2), .gate(transistor_2536_out));
  Transistor transistor_2547 (.in(1'b1), .out(transistor_2547_out), .gate(transistor_2536_out));
  Transistor #(.\type ("n")) transistor_2548 (.in(1'b0), .out(transistor_2547_out), .gate(transistor_2536_out));
  Transistor #(.\type ("n")) transistor_2549 (.in(transistor_2447_out), .out(_3), .gate(transistor_2536_out));
  Transistor transistor_2550 (.in(1'b1), .out(transistor_2550_out), .gate(transistor_2536_out));
  Transistor #(.\type ("n")) transistor_2551 (.in(1'b0), .out(transistor_2550_out), .gate(transistor_2536_out));
  Transistor #(.\type ("n")) transistor_2552 (.in(transistor_2453_out), .out(_4), .gate(transistor_2536_out));
  Transistor transistor_2553 (.in(1'b1), .out(transistor_2553_out), .gate(transistor_2536_out));
  Transistor #(.\type ("n")) transistor_2554 (.in(1'b0), .out(transistor_2553_out), .gate(transistor_2536_out));
  Transistor #(.\type ("n")) transistor_2555 (.in(transistor_2459_out), .out(_5), .gate(transistor_2536_out));
  Transistor transistor_2556 (.in(1'b1), .out(transistor_2556_out), .gate(transistor_2536_out));
  Transistor #(.\type ("n")) transistor_2557 (.in(1'b0), .out(transistor_2556_out), .gate(transistor_2536_out));
  Transistor #(.\type ("n")) transistor_2558 (.in(transistor_2465_out), .out(_6), .gate(transistor_2536_out));
  Transistor transistor_2559 (.in(1'b1), .out(transistor_2559_out), .gate(transistor_2536_out));
  Transistor #(.\type ("n")) transistor_2560 (.in(1'b0), .out(transistor_2559_out), .gate(transistor_2536_out));
  Transistor #(.\type ("n")) transistor_2561 (.in(transistor_2471_out), .out(_7), .gate(transistor_2536_out));
  Transistor transistor_2562 (.in(1'b1), .out(transistor_2535_out), .gate(rd_r));
  Transistor #(.\type ("n")) transistor_2563 (.in(transistor_2564_out), .out(transistor_2535_out), .gate(clk_r));
  Transistor #(.\type ("n")) transistor_2564 (.in(1'b0), .out(transistor_2564_out), .gate(rd_r));
  Transistor #(.gate("br")) transistor_2565 (.in(transistor_2429_out), .out(_0), .gate(transistor_2538_out));
  Transistor #(.gate("br")) transistor_2566 (.in(transistor_2435_out), .out(_1), .gate(transistor_2541_out));
  Transistor #(.gate("br")) transistor_2567 (.in(transistor_2441_out), .out(_2), .gate(transistor_2544_out));
  Transistor #(.gate("br")) transistor_2568 (.in(transistor_2447_out), .out(_3), .gate(transistor_2547_out));
  Transistor #(.gate("br")) transistor_2569 (.in(transistor_2453_out), .out(_4), .gate(transistor_2550_out));
  Transistor #(.gate("br")) transistor_2570 (.in(transistor_2459_out), .out(_5), .gate(transistor_2553_out));
  Transistor #(.gate("br")) transistor_2571 (.in(transistor_2465_out), .out(_6), .gate(transistor_2556_out));
  Transistor #(.gate("br")) transistor_2572 (.in(transistor_2471_out), .out(_7), .gate(transistor_2559_out));
  Pull_Resistor pull_resistor_21 (.node(_4));
  Pull_Resistor pull_resistor_22 (.node(_5));
  Pull_Resistor pull_resistor_23 (.node(_6));
  Pull_Resistor pull_resistor_24 (.node(_7));
  Pull_Resistor pull_resistor_25 (.node(_0));
  Pull_Resistor pull_resistor_26 (.node(_1));
  Pull_Resistor pull_resistor_27 (.node(_2));
  Pull_Resistor pull_resistor_28 (.node(_3));

  // Notes on the sheet:
  //   Decoder destroys data in the registers. Logisim simply cannot determine the final singal values and propagates E. :(
  //   ScottE Processor v2
endmodule

module CONTROLUNIT (
  input  w,
  input  rst,
  input  _0,
  input  _1,
  input  _2,
  input  _3,
  input  _4,
  input  _5,
  input  _6,
  input  _7,
  output ir_0,
  output ir_1,
  output ir_2,
  output ir_3,
  output ir_4,
  output ir_5,
  output ir_6,
  output ir_7
);

  wire transistor_1_out, transistor_3_out, transistor_5_out, transistor_7_out, transistor_9_out,
       transistor_11_out, transistor_13_out, transistor_15_out, transistor_17_out, transistor_21_out,
       transistor_25_out, transistor_29_out, transistor_33_out, transistor_37_out, transistor_41_out,
       transistor_45_out, transistor_49_out, transistor_51_out, transistor_53_out, transistor_55_out,
       transistor_57_out, transistor_59_out, transistor_61_out, transistor_63_out;

  Transistor transistor_1 (.in(1'b1), .out(transistor_1_out), .gate(w));
  Transistor #(.\type ("n")) transistor_2 (.in(1'b0), .out(transistor_1_out), .gate(w));
  Transistor transistor_3 (.in(1'b1), .out(transistor_3_out), .gate(w));
  Transistor #(.\type ("n")) transistor_4 (.in(1'b0), .out(transistor_3_out), .gate(w));
  Transistor transistor_5 (.in(1'b1), .out(transistor_5_out), .gate(w));
  Transistor #(.\type ("n")) transistor_6 (.in(1'b0), .out(transistor_5_out), .gate(w));
  Transistor transistor_7 (.in(1'b1), .out(transistor_7_out), .gate(w));
  Transistor #(.\type ("n")) transistor_8 (.in(1'b0), .out(transistor_7_out), .gate(w));
  Transistor transistor_9 (.in(1'b1), .out(transistor_9_out), .gate(w));
  Transistor #(.\type ("n")) transistor_10 (.in(1'b0), .out(transistor_9_out), .gate(w));
  Transistor transistor_11 (.in(1'b1), .out(transistor_11_out), .gate(w));
  Transistor #(.\type ("n")) transistor_12 (.in(1'b0), .out(transistor_11_out), .gate(w));
  Transistor transistor_13 (.in(1'b1), .out(transistor_13_out), .gate(w));
  Transistor #(.\type ("n")) transistor_14 (.in(1'b0), .out(transistor_13_out), .gate(w));
  Transistor transistor_15 (.in(1'b1), .out(transistor_15_out), .gate(w));
  Transistor #(.\type ("n")) transistor_16 (.in(1'b0), .out(transistor_15_out), .gate(w));
  Transistor #(.\type ("n")) transistor_17 (.in(_0), .out(transistor_17_out), .gate(w));
  Transistor #(.gate("br")) transistor_18 (.in(_0), .out(transistor_17_out), .gate(transistor_1_out));
  Transistor #(.\type ("n")) transistor_19 (.in(ir_0), .out(transistor_17_out), .gate(transistor_1_out));
  Transistor #(.gate("br")) transistor_20 (.in(ir_0), .out(transistor_17_out), .gate(w));
  Transistor #(.\type ("n")) transistor_21 (.in(_1), .out(transistor_21_out), .gate(w));
  Transistor #(.gate("br")) transistor_22 (.in(_1), .out(transistor_21_out), .gate(transistor_3_out));
  Transistor #(.\type ("n")) transistor_23 (.in(ir_1), .out(transistor_21_out), .gate(transistor_3_out));
  Transistor #(.gate("br")) transistor_24 (.in(ir_1), .out(transistor_21_out), .gate(w));
  Transistor #(.\type ("n")) transistor_25 (.in(_2), .out(transistor_25_out), .gate(w));
  Transistor #(.gate("br")) transistor_26 (.in(_2), .out(transistor_25_out), .gate(transistor_5_out));
  Transistor #(.\type ("n")) transistor_27 (.in(ir_2), .out(transistor_25_out), .gate(transistor_5_out));
  Transistor #(.gate("br")) transistor_28 (.in(ir_2), .out(transistor_25_out), .gate(w));
  Transistor #(.\type ("n")) transistor_29 (.in(_3), .out(transistor_29_out), .gate(w));
  Transistor #(.gate("br")) transistor_30 (.in(_3), .out(transistor_29_out), .gate(transistor_7_out));
  Transistor #(.\type ("n")) transistor_31 (.in(ir_3), .out(transistor_29_out), .gate(transistor_7_out));
  Transistor #(.gate("br")) transistor_32 (.in(ir_3), .out(transistor_29_out), .gate(w));
  Transistor #(.\type ("n")) transistor_33 (.in(_4), .out(transistor_33_out), .gate(w));
  Transistor #(.gate("br")) transistor_34 (.in(_4), .out(transistor_33_out), .gate(transistor_9_out));
  Transistor #(.\type ("n")) transistor_35 (.in(ir_4), .out(transistor_33_out), .gate(transistor_9_out));
  Transistor #(.gate("br")) transistor_36 (.in(ir_4), .out(transistor_33_out), .gate(w));
  Transistor #(.\type ("n")) transistor_37 (.in(_5), .out(transistor_37_out), .gate(w));
  Transistor #(.gate("br")) transistor_38 (.in(_5), .out(transistor_37_out), .gate(transistor_11_out));
  Transistor #(.\type ("n")) transistor_39 (.in(ir_5), .out(transistor_37_out), .gate(transistor_11_out));
  Transistor #(.gate("br")) transistor_40 (.in(ir_5), .out(transistor_37_out), .gate(w));
  Transistor #(.\type ("n")) transistor_41 (.in(_6), .out(transistor_41_out), .gate(w));
  Transistor #(.gate("br")) transistor_42 (.in(_6), .out(transistor_41_out), .gate(transistor_13_out));
  Transistor #(.\type ("n")) transistor_43 (.in(ir_6), .out(transistor_41_out), .gate(transistor_13_out));
  Transistor #(.gate("br")) transistor_44 (.in(ir_6), .out(transistor_41_out), .gate(w));
  Transistor #(.\type ("n")) transistor_45 (.in(_7), .out(transistor_45_out), .gate(w));
  Transistor #(.gate("br")) transistor_46 (.in(_7), .out(transistor_45_out), .gate(transistor_15_out));
  Transistor #(.\type ("n")) transistor_47 (.in(ir_7), .out(transistor_45_out), .gate(transistor_15_out));
  Transistor #(.gate("br")) transistor_48 (.in(ir_7), .out(transistor_45_out), .gate(w));
  Transistor transistor_49 (.in(1'b1), .out(transistor_49_out), .gate(rst));
  Transistor #(.\type ("n")) transistor_50 (.in(1'b0), .out(transistor_49_out), .gate(rst));
  Transistor transistor_51 (.in(1'b1), .out(transistor_51_out), .gate(rst));
  Transistor #(.\type ("n")) transistor_52 (.in(1'b0), .out(transistor_51_out), .gate(rst));
  Transistor transistor_53 (.in(1'b1), .out(transistor_53_out), .gate(rst));
  Transistor #(.\type ("n")) transistor_54 (.in(1'b0), .out(transistor_53_out), .gate(rst));
  Transistor transistor_55 (.in(1'b1), .out(transistor_55_out), .gate(rst));
  Transistor #(.\type ("n")) transistor_56 (.in(1'b0), .out(transistor_55_out), .gate(rst));
  Transistor transistor_57 (.in(1'b1), .out(transistor_57_out), .gate(rst));
  Transistor #(.\type ("n")) transistor_58 (.in(1'b0), .out(transistor_57_out), .gate(rst));
  Transistor transistor_59 (.in(1'b1), .out(transistor_59_out), .gate(rst));
  Transistor #(.\type ("n")) transistor_60 (.in(1'b0), .out(transistor_59_out), .gate(rst));
  Transistor transistor_61 (.in(1'b1), .out(transistor_61_out), .gate(rst));
  Transistor #(.\type ("n")) transistor_62 (.in(1'b0), .out(transistor_61_out), .gate(rst));
  Transistor transistor_63 (.in(1'b1), .out(transistor_63_out), .gate(rst));
  Transistor #(.\type ("n")) transistor_64 (.in(1'b0), .out(transistor_63_out), .gate(rst));
  Transistor #(.\type ("n")) transistor_65 (.in(1'b0), .out(ir_0), .gate(rst));
  Transistor #(.gate("br")) transistor_66 (.in(1'b0), .out(ir_0), .gate(transistor_49_out));
  Transistor #(.\type ("n")) transistor_67 (.in(transistor_17_out), .out(ir_0), .gate(transistor_49_out));
  Transistor #(.gate("br")) transistor_68 (.in(transistor_17_out), .out(ir_0), .gate(rst));
  Transistor #(.\type ("n")) transistor_69 (.in(1'b0), .out(ir_1), .gate(rst));
  Transistor #(.gate("br")) transistor_70 (.in(1'b0), .out(ir_1), .gate(transistor_51_out));
  Transistor #(.\type ("n")) transistor_71 (.in(transistor_21_out), .out(ir_1), .gate(transistor_51_out));
  Transistor #(.gate("br")) transistor_72 (.in(transistor_21_out), .out(ir_1), .gate(rst));
  Transistor #(.\type ("n")) transistor_73 (.in(1'b0), .out(ir_2), .gate(rst));
  Transistor #(.gate("br")) transistor_74 (.in(1'b0), .out(ir_2), .gate(transistor_53_out));
  Transistor #(.\type ("n")) transistor_75 (.in(transistor_25_out), .out(ir_2), .gate(transistor_53_out));
  Transistor #(.gate("br")) transistor_76 (.in(transistor_25_out), .out(ir_2), .gate(rst));
  Transistor #(.\type ("n")) transistor_77 (.in(1'b0), .out(ir_3), .gate(rst));
  Transistor #(.gate("br")) transistor_78 (.in(1'b0), .out(ir_3), .gate(transistor_55_out));
  Transistor #(.\type ("n")) transistor_79 (.in(transistor_29_out), .out(ir_3), .gate(transistor_55_out));
  Transistor #(.gate("br")) transistor_80 (.in(transistor_29_out), .out(ir_3), .gate(rst));
  Transistor #(.\type ("n")) transistor_81 (.in(1'b0), .out(ir_4), .gate(rst));
  Transistor #(.gate("br")) transistor_82 (.in(1'b0), .out(ir_4), .gate(transistor_57_out));
  Transistor #(.\type ("n")) transistor_83 (.in(transistor_33_out), .out(ir_4), .gate(transistor_57_out));
  Transistor #(.gate("br")) transistor_84 (.in(transistor_33_out), .out(ir_4), .gate(rst));
  Transistor #(.\type ("n")) transistor_85 (.in(1'b0), .out(ir_5), .gate(rst));
  Transistor #(.gate("br")) transistor_86 (.in(1'b0), .out(ir_5), .gate(transistor_59_out));
  Transistor #(.\type ("n")) transistor_87 (.in(transistor_37_out), .out(ir_5), .gate(transistor_59_out));
  Transistor #(.gate("br")) transistor_88 (.in(transistor_37_out), .out(ir_5), .gate(rst));
  Transistor #(.\type ("n")) transistor_89 (.in(1'b0), .out(ir_6), .gate(rst));
  Transistor #(.gate("br")) transistor_90 (.in(1'b0), .out(ir_6), .gate(transistor_61_out));
  Transistor #(.\type ("n")) transistor_91 (.in(transistor_41_out), .out(ir_6), .gate(transistor_61_out));
  Transistor #(.gate("br")) transistor_92 (.in(transistor_41_out), .out(ir_6), .gate(rst));
  Transistor #(.\type ("n")) transistor_93 (.in(1'b0), .out(ir_7), .gate(rst));
  Transistor #(.gate("br")) transistor_94 (.in(1'b0), .out(ir_7), .gate(transistor_63_out));
  Transistor #(.\type ("n")) transistor_95 (.in(transistor_45_out), .out(ir_7), .gate(transistor_63_out));
  Transistor #(.gate("br")) transistor_96 (.in(transistor_45_out), .out(ir_7), .gate(rst));
endmodule

module NAND2x1x1 (
  input  a,
  input  b,
  output out
);

  wire transistor_4_out;

  Transistor transistor_1 (.in(1'b1), .out(out), .gate(a));
  Transistor transistor_2 (.in(1'b1), .out(out), .gate(b));
  Transistor #(.\type ("n")) transistor_3 (.in(transistor_4_out), .out(out), .gate(a));
  Transistor #(.\type ("n")) transistor_4 (.in(1'b0), .out(transistor_4_out), .gate(b));
endmodule

module NAND3x1x1 (
  input  a,
  input  b,
  input  c,
  output out
);

  wire transistor_5_out, transistor_6_out;

  Transistor transistor_1 (.in(1'b1), .out(out), .gate(a));
  Transistor transistor_2 (.in(1'b1), .out(out), .gate(b));
  Transistor transistor_3 (.in(1'b1), .out(out), .gate(c));
  Transistor #(.\type ("n")) transistor_4 (.in(transistor_5_out), .out(out), .gate(a));
  Transistor #(.\type ("n")) transistor_5 (.in(transistor_6_out), .out(transistor_5_out), .gate(b));
  Transistor #(.\type ("n")) transistor_6 (.in(1'b0), .out(transistor_6_out), .gate(c));
endmodule

module NOR2x1x1 (
  input  a,
  input  b,
  output out
);

  wire transistor_1_out;

  Transistor transistor_1 (.in(1'b1), .out(transistor_1_out), .gate(a));
  Transistor transistor_2 (.in(transistor_1_out), .out(out), .gate(b));
  Transistor #(.\type ("n")) transistor_3 (.in(1'b0), .out(out), .gate(b));
  Transistor #(.\type ("n")) transistor_4 (.in(1'b0), .out(out), .gate(a));
endmodule

module NOR3x1x1 (
  input  a,
  input  b,
  input  c,
  output out
);

  wire transistor_3_out, transistor_4_out;

  Transistor #(.\type ("n")) transistor_1 (.in(1'b0), .out(out), .gate(b));
  Transistor #(.\type ("n")) transistor_2 (.in(1'b0), .out(out), .gate(a));
  Transistor transistor_3 (.in(1'b1), .out(transistor_3_out), .gate(a));
  Transistor transistor_4 (.in(transistor_3_out), .out(transistor_4_out), .gate(b));
  Transistor transistor_5 (.in(transistor_4_out), .out(out), .gate(c));
  Transistor #(.\type ("n")) transistor_6 (.in(1'b0), .out(out), .gate(c));
endmodule

module XOR2x1x1 (
  input  a,
  input  b,
  output out
);

  wire transistor_1_out, transistor_4_out, transistor_5_out, transistor_6_out, transistor_9_out,
       transistor_13_out, transistor_16_out;

  Transistor transistor_1 (.in(1'b1), .out(transistor_1_out), .gate(a));
  Transistor transistor_2 (.in(1'b1), .out(transistor_1_out), .gate(b));
  Transistor #(.\type ("n")) transistor_3 (.in(transistor_4_out), .out(transistor_1_out), .gate(a));
  Transistor #(.\type ("n")) transistor_4 (.in(1'b0), .out(transistor_4_out), .gate(b));
  Transistor transistor_5 (.in(1'b1), .out(transistor_5_out), .gate(a));
  Transistor transistor_6 (.in(1'b1), .out(transistor_6_out), .gate(transistor_1_out));
  Transistor transistor_7 (.in(1'b1), .out(transistor_5_out), .gate(transistor_1_out));
  Transistor #(.\type ("n")) transistor_8 (.in(transistor_9_out), .out(transistor_5_out), .gate(a));
  Transistor #(.\type ("n")) transistor_9 (.in(1'b0), .out(transistor_9_out), .gate(transistor_1_out));
  Transistor transistor_10 (.in(1'b1), .out(out), .gate(transistor_5_out));
  Transistor transistor_11 (.in(1'b1), .out(transistor_6_out), .gate(b));
  Transistor #(.\type ("n")) transistor_12 (.in(transistor_13_out), .out(transistor_6_out), .gate(transistor_1_out));
  Transistor #(.\type ("n")) transistor_13 (.in(1'b0), .out(transistor_13_out), .gate(b));
  Transistor transistor_14 (.in(1'b1), .out(out), .gate(transistor_6_out));
  Transistor #(.\type ("n")) transistor_15 (.in(transistor_16_out), .out(out), .gate(transistor_5_out));
  Transistor #(.\type ("n")) transistor_16 (.in(1'b0), .out(transistor_16_out), .gate(transistor_6_out));
endmodule

module NOT1x1x1 (
  input  in,
  output out
);

  Transistor transistor_1 (.in(1'b1), .out(out), .gate(in));
  Transistor #(.\type ("n")) transistor_2 (.in(1'b0), .out(out), .gate(in));
endmodule

module EN1x1x1 (
  input  in,
  input  en,
  output out
);

  wire transistor_1_out;

  Transistor #(.gate("br")) transistor_1 (.in(1'b1), .out(transistor_1_out), .gate(en));
  Transistor #(.\type ("n")) transistor_2 (.in(in), .out(out), .gate(en));
  Transistor #(.gate("br")) transistor_3 (.in(in), .out(out), .gate(transistor_1_out));
  Transistor #(.\type ("n"), .gate("br")) transistor_4 (.in(1'b0), .out(transistor_1_out), .gate(en));
endmodule

module MUX2x1x1 (
  input  in_1,
  input  a,
  input  sel,
  input  b,
  input  in_5,
  input  in_6,
  output out,
  output out_8
);

  wire transistor_1_out, transistor_7_out, transistor_10_out, transistor_11_out, transistor_13_out,
       transistor_16_out, transistor_17_out, transistor_19_out, transistor_21_out, transistor_22_out;

  Transistor transistor_1 (.in(1'b1), .out(transistor_1_out), .gate(sel));
  Transistor #(.\type ("n")) transistor_2 (.in(1'b0), .out(transistor_1_out), .gate(sel));
  Transistor transistor_3 (.in(a), .out(out), .gate(sel));
  Transistor #(.\type ("n"), .gate("br")) transistor_4 (.in(a), .out(out), .gate(transistor_1_out));
  Transistor transistor_5 (.in(b), .out(out), .gate(transistor_1_out));
  Transistor #(.\type ("n"), .gate("br")) transistor_6 (.in(b), .out(out), .gate(sel));
  Transistor transistor_7 (.in(1'b1), .out(transistor_7_out), .gate(in_1));
  Transistor transistor_8 (.in(1'b1), .out(transistor_7_out), .gate(transistor_11_out));
  Transistor #(.\type ("n")) transistor_9 (.in(transistor_10_out), .out(transistor_7_out), .gate(in_1));
  Transistor #(.\type ("n")) transistor_10 (.in(1'b0), .out(transistor_10_out), .gate(transistor_11_out));
  Transistor transistor_11 (.in(1'b1), .out(transistor_11_out), .gate(in_5));
  Transistor #(.\type ("n")) transistor_12 (.in(1'b0), .out(transistor_11_out), .gate(in_5));
  Transistor transistor_13 (.in(1'b1), .out(transistor_13_out), .gate(in_5));
  Transistor transistor_14 (.in(1'b1), .out(transistor_13_out), .gate(in_6));
  Transistor #(.\type ("n")) transistor_15 (.in(transistor_16_out), .out(transistor_13_out), .gate(in_5));
  Transistor #(.\type ("n")) transistor_16 (.in(1'b0), .out(transistor_16_out), .gate(in_6));
  Transistor transistor_17 (.in(1'b1), .out(transistor_17_out), .gate(transistor_7_out));
  Transistor #(.\type ("n")) transistor_18 (.in(1'b0), .out(transistor_17_out), .gate(transistor_7_out));
  Transistor transistor_19 (.in(1'b1), .out(transistor_19_out), .gate(transistor_13_out));
  Transistor #(.\type ("n")) transistor_20 (.in(1'b0), .out(transistor_19_out), .gate(transistor_13_out));
  Transistor transistor_21 (.in(1'b1), .out(transistor_21_out), .gate(transistor_17_out));
  Transistor transistor_22 (.in(transistor_21_out), .out(transistor_22_out), .gate(transistor_19_out));
  Transistor #(.\type ("n")) transistor_23 (.in(1'b0), .out(transistor_22_out), .gate(transistor_17_out));
  Transistor #(.\type ("n")) transistor_24 (.in(1'b0), .out(transistor_22_out), .gate(transistor_19_out));
  Transistor transistor_25 (.in(1'b1), .out(out_8), .gate(transistor_22_out));
  Transistor #(.\type ("n")) transistor_26 (.in(1'b0), .out(out_8), .gate(transistor_22_out));
endmodule

module MUX4x1x1 (
  input  a,
  input  b,
  input  c,
  input  d,
  input  sel0,
  input  sel1,
  output out
);

  wire transistor_1_out, transistor_3_out, transistor_5_out, transistor_9_out, transistor_15_out;

  Transistor transistor_1 (.in(1'b1), .out(transistor_1_out), .gate(sel0));
  Transistor #(.\type ("n")) transistor_2 (.in(1'b0), .out(transistor_1_out), .gate(sel0));
  Transistor transistor_3 (.in(1'b1), .out(transistor_3_out), .gate(sel0));
  Transistor #(.\type ("n")) transistor_4 (.in(1'b0), .out(transistor_3_out), .gate(sel0));
  Transistor transistor_5 (.in(a), .out(transistor_5_out), .gate(sel0));
  Transistor #(.\type ("n"), .gate("br")) transistor_6 (.in(a), .out(transistor_5_out), .gate(transistor_1_out));
  Transistor transistor_7 (.in(b), .out(transistor_5_out), .gate(transistor_1_out));
  Transistor #(.\type ("n"), .gate("br")) transistor_8 (.in(b), .out(transistor_5_out), .gate(sel0));
  Transistor transistor_9 (.in(c), .out(transistor_9_out), .gate(sel0));
  Transistor #(.\type ("n"), .gate("br")) transistor_10 (.in(c), .out(transistor_9_out), .gate(transistor_3_out));
  Transistor transistor_11 (.in(d), .out(transistor_9_out), .gate(transistor_3_out));
  Transistor #(.\type ("n"), .gate("br")) transistor_12 (.in(d), .out(transistor_9_out), .gate(sel0));
  Transistor transistor_13 (.in(transistor_5_out), .out(out), .gate(sel1));
  Transistor #(.\type ("n"), .gate("br")) transistor_14 (.in(transistor_5_out), .out(out), .gate(transistor_15_out));
  Transistor transistor_15 (.in(1'b1), .out(transistor_15_out), .gate(sel1));
  Transistor #(.\type ("n")) transistor_16 (.in(1'b0), .out(transistor_15_out), .gate(sel1));
  Transistor transistor_17 (.in(transistor_9_out), .out(out), .gate(transistor_15_out));
  Transistor #(.\type ("n"), .gate("br")) transistor_18 (.in(transistor_9_out), .out(out), .gate(sel1));
endmodule

module MUX8x1x1 (
  input  a,
  input  b,
  input  c,
  input  d,
  input  e,
  input  f,
  input  g,
  input  h,
  input  sel0,
  input  sel1,
  input  sel2,
  output out
);

  wire transistor_1_out, transistor_3_out, transistor_5_out, transistor_7_out, transistor_9_out,
       transistor_13_out, transistor_17_out, transistor_21_out, transistor_25_out, transistor_27_out,
       transistor_31_out, transistor_33_out, transistor_37_out;

  Transistor transistor_1 (.in(1'b1), .out(transistor_1_out), .gate(sel0));
  Transistor #(.\type ("n")) transistor_2 (.in(1'b0), .out(transistor_1_out), .gate(sel0));
  Transistor transistor_3 (.in(1'b1), .out(transistor_3_out), .gate(sel0));
  Transistor #(.\type ("n")) transistor_4 (.in(1'b0), .out(transistor_3_out), .gate(sel0));
  Transistor transistor_5 (.in(1'b1), .out(transistor_5_out), .gate(sel0));
  Transistor #(.\type ("n")) transistor_6 (.in(1'b0), .out(transistor_5_out), .gate(sel0));
  Transistor transistor_7 (.in(1'b1), .out(transistor_7_out), .gate(sel0));
  Transistor #(.\type ("n")) transistor_8 (.in(1'b0), .out(transistor_7_out), .gate(sel0));
  Transistor transistor_9 (.in(a), .out(transistor_9_out), .gate(sel0));
  Transistor #(.\type ("n"), .gate("br")) transistor_10 (.in(a), .out(transistor_9_out), .gate(transistor_1_out));
  Transistor transistor_11 (.in(b), .out(transistor_9_out), .gate(transistor_1_out));
  Transistor #(.\type ("n"), .gate("br")) transistor_12 (.in(b), .out(transistor_9_out), .gate(sel0));
  Transistor transistor_13 (.in(c), .out(transistor_13_out), .gate(sel0));
  Transistor #(.\type ("n"), .gate("br")) transistor_14 (.in(c), .out(transistor_13_out), .gate(transistor_3_out));
  Transistor transistor_15 (.in(d), .out(transistor_13_out), .gate(transistor_3_out));
  Transistor #(.\type ("n"), .gate("br")) transistor_16 (.in(d), .out(transistor_13_out), .gate(sel0));
  Transistor transistor_17 (.in(e), .out(transistor_17_out), .gate(sel0));
  Transistor #(.\type ("n"), .gate("br")) transistor_18 (.in(e), .out(transistor_17_out), .gate(transistor_5_out));
  Transistor transistor_19 (.in(f), .out(transistor_17_out), .gate(transistor_5_out));
  Transistor #(.\type ("n"), .gate("br")) transistor_20 (.in(f), .out(transistor_17_out), .gate(sel0));
  Transistor transistor_21 (.in(g), .out(transistor_21_out), .gate(sel0));
  Transistor #(.\type ("n"), .gate("br")) transistor_22 (.in(g), .out(transistor_21_out), .gate(transistor_7_out));
  Transistor transistor_23 (.in(h), .out(transistor_21_out), .gate(transistor_7_out));
  Transistor #(.\type ("n"), .gate("br")) transistor_24 (.in(h), .out(transistor_21_out), .gate(sel0));
  Transistor transistor_25 (.in(transistor_9_out), .out(transistor_25_out), .gate(sel1));
  Transistor #(.\type ("n"), .gate("br")) transistor_26 (
    .in(transistor_9_out), .out(transistor_25_out), .gate(transistor_27_out));
  Transistor transistor_27 (.in(1'b1), .out(transistor_27_out), .gate(sel1));
  Transistor #(.\type ("n")) transistor_28 (.in(1'b0), .out(transistor_27_out), .gate(sel1));
  Transistor transistor_29 (.in(transistor_13_out), .out(transistor_25_out), .gate(transistor_27_out));
  Transistor #(.\type ("n"), .gate("br")) transistor_30 (.in(transistor_13_out), .out(transistor_25_out), .gate(sel1));
  Transistor transistor_31 (.in(transistor_17_out), .out(transistor_31_out), .gate(sel1));
  Transistor #(.\type ("n"), .gate("br")) transistor_32 (
    .in(transistor_17_out), .out(transistor_31_out), .gate(transistor_33_out));
  Transistor transistor_33 (.in(1'b1), .out(transistor_33_out), .gate(sel1));
  Transistor #(.\type ("n")) transistor_34 (.in(1'b0), .out(transistor_33_out), .gate(sel1));
  Transistor transistor_35 (.in(transistor_21_out), .out(transistor_31_out), .gate(transistor_33_out));
  Transistor #(.\type ("n"), .gate("br")) transistor_36 (.in(transistor_21_out), .out(transistor_31_out), .gate(sel1));
  Transistor transistor_37 (.in(1'b1), .out(transistor_37_out), .gate(sel2));
  Transistor #(.\type ("n")) transistor_38 (.in(1'b0), .out(transistor_37_out), .gate(sel2));
  Transistor transistor_39 (.in(transistor_25_out), .out(out), .gate(sel2));
  Transistor #(.\type ("n"), .gate("br")) transistor_40 (.in(transistor_25_out), .out(out), .gate(transistor_37_out));
  Transistor transistor_41 (.in(transistor_31_out), .out(out), .gate(transistor_37_out));
  Transistor #(.\type ("n"), .gate("br")) transistor_42 (.in(transistor_31_out), .out(out), .gate(sel2));
endmodule

module DEC1x2x4 (
  input  in1,
  input  in0,
  output _00,
  output _01,
  output _10,
  output _11
);

  wire transistor_1_out, transistor_3_out, transistor_5_out, transistor_7_out, transistor_9_out,
       transistor_12_out, transistor_13_out, transistor_16_out, transistor_17_out, transistor_20_out,
       transistor_21_out, transistor_24_out;

  Transistor #(.\type ("n")) transistor_1 (.in(1'b0), .out(transistor_1_out), .gate(in0));
  Transistor transistor_2 (.in(1'b1), .out(transistor_1_out), .gate(in0));
  Transistor #(.\type ("n")) transistor_3 (.in(1'b0), .out(transistor_3_out), .gate(in1));
  Transistor transistor_4 (.in(1'b1), .out(transistor_3_out), .gate(in1));
  Transistor transistor_5 (.in(1'b1), .out(transistor_5_out), .gate(in1));
  Transistor #(.\type ("n")) transistor_6 (.in(1'b0), .out(transistor_5_out), .gate(in1));
  Transistor #(.\type ("n")) transistor_7 (.in(1'b0), .out(transistor_7_out), .gate(in0));
  Transistor transistor_8 (.in(1'b1), .out(transistor_7_out), .gate(in0));
  Transistor transistor_9 (.in(1'b1), .out(transistor_9_out), .gate(transistor_3_out));
  Transistor transistor_10 (.in(1'b1), .out(transistor_9_out), .gate(transistor_1_out));
  Transistor #(.\type ("n")) transistor_11 (.in(transistor_12_out), .out(transistor_9_out), .gate(transistor_1_out));
  Transistor #(.\type ("n")) transistor_12 (.in(1'b0), .out(transistor_12_out), .gate(transistor_3_out));
  Transistor transistor_13 (.in(1'b1), .out(transistor_13_out), .gate(transistor_5_out));
  Transistor transistor_14 (.in(1'b1), .out(transistor_13_out), .gate(in0));
  Transistor #(.\type ("n")) transistor_15 (.in(transistor_16_out), .out(transistor_13_out), .gate(in0));
  Transistor #(.\type ("n")) transistor_16 (.in(1'b0), .out(transistor_16_out), .gate(transistor_5_out));
  Transistor transistor_17 (.in(1'b1), .out(transistor_17_out), .gate(in1));
  Transistor transistor_18 (.in(1'b1), .out(transistor_17_out), .gate(transistor_7_out));
  Transistor #(.\type ("n")) transistor_19 (.in(transistor_20_out), .out(transistor_17_out), .gate(transistor_7_out));
  Transistor #(.\type ("n")) transistor_20 (.in(1'b0), .out(transistor_20_out), .gate(in1));
  Transistor transistor_21 (.in(1'b1), .out(transistor_21_out), .gate(in0));
  Transistor transistor_22 (.in(1'b1), .out(transistor_21_out), .gate(in1));
  Transistor #(.\type ("n")) transistor_23 (.in(transistor_24_out), .out(transistor_21_out), .gate(in0));
  Transistor #(.\type ("n")) transistor_24 (.in(1'b0), .out(transistor_24_out), .gate(in1));
  Transistor transistor_25 (.in(1'b1), .out(_00), .gate(transistor_9_out));
  Transistor #(.\type ("n")) transistor_26 (.in(1'b0), .out(_00), .gate(transistor_9_out));
  Transistor transistor_27 (.in(1'b1), .out(_01), .gate(transistor_13_out));
  Transistor #(.\type ("n")) transistor_28 (.in(1'b0), .out(_01), .gate(transistor_13_out));
  Transistor transistor_29 (.in(1'b1), .out(_10), .gate(transistor_17_out));
  Transistor #(.\type ("n")) transistor_30 (.in(1'b0), .out(_10), .gate(transistor_17_out));
  Transistor transistor_31 (.in(1'b1), .out(_11), .gate(transistor_21_out));
  Transistor #(.\type ("n")) transistor_32 (.in(1'b0), .out(_11), .gate(transistor_21_out));
endmodule

module DEC1x3x8 (
  input  in2,
  input  in1,
  input  in0,
  output _000,
  output _001,
  output _010,
  output _011,
  output _100,
  output _101,
  output _110,
  output _111
);

  wire transistor_1_out, transistor_2_out, transistor_3_out, transistor_4_out, transistor_5_out,
       transistor_6_out, transistor_7_out, transistor_8_out, transistor_9_out, transistor_10_out,
       transistor_11_out, transistor_12_out, transistor_25_out, transistor_27_out, transistor_29_out,
       transistor_31_out, transistor_33_out, transistor_35_out, transistor_37_out, transistor_39_out,
       transistor_43_out, transistor_44_out, transistor_47_out, transistor_48_out, transistor_51_out,
       transistor_52_out, transistor_55_out, transistor_56_out, transistor_59_out, transistor_60_out,
       transistor_63_out, transistor_64_out, transistor_67_out, transistor_68_out, transistor_71_out,
       transistor_72_out;

  Transistor transistor_1 (.in(1'b1), .out(transistor_1_out), .gate(in0));
  Transistor transistor_2 (.in(1'b1), .out(transistor_2_out), .gate(in1));
  Transistor transistor_3 (.in(1'b1), .out(transistor_3_out), .gate(in2));
  Transistor transistor_4 (.in(1'b1), .out(transistor_4_out), .gate(in1));
  Transistor transistor_5 (.in(1'b1), .out(transistor_5_out), .gate(in2));
  Transistor transistor_6 (.in(1'b1), .out(transistor_6_out), .gate(in0));
  Transistor transistor_7 (.in(1'b1), .out(transistor_7_out), .gate(in2));
  Transistor transistor_8 (.in(1'b1), .out(transistor_8_out), .gate(in2));
  Transistor transistor_9 (.in(1'b1), .out(transistor_9_out), .gate(in0));
  Transistor transistor_10 (.in(1'b1), .out(transistor_10_out), .gate(in1));
  Transistor transistor_11 (.in(1'b1), .out(transistor_11_out), .gate(in1));
  Transistor transistor_12 (.in(1'b1), .out(transistor_12_out), .gate(in0));
  Transistor #(.\type ("n")) transistor_13 (.in(1'b0), .out(transistor_1_out), .gate(in0));
  Transistor #(.\type ("n")) transistor_14 (.in(1'b0), .out(transistor_2_out), .gate(in1));
  Transistor #(.\type ("n")) transistor_15 (.in(1'b0), .out(transistor_3_out), .gate(in2));
  Transistor #(.\type ("n")) transistor_16 (.in(1'b0), .out(transistor_4_out), .gate(in1));
  Transistor #(.\type ("n")) transistor_17 (.in(1'b0), .out(transistor_5_out), .gate(in2));
  Transistor #(.\type ("n")) transistor_18 (.in(1'b0), .out(transistor_6_out), .gate(in0));
  Transistor #(.\type ("n")) transistor_19 (.in(1'b0), .out(transistor_7_out), .gate(in2));
  Transistor #(.\type ("n")) transistor_20 (.in(1'b0), .out(transistor_8_out), .gate(in2));
  Transistor #(.\type ("n")) transistor_21 (.in(1'b0), .out(transistor_9_out), .gate(in0));
  Transistor #(.\type ("n")) transistor_22 (.in(1'b0), .out(transistor_10_out), .gate(in1));
  Transistor #(.\type ("n")) transistor_23 (.in(1'b0), .out(transistor_11_out), .gate(in1));
  Transistor #(.\type ("n")) transistor_24 (.in(1'b0), .out(transistor_12_out), .gate(in0));
  Transistor transistor_25 (.in(1'b1), .out(transistor_25_out), .gate(transistor_1_out));
  Transistor transistor_26 (.in(1'b1), .out(transistor_25_out), .gate(transistor_2_out));
  Transistor transistor_27 (.in(1'b1), .out(transistor_27_out), .gate(transistor_4_out));
  Transistor transistor_28 (.in(1'b1), .out(transistor_27_out), .gate(in0));
  Transistor transistor_29 (.in(1'b1), .out(transistor_29_out), .gate(transistor_6_out));
  Transistor transistor_30 (.in(1'b1), .out(transistor_29_out), .gate(in1));
  Transistor transistor_31 (.in(1'b1), .out(transistor_31_out), .gate(in0));
  Transistor transistor_32 (.in(1'b1), .out(transistor_31_out), .gate(in1));
  Transistor transistor_33 (.in(1'b1), .out(transistor_33_out), .gate(transistor_9_out));
  Transistor transistor_34 (.in(1'b1), .out(transistor_33_out), .gate(transistor_10_out));
  Transistor transistor_35 (.in(1'b1), .out(transistor_35_out), .gate(transistor_11_out));
  Transistor transistor_36 (.in(1'b1), .out(transistor_35_out), .gate(in0));
  Transistor transistor_37 (.in(1'b1), .out(transistor_37_out), .gate(transistor_12_out));
  Transistor transistor_38 (.in(1'b1), .out(transistor_37_out), .gate(in1));
  Transistor transistor_39 (.in(1'b1), .out(transistor_39_out), .gate(in1));
  Transistor transistor_40 (.in(1'b1), .out(transistor_39_out), .gate(in0));
  Transistor transistor_41 (.in(1'b1), .out(transistor_25_out), .gate(transistor_3_out));
  Transistor #(.\type ("n")) transistor_42 (.in(transistor_43_out), .out(transistor_25_out), .gate(transistor_1_out));
  Transistor #(.\type ("n")) transistor_43 (.in(transistor_44_out), .out(transistor_43_out), .gate(transistor_2_out));
  Transistor #(.\type ("n")) transistor_44 (.in(1'b0), .out(transistor_44_out), .gate(transistor_3_out));
  Transistor transistor_45 (.in(1'b1), .out(transistor_27_out), .gate(transistor_5_out));
  Transistor #(.\type ("n")) transistor_46 (.in(transistor_47_out), .out(transistor_27_out), .gate(in0));
  Transistor #(.\type ("n")) transistor_47 (.in(transistor_48_out), .out(transistor_47_out), .gate(transistor_4_out));
  Transistor #(.\type ("n")) transistor_48 (.in(1'b0), .out(transistor_48_out), .gate(transistor_5_out));
  Transistor transistor_49 (.in(1'b1), .out(transistor_29_out), .gate(transistor_7_out));
  Transistor #(.\type ("n")) transistor_50 (.in(transistor_51_out), .out(transistor_29_out), .gate(transistor_6_out));
  Transistor #(.\type ("n")) transistor_51 (.in(transistor_52_out), .out(transistor_51_out), .gate(in1));
  Transistor #(.\type ("n")) transistor_52 (.in(1'b0), .out(transistor_52_out), .gate(transistor_7_out));
  Transistor transistor_53 (.in(1'b1), .out(transistor_31_out), .gate(transistor_8_out));
  Transistor #(.\type ("n")) transistor_54 (.in(transistor_55_out), .out(transistor_31_out), .gate(in0));
  Transistor #(.\type ("n")) transistor_55 (.in(transistor_56_out), .out(transistor_55_out), .gate(in1));
  Transistor #(.\type ("n")) transistor_56 (.in(1'b0), .out(transistor_56_out), .gate(transistor_8_out));
  Transistor transistor_57 (.in(1'b1), .out(transistor_33_out), .gate(in2));
  Transistor #(.\type ("n")) transistor_58 (.in(transistor_59_out), .out(transistor_33_out), .gate(transistor_9_out));
  Transistor #(.\type ("n")) transistor_59 (.in(transistor_60_out), .out(transistor_59_out), .gate(transistor_10_out));
  Transistor #(.\type ("n")) transistor_60 (.in(1'b0), .out(transistor_60_out), .gate(in2));
  Transistor transistor_61 (.in(1'b1), .out(transistor_35_out), .gate(in2));
  Transistor #(.\type ("n")) transistor_62 (.in(transistor_63_out), .out(transistor_35_out), .gate(in0));
  Transistor #(.\type ("n")) transistor_63 (.in(transistor_64_out), .out(transistor_63_out), .gate(transistor_11_out));
  Transistor #(.\type ("n")) transistor_64 (.in(1'b0), .out(transistor_64_out), .gate(in2));
  Transistor transistor_65 (.in(1'b1), .out(transistor_37_out), .gate(in2));
  Transistor #(.\type ("n")) transistor_66 (.in(transistor_67_out), .out(transistor_37_out), .gate(transistor_12_out));
  Transistor #(.\type ("n")) transistor_67 (.in(transistor_68_out), .out(transistor_67_out), .gate(in1));
  Transistor #(.\type ("n")) transistor_68 (.in(1'b0), .out(transistor_68_out), .gate(in2));
  Transistor transistor_69 (.in(1'b1), .out(transistor_39_out), .gate(in2));
  Transistor #(.\type ("n")) transistor_70 (.in(transistor_71_out), .out(transistor_39_out), .gate(in0));
  Transistor #(.\type ("n")) transistor_71 (.in(transistor_72_out), .out(transistor_71_out), .gate(in1));
  Transistor #(.\type ("n")) transistor_72 (.in(1'b0), .out(transistor_72_out), .gate(in2));
  Transistor transistor_73 (.in(1'b1), .out(_000), .gate(transistor_25_out));
  Transistor #(.\type ("n")) transistor_74 (.in(1'b0), .out(_000), .gate(transistor_25_out));
  Transistor transistor_75 (.in(1'b1), .out(_001), .gate(transistor_27_out));
  Transistor #(.\type ("n")) transistor_76 (.in(1'b0), .out(_001), .gate(transistor_27_out));
  Transistor transistor_77 (.in(1'b1), .out(_010), .gate(transistor_29_out));
  Transistor #(.\type ("n")) transistor_78 (.in(1'b0), .out(_010), .gate(transistor_29_out));
  Transistor transistor_79 (.in(1'b1), .out(_011), .gate(transistor_31_out));
  Transistor #(.\type ("n")) transistor_80 (.in(1'b0), .out(_011), .gate(transistor_31_out));
  Transistor transistor_81 (.in(1'b1), .out(_100), .gate(transistor_33_out));
  Transistor #(.\type ("n")) transistor_82 (.in(1'b0), .out(_100), .gate(transistor_33_out));
  Transistor transistor_83 (.in(1'b1), .out(_101), .gate(transistor_35_out));
  Transistor #(.\type ("n")) transistor_84 (.in(1'b0), .out(_101), .gate(transistor_35_out));
  Transistor transistor_85 (.in(1'b1), .out(_110), .gate(transistor_37_out));
  Transistor #(.\type ("n")) transistor_86 (.in(1'b0), .out(_110), .gate(transistor_37_out));
  Transistor transistor_87 (.in(1'b1), .out(_111), .gate(transistor_39_out));
  Transistor #(.\type ("n")) transistor_88 (.in(1'b0), .out(_111), .gate(transistor_39_out));
endmodule

module DLATCH (
  input  w,
  input  rst,
  input  r,
  input  in,
  output out
);

  wire transistor_1_out, transistor_3_out, transistor_7_out, transistor_9_out, transistor_13_out;

  Transistor transistor_1 (.in(1'b1), .out(transistor_1_out), .gate(w));
  Transistor #(.\type ("n")) transistor_2 (.in(1'b0), .out(transistor_1_out), .gate(w));
  Transistor #(.\type ("n")) transistor_3 (.in(in), .out(transistor_3_out), .gate(w));
  Transistor #(.gate("br")) transistor_4 (.in(in), .out(transistor_3_out), .gate(transistor_1_out));
  Transistor #(.\type ("n")) transistor_5 (.in(transistor_7_out), .out(transistor_3_out), .gate(transistor_1_out));
  Transistor #(.gate("br")) transistor_6 (.in(transistor_7_out), .out(transistor_3_out), .gate(w));
  Transistor #(.\type ("n")) transistor_7 (.in(1'b0), .out(transistor_7_out), .gate(rst));
  Transistor #(.gate("br")) transistor_8 (.in(1'b0), .out(transistor_7_out), .gate(transistor_9_out));
  Transistor transistor_9 (.in(1'b1), .out(transistor_9_out), .gate(rst));
  Transistor #(.\type ("n")) transistor_10 (.in(1'b0), .out(transistor_9_out), .gate(rst));
  Transistor #(.\type ("n")) transistor_11 (.in(transistor_3_out), .out(transistor_7_out), .gate(transistor_9_out));
  Transistor #(.gate("br")) transistor_12 (.in(transistor_3_out), .out(transistor_7_out), .gate(rst));
  Transistor transistor_13 (.in(1'b1), .out(transistor_13_out), .gate(r));
  Transistor #(.\type ("n")) transistor_14 (.in(1'b0), .out(transistor_13_out), .gate(r));
  Transistor transistor_15 (.in(transistor_7_out), .out(out), .gate(transistor_13_out));
  Transistor #(.\type ("n"), .gate("br")) transistor_16 (.in(transistor_7_out), .out(out), .gate(r));
endmodule

module FLIPFLOP (
  input  rst,
  input  w,
  input  r,
  input  in,
  output out
);

  wire transistor_1_out, transistor_3_out, transistor_5_out, transistor_9_out, transistor_11_out,
       transistor_15_out, transistor_19_out, transistor_23_out, transistor_25_out, transistor_29_out;

  Transistor transistor_1 (.in(1'b1), .out(transistor_1_out), .gate(transistor_3_out));
  Transistor #(.\type ("n")) transistor_2 (.in(1'b0), .out(transistor_1_out), .gate(transistor_3_out));
  Transistor transistor_3 (.in(1'b1), .out(transistor_3_out), .gate(w));
  Transistor #(.\type ("n")) transistor_4 (.in(1'b0), .out(transistor_3_out), .gate(w));
  Transistor #(.\type ("n")) transistor_5 (.in(in), .out(transistor_5_out), .gate(transistor_3_out));
  Transistor #(.gate("br")) transistor_6 (.in(in), .out(transistor_5_out), .gate(transistor_1_out));
  Transistor #(.\type ("n")) transistor_7 (.in(transistor_11_out), .out(transistor_5_out), .gate(transistor_1_out));
  Transistor #(.gate("br")) transistor_8 (.in(transistor_11_out), .out(transistor_5_out), .gate(transistor_3_out));
  Transistor transistor_9 (.in(1'b1), .out(transistor_9_out), .gate(rst));
  Transistor #(.\type ("n")) transistor_10 (.in(1'b0), .out(transistor_9_out), .gate(rst));
  Transistor #(.\type ("n")) transistor_11 (.in(1'b0), .out(transistor_11_out), .gate(rst));
  Transistor #(.gate("br")) transistor_12 (.in(1'b0), .out(transistor_11_out), .gate(transistor_9_out));
  Transistor #(.\type ("n")) transistor_13 (.in(transistor_5_out), .out(transistor_11_out), .gate(transistor_9_out));
  Transistor #(.gate("br")) transistor_14 (.in(transistor_5_out), .out(transistor_11_out), .gate(rst));
  Transistor transistor_15 (.in(1'b1), .out(transistor_15_out), .gate(rst));
  Transistor #(.\type ("n")) transistor_16 (.in(1'b0), .out(transistor_15_out), .gate(rst));
  Transistor transistor_17 (.in(1'b1), .out(rst), .gate(transistor_3_out));
  Transistor #(.\type ("n")) transistor_18 (.in(1'b0), .out(rst), .gate(transistor_3_out));
  Transistor #(.\type ("n")) transistor_19 (.in(transistor_11_out), .out(transistor_19_out), .gate(rst));
  Transistor #(.gate("br")) transistor_20 (.in(transistor_11_out), .out(transistor_19_out), .gate(transistor_15_out));
  Transistor #(.\type ("n")) transistor_21 (.in(transistor_25_out), .out(transistor_19_out), .gate(transistor_15_out));
  Transistor #(.gate("br")) transistor_22 (.in(transistor_25_out), .out(transistor_19_out), .gate(rst));
  Transistor transistor_23 (.in(1'b1), .out(transistor_23_out), .gate(rst));
  Transistor #(.\type ("n")) transistor_24 (.in(1'b0), .out(transistor_23_out), .gate(rst));
  Transistor #(.\type ("n")) transistor_25 (.in(1'b0), .out(transistor_25_out), .gate(rst));
  Transistor #(.gate("br")) transistor_26 (.in(1'b0), .out(transistor_25_out), .gate(transistor_23_out));
  Transistor #(.\type ("n")) transistor_27 (.in(transistor_19_out), .out(transistor_25_out), .gate(transistor_23_out));
  Transistor #(.gate("br")) transistor_28 (.in(transistor_19_out), .out(transistor_25_out), .gate(rst));
  Transistor transistor_29 (.in(1'b1), .out(transistor_29_out), .gate(r));
  Transistor #(.\type ("n")) transistor_30 (.in(1'b0), .out(transistor_29_out), .gate(r));
  Transistor transistor_31 (.in(transistor_25_out), .out(out), .gate(transistor_29_out));
  Transistor #(.\type ("n"), .gate("br")) transistor_32 (.in(transistor_25_out), .out(out), .gate(r));
endmodule

module DLatch (
  input  data,
  input  write,
  input  reset,
  output out
);

  wire nand_1_out, nand_2_out, nand_3_out, nand_4_out, nand_6_out;

  nand nand_1 (nand_1_out, data, data);
  nand nand_2 (nand_2_out, data, write);
  nand nand_3 (nand_3_out, write, nand_1_out);
  nand nand_4 (nand_4_out, reset, reset);
  nand nand_5 (out, nand_2_out, nand_6_out);
  nand nand_6 (nand_6_out, out, nand_3_out, nand_4_out);
endmodule

module Reg4 (
  input  in0,
  input  in1,
  input  in2,
  input  in3,
  input  read,
  input  write,
  input  reset,
  output out0,
  output out1,
  output out2,
  output out3
);

  wire dlatch_1_out, dlatch_2_out, dlatch_3_out, dlatch_4_out;

  DLatch dlatch_1 (.data(in0), .write(write), .out(dlatch_1_out), .reset(reset));
  DLatch dlatch_2 (.data(in1), .write(write), .out(dlatch_2_out), .reset(reset));
  DLatch dlatch_3 (.data(in2), .write(write), .out(dlatch_3_out), .reset(reset));
  DLatch dlatch_4 (.data(in3), .write(write), .out(dlatch_4_out), .reset(reset));
  assign out0 = read ? dlatch_1_out : 1'bz;  // Controlled_Buffer controlled_buffer_1
  assign out1 = read ? dlatch_2_out : 1'bz;  // Controlled_Buffer controlled_buffer_2
  assign out2 = read ? dlatch_3_out : 1'bz;  // Controlled_Buffer controlled_buffer_3
  assign out3 = read ? dlatch_4_out : 1'bz;  // Controlled_Buffer controlled_buffer_4
endmodule

module Reg8 (
  input  read,
  input  write,
  input  reset,
  input  in0,
  input  in1,
  input  in2,
  input  in3,
  input  in4,
  input  in5,
  input  in6,
  input  in7,
  output out0,
  output out1,
  output out2,
  output out3,
  output out4,
  output out5,
  output out6,
  output out7
);

  Reg4 reg4_1 (
    .in0(in0), .in1(in1), .in2(in2), .in3(in3), .read(read), .write(write), .out0(out0), .out1(out1),
    .out2(out2), .out3(out3), .reset(reset));
  Reg4 reg4_2 (
    .in0(in4), .in1(in5), .in2(in6), .in3(in7), .read(read), .write(write), .out0(out4), .out1(out5),
    .out2(out6), .out3(out7), .reset(reset));
endmodule

module Ram256 (
  input  addr0,
  input  addr1,
  input  addr2,
  input  addr3,
  input  addr4,
  input  addr5,
  input  addr6,
  input  addr7,
  input  marw,
  input  read,
  input  write,
  input  clk,
  input  reset,
  input  in0,
  input  in1,
  input  in2,
  input  in3,
  input  in4,
  input  in5,
  input  in6,
  input  in7,
  output out0,
  output out1,
  output out2,
  output out3,
  output out4,
  output out5,
  output out6,
  output out7
);

  wire delayer_1_out, or_1_out;
  wire [7:0] MAR_out0;

  Reg8 MAR (
    .in0(addr0), .in1(addr1), .in2(addr2), .in3(addr3), .in4(addr4), .in5(addr5), .in6(addr6), .in7(addr7),
    .read(1'b1), .write(marw), .reset(reset), .out0(MAR_out0[0]), .out1(MAR_out0[1]), .out2(MAR_out0[2]),
    .out3(MAR_out0[3]), .out4(MAR_out0[4]), .out5(MAR_out0[5]), .out6(MAR_out0[6]), .out7(MAR_out0[7]));
  Delayer delayer_1 (.in(clk), .out(delayer_1_out));
  or or_1 (or_1_out, read, write);
  RAM #(.bus("separate")) ram_1 (
    .addr(MAR_out0), .din({in7, in6, in5, in4, in3, in2, in1, in0}),
    .data({out7, out6, out5, out4, out3, out2, out1, out0}), .str(write), .sel(or_1_out),
    .clk(delayer_1_out), .ld(read), .clr(reset));
endmodule

module LeftShifter8 (
  input  cin,
  input  in0,
  input  in1,
  input  in2,
  input  in3,
  input  in4,
  input  in5,
  input  in6,
  input  in7,
  output out0,
  output out1,
  output out2,
  output out3,
  output out4,
  output out6,
  output out6_2,
  output out7,
  output cout
);


  assign cout = in7;
  assign out0 = cin;
  assign out1 = in0;
  assign out2 = in1;
  assign out3 = in2;
  assign out4 = in3;
  assign out6 = in4;
  assign out6_2 = in5;
  assign out7 = in6;
endmodule

module RightShifter8 (
  input  in0,
  input  in1,
  input  in2,
  input  in3,
  input  in4,
  input  in5,
  input  in6,
  input  in7,
  input  cin,
  output cout,
  output out0,
  output out1,
  output out2,
  output out3,
  output out4,
  output out6,
  output out6_2,
  output out7
);


  assign cout = in0;
  assign out0 = in1;
  assign out1 = in2;
  assign out2 = in3;
  assign out3 = in4;
  assign out4 = in5;
  assign out6 = in6;
  assign out6_2 = in7;
  assign out7 = cin;
endmodule

module Ander8 (
  input  a0,
  input  b0,
  input  a1,
  input  b1,
  input  a2,
  input  b2,
  input  a3,
  input  b3,
  input  a4,
  input  b4,
  input  a5,
  input  b5,
  input  a6,
  input  b6,
  input  a7,
  input  b7,
  output out0,
  output out1,
  output out2,
  output out3,
  output out4,
  output out5,
  output out6,
  output out7
);

  and and_1 (out0, a0, b0);
  and and_2 (out1, a1, b1);
  and and_3 (out2, a2, b2);
  and and_4 (out3, a3, b3);
  and and_5 (out4, a4, b4);
  and and_6 (out5, a5, b5);
  and and_7 (out6, a6, b6);
  and and_8 (out7, a7, b7);
endmodule

module Orer8 (
  input  a0,
  input  b0,
  input  a1,
  input  b1,
  input  a2,
  input  b2,
  input  a3,
  input  b3,
  input  a4,
  input  b4,
  input  a5,
  input  b5,
  input  a6,
  input  b6,
  input  a7,
  input  b7,
  output out0,
  output out1,
  output out2,
  output out3,
  output out4,
  output out5,
  output out6,
  output out7
);

  or or_1 (out0, a0, b0);
  or or_2 (out1, a1, b1);
  or or_3 (out2, a2, b2);
  or or_4 (out3, a3, b3);
  or or_5 (out4, a4, b4);
  or or_6 (out5, a5, b5);
  or or_7 (out6, a6, b6);
  or or_8 (out7, a7, b7);
endmodule

module Xorer8 (
  input  a0,
  input  b0,
  input  a1,
  input  b1,
  input  a2,
  input  b2,
  input  a3,
  input  b3,
  input  a4,
  input  b4,
  input  a5,
  input  b5,
  input  a6,
  input  b6,
  input  a7,
  input  b7,
  output out0,
  output out1,
  output out2,
  output out3,
  output out4,
  output out5,
  output out6,
  output out7
);

  xor xor_1 (out0, a0, b0);
  xor xor_2 (out1, a1, b1);
  xor xor_3 (out2, a2, b2);
  xor xor_4 (out3, a3, b3);
  xor xor_5 (out4, a4, b4);
  xor xor_6 (out5, a5, b5);
  xor xor_7 (out6, a6, b6);
  xor xor_8 (out7, a7, b7);
endmodule

module FullAdder (
  input  a,
  input  b,
  input  cin,
  output sum,
  output cout
);

  wire and_1_out, and_2_out, xor_1_out;

  xor xor_1 (xor_1_out, a, b);
  xor xor_2 (sum, xor_1_out, cin);
  and and_1 (and_1_out, xor_1_out, cin);
  and and_2 (and_2_out, a, b);
  or or_1 (cout, and_1_out, and_2_out);
endmodule

module Adder8 (
  input  cin,
  input  a0,
  input  b0,
  input  a1,
  input  b1,
  input  a2,
  input  b2,
  input  a3,
  input  b3,
  input  a4,
  input  b4,
  input  a5,
  input  b5,
  input  a6,
  input  b6,
  input  a7,
  input  b7,
  output out0,
  output out1,
  output out2,
  output out3,
  output out4,
  output out5,
  output out6,
  output out7,
  output ovcarry,
  output cout
);

  wire fulladder_1_cout, fulladder_2_cout, fulladder_3_cout, fulladder_4_cout, fulladder_5_cout,
       fulladder_6_cout;

  FullAdder fulladder_1 (.a(a0), .b(b0), .cin(cin), .sum(out0), .cout(fulladder_1_cout));
  FullAdder fulladder_2 (.a(a1), .b(b1), .cin(fulladder_1_cout), .sum(out1), .cout(fulladder_2_cout));
  FullAdder fulladder_3 (.a(a2), .b(b2), .cin(fulladder_2_cout), .sum(out2), .cout(fulladder_3_cout));
  FullAdder fulladder_4 (.a(a3), .b(b3), .cin(fulladder_3_cout), .sum(out3), .cout(fulladder_4_cout));
  FullAdder fulladder_5 (.a(a4), .b(b4), .cin(fulladder_4_cout), .sum(out4), .cout(fulladder_5_cout));
  FullAdder fulladder_6 (.a(a5), .b(b5), .cin(fulladder_5_cout), .sum(out5), .cout(fulladder_6_cout));
  FullAdder fulladder_7 (.a(a6), .b(b6), .cin(fulladder_6_cout), .sum(out6), .cout(ovcarry));
  FullAdder fulladder_8 (.a(a7), .b(b7), .cin(ovcarry), .sum(out7), .cout(cout));
endmodule

module AddSub8 (
  input  sub,
  input  a0,
  input  b0,
  input  a1,
  input  b1,
  input  a2,
  input  b2,
  input  a3,
  input  b3,
  input  a4,
  input  b4,
  input  a5,
  input  b5,
  input  a6,
  input  b6,
  input  a7,
  input  b7,
  input  cin,
  output carry,
  output overflow,
  output out7,
  output out6,
  output out5,
  output out4,
  output out3,
  output out2,
  output out1,
  output out0
);

  wire adder8_1_cout, adder8_1_ovcarry, xor_3_out, xor_4_out, xor_5_out, xor_6_out, xor_7_out, xor_8_out,
       xor_9_out, xor_10_out, xor_11_out;

  xor xor_1 (carry, sub, adder8_1_cout);
  xor xor_2 (overflow, adder8_1_ovcarry, adder8_1_cout);
  xor xor_3 (xor_3_out, sub, b0);
  xor xor_4 (xor_4_out, sub, b1);
  xor xor_5 (xor_5_out, sub, b2);
  xor xor_6 (xor_6_out, sub, b3);
  xor xor_7 (xor_7_out, sub, b4);
  xor xor_8 (xor_8_out, sub, b5);
  xor xor_9 (xor_9_out, sub, b6);
  xor xor_10 (xor_10_out, sub, b7);
  Adder8 adder8_1 (
    .cin(xor_11_out), .a0(a0), .b0(xor_3_out), .a1(a1), .b1(xor_4_out), .a2(a2), .b2(xor_5_out), .a3(a3),
    .b3(xor_6_out), .a4(a4), .b4(xor_7_out), .a5(a5), .b5(xor_8_out), .a6(a6), .b6(xor_9_out), .a7(a7),
    .b7(xor_10_out), .out0(out0), .out1(out1), .out2(out2), .out3(out3), .out4(out4), .out5(out5),
    .out6(out6), .out7(out7), .ovcarry(adder8_1_ovcarry), .cout(adder8_1_cout));
  xor xor_11 (xor_11_out, sub, cin);
endmodule

module Bus0Gate (
  input  in7,
  input  in6,
  input  in5,
  input  in4,
  input  in3,
  input  in2,
  input  in1,
  input  in0,
  input  _0_bus,
  output out7,
  output out6,
  output out5,
  output out4,
  output out3,
  output out2,
  output out1,
  output out0
);

  and and_1 (out7, in7, _0_bus);
  and and_2 (out6, in6, _0_bus);
  and and_3 (out4, in4, _0_bus);
  and and_4 (out5, in5, _0_bus);
  and and_5 (out2, in2, _0_bus);
  and and_6 (out3, in3, _0_bus);
  and and_7 (out1, in1, _0_bus);
  and and_8 (out0, in0, _0_bus);
endmodule

module Enable8 (
  input  in0,
  input  in1,
  input  in2,
  input  in3,
  input  in4,
  input  in5,
  input  in6,
  input  in7,
  input  en,
  output out0,
  output out1,
  output out2,
  output out3,
  output out4,
  output out6,
  output out6_2,
  output out7
);

  wire transistor_1_out, transistor_2_out, transistor_3_out, transistor_4_out, transistor_5_out,
       transistor_6_out, transistor_7_out, transistor_8_out;

  Transistor #(.gate("br")) transistor_1 (.in(1'b1), .out(transistor_1_out), .gate(en));
  Transistor #(.gate("br")) transistor_2 (.in(1'b1), .out(transistor_2_out), .gate(en));
  Transistor #(.gate("br")) transistor_3 (.in(1'b1), .out(transistor_3_out), .gate(en));
  Transistor #(.gate("br")) transistor_4 (.in(1'b1), .out(transistor_4_out), .gate(en));
  Transistor #(.gate("br")) transistor_5 (.in(1'b1), .out(transistor_5_out), .gate(en));
  Transistor #(.gate("br")) transistor_6 (.in(1'b1), .out(transistor_6_out), .gate(en));
  Transistor #(.gate("br")) transistor_7 (.in(1'b1), .out(transistor_7_out), .gate(en));
  Transistor #(.gate("br")) transistor_8 (.in(1'b1), .out(transistor_8_out), .gate(en));
  Transistor #(.\type ("n")) transistor_9 (.in(in0), .out(out0), .gate(en));
  Transistor #(.gate("br")) transistor_10 (.in(in0), .out(out0), .gate(transistor_1_out));
  Transistor #(.\type ("n"), .gate("br")) transistor_11 (.in(1'b0), .out(transistor_1_out), .gate(en));
  Transistor #(.\type ("n")) transistor_12 (.in(in1), .out(out1), .gate(en));
  Transistor #(.gate("br")) transistor_13 (.in(in1), .out(out1), .gate(transistor_2_out));
  Transistor #(.\type ("n"), .gate("br")) transistor_14 (.in(1'b0), .out(transistor_2_out), .gate(en));
  Transistor #(.\type ("n")) transistor_15 (.in(in2), .out(out2), .gate(en));
  Transistor #(.gate("br")) transistor_16 (.in(in2), .out(out2), .gate(transistor_3_out));
  Transistor #(.\type ("n"), .gate("br")) transistor_17 (.in(1'b0), .out(transistor_3_out), .gate(en));
  Transistor #(.\type ("n")) transistor_18 (.in(in3), .out(out3), .gate(en));
  Transistor #(.gate("br")) transistor_19 (.in(in3), .out(out3), .gate(transistor_4_out));
  Transistor #(.\type ("n"), .gate("br")) transistor_20 (.in(1'b0), .out(transistor_4_out), .gate(en));
  Transistor #(.\type ("n")) transistor_21 (.in(in4), .out(out4), .gate(en));
  Transistor #(.gate("br")) transistor_22 (.in(in4), .out(out4), .gate(transistor_5_out));
  Transistor #(.\type ("n"), .gate("br")) transistor_23 (.in(1'b0), .out(transistor_5_out), .gate(en));
  Transistor #(.\type ("n")) transistor_24 (.in(in5), .out(out6), .gate(en));
  Transistor #(.gate("br")) transistor_25 (.in(in5), .out(out6), .gate(transistor_6_out));
  Transistor #(.\type ("n"), .gate("br")) transistor_26 (.in(1'b0), .out(transistor_6_out), .gate(en));
  Transistor #(.\type ("n")) transistor_27 (.in(in6), .out(out6_2), .gate(en));
  Transistor #(.gate("br")) transistor_28 (.in(in6), .out(out6_2), .gate(transistor_7_out));
  Transistor #(.\type ("n"), .gate("br")) transistor_29 (.in(1'b0), .out(transistor_7_out), .gate(en));
  Transistor #(.\type ("n")) transistor_30 (.in(in7), .out(out7), .gate(en));
  Transistor #(.gate("br")) transistor_31 (.in(in7), .out(out7), .gate(transistor_8_out));
  Transistor #(.\type ("n"), .gate("br")) transistor_32 (.in(1'b0), .out(transistor_8_out), .gate(en));
endmodule

module ALU (
  input  a7,
  input  a6,
  input  a5,
  input  a4,
  input  a3,
  input  a2,
  input  a1,
  input  a0,
  input  b7,
  input  b6,
  input  b5,
  input  b4,
  input  b3,
  input  b2,
  input  b1,
  input  b0,
  input  op2,
  input  op1,
  input  op0,
  input  cin,
  output out0,
  output out1,
  output out2,
  output out3,
  output out4,
  output out5,
  output out6,
  output out7,
  output overflow,
  output carry,
  output sign,
  output zero
);

  wire addsub8_1_carry, addsub8_1_out0, addsub8_1_out1, addsub8_1_out2, addsub8_1_out3, addsub8_1_out4,
       addsub8_1_out5, addsub8_1_out6, addsub8_1_out7, addsub8_1_overflow, ander8_1_out0, ander8_1_out1,
       ander8_1_out2, ander8_1_out3, ander8_1_out4, ander8_1_out5, ander8_1_out6, ander8_1_out7,
       leftshifter8_1_cout, leftshifter8_1_out0, leftshifter8_1_out1, leftshifter8_1_out2,
       leftshifter8_1_out3, leftshifter8_1_out4, leftshifter8_1_out6, leftshifter8_1_out6_2,
       leftshifter8_1_out7, nor_2_out, or_1_out, orer8_1_out0, orer8_1_out1, orer8_1_out2, orer8_1_out3,
       orer8_1_out4, orer8_1_out5, orer8_1_out6, orer8_1_out7, rightshifter8_1_cout, rightshifter8_1_out0,
       rightshifter8_1_out1, rightshifter8_1_out2, rightshifter8_1_out3, rightshifter8_1_out4,
       rightshifter8_1_out6, rightshifter8_1_out6_2, rightshifter8_1_out7, xorer8_1_out0, xorer8_1_out1,
       xorer8_1_out2, xorer8_1_out3, xorer8_1_out4, xorer8_1_out5, xorer8_1_out6, xorer8_1_out7;
  wire [7:0] decoder_1_out0;

  Ander8 ander8_1 (
    .a0(a0), .b0(b0), .a1(a1), .b1(b1), .a2(a2), .b2(b2), .a3(a3), .b3(b3), .a4(a4), .b4(b4), .a5(a5),
    .b5(b5), .a6(a6), .b6(b6), .a7(a7), .b7(b7), .out0(ander8_1_out0), .out1(ander8_1_out1),
    .out2(ander8_1_out2), .out3(ander8_1_out3), .out4(ander8_1_out4), .out5(ander8_1_out5),
    .out6(ander8_1_out6), .out7(ander8_1_out7));
  Orer8 orer8_1 (
    .a0(a0), .b0(b0), .a1(a1), .b1(b1), .a2(a2), .b2(b2), .a3(a3), .b3(b3), .a4(a4), .b4(b4), .a5(a5),
    .b5(b5), .a6(a6), .b6(b6), .a7(a7), .b7(b7), .out0(orer8_1_out0), .out1(orer8_1_out1),
    .out2(orer8_1_out2), .out3(orer8_1_out3), .out4(orer8_1_out4), .out5(orer8_1_out5), .out6(orer8_1_out6),
    .out7(orer8_1_out7));
  Xorer8 xorer8_1 (
    .a0(a0), .b0(b0), .a1(a1), .b1(b1), .a2(a2), .b2(b2), .a3(a3), .b3(b3), .a4(a4), .b4(b4), .a5(a5),
    .b5(b5), .a6(a6), .b6(b6), .a7(a7), .b7(b7), .out0(xorer8_1_out0), .out1(xorer8_1_out1),
    .out2(xorer8_1_out2), .out3(xorer8_1_out3), .out4(xorer8_1_out4), .out5(xorer8_1_out5),
    .out6(xorer8_1_out6), .out7(xorer8_1_out7));
  AddSub8 addsub8_1 (
    .cin(cin), .a0(a0), .b0(b0), .a1(a1), .b1(b1), .a2(a2), .b2(b2), .a3(a3), .b3(b3), .a4(a4), .b4(b4),
    .a5(a5), .b5(b5), .a6(a6), .b6(b6), .a7(a7), .b7(b7), .out0(addsub8_1_out0), .out1(addsub8_1_out1),
    .out2(addsub8_1_out2), .out3(addsub8_1_out3), .out4(addsub8_1_out4), .out5(addsub8_1_out5),
    .out6(addsub8_1_out6), .out7(addsub8_1_out7), .carry(addsub8_1_carry), .sub(decoder_1_out0[5]),
    .overflow(addsub8_1_overflow));
  LeftShifter8 leftshifter8_1 (
    .cin(cin), .in0(a0), .in1(a1), .in2(a2), .in3(a3), .in4(a4), .in5(a5), .in6(a6), .in7(a7),
    .out0(leftshifter8_1_out0), .out1(leftshifter8_1_out1), .out2(leftshifter8_1_out2),
    .out3(leftshifter8_1_out3), .out4(leftshifter8_1_out4), .out6(leftshifter8_1_out6),
    .out6_2(leftshifter8_1_out6_2), .out7(leftshifter8_1_out7), .cout(leftshifter8_1_cout));
  RightShifter8 rightshifter8_1 (
    .in0(a0), .in1(a1), .in2(a2), .in3(a3), .in4(a4), .in5(a5), .in6(a6), .in7(a7), .cin(cin),
    .cout(rightshifter8_1_cout), .out0(rightshifter8_1_out0), .out1(rightshifter8_1_out1),
    .out2(rightshifter8_1_out2), .out3(rightshifter8_1_out3), .out4(rightshifter8_1_out4),
    .out6(rightshifter8_1_out6), .out6_2(rightshifter8_1_out6_2), .out7(rightshifter8_1_out7));
  Decoder #(.select(3), .enable("false")) decoder_1 (
    .out0(decoder_1_out0[0]), .out1(decoder_1_out0[1]), .out2(decoder_1_out0[2]), .out3(decoder_1_out0[3]),
    .out4(decoder_1_out0[4]), .out5(decoder_1_out0[5]), .out6(decoder_1_out0[6]), .out7(decoder_1_out0[7]),
    .sel({op2, op1, op0}));
  Enable8 enable8_1 (
    .in0(a0), .in1(a1), .in2(a2), .in3(a3), .in4(a4), .in5(a5), .in6(a6), .in7(a7), .en(decoder_1_out0[0]),
    .out0(out0), .out1(out1), .out2(out2), .out3(out3), .out4(out4), .out6(out5), .out6_2(out6), .out7(out7));
  Enable8 enable8_2 (
    .in0(ander8_1_out0), .in1(ander8_1_out1), .in2(ander8_1_out2), .in3(ander8_1_out3), .in4(ander8_1_out4),
    .in5(ander8_1_out5), .in6(ander8_1_out6), .in7(ander8_1_out7), .en(decoder_1_out0[1]), .out0(out0),
    .out1(out1), .out2(out2), .out3(out3), .out4(out4), .out6(out5), .out6_2(out6), .out7(out7));
  Enable8 enable8_3 (
    .in0(orer8_1_out0), .in1(orer8_1_out1), .in2(orer8_1_out2), .in3(orer8_1_out3), .in4(orer8_1_out4),
    .in5(orer8_1_out5), .in6(orer8_1_out6), .in7(orer8_1_out7), .en(decoder_1_out0[2]), .out0(out0),
    .out1(out1), .out2(out2), .out3(out3), .out4(out4), .out6(out5), .out6_2(out6), .out7(out7));
  Enable8 enable8_4 (
    .in0(xorer8_1_out0), .in1(xorer8_1_out1), .in2(xorer8_1_out2), .in3(xorer8_1_out3), .in4(xorer8_1_out4),
    .in5(xorer8_1_out5), .in6(xorer8_1_out6), .in7(xorer8_1_out7), .en(decoder_1_out0[3]), .out0(out0),
    .out1(out1), .out2(out2), .out3(out3), .out4(out4), .out6(out5), .out6_2(out6), .out7(out7));
  or or_1 (or_1_out, decoder_1_out0[4], decoder_1_out0[5]);
  Enable8 enable8_5 (
    .in0(addsub8_1_out0), .in1(addsub8_1_out1), .in2(addsub8_1_out2), .in3(addsub8_1_out3),
    .in4(addsub8_1_out4), .in5(addsub8_1_out5), .in6(addsub8_1_out6), .in7(addsub8_1_out7), .en(or_1_out),
    .out0(out0), .out1(out1), .out2(out2), .out3(out3), .out4(out4), .out6(out5), .out6_2(out6), .out7(out7));
  Enable8 enable8_6 (
    .in0(leftshifter8_1_out0), .in1(leftshifter8_1_out1), .in2(leftshifter8_1_out2),
    .in3(leftshifter8_1_out3), .in4(leftshifter8_1_out4), .in5(leftshifter8_1_out6),
    .in6(leftshifter8_1_out6_2), .in7(leftshifter8_1_out7), .en(decoder_1_out0[6]), .out0(out0), .out1(out1),
    .out2(out2), .out3(out3), .out4(out4), .out6(out5), .out6_2(out6), .out7(out7));
  Enable8 enable8_7 (
    .in0(rightshifter8_1_out0), .in1(rightshifter8_1_out1), .in2(rightshifter8_1_out2),
    .in3(rightshifter8_1_out3), .in4(rightshifter8_1_out4), .in5(rightshifter8_1_out6),
    .in6(rightshifter8_1_out6_2), .in7(rightshifter8_1_out7), .en(decoder_1_out0[7]), .out0(out0),
    .out1(out1), .out2(out2), .out3(out3), .out4(out4), .out6(out5), .out6_2(out6), .out7(out7));
  nor nor_1 (zero, out7, out6, out5, out4, out3, out2, out1, out0);
  Multiplexer #(.enable("false")) multiplexer_1 (.in0(1'b0), .in1(addsub8_1_overflow), .out(overflow), .sel(or_1_out));
  nor nor_2 (nor_2_out, or_1_out, decoder_1_out0[6], decoder_1_out0[7]);
  assign carry = nor_2_out ? 1'b0 : 1'bz;  // Controlled_Buffer controlled_buffer_1
  assign carry = or_1_out ? addsub8_1_carry : 1'bz;  // Controlled_Buffer controlled_buffer_2
  assign carry = decoder_1_out0[6] ? leftshifter8_1_cout : 1'bz;  // Controlled_Buffer controlled_buffer_3
  assign carry = decoder_1_out0[7] ? rightshifter8_1_cout : 1'bz;  // Controlled_Buffer controlled_buffer_4

  assign sign = out7;
endmodule

module Clock (
  input  clk,
  input  rst,
  output clk_r,
  output clk_w
);

  wire j_k_ff_1_q, j_k_ff_1_qn, nand_1_out, nand_2_out, not_1_out;

  not not_1 (not_1_out, clk);
  nand nand_1 (nand_1_out, clk, j_k_ff_1_q);
  J_K_Flip_Flop j_k_ff_1 (
    .J(1'b1), .clk(not_1_out), .K(1'b1), .Q(j_k_ff_1_q), .Qn(j_k_ff_1_qn), .preset(rst), .en(1'b1),
    .reset(1'b0));
  nand nand_2 (nand_2_out, j_k_ff_1_qn, clk);
  buf buffer_1 (clk_r, nand_1_out);
  not not_2 (clk_w, nand_2_out);
endmodule

module Delayer (
  input  in,
  output out
);

  wire not_1_out, not_2_out, not_3_out, not_4_out, not_5_out, not_6_out, not_7_out;

  not not_1 (not_1_out, in);
  not not_2 (not_2_out, not_1_out);
  not not_3 (not_3_out, not_5_out);
  not not_4 (not_4_out, not_2_out);
  not not_5 (not_5_out, not_4_out);
  not not_6 (not_6_out, not_7_out);
  not not_7 (not_7_out, not_3_out);
  not not_8 (out, not_6_out);
endmodule

module BranchChecker (
  input  zero,
  input  sign,
  input  carry,
  input  overflow,
  input  op2,
  input  op1,
  input  op0,
  output result
);

  wire and_1_out, and_2_out, and_3_out, and_4_out, and_5_out, and_6_out, and_7_out, decoder_1_out0,
       decoder_1_out1, decoder_1_out2, decoder_1_out3, decoder_1_out4, decoder_1_out5, decoder_1_out6,
       decoder_1_out7, or_1_out, or_2_out, xor_1_out;

  Decoder #(.select(3), .enable("false")) decoder_1 (
    .out0(decoder_1_out0), .out1(decoder_1_out1), .out2(decoder_1_out2), .out3(decoder_1_out3),
    .out4(decoder_1_out4), .out5(decoder_1_out5), .out6(decoder_1_out6), .out7(decoder_1_out7),
    .sel({op2, op1, op0}));
  or or_1 (or_1_out, zero, xor_1_out);
  or or_2 (or_2_out, carry, zero);
  xor xor_1 (xor_1_out, overflow, sign);
  and and_1 (and_1_out, decoder_1_out1, zero);
  and and_2 (and_2_out, decoder_1_out2, sign);
  and and_3 (and_3_out, decoder_1_out3, overflow);
  and and_4 (and_4_out, decoder_1_out4, carry);
  and and_5 (and_5_out, decoder_1_out5, or_2_out);
  and and_6 (and_6_out, decoder_1_out6, xor_1_out);
  and and_7 (and_7_out, decoder_1_out7, or_1_out);
  or or_3 (result, and_7_out, and_6_out, and_5_out, and_4_out, and_3_out, and_2_out, and_1_out, decoder_1_out0);
endmodule

module ControlUnit (
  input  rst,
  input  zero,
  input  sign,
  input  carry,
  input  overflow,
  input  clk,
  input  ir7,
  input  ir6,
  input  ir5,
  input  ir4,
  input  ir3,
  input  ir2,
  input  ir1,
  input  ir0,
  output rd_r,
  output ra_w,
  output rb_w,
  output bus_0,
  output io,
  output io_in_out,
  output io_data_addr,
  output rx_r,
  output rx_w,
  output fr_w,
  output rx1,
  output pc_w,
  output rx0,
  output pc_r,
  output ir_w,
  output cin,
  output mar_w,
  output op2,
  output ram_w,
  output op1,
  output op0,
  output ram_r,
  output halt,
  output new_cycle,
  output new_instr
);

  wire and_10_out, and_13_out, and_14_out, and_15_out, branchchecker_1_result, clock_1_clk_r, clock_1_clk_w,
       delayer_1_out, instr_state_qn, or_1_out, or_2_out, or_3_out;
  wire [1:0] multiplexer_2_out, multiplexer_3_out;
  wire [6:0] adder_1_out, mPC_q, multiplexer_1_out, rom_1_data;
  wire [6:6] instr_state_q;
  wire [31:4] rom_1_data_2;

  and and_1 (fr_w, rom_1_data_2[12], clock_1_clk_w);
  and and_2 (pc_w, rom_1_data_2[13], clock_1_clk_w);
  and and_3 (pc_r, rom_1_data_2[14], clock_1_clk_r);
  and and_4 (ir_w, rom_1_data_2[15], clock_1_clk_w);
  and and_5 (mar_w, rom_1_data_2[16], clock_1_clk_w);
  and and_6 (ram_w, rom_1_data_2[17], clock_1_clk_w);
  and and_7 (ram_r, rom_1_data_2[18], clock_1_clk_r);
  Clock clock_1 (.clk_r(clock_1_clk_r), .clk(clk), .clk_w(clock_1_clk_w), .rst(or_1_out));
  nor nor_1 (new_cycle, clock_1_clk_r, clock_1_clk_w);
  or or_1 (or_1_out, rst, halt);
  and and_8 (ra_w, clock_1_clk_w, rom_1_data_2[10]);
  and and_9 (rd_r, clock_1_clk_r, rom_1_data_2[11]);
  Register #(.width(7)) mPC (.D(multiplexer_1_out), .en(1'b1), .Q(mPC_q), .clk(new_cycle), .clr(or_1_out));
  Multiplexer #(.select(2), .width(7), .enable("false")) multiplexer_1 (
    .in0(adder_1_out), .in1(adder_1_out), .in2(rom_1_data),
    .in3({instr_state_q[6], ir7, ir6, ir5, ir4, 2'b00}), .out(multiplexer_1_out), .sel(multiplexer_2_out));
  and and_10 (and_10_out, clock_1_clk_w, rom_1_data_2[31]);
  and and_11 (rb_w, clock_1_clk_w, rom_1_data_2[9]);
  Delayer delayer_1 (.in(new_cycle), .out(delayer_1_out));
  and and_12 (new_instr, delayer_1_out, and_13_out);
  and and_13 (and_13_out, ~mPC_q[6], ~mPC_q[5], ~mPC_q[4], ~mPC_q[3], ~mPC_q[2], ~mPC_q[1], mPC_q[0]);  // AND_Gate
  Adder #(.width(7)) adder_1 (.a(mPC_q), .b({7{1'b0}}), .out(adder_1_out), .cin(1'b1));  // open: cout
  D_Flip_Flop instr_state (
    .clk(and_10_out), .D(instr_state_qn), .Q(instr_state_q[6]), .Qn(instr_state_qn), .en(1'b1),
    .reset(or_1_out));  // open: preset
  ROM #(.addrWidth(7), .dataWidth(32)) rom_1 (
    .addr(mPC_q),
    .data({rom_1_data_2[31:27], rom_1_data, halt, rom_1_data_2[18:9], bus_0, io, rom_1_data_2[6:4], cin, op2, op1, op0}),
    .sel(1'b1));
  Multiplexer #(.select(2), .width(2), .enable("false")) multiplexer_2 (
    .in0(2'b00), .in1(multiplexer_3_out), .in2(2'b10), .in3(2'b11), .out(multiplexer_2_out),
    .sel(rom_1_data_2[29:28]));
  and and_14 (and_14_out, ir3, io);
  and and_15 (and_15_out, io, ~ir3);  // AND_Gate
  BranchChecker branchchecker_1 (
    .zero(zero), .sign(sign), .carry(carry), .overflow(overflow), .op0(ir0), .op1(ir1), .op2(ir2),
    .result(branchchecker_1_result));
  Multiplexer #(.width(2), .enable("false")) multiplexer_3 (
    .in0(2'b00), .in1(2'b10), .out(multiplexer_3_out), .sel(branchchecker_1_result));
  or or_2 (or_2_out, rom_1_data_2[6], and_15_out);
  or or_3 (or_3_out, rom_1_data_2[5], and_14_out);
  Multiplexer #(.width(2), .enable("false")) multiplexer_4 (
    .in0({ir3, ir2}), .in1({ir1, ir0}), .out({rx1, rx0}), .sel(rom_1_data_2[4]));
  and and_16 (rx_r, clock_1_clk_r, or_2_out);
  and and_17 (rx_w, clock_1_clk_w, or_3_out);

  assign io_data_addr = ir2;
  assign io_in_out = ir3;

  // Notes on the sheet:
  //   Map instructions to 1xxxx00 with xxxx=OPCODE
  //   to avoid collision with IFETCH.
  //   Instructions must complete in 4 steps.
  //   0x00 has no instruction since after reset it won't be executed.
  //   00xy -> jump to addr mPC+1
  //   01xy -> branch to either addr mPC+1 or ROM[mPC]
  //   10xy -> jump to addr ROM[mPC]
  //   11xy -> jump to instr in IR
  //   contents of rom_1 (hex, n*v repeats v):
  //   0 14700 280c b0048000 60*0 450 a0100820 0 0 14700 280c a0140030 0 10050 a0140020 0 0 10050 a0120040
  //   0 0 4400 2050 a0100830 0 15614400 a0102b0c 40200 a0102804 a0080000 0 0 0 a0100000 0 0 0 440 250
  //   a0101824 0 440 250 a0101825 0 450 a0101826 0 0 450 a0101827 0 0 440 250 a0101821 0 440 250 a0101822
  //   0 440 250 a0101823 0 440 a0101255
endmodule

module CPU (
  input  in_1,
  input  in_2,
  input  in_3,
  input  in_4,
  input  in_5,
  input  in_6,
  input  in_7,
  input  in_8,
  input  MANUAL,
  input  in_10,
  input  in_11,
  input  in_12,
  input  in_13,
  input  in_14,
  input  in_15,
  input  in_16,
  input  in_17,
  output out_18,
  output out_19,
  output out_20,
  output out_21,
  output out_22,
  output out_23,
  output out_24,
  output out_25
);

  wire ADDR_out, alu_1_carry, alu_1_out0, alu_1_out1, alu_1_out2, alu_1_out3, alu_1_out4, alu_1_out5,
       alu_1_out6, alu_1_out7, alu_1_overflow, alu_1_sign, alu_1_zero, and_1_out, and_2_out, and_3_out,
       and_4_out, and_5_out, and_6_out, and_7_out, and_8_out, and_9_out, and_10_out, and_11_out, and_12_out,
       bus0gate_1_out0, bus0gate_1_out1, bus0gate_1_out2, bus0gate_1_out3, bus0gate_1_out4, bus0gate_1_out5,
       bus0gate_1_out6, bus0gate_1_out7, CLOCK_out, controlled_buffer_1_out, controlled_buffer_2_out,
       controlunit_1_bus_0, controlunit_1_cin, controlunit_1_fr_w, controlunit_1_halt, controlunit_1_ir_w,
       controlunit_1_mar_w, controlunit_1_new_cycle, controlunit_1_new_instr, controlunit_1_op0,
       controlunit_1_op1, controlunit_1_op2, controlunit_1_pc_r, controlunit_1_pc_w, controlunit_1_ra_w,
       controlunit_1_ram_r, controlunit_1_ram_w, controlunit_1_rb_w, controlunit_1_rd_r, controlunit_1_rx_r,
       controlunit_1_rx_w, decoder_1_out0, decoder_1_out1, decoder_1_out2, decoder_1_out3, FR_out0, FR_out1,
       FR_out2, FR_out3, HALT_2_q, HALT_2_qn, LDR_out, not_1_out, not_2_out, not_3_out, not_4_out, or_1_out,
       or_2_out, or_3_out, or_4_out, or_5_out, or_6_out, or_7_out, RA_out0, RA_out1, RA_out2, RA_out3,
       RA_out4, RA_out5, RA_out6, RA_out7, RB_out0, RB_out1, RB_out2, RB_out3, RB_out4, RB_out5, RB_out6,
       RB_out7, RESET_2_out, RESET_3_out, RESUME_out, STEP_out, STR_out;
  wire [1:0] controlunit_1_rx0;
  wire [3:0] CYCLES_q, CYCLES_q_2;
  wire [7:0] INSTR_q, IR_out0;

  ALU alu_1 (
    .a7(RA_out7), .a6(RA_out6), .a5(RA_out5), .a4(RA_out4), .a3(RA_out3), .a2(RA_out2), .a1(RA_out1),
    .a0(RA_out0), .b7(RB_out7), .b6(RB_out6), .b5(RB_out5), .b4(RB_out4), .b3(RB_out3), .b2(RB_out2),
    .b1(RB_out1), .b0(RB_out0), .cin(controlunit_1_cin), .op2(controlunit_1_op2), .op1(controlunit_1_op1),
    .op0(controlunit_1_op0), .out0(alu_1_out0), .out1(alu_1_out1), .out2(alu_1_out2), .out3(alu_1_out3),
    .out4(alu_1_out4), .out5(alu_1_out5), .out6(alu_1_out6), .out7(alu_1_out7), .overflow(alu_1_overflow),
    .sign(alu_1_sign), .zero(alu_1_zero), .carry(alu_1_carry));
  LED Reset (.in(RESET_2_out));
  Button RESET_2 (.out(RESET_2_out));
  Button RESUME (.out(RESUME_out));
  not not_1 (not_1_out, MANUAL);
  assign controlled_buffer_1_out = MANUAL ? STEP_out : 1'bz;  // Controlled_Buffer controlled_buffer_1
  Button STEP (.out(STEP_out));
  Clock_part CLOCK (.out(CLOCK_out));
  Pull_Resistor pull_resistor_1 (.node(controlled_buffer_1_out));
  Reg8 RA (
    .in0(out_25), .in1(out_24), .in2(out_23), .in3(out_22), .in4(out_21), .in5(out_20), .in6(out_19),
    .in7(out_18), .read(1'b1), .write(controlunit_1_ra_w), .reset(RESET_2_out), .out0(RA_out0),
    .out1(RA_out1), .out2(RA_out2), .out3(RA_out3), .out4(RA_out4), .out5(RA_out5), .out6(RA_out6),
    .out7(RA_out7));
  LED Auto (.in(not_2_out));
  LED u_Manual (.in(MANUAL));
  not not_2 (not_2_out, MANUAL);
  or or_1 (or_1_out, controlled_buffer_1_out, controlled_buffer_2_out);
  assign controlled_buffer_2_out = not_1_out ? CLOCK_out : 1'bz;  // Controlled_Buffer controlled_buffer_2
  Pull_Resistor pull_resistor_2 (.node(controlled_buffer_2_out));
  Reg8 RB (
    .in0(bus0gate_1_out0), .in1(bus0gate_1_out1), .in2(bus0gate_1_out2), .in3(bus0gate_1_out3),
    .in4(bus0gate_1_out4), .in5(bus0gate_1_out5), .in6(bus0gate_1_out6), .in7(bus0gate_1_out7), .read(1'b1),
    .write(controlunit_1_rb_w), .reset(RESET_2_out), .out0(RB_out0), .out1(RB_out1), .out2(RB_out2),
    .out3(RB_out3), .out4(RB_out4), .out5(RB_out5), .out6(RB_out6), .out7(RB_out7));
  Reg8 RD (
    .in0(alu_1_out0), .in1(alu_1_out1), .in2(alu_1_out2), .in3(alu_1_out3), .in4(alu_1_out4),
    .in5(alu_1_out5), .in6(alu_1_out6), .in7(alu_1_out7), .read(controlunit_1_rd_r), .write(1'b1),
    .reset(RESET_2_out), .out0(out_25), .out1(out_24), .out2(out_23), .out3(out_22), .out4(out_21),
    .out5(out_20), .out6(out_19), .out7(out_18));
  LED Clock_2 (.in(or_1_out));
  LED Halt (.in(HALT_2_q));
  not not_3 (not_3_out, not_2_out);
  not not_4 (not_4_out, controlunit_1_bus_0);
  Bus0Gate bus0gate_1 (
    .in7(out_18), .in6(out_19), .in5(out_20), .in4(out_21), .in3(out_22), .in2(out_23), .in1(out_24),
    .in0(out_25), ._0_bus(not_4_out), .out7(bus0gate_1_out7), .out6(bus0gate_1_out6), .out5(bus0gate_1_out5),
    .out4(bus0gate_1_out4), .out3(bus0gate_1_out3), .out2(bus0gate_1_out2), .out1(bus0gate_1_out1),
    .out0(bus0gate_1_out0));
  and and_1 (and_1_out, ~HALT_2_q, or_1_out);  // AND_Gate
  Reg4 FR (
    .in0(alu_1_zero), .in1(alu_1_sign), .in2(alu_1_carry), .in3(alu_1_overflow), .read(1'b1),
    .write(controlunit_1_fr_w), .out0(FR_out0), .out1(FR_out1), .out2(FR_out2), .out3(FR_out3),
    .reset(RESET_2_out));
  ControlUnit controlunit_1 (
    .op0(controlunit_1_op0), .op1(controlunit_1_op1), .op2(controlunit_1_op2), .fr_w(controlunit_1_fr_w),
    .mar_w(controlunit_1_mar_w), .ram_r(controlunit_1_ram_r), .ram_w(controlunit_1_ram_w), .carry(FR_out2),
    .sign(FR_out1), .zero(FR_out0), .ra_w(controlunit_1_ra_w), .rb_w(controlunit_1_rb_w),
    .bus_0(controlunit_1_bus_0), .rx_r(controlunit_1_rx_r), .rx_w(controlunit_1_rx_w), .clk(and_1_out),
    .rst(RESET_2_out), .rd_r(controlunit_1_rd_r), .ir0(IR_out0[0]), .ir1(IR_out0[1]), .ir2(IR_out0[2]),
    .ir3(IR_out0[3]), .ir4(IR_out0[4]), .ir5(IR_out0[5]), .ir6(IR_out0[6]), .ir7(IR_out0[7]),
    .ir_w(controlunit_1_ir_w), .pc_w(controlunit_1_pc_w), .pc_r(controlunit_1_pc_r), .overflow(FR_out3),
    .halt(controlunit_1_halt), .cin(controlunit_1_cin), .new_instr(controlunit_1_new_instr),
    .new_cycle(controlunit_1_new_cycle), .rx0(controlunit_1_rx0[0]), .rx1(controlunit_1_rx0[1]));  // open: io_in_out, io_data_addr, io
  D_Flip_Flop HALT_2 (
    .clk(controlunit_1_halt), .D(HALT_2_qn), .Q(HALT_2_q), .Qn(HALT_2_qn), .en(1'b1), .reset(or_2_out));  // open: preset
  or or_2 (or_2_out, RESUME_out, RESET_2_out);
  Reg8 R0 (
    .in0(out_25), .in1(out_24), .in2(out_23), .in3(out_22), .in4(out_21), .in5(out_20), .in6(out_19),
    .in7(out_18), .read(and_2_out), .write(and_3_out), .reset(RESET_2_out), .out0(out_25), .out1(out_24),
    .out2(out_23), .out3(out_22), .out4(out_21), .out5(out_20), .out6(out_19), .out7(out_18));
  and and_2 (and_2_out, controlunit_1_rx_r, decoder_1_out0);
  Decoder #(.select(2), .enable("false")) decoder_1 (
    .out0(decoder_1_out0), .out1(decoder_1_out1), .out2(decoder_1_out2), .out3(decoder_1_out3),
    .sel(controlunit_1_rx0));
  Counter #(.trigger("falling")) INSTR (
    .load(1'b0), .count(1'b1), .Q(INSTR_q), .clk(controlunit_1_new_instr), .clr(RESET_2_out));  // open: D, carry
  Hex_Digit_Display hex_digit_display_1 (.value(INSTR_q[7:4]));  // open: dp
  Hex_Digit_Display hex_digit_display_2 (.value(INSTR_q[3:0]));  // open: dp
  and and_3 (and_3_out, decoder_1_out0, controlunit_1_rx_w);
  Counter CYCLES (
    .load(1'b0), .count(1'b1), .Q({CYCLES_q_2, CYCLES_q}), .clk(controlunit_1_new_cycle), .clr(or_3_out));  // open: D, carry
  or or_3 (or_3_out, controlunit_1_new_instr, RESET_2_out);
  Hex_Digit_Display hex_digit_display_3 (.value(CYCLES_q_2));  // open: dp
  Reg8 IR (
    .in0(out_25), .in1(out_24), .in2(out_23), .in3(out_22), .in4(out_21), .in5(out_20), .in6(out_19),
    .in7(out_18), .read(1'b1), .write(controlunit_1_ir_w), .reset(RESET_2_out), .out0(IR_out0[0]),
    .out1(IR_out0[1]), .out2(IR_out0[2]), .out3(IR_out0[3]), .out4(IR_out0[4]), .out5(IR_out0[5]),
    .out6(IR_out0[6]), .out7(IR_out0[7]));
  Hex_Digit_Display hex_digit_display_4 (.value(CYCLES_q));  // open: dp
  Reg8 R1 (
    .in0(out_25), .in1(out_24), .in2(out_23), .in3(out_22), .in4(out_21), .in5(out_20), .in6(out_19),
    .in7(out_18), .read(and_5_out), .write(and_4_out), .reset(RESET_2_out), .out0(out_25), .out1(out_24),
    .out2(out_23), .out3(out_22), .out4(out_21), .out5(out_20), .out6(out_19), .out7(out_18));
  and and_4 (and_4_out, decoder_1_out1, controlunit_1_rx_w);
  and and_5 (and_5_out, controlunit_1_rx_r, decoder_1_out1);
  and and_6 (and_6_out, ADDR_out, not_3_out);
  and and_7 (and_7_out, not_3_out, LDR_out);
  Button ADDR (.out(ADDR_out));
  Button LDR (.out(LDR_out));
  Reg8 R2 (
    .in0(out_25), .in1(out_24), .in2(out_23), .in3(out_22), .in4(out_21), .in5(out_20), .in6(out_19),
    .in7(out_18), .read(and_8_out), .write(and_10_out), .reset(RESET_2_out), .out0(out_25), .out1(out_24),
    .out2(out_23), .out3(out_22), .out4(out_21), .out5(out_20), .out6(out_19), .out7(out_18));
  and and_8 (and_8_out, controlunit_1_rx_r, decoder_1_out2);
  Reg8 PC (
    .in0(out_25), .in1(out_24), .in2(out_23), .in3(out_22), .in4(out_21), .in5(out_20), .in6(out_19),
    .in7(out_18), .read(controlunit_1_pc_r), .write(controlunit_1_pc_w), .reset(RESET_2_out), .out0(out_25),
    .out1(out_24), .out2(out_23), .out3(out_22), .out4(out_21), .out5(out_20), .out6(out_19), .out7(out_18));
  and and_9 (and_9_out, not_3_out, STR_out);
  Button STR (.out(STR_out));
  and and_10 (and_10_out, decoder_1_out2, controlunit_1_rx_w);
  assign out_20 = and_6_out ? in_3 : 1'bz;  // Controlled_Buffer controlled_buffer_3
  assign out_19 = and_6_out ? in_2 : 1'bz;  // Controlled_Buffer controlled_buffer_4
  assign out_21 = and_6_out ? in_4 : 1'bz;  // Controlled_Buffer controlled_buffer_5
  assign out_18 = and_6_out ? in_1 : 1'bz;  // Controlled_Buffer controlled_buffer_6
  assign out_20 = and_9_out ? in_12 : 1'bz;  // Controlled_Buffer controlled_buffer_7
  assign out_18 = and_9_out ? in_10 : 1'bz;  // Controlled_Buffer controlled_buffer_8
  assign out_19 = and_9_out ? in_11 : 1'bz;  // Controlled_Buffer controlled_buffer_9
  assign out_21 = and_9_out ? in_13 : 1'bz;  // Controlled_Buffer controlled_buffer_10
  assign out_23 = and_6_out ? in_6 : 1'bz;  // Controlled_Buffer controlled_buffer_11
  assign out_25 = and_6_out ? in_8 : 1'bz;  // Controlled_Buffer controlled_buffer_12
  assign out_24 = and_6_out ? in_7 : 1'bz;  // Controlled_Buffer controlled_buffer_13
  assign out_22 = and_6_out ? in_5 : 1'bz;  // Controlled_Buffer controlled_buffer_14
  assign out_22 = and_9_out ? in_14 : 1'bz;  // Controlled_Buffer controlled_buffer_15
  assign out_23 = and_9_out ? in_15 : 1'bz;  // Controlled_Buffer controlled_buffer_16
  assign out_24 = and_9_out ? in_16 : 1'bz;  // Controlled_Buffer controlled_buffer_17
  assign out_25 = and_9_out ? in_17 : 1'bz;  // Controlled_Buffer controlled_buffer_18
  Reg8 R3 (
    .in0(out_25), .in1(out_24), .in2(out_23), .in3(out_22), .in4(out_21), .in5(out_20), .in6(out_19),
    .in7(out_18), .read(and_12_out), .write(and_11_out), .reset(RESET_2_out), .out0(out_25), .out1(out_24),
    .out2(out_23), .out3(out_22), .out4(out_21), .out5(out_20), .out6(out_19), .out7(out_18));
  and and_11 (and_11_out, decoder_1_out3, controlunit_1_rx_w);
  and and_12 (and_12_out, controlunit_1_rx_r, decoder_1_out3);
  or or_4 (or_4_out, controlunit_1_mar_w, and_6_out);
  or or_5 (or_5_out, controlunit_1_ram_r, and_7_out);
  or or_6 (or_6_out, controlunit_1_ram_w, and_9_out);
  or or_7 (or_7_out, and_1_out, and_6_out, and_7_out, and_9_out);
  Button RESET_3 (.out(RESET_3_out));
  Ram256 ram256_1 (
    .addr0(out_25), .addr1(out_24), .addr2(out_23), .addr3(out_22), .addr4(out_21), .addr5(out_20),
    .addr6(out_19), .addr7(out_18), .marw(or_4_out), .read(or_5_out), .write(or_6_out), .reset(RESET_3_out),
    .in0(out_25), .in1(out_24), .in2(out_23), .in3(out_22), .in4(out_21), .in5(out_20), .in6(out_19),
    .in7(out_18), .out0(out_25), .out1(out_24), .out2(out_23), .out3(out_22), .out4(out_21), .out5(out_20),
    .out6(out_19), .out7(out_18), .clk(or_7_out));

  // Notes on the sheet:
  //   bits | cond   | flag test  | description
  //   0000 | r      | -----      | branch always
  //   0001 | zs/eq  | z=1        | branch if equal
  //   0010 | ss/neg | s=1        | branch if negative
  //   0011 | ov     | v=1        | branch if overflow
  //   0100 | cs/ltu | c=1        | branch if uint <
  //   0101 | leu    | c=1 or z=1 | branch if uint <=
  //   0110 | lt     | v+s        | branch if int <
  //   0111 | le     | v+s or z=1 | branch if int <=
  //   0000 00 00  ->  mov  ra, rb    ->  ra = rb
  //   0001 00 rb  ->  data rb, imm8  ->  rb = ram[pc++]
  //   0010 ra rb  ->  ldr  ra, [rb]  ->  ra = ram[rb]
  //   0011 ra rb  ->  str  ra, [rb]  ->  ram[rb] = ra
  //   0100 00 rb  ->  jalr rb        ->  pc <-> rb
  //   0101  cond  ->  b<cond> imm8   ->  pc += cond ? ram[pc] : 1
  //   0110 00 00  ->  halt           ->  stop computer
  //   0111 00 rb  ->  in   data, rb  ->  rb = io[active].data
  //   0111 10 rb  ->  out  data, rb  ->  io[active].data = rb
  //   0111 01 rb  ->  in   addr, rb  ->  rb = io[active].addr
  //   0111 11 rb  ->  out  addr, rb  ->  io[rb].active = true
  //   1000 ra rb  ->  add ra, rb  ->  ra = ra + rb       [vcsz]
  //   1001 ra rb  ->  sub ra, rb  ->  ra = ra - rb       [vcsz]
  //   1010 ra rb  ->  shl ra, rb  ->  ra = [rb << 1, 0]  [0csz]
  //   1011 ra rb  ->  shr ra, rb  ->  ra = [0, rb >> 1]  [0csz]
  //   1100 ra rb  ->  and ra, rb  ->  ra = ra & rb       [00sz]
  //   1101 ra rb  ->  orr ra, rb  ->  ra = ra | rb       [00sz]
  //   1110 ra rb  ->  xor ra, rb  ->  ra = ra ^ rb       [00sz]
  //   1111 ra rb  ->  cmp ra, rb  ->  fr = ra - rb       [vcsz]
endmodule
