// Logisim project scott.circ as structural Verilog
module Main (
  input  MANUAL
);

  wire and_1_out, CLOCK_out, cpu_1_halt, cpu_1_io_data_addr, cpu_1_io_en, cpu_1_r_w, cpu_1_ram_en, FR_out_2,
       FR_out_3, FR_out_4, FR_out_5, HALT_q, HALT_qn, IR_out_2, IR_out_3, IR_out_4, IR_out_5, IR_out_6,
       IR_out_7, IR_out_8, IR_out_9, multiplexer_1_out, not_1_out, not_2_out, not_3_out, not_4_out,
       NPC_out_2, NPC_out_3, NPC_out_4, NPC_out_5, NPC_out_6, NPC_out_7, NPC_out_8, NPC_out_9, or_1_out,
       PC_out_2, PC_out_3, PC_out_4, PC_out_5, PC_out_6, PC_out_7, PC_out_8, PC_out_9, R0_out_2, R0_out_3,
       R0_out_4, R0_out_5, R0_out_6, R0_out_7, R0_out_8, R0_out_9, R1_out_2, R1_out_3, R1_out_4, R1_out_5,
       R1_out_6, R1_out_7, R1_out_8, R1_out_9, R2_out_2, R2_out_3, R2_out_4, R2_out_5, R2_out_6, R2_out_7,
       R2_out_8, R2_out_9, R3_out_2, R3_out_3, R3_out_4, R3_out_5, R3_out_6, R3_out_7, R3_out_8, R3_out_9,
       RESET_out, RESUME_out, STEP_out;
  wire [3:0] cpu_1_dbg_fr;
  wire [7:0] cpu_1_bus_out, cpu_1_dbg_ir, cpu_1_dbg_npc, cpu_1_dbg_pc, cpu_1_dbg_r0, cpu_1_dbg_r1,
       cpu_1_dbg_r2, cpu_1_dbg_r3, cpu_1_ram_addr, cpu_1_rom_addr, INSTR_q, ram_1_data, rom_1_data;

  Button RESET (.out(RESET_out));
  Button RESUME (.out(RESUME_out));
  not not_1 (not_1_out, MANUAL);
  Button STEP (.out(STEP_out));
  Clock CLOCK (.out(CLOCK_out));
  LED led_1 (.in(NPC_out_5));
  LED led_2 (.in(NPC_out_2));
  LED led_3 (.in(NPC_out_3));
  LED led_4 (.in(NPC_out_4));
  LED led_5 (.in(PC_out_5));
  LED led_6 (.in(PC_out_4));
  LED led_7 (.in(PC_out_3));
  LED led_8 (.in(PC_out_2));
  LED led_9 (.in(IR_out_3));
  LED led_10 (.in(IR_out_4));
  LED led_11 (.in(IR_out_5));
  LED led_12 (.in(IR_out_2));
  D_Flip_Flop HALT (
    .clk(cpu_1_halt), .D(HALT_qn), .Q(HALT_q), .Qn(HALT_qn), .en(1'b1), .reset(or_1_out));  // open: preset
  or or_1 (or_1_out, RESUME_out, RESET_out);
  Multiplexer #(.enable("false")) multiplexer_1 (
    .in0(STEP_out), .in1(CLOCK_out), .out(multiplexer_1_out), .sel(not_1_out));
  LED led_13 (.in(NPC_out_6));
  LED led_14 (.in(NPC_out_9));
  LED led_15 (.in(NPC_out_7));
  LED led_16 (.in(NPC_out_8));
  LED8L NPC (
    .in_1(cpu_1_dbg_npc), .out_2(NPC_out_2), .out_3(NPC_out_3), .out_4(NPC_out_4), .out_5(NPC_out_5),
    .out_6(NPC_out_6), .out_7(NPC_out_7), .out_8(NPC_out_8), .out_9(NPC_out_9));
  LED led_17 (.in(PC_out_9));
  LED led_18 (.in(PC_out_8));
  LED led_19 (.in(PC_out_6));
  LED led_20 (.in(PC_out_7));
  LED8L PC (
    .in_1(cpu_1_dbg_pc), .out_2(PC_out_2), .out_3(PC_out_3), .out_4(PC_out_4), .out_5(PC_out_5),
    .out_6(PC_out_6), .out_7(PC_out_7), .out_8(PC_out_8), .out_9(PC_out_9));
  LED led_21 (.in(IR_out_7));
  LED led_22 (.in(IR_out_8));
  LED led_23 (.in(IR_out_6));
  LED led_24 (.in(IR_out_9));
  LED8L IR (
    .in_1(cpu_1_dbg_ir), .out_2(IR_out_2), .out_3(IR_out_3), .out_4(IR_out_4), .out_5(IR_out_5),
    .out_6(IR_out_6), .out_7(IR_out_7), .out_8(IR_out_8), .out_9(IR_out_9));
  LED s (.in(FR_out_4));
  LED c (.in(FR_out_3));
  LED z (.in(FR_out_5));
  LED v (.in(FR_out_2));
  LED4L FR (.in_1(cpu_1_dbg_fr), .out_2(FR_out_2), .out_3(FR_out_3), .out_4(FR_out_4), .out_5(FR_out_5));
  ROM rom_1 (.addr(cpu_1_rom_addr), .data(rom_1_data), .sel(1'b1));
  and and_1 (and_1_out, ~HALT_q, multiplexer_1_out);  // AND_Gate
  LED Reset_2 (.in(RESET_out));
  Counter INSTR (.load(1'b0), .count(1'b1), .Q(INSTR_q), .clk(not_2_out), .clr(RESET_out));  // open: D, carry
  not not_2 (not_2_out, and_1_out);
  Hex_Digit_Display hex_digit_display_1 (.value(INSTR_q[7:4]));  // open: dp
  LED Auto (.in(not_1_out));
  LED u_Manual (.in(MANUAL));
  CPU cpu_1 (
    .dbg_ir(cpu_1_dbg_ir), .halt(cpu_1_halt), .clk(and_1_out), .rst(RESET_out), .r_w(cpu_1_r_w),
    .dbg_r0(cpu_1_dbg_r0), .dbg_r1(cpu_1_dbg_r1), .io_data_addr(cpu_1_io_data_addr), .dbg_r2(cpu_1_dbg_r2),
    .dbg_r3(cpu_1_dbg_r3), .ram_en(cpu_1_ram_en), .io_en(cpu_1_io_en), .ram_addr(cpu_1_ram_addr),
    .bus_out(cpu_1_bus_out), .bus_in(ram_1_data), .dbg_npc(cpu_1_dbg_npc), .dbg_pc(cpu_1_dbg_pc),
    .dbg_fr(cpu_1_dbg_fr), .rom_addr(cpu_1_rom_addr), .rom_in(rom_1_data));
  Hex_Digit_Display hex_digit_display_2 (.value(INSTR_q[3:0]));  // open: dp
  LED Halt_2 (.in(HALT_q));
  LED Clock_2 (.in(multiplexer_1_out));
  LED led_25 (.in(R0_out_3));
  LED led_26 (.in(R0_out_4));
  LED led_27 (.in(R0_out_2));
  LED led_28 (.in(R0_out_5));
  LED led_29 (.in(R1_out_5));
  LED led_30 (.in(R1_out_4));
  LED led_31 (.in(R1_out_3));
  LED led_32 (.in(R1_out_2));
  LED led_33 (.in(R2_out_5));
  LED led_34 (.in(R2_out_3));
  LED led_35 (.in(R2_out_4));
  LED led_36 (.in(R2_out_2));
  LED led_37 (.in(R3_out_4));
  LED led_38 (.in(R3_out_2));
  LED led_39 (.in(R3_out_5));
  LED led_40 (.in(R3_out_3));
  LED led_41 (.in(R0_out_6));
  LED led_42 (.in(R0_out_7));
  LED led_43 (.in(R0_out_8));
  LED8R R0 (
    .in_1(cpu_1_dbg_r0), .out_2(R0_out_2), .out_3(R0_out_3), .out_4(R0_out_4), .out_5(R0_out_5),
    .out_6(R0_out_6), .out_7(R0_out_7), .out_8(R0_out_8), .out_9(R0_out_9));
  LED led_44 (.in(R1_out_8));
  LED led_45 (.in(R1_out_6));
  LED led_46 (.in(R1_out_7));
  LED8R R1 (
    .in_1(cpu_1_dbg_r1), .out_2(R1_out_2), .out_3(R1_out_3), .out_4(R1_out_4), .out_5(R1_out_5),
    .out_6(R1_out_6), .out_7(R1_out_7), .out_8(R1_out_8), .out_9(R1_out_9));
  LED led_47 (.in(R2_out_7));
  LED led_48 (.in(R2_out_6));
  LED led_49 (.in(R2_out_8));
  LED8R R2 (
    .in_1(cpu_1_dbg_r2), .out_2(R2_out_2), .out_3(R2_out_3), .out_4(R2_out_4), .out_5(R2_out_5),
    .out_6(R2_out_6), .out_7(R2_out_7), .out_8(R2_out_8), .out_9(R2_out_9));
  LED led_50 (.in(R3_out_6));
  LED led_51 (.in(R3_out_8));
  LED led_52 (.in(R3_out_7));
  LED8R R3 (
    .in_1(cpu_1_dbg_r3), .out_2(R3_out_2), .out_3(R3_out_3), .out_4(R3_out_4), .out_5(R3_out_5),
    .out_6(R3_out_6), .out_7(R3_out_7), .out_8(R3_out_8), .out_9(R3_out_9));
  LED led_53 (.in(R0_out_9));
  LED led_54 (.in(R1_out_9));
  LED led_55 (.in(R2_out_9));
  LED led_56 (.in(R3_out_9));
  not not_3 (not_3_out, cpu_1_r_w);
  not not_4 (not_4_out, and_1_out);
  RAM #(.bus("separate")) ram_1 (
    .addr(cpu_1_ram_addr), .din(cpu_1_bus_out), .data(ram_1_data), .str(cpu_1_r_w), .sel(cpu_1_ram_en),
    .clk(not_4_out), .ld(not_3_out), .clr(RESET_out));

  // Notes on the sheet:
  //   contents of rom_1 (hex, n*v repeats v):
  //   1c 5 14 1 9 10 2 fc 54 a 1 82 9 4 10 1 9c 50 f3 10 1 34 60
  //   0000 ra rb  ->  mov  ra, rb    ->  ra = rb
  //   0001 ra xx  ->  data ra, imm8  ->  ra = ram[pc++]
  //   0010 ra rb  ->  ldr  ra, [rb]  ->  ra = ram[rb]
  //   0011 ra rb  ->  str  ra, [rb]  ->  ram[rb] = ra
  //   0100 ra ra  ->  jalr ra        ->  pc <-> ra
  //   0101  cond  ->  b<cond> imm8   ->  pc += cond ? ram[pc] : 1
  //   0110 00 00  ->  halt           ->  stop computer
  //   0111 ra 00  ->  in   ra, data  ->  ra = io[active].data
  //   0111 ra 10  ->  out  ra, data  ->  io[active].data = ra
  //   0111 ra 01  ->  in   ra, addr  ->  ra = io[active].addr
  //   0111 ra 11  ->  out  ra, addr  ->  io[ra].active = true
  //   1000 ra rb  ->  add  ra, rb    ->  ra = ra + rb       [vcsz]
  //   1001 ra rb  ->  sub  ra, rb    ->  ra = ra - rb       [vcsz]
  //   1010 ra rb  ->  shl  ra, rb    ->  ra = [rb << 1, 0]  [0csz]
  //   1011 ra rb  ->  shr  ra, rb    ->  ra = [0, rb >> 1]  [0csz]
  //   1100 ra rb  ->  and  ra, rb    ->  ra = ra & rb       [00sz]
  //   1101 ra rb  ->  orr  ra, rb    ->  ra = ra | rb       [00sz]
  //   1110 ra rb  ->  xor  ra, rb    ->  ra = ra ^ rb       [00sz]
  //   1111 ra rb  ->  cmp  ra, rb    ->  fr = ra - rb       [vcsz]
  //   bits | cond   | flag test  | description
  //   0000 | r      | -----      | branch always
  //   0001 | zs/eq  | z=1        | branch if equal
  //   0010 | ss/neg | s=1        | branch if negative
  //   0011 | ov     | v=1        | branch if overflow
  //   0100 | cs/ltu | c=1        | branch if uint <
  //   0101 | leu    | c=1 or z=1 | branch if uint <=
  //   0110 | lt     | v+s        | branch if int <
  //   0111 | le     | v+s or z=1 | branch if int <=
endmodule

module CPU (
  input  [7:0] bus_in,
  input  clk,
  input  rst,
  input  [7:0] rom_in,
  output [7:0] dbg_ir,
  output io_data_addr,
  output r_w,
  output ram_en,
  output io_en,
  output [7:0] dbg_r0,
  output halt,
  output [3:0] dbg_fr,
  output [7:0] dbg_r1,
  output [7:0] dbg_r2,
  output [7:0] dbg_r3,
  output [7:0] dbg_npc,
  output [7:0] dbg_pc,
  output [7:0] ram_addr,
  output [7:0] bus_out,
  output [7:0] rom_addr
);

  wire and_2_out, and_3_out, and_4_out, and_5_out, and_6_out, branchchecker_1_result, d_ff_1_q, d_ff_1_qn,
       not_1_out, not_2_out, not_3_out, or_1_out, or_2_out, or_4_out;
  wire [3:0] alu_1_zero, reg4_1_out_3__0;
  wire [7:0] alu_1_out, controlled_buffer_1_out, inc8_1_in_2, multiplexer_1_out, multiplexer_3_out,
       multiplexer_4_out, multiplexer_5_out, multiplexer_6_out, reg8_1_out, regfile_1_ra, regfile_1_rb;
  wire [15:0] rom_1_data;

  and and_1 (halt, rom_1_data[15], not_1_out);
  not not_1 (not_1_out, clk);
  and and_2 (and_2_out, rom_1_data[13], branchchecker_1_result, d_ff_1_q);
  or or_1 (or_1_out, rom_1_data[12], and_2_out);
  Multiplexer #(.width(8), .enable("false")) multiplexer_1 (
    .in0(inc8_1_in_2), .in1(alu_1_out), .out(multiplexer_1_out), .sel(or_1_out));
  BranchChecker branchchecker_1 (
    .zero(reg4_1_out_3__0[0]), .sign(reg4_1_out_3__0[1]), .carry(reg4_1_out_3__0[2]),
    .overflow(reg4_1_out_3__0[3]), .op0(dbg_ir[0]), .op1(dbg_ir[1]), .op2(dbg_ir[2]),
    .result(branchchecker_1_result));
  Reg8 reg8_1 (
    .in(multiplexer_1_out), .dbg(dbg_npc), .r(1'b1), .w(1'b1), .en(1'b1), .clk(not_1_out), .rst(rst),
    .out(reg8_1_out));
  Inc8 inc8_1 (.in(rom_addr), .in_2(inc8_1_in_2));
  Reg8 reg8_2 (
    .in(reg8_1_out), .dbg(dbg_pc), .r(1'b1), .w(1'b1), .en(1'b1), .clk(not_2_out), .rst(rst), .out(rom_addr));
  not not_2 (not_2_out, not_1_out);
  D_Flip_Flop d_ff_1 (
    .clk(and_3_out), .D(d_ff_1_qn), .Q(d_ff_1_q), .Qn(d_ff_1_qn), .en(1'b1), .reset(rst));  // open: preset
  and and_3 (and_3_out, rom_1_data[14], not_1_out);
  Multiplexer #(.width(8), .enable("false")) multiplexer_2 (.in0(rom_in), .in1(dbg_ir), .out(dbg_ir), .sel(d_ff_1_q));
  ROM #(.addrWidth(4), .dataWidth(16)) rom_1 (
    .addr(dbg_ir[7:4]), .data({rom_1_data[15:12], io_en, ram_en, rom_1_data[9:0]}), .sel(1'b1));
  RegFile regfile_1 (
    .rd(multiplexer_3_out), .reg_w(or_2_out), .selRD0(dbg_ir[2]), .selRD1(dbg_ir[3]), .clk(not_1_out),
    .rst(rst), .selRA0(dbg_ir[2]), .selRA1(dbg_ir[3]), .selRB0(dbg_ir[0]), .selRB1(dbg_ir[1]),
    .ra(regfile_1_ra), .rb(regfile_1_rb), .dbgR0(dbg_r0), .dbgR1(dbg_r1), .dbgR3(dbg_r3), .dbgR2(dbg_r2));
  or or_2 (or_2_out, and_4_out, rom_1_data[8]);
  and and_4 (and_4_out, dbg_ir[1], io_en);
  Multiplexer #(.width(8), .enable("false")) multiplexer_3 (
    .in0(alu_1_out), .in1(multiplexer_4_out), .out(multiplexer_3_out), .sel(rom_1_data[6]));
  Multiplexer #(.width(8), .enable("false")) multiplexer_4 (
    .in0(inc8_1_in_2), .in1(controlled_buffer_1_out), .out(multiplexer_4_out), .sel(rom_1_data[7]));
  Multiplexer #(.width(8), .enable("false")) multiplexer_5 (
    .in0(regfile_1_ra), .in1(rom_addr), .out(multiplexer_5_out), .sel(rom_1_data[5]));
  Multiplexer #(.width(8), .enable("false")) multiplexer_6 (
    .in0(regfile_1_rb), .in1(rom_in), .out(multiplexer_6_out), .sel(rom_1_data[4]));
  Reg4 reg4_1 (
    .r(1'b1), .w(rom_1_data[3]), .en(1'b1), .clk(not_1_out), .rst(rst), .in_3__0(alu_1_zero),
    .out_3__0(reg4_1_out_3__0), .dbg_3__0(dbg_fr));
  ALU_2 alu_1 (
    .cin(1'b0), .op2(rom_1_data[2]), .op1(rom_1_data[1]), .op0(rom_1_data[0]), .overflow(alu_1_zero[3]),
    .sign(alu_1_zero[1]), .zero(alu_1_zero[0]), .carry(alu_1_zero[2]), .out(alu_1_out),
    .b(multiplexer_6_out), .a(multiplexer_5_out));
  assign controlled_buffer_1_out = and_6_out ? bus_in : 8'bz;  // Controlled_Buffer controlled_buffer_1
  or or_3 (r_w, dbg_ir[1], rom_1_data[9]);
  or or_4 (or_4_out, io_en, ram_en);
  Pull_Resistor pull_resistor_1 (.node(ram_addr));
  Multiplexer #(.width(8), .disabled(0), .enable("false")) multiplexer_7 (
    .in0(ram_addr), .in1(alu_1_out), .out(ram_addr), .sel(ram_en));
  assign bus_out = and_5_out ? regfile_1_ra : 8'bz;  // Controlled_Buffer controlled_buffer_2
  and and_5 (and_5_out, or_4_out, r_w);
  and and_6 (and_6_out, or_4_out, not_3_out);
  not not_3 (not_3_out, r_w);

  assign io_data_addr = dbg_ir[0];

  // Notes on the sheet:
  //   contents of rom_1 (hex, n*v repeats v):
  //   100 4110 5c0 6c0 1180 6034 8000 8c0 10c 10d 10e 10f 109 10a 10b d
endmodule

module LED8L (
  input  [7:0] in_1,
  output out_2,
  output out_3,
  output out_4,
  output out_5,
  output out_6,
  output out_7,
  output out_8,
  output out_9
);


  assign out_2 = in_1[7];
  assign out_3 = in_1[6];
  assign out_4 = in_1[5];
  assign out_5 = in_1[4];
  assign out_6 = in_1[3];
  assign out_7 = in_1[2];
  assign out_8 = in_1[1];
  assign out_9 = in_1[0];
endmodule

module LED8R (
  input  [7:0] in_1,
  output out_2,
  output out_3,
  output out_4,
  output out_5,
  output out_6,
  output out_7,
  output out_8,
  output out_9
);


  assign out_2 = in_1[7];
  assign out_3 = in_1[6];
  assign out_4 = in_1[5];
  assign out_5 = in_1[4];
  assign out_6 = in_1[3];
  assign out_7 = in_1[2];
  assign out_8 = in_1[1];
  assign out_9 = in_1[0];
endmodule

module LED4L (
  input  [3:0] in_1,
  output out_2,
  output out_3,
  output out_4,
  output out_5
);


  assign out_2 = in_1[3];
  assign out_3 = in_1[2];
  assign out_4 = in_1[1];
  assign out_5 = in_1[0];
endmodule

module RegFile (
  input  [7:0] rd,
  input  reg_w,
  input  selRD0,
  input  selRD1,
  input  clk,
  input  rst,
  input  selRA0,
  input  selRA1,
  input  selRB0,
  input  selRB1,
  output [7:0] dbgR3,
  output [7:0] dbgR2,
  output [7:0] dbgR1,
  output [7:0] dbgR0,
  output [7:0] ra,
  output [7:0] rb
);

  wire and_1_out, and_2_out, and_3_out, and_4_out, decoder_1_out0, decoder_1_out1, decoder_1_out2,
       decoder_1_out3;
  wire [7:0] reg8_1_out, reg8_2_out, reg8_3_out, reg8_4_out;

  Decoder #(.select(2), .enable("false")) decoder_1 (
    .out0(decoder_1_out0), .out1(decoder_1_out1), .out2(decoder_1_out2), .out3(decoder_1_out3),
    .sel({selRD1, selRD0}));
  and and_1 (and_1_out, reg_w, decoder_1_out3);
  Reg8 reg8_1 (.in(rd), .dbg(dbgR3), .r(1'b1), .w(and_1_out), .en(1'b1), .clk(clk), .rst(rst), .out(reg8_1_out));
  and and_2 (and_2_out, reg_w, decoder_1_out2);
  Reg8 reg8_2 (.in(rd), .dbg(dbgR2), .r(1'b1), .w(and_2_out), .en(1'b1), .clk(clk), .rst(rst), .out(reg8_2_out));
  Reg8 reg8_3 (.in(rd), .dbg(dbgR1), .r(1'b1), .w(and_3_out), .en(1'b1), .clk(clk), .rst(rst), .out(reg8_3_out));
  and and_3 (and_3_out, reg_w, decoder_1_out1);
  Reg8 reg8_4 (.in(rd), .dbg(dbgR0), .r(1'b1), .w(and_4_out), .en(1'b1), .clk(clk), .rst(rst), .out(reg8_4_out));
  and and_4 (and_4_out, reg_w, decoder_1_out0);
  Multiplexer #(.select(2), .width(8), .enable("false")) multiplexer_1 (
    .in0(reg8_4_out), .in1(reg8_3_out), .in2(reg8_2_out), .in3(reg8_1_out), .out(ra), .sel({selRA1, selRA0}));
  Multiplexer #(.select(2), .width(8), .enable("false")) multiplexer_2 (
    .in0(reg8_4_out), .in1(reg8_3_out), .in2(reg8_2_out), .in3(reg8_1_out), .out(rb), .sel({selRB1, selRB0}));
endmodule

module Reg4 (
  input  [3:0] in_3__0,
  input  r,
  input  w,
  input  en,
  input  clk,
  input  rst,
  output [3:0] dbg_3__0,
  output [3:0] out_3__0
);

  wire and_1_out, and_2_out, and_3_out, and_4_out, multiplexer_1_out, multiplexer_2_out, multiplexer_3_out,
       multiplexer_4_out, nand_1_out, nand_2_out, nand_3_out, nand_4_out;

  Multiplexer #(.enable("false")) multiplexer_1 (
    .in0(in_3__0[3]), .in1(dbg_3__0[3]), .out(multiplexer_1_out), .sel(nand_1_out));
  nand nand_1 (nand_1_out, w, en);
  D_Flip_Flop d_ff_1 (
    .clk(clk), .D(multiplexer_1_out), .Q(dbg_3__0[3]), .preset(1'b0), .en(en), .reset(rst));  // open: Qn
  assign out_3__0[3] = and_1_out ? dbg_3__0[3] : 1'bz;  // Controlled_Buffer controlled_buffer_1
  nand nand_2 (nand_2_out, w, en);
  and and_1 (and_1_out, r, en);
  Multiplexer #(.enable("false")) multiplexer_2 (
    .in0(in_3__0[2]), .in1(dbg_3__0[2]), .out(multiplexer_2_out), .sel(nand_2_out));
  D_Flip_Flop d_ff_2 (
    .clk(clk), .D(multiplexer_2_out), .Q(dbg_3__0[2]), .preset(1'b0), .en(en), .reset(rst));  // open: Qn
  assign out_3__0[2] = and_2_out ? dbg_3__0[2] : 1'bz;  // Controlled_Buffer controlled_buffer_2
  nand nand_3 (nand_3_out, w, en);
  and and_2 (and_2_out, r, en);
  Multiplexer #(.enable("false")) multiplexer_3 (
    .in0(in_3__0[1]), .in1(dbg_3__0[1]), .out(multiplexer_3_out), .sel(nand_3_out));
  D_Flip_Flop d_ff_3 (
    .clk(clk), .D(multiplexer_3_out), .Q(dbg_3__0[1]), .preset(1'b0), .en(en), .reset(rst));  // open: Qn
  assign out_3__0[1] = and_3_out ? dbg_3__0[1] : 1'bz;  // Controlled_Buffer controlled_buffer_3
  and and_3 (and_3_out, r, en);
  Multiplexer #(.enable("false")) multiplexer_4 (
    .in0(in_3__0[0]), .in1(dbg_3__0[0]), .out(multiplexer_4_out), .sel(nand_4_out));
  nand nand_4 (nand_4_out, w, en);
  assign out_3__0[0] = and_4_out ? dbg_3__0[0] : 1'bz;  // Controlled_Buffer controlled_buffer_4
  D_Flip_Flop d_ff_4 (
    .clk(clk), .D(multiplexer_4_out), .Q(dbg_3__0[0]), .preset(1'b0), .en(en), .reset(rst));  // open: Qn
  and and_4 (and_4_out, r, en);
endmodule

module Reg8 (
  input  [7:0] in,
  input  r,
  input  w,
  input  en,
  input  clk,
  input  rst,
  output [7:0] dbg,
  output [7:0] out
);

  wire and_1_out, and_2_out, and_3_out, and_4_out, and_5_out, and_6_out, and_7_out, and_8_out,
       multiplexer_1_out, multiplexer_2_out, multiplexer_3_out, multiplexer_4_out, multiplexer_5_out,
       multiplexer_6_out, multiplexer_7_out, multiplexer_8_out, nand_1_out, nand_2_out, nand_3_out,
       nand_4_out, nand_5_out, nand_6_out, nand_7_out, nand_8_out;

  nand nand_1 (nand_1_out, w, en);
  Multiplexer #(.enable("false")) multiplexer_1 (.in0(in[7]), .in1(dbg[7]), .out(multiplexer_1_out), .sel(nand_1_out));
  D_Flip_Flop d_ff_1 (.clk(clk), .D(multiplexer_1_out), .Q(dbg[7]), .preset(1'b0), .en(en), .reset(rst));  // open: Qn
  assign out[7] = and_1_out ? dbg[7] : 1'bz;  // Controlled_Buffer controlled_buffer_1
  nand nand_2 (nand_2_out, w, en);
  and and_1 (and_1_out, r, en);
  Multiplexer #(.enable("false")) multiplexer_2 (.in0(in[6]), .in1(dbg[6]), .out(multiplexer_2_out), .sel(nand_2_out));
  D_Flip_Flop d_ff_2 (.clk(clk), .D(multiplexer_2_out), .Q(dbg[6]), .preset(1'b0), .en(en), .reset(rst));  // open: Qn
  assign out[6] = and_2_out ? dbg[6] : 1'bz;  // Controlled_Buffer controlled_buffer_2
  and and_2 (and_2_out, r, en);
  Multiplexer #(.enable("false")) multiplexer_3 (.in0(in[5]), .in1(dbg[5]), .out(multiplexer_3_out), .sel(nand_3_out));
  nand nand_3 (nand_3_out, w, en);
  D_Flip_Flop d_ff_3 (.clk(clk), .D(multiplexer_3_out), .Q(dbg[5]), .preset(1'b0), .en(en), .reset(rst));  // open: Qn
  assign out[5] = and_3_out ? dbg[5] : 1'bz;  // Controlled_Buffer controlled_buffer_3
  and and_3 (and_3_out, r, en);
  Multiplexer #(.enable("false")) multiplexer_4 (.in0(in[4]), .in1(dbg[4]), .out(multiplexer_4_out), .sel(nand_4_out));
  nand nand_4 (nand_4_out, w, en);
  D_Flip_Flop d_ff_4 (.clk(clk), .D(multiplexer_4_out), .Q(dbg[4]), .preset(1'b0), .en(en), .reset(rst));  // open: Qn
  assign out[4] = and_4_out ? dbg[4] : 1'bz;  // Controlled_Buffer controlled_buffer_4
  and and_4 (and_4_out, r, en);
  Multiplexer #(.enable("false")) multiplexer_5 (.in0(in[3]), .in1(dbg[3]), .out(multiplexer_5_out), .sel(nand_5_out));
  nand nand_5 (nand_5_out, w, en);
  D_Flip_Flop d_ff_5 (.clk(clk), .D(multiplexer_5_out), .Q(dbg[3]), .preset(1'b0), .en(en), .reset(rst));  // open: Qn
  assign out[3] = and_5_out ? dbg[3] : 1'bz;  // Controlled_Buffer controlled_buffer_5
  and and_5 (and_5_out, r, en);
  Multiplexer #(.enable("false")) multiplexer_6 (.in0(in[2]), .in1(dbg[2]), .out(multiplexer_6_out), .sel(nand_6_out));
  nand nand_6 (nand_6_out, w, en);
  D_Flip_Flop d_ff_6 (.clk(clk), .D(multiplexer_6_out), .Q(dbg[2]), .preset(1'b0), .en(en), .reset(rst));  // open: Qn
  assign out[2] = and_6_out ? dbg[2] : 1'bz;  // Controlled_Buffer controlled_buffer_6
  and and_6 (and_6_out, r, en);
  Multiplexer #(.enable("false")) multiplexer_7 (.in0(in[1]), .in1(dbg[1]), .out(multiplexer_7_out), .sel(nand_7_out));
  nand nand_7 (nand_7_out, w, en);
  D_Flip_Flop d_ff_7 (.clk(clk), .D(multiplexer_7_out), .Q(dbg[1]), .preset(1'b0), .en(en), .reset(rst));  // open: Qn
  and and_7 (and_7_out, r, en);
  Multiplexer #(.enable("false")) multiplexer_8 (.in0(in[0]), .in1(dbg[0]), .out(multiplexer_8_out), .sel(nand_8_out));
  assign out[1] = and_7_out ? dbg[1] : 1'bz;  // Controlled_Buffer controlled_buffer_7
  nand nand_8 (nand_8_out, w, en);
  D_Flip_Flop d_ff_8 (.clk(clk), .D(multiplexer_8_out), .Q(dbg[0]), .preset(1'b0), .en(en), .reset(rst));  // open: Qn
  assign out[0] = and_8_out ? dbg[0] : 1'bz;  // Controlled_Buffer controlled_buffer_8
  and and_8 (and_8_out, r, en);
endmodule

module ALU_2 (
  input  [7:0] a,
  input  [7:0] b,
  input  op2,
  input  op1,
  input  op0,
  input  cin,
  output [7:0] out,
  output overflow,
  output carry,
  output sign,
  output zero
);

  wire addsub8_1_carry, addsub8_1_out0, addsub8_1_out1, addsub8_1_out2, addsub8_1_out3, addsub8_1_out4,
       addsub8_1_out5, addsub8_1_out6, addsub8_1_out7, addsub8_1_overflow, ander8_1_out0, ander8_1_out1,
       ander8_1_out2, ander8_1_out3, ander8_1_out4, ander8_1_out5, ander8_1_out6, ander8_1_out7,
       leftshifter8_1_cout, leftshifter8_1_out0, leftshifter8_1_out1, leftshifter8_1_out2,
       leftshifter8_1_out3, leftshifter8_1_out4, leftshifter8_1_out6, leftshifter8_1_out6_2,
       leftshifter8_1_out7, nor_2_out, or_1_out, orer8_1_out0, orer8_1_out1, orer8_1_out2, orer8_1_out3,
       orer8_1_out4, orer8_1_out5, orer8_1_out6, orer8_1_out7, rightshifter8_1_cout, rightshifter8_1_out0,
       rightshifter8_1_out1, rightshifter8_1_out2, rightshifter8_1_out3, rightshifter8_1_out4,
       rightshifter8_1_out6, rightshifter8_1_out6_2, rightshifter8_1_out7, xorer8_1_out0, xorer8_1_out1,
       xorer8_1_out2, xorer8_1_out3, xorer8_1_out4, xorer8_1_out5, xorer8_1_out6, xorer8_1_out7;
  wire [7:0] decoder_1_out0;

  Ander8 ander8_1 (
    .a0(a[0]), .b0(b[0]), .a1(a[1]), .b1(b[1]), .a2(a[2]), .b2(b[2]), .a3(a[3]), .b3(b[3]), .a4(a[4]),
    .b4(b[4]), .a5(a[5]), .b5(b[5]), .a6(a[6]), .b6(b[6]), .a7(a[7]), .b7(b[7]), .out0(ander8_1_out0),
    .out1(ander8_1_out1), .out2(ander8_1_out2), .out3(ander8_1_out3), .out4(ander8_1_out4),
    .out5(ander8_1_out5), .out6(ander8_1_out6), .out7(ander8_1_out7));
  Orer8 orer8_1 (
    .a0(a[0]), .b0(b[0]), .a1(a[1]), .b1(b[1]), .a2(a[2]), .b2(b[2]), .a3(a[3]), .b3(b[3]), .a4(a[4]),
    .b4(b[4]), .a5(a[5]), .b5(b[5]), .a6(a[6]), .b6(b[6]), .a7(a[7]), .b7(b[7]), .out0(orer8_1_out0),
    .out1(orer8_1_out1), .out2(orer8_1_out2), .out3(orer8_1_out3), .out4(orer8_1_out4), .out5(orer8_1_out5),
    .out6(orer8_1_out6), .out7(orer8_1_out7));
  Xorer8 xorer8_1 (
    .a0(a[0]), .b0(b[0]), .a1(a[1]), .b1(b[1]), .a2(a[2]), .b2(b[2]), .a3(a[3]), .b3(b[3]), .a4(a[4]),
    .b4(b[4]), .a5(a[5]), .b5(b[5]), .a6(a[6]), .b6(b[6]), .a7(a[7]), .b7(b[7]), .out0(xorer8_1_out0),
    .out1(xorer8_1_out1), .out2(xorer8_1_out2), .out3(xorer8_1_out3), .out4(xorer8_1_out4),
    .out5(xorer8_1_out5), .out6(xorer8_1_out6), .out7(xorer8_1_out7));
  AddSub8 addsub8_1 (
    .cin(cin), .a0(a[0]), .b0(b[0]), .a1(a[1]), .b1(b[1]), .a2(a[2]), .b2(b[2]), .a3(a[3]), .b3(b[3]),
    .a4(a[4]), .b4(b[4]), .a5(a[5]), .b5(b[5]), .a6(a[6]), .b6(b[6]), .a7(a[7]), .b7(b[7]),
    .out0(addsub8_1_out0), .out1(addsub8_1_out1), .out2(addsub8_1_out2), .out3(addsub8_1_out3),
    .out4(addsub8_1_out4), .out5(addsub8_1_out5), .out6(addsub8_1_out6), .out7(addsub8_1_out7),
    .carry(addsub8_1_carry), .sub(decoder_1_out0[5]), .overflow(addsub8_1_overflow));
  LeftShifter8 leftshifter8_1 (
    .cin(cin), .in0(b[0]), .in1(b[1]), .in2(b[2]), .in3(b[3]), .in4(b[4]), .in5(b[5]), .in6(b[6]),
    .in7(b[7]), .out0(leftshifter8_1_out0), .out1(leftshifter8_1_out1), .out2(leftshifter8_1_out2),
    .out3(leftshifter8_1_out3), .out4(leftshifter8_1_out4), .out6(leftshifter8_1_out6),
    .out6_2(leftshifter8_1_out6_2), .out7(leftshifter8_1_out7), .cout(leftshifter8_1_cout));
  RightShifter8 rightshifter8_1 (
    .in0(b[0]), .in1(b[1]), .in2(b[2]), .in3(b[3]), .in4(b[4]), .in5(b[5]), .in6(b[6]), .in7(b[7]),
    .cin(cin), .cout(rightshifter8_1_cout), .out0(rightshifter8_1_out0), .out1(rightshifter8_1_out1),
    .out2(rightshifter8_1_out2), .out3(rightshifter8_1_out3), .out4(rightshifter8_1_out4),
    .out6(rightshifter8_1_out6), .out6_2(rightshifter8_1_out6_2), .out7(rightshifter8_1_out7));
  Decoder #(.select(3), .enable("false")) decoder_1 (
    .out0(decoder_1_out0[0]), .out1(decoder_1_out0[1]), .out2(decoder_1_out0[2]), .out3(decoder_1_out0[3]),
    .out4(decoder_1_out0[4]), .out5(decoder_1_out0[5]), .out6(decoder_1_out0[6]), .out7(decoder_1_out0[7]),
    .sel({op2, op1, op0}));
  Enabler8 enabler8_1 (
    .in0(b[0]), .in1(b[1]), .in2(b[2]), .in3(b[3]), .in4(b[4]), .in5(b[5]), .in6(b[6]), .in7(b[7]),
    .enable(decoder_1_out0[0]), .out0(out[0]), .out1(out[1]), .out2(out[2]), .out3(out[3]), .out4(out[4]),
    .out6(out[5]), .out6_2(out[6]), .out7(out[7]));
  Enabler8 enabler8_2 (
    .in0(ander8_1_out0), .in1(ander8_1_out1), .in2(ander8_1_out2), .in3(ander8_1_out3), .in4(ander8_1_out4),
    .in5(ander8_1_out5), .in6(ander8_1_out6), .in7(ander8_1_out7), .enable(decoder_1_out0[1]), .out0(out[0]),
    .out1(out[1]), .out2(out[2]), .out3(out[3]), .out4(out[4]), .out6(out[5]), .out6_2(out[6]), .out7(out[7]));
  Enabler8 enabler8_3 (
    .in0(orer8_1_out0), .in1(orer8_1_out1), .in2(orer8_1_out2), .in3(orer8_1_out3), .in4(orer8_1_out4),
    .in5(orer8_1_out5), .in6(orer8_1_out6), .in7(orer8_1_out7), .enable(decoder_1_out0[2]), .out0(out[0]),
    .out1(out[1]), .out2(out[2]), .out3(out[3]), .out4(out[4]), .out6(out[5]), .out6_2(out[6]), .out7(out[7]));
  Enabler8 enabler8_4 (
    .in0(xorer8_1_out0), .in1(xorer8_1_out1), .in2(xorer8_1_out2), .in3(xorer8_1_out3), .in4(xorer8_1_out4),
    .in5(xorer8_1_out5), .in6(xorer8_1_out6), .in7(xorer8_1_out7), .enable(decoder_1_out0[3]), .out0(out[0]),
    .out1(out[1]), .out2(out[2]), .out3(out[3]), .out4(out[4]), .out6(out[5]), .out6_2(out[6]), .out7(out[7]));
  or or_1 (or_1_out, decoder_1_out0[4], decoder_1_out0[5]);
  Enabler8 enabler8_5 (
    .in0(addsub8_1_out0), .in1(addsub8_1_out1), .in2(addsub8_1_out2), .in3(addsub8_1_out3),
    .in4(addsub8_1_out4), .in5(addsub8_1_out5), .in6(addsub8_1_out6), .in7(addsub8_1_out7),
    .enable(or_1_out), .out0(out[0]), .out1(out[1]), .out2(out[2]), .out3(out[3]), .out4(out[4]),
    .out6(out[5]), .out6_2(out[6]), .out7(out[7]));
  Enabler8 enabler8_6 (
    .in0(leftshifter8_1_out0), .in1(leftshifter8_1_out1), .in2(leftshifter8_1_out2),
    .in3(leftshifter8_1_out3), .in4(leftshifter8_1_out4), .in5(leftshifter8_1_out6),
    .in6(leftshifter8_1_out6_2), .in7(leftshifter8_1_out7), .enable(decoder_1_out0[6]), .out0(out[0]),
    .out1(out[1]), .out2(out[2]), .out3(out[3]), .out4(out[4]), .out6(out[5]), .out6_2(out[6]), .out7(out[7]));
  Enabler8 enabler8_7 (
    .in0(rightshifter8_1_out0), .in1(rightshifter8_1_out1), .in2(rightshifter8_1_out2),
    .in3(rightshifter8_1_out3), .in4(rightshifter8_1_out4), .in5(rightshifter8_1_out6),
    .in6(rightshifter8_1_out6_2), .in7(rightshifter8_1_out7), .enable(decoder_1_out0[7]), .out0(out[0]),
    .out1(out[1]), .out2(out[2]), .out3(out[3]), .out4(out[4]), .out6(out[5]), .out6_2(out[6]), .out7(out[7]));
  nor nor_1 (zero, out[7], out[6], out[5], out[4], out[3], out[2], out[1], out[0]);
  Multiplexer #(.enable("false")) multiplexer_1 (.in0(1'b0), .in1(addsub8_1_overflow), .out(overflow), .sel(or_1_out));
  nor nor_2 (nor_2_out, or_1_out, decoder_1_out0[6], decoder_1_out0[7]);
  assign carry = nor_2_out ? 1'b0 : 1'bz;  // Controlled_Buffer controlled_buffer_1
  assign carry = or_1_out ? addsub8_1_carry : 1'bz;  // Controlled_Buffer controlled_buffer_2
  assign carry = decoder_1_out0[6] ? leftshifter8_1_cout : 1'bz;  // Controlled_Buffer controlled_buffer_3
  assign carry = decoder_1_out0[7] ? rightshifter8_1_cout : 1'bz;  // Controlled_Buffer controlled_buffer_4

  assign sign = out[7];
endmodule

module Enabler8 (
  input  enable,
  input  in0,
  input  in1,
  input  in2,
  input  in3,
  input  in4,
  input  in5,
  input  in6,
  input  in7,
  output out0,
  output out1,
  output out2,
  output out3,
  output out4,
  output out6,
  output out6_2,
  output out7
);

  assign out0 = enable ? in0 : 1'bz;  // Controlled_Buffer controlled_buffer_1
  assign out1 = enable ? in1 : 1'bz;  // Controlled_Buffer controlled_buffer_2
  assign out2 = enable ? in2 : 1'bz;  // Controlled_Buffer controlled_buffer_3
  assign out3 = enable ? in3 : 1'bz;  // Controlled_Buffer controlled_buffer_4
  assign out4 = enable ? in4 : 1'bz;  // Controlled_Buffer controlled_buffer_5
  assign out6 = enable ? in5 : 1'bz;  // Controlled_Buffer controlled_buffer_6
  assign out6_2 = enable ? in6 : 1'bz;  // Controlled_Buffer controlled_buffer_7
  assign out7 = enable ? in7 : 1'bz;  // Controlled_Buffer controlled_buffer_8
endmodule

module LeftShifter8 (
  input  cin,
  input  in0,
  input  in1,
  input  in2,
  input  in3,
  input  in4,
  input  in5,
  input  in6,
  input  in7,
  output out0,
  output out1,
  output out2,
  output out3,
  output out4,
  output out6,
  output out6_2,
  output out7,
  output cout
);


  assign cout = in7;
  assign out0 = cin;
  assign out1 = in0;
  assign out2 = in1;
  assign out3 = in2;
  assign out4 = in3;
  assign out6 = in4;
  assign out6_2 = in5;
  assign out7 = in6;
endmodule

module RightShifter8 (
  input  in0,
  input  in1,
  input  in2,
  input  in3,
  input  in4,
  input  in5,
  input  in6,
  input  in7,
  input  cin,
  output cout,
  output out0,
  output out1,
  output out2,
  output out3,
  output out4,
  output out6,
  output out6_2,
  output out7
);


  assign cout = in0;
  assign out0 = in1;
  assign out1 = in2;
  assign out2 = in3;
  assign out3 = in4;
  assign out4 = in5;
  assign out6 = in6;
  assign out6_2 = in7;
  assign out7 = cin;
endmodule

module Notter8 (
  input  in0,
  input  in1,
  input  in2,
  input  in3,
  input  in4,
  input  in5,
  input  in6,
  input  in7,
  output out0,
  output out1,
  output out2,
  output out3,
  output out4,
  output out6,
  output out6_2,
  output out7
);

  not not_1 (out0, in0);
  not not_2 (out1, in1);
  not not_3 (out2, in2);
  not not_4 (out3, in3);
  not not_5 (out4, in4);
  not not_6 (out6, in5);
  not not_7 (out6_2, in6);
  not not_8 (out7, in7);
endmodule

module Ander8 (
  input  a0,
  input  b0,
  input  a1,
  input  b1,
  input  a2,
  input  b2,
  input  a3,
  input  b3,
  input  a4,
  input  b4,
  input  a5,
  input  b5,
  input  a6,
  input  b6,
  input  a7,
  input  b7,
  output out0,
  output out1,
  output out2,
  output out3,
  output out4,
  output out5,
  output out6,
  output out7
);

  and and_1 (out0, a0, b0);
  and and_2 (out1, a1, b1);
  and and_3 (out2, a2, b2);
  and and_4 (out3, a3, b3);
  and and_5 (out4, a4, b4);
  and and_6 (out5, a5, b5);
  and and_7 (out6, a6, b6);
  and and_8 (out7, a7, b7);
endmodule

module Orer8 (
  input  a0,
  input  b0,
  input  a1,
  input  b1,
  input  a2,
  input  b2,
  input  a3,
  input  b3,
  input  a4,
  input  b4,
  input  a5,
  input  b5,
  input  a6,
  input  b6,
  input  a7,
  input  b7,
  output out0,
  output out1,
  output out2,
  output out3,
  output out4,
  output out5,
  output out6,
  output out7
);

  or or_1 (out0, a0, b0);
  or or_2 (out1, a1, b1);
  or or_3 (out2, a2, b2);
  or or_4 (out3, a3, b3);
  or or_5 (out4, a4, b4);
  or or_6 (out5, a5, b5);
  or or_7 (out6, a6, b6);
  or or_8 (out7, a7, b7);
endmodule

module Xorer8 (
  input  a0,
  input  b0,
  input  a1,
  input  b1,
  input  a2,
  input  b2,
  input  a3,
  input  b3,
  input  a4,
  input  b4,
  input  a5,
  input  b5,
  input  a6,
  input  b6,
  input  a7,
  input  b7,
  output out0,
  output out1,
  output out2,
  output out3,
  output out4,
  output out5,
  output out6,
  output out7
);

  xor xor_1 (out0, a0, b0);
  xor xor_2 (out1, a1, b1);
  xor xor_3 (out2, a2, b2);
  xor xor_4 (out3, a3, b3);
  xor xor_5 (out4, a4, b4);
  xor xor_6 (out5, a5, b5);
  xor xor_7 (out6, a6, b6);
  xor xor_8 (out7, a7, b7);
endmodule

module FullAdder (
  input  a,
  input  b,
  input  cin,
  output sum,
  output cout
);

  wire and_1_out, and_2_out, xor_1_out;

  xor xor_1 (xor_1_out, a, b);
  xor xor_2 (sum, xor_1_out, cin);
  and and_1 (and_1_out, xor_1_out, cin);
  and and_2 (and_2_out, a, b);
  or or_1 (cout, and_1_out, and_2_out);
endmodule

module Adder8 (
  input  cin,
  input  a0,
  input  b0,
  input  a1,
  input  b1,
  input  a2,
  input  b2,
  input  a3,
  input  b3,
  input  a4,
  input  b4,
  input  a5,
  input  b5,
  input  a6,
  input  b6,
  input  a7,
  input  b7,
  output out0,
  output out1,
  output out2,
  output out3,
  output out4,
  output out5,
  output out6,
  output out7,
  output ovcarry,
  output cout
);

  wire fulladder_1_cout, fulladder_2_cout, fulladder_3_cout, fulladder_4_cout, fulladder_5_cout,
       fulladder_6_cout;

  FullAdder fulladder_1 (.a(a0), .b(b0), .cin(cin), .sum(out0), .cout(fulladder_1_cout));
  FullAdder fulladder_2 (.a(a1), .b(b1), .cin(fulladder_1_cout), .sum(out1), .cout(fulladder_2_cout));
  FullAdder fulladder_3 (.a(a2), .b(b2), .cin(fulladder_2_cout), .sum(out2), .cout(fulladder_3_cout));
  FullAdder fulladder_4 (.a(a3), .b(b3), .cin(fulladder_3_cout), .sum(out3), .cout(fulladder_4_cout));
  FullAdder fulladder_5 (.a(a4), .b(b4), .cin(fulladder_4_cout), .sum(out4), .cout(fulladder_5_cout));
  FullAdder fulladder_6 (.a(a5), .b(b5), .cin(fulladder_5_cout), .sum(out5), .cout(fulladder_6_cout));
  FullAdder fulladder_7 (.a(a6), .b(b6), .cin(fulladder_6_cout), .sum(out6), .cout(ovcarry));
  FullAdder fulladder_8 (.a(a7), .b(b7), .cin(ovcarry), .sum(out7), .cout(cout));
endmodule

module AddSub8 (
  input  sub,
  input  a0,
  input  b0,
  input  a1,
  input  b1,
  input  a2,
  input  b2,
  input  a3,
  input  b3,
  input  a4,
  input  b4,
  input  a5,
  input  b5,
  input  a6,
  input  b6,
  input  a7,
  input  b7,
  input  cin,
  output carry,
  output overflow,
  output out7,
  output out6,
  output out5,
  output out4,
  output out3,
  output out2,
  output out1,
  output out0
);

  wire adder8_1_cout, adder8_1_ovcarry, xor_3_out, xor_4_out, xor_5_out, xor_6_out, xor_7_out, xor_8_out,
       xor_9_out, xor_10_out, xor_11_out;

  xor xor_1 (carry, sub, adder8_1_cout);
  xor xor_2 (overflow, adder8_1_ovcarry, adder8_1_cout);
  xor xor_3 (xor_3_out, sub, b0);
  xor xor_4 (xor_4_out, sub, b1);
  xor xor_5 (xor_5_out, sub, b2);
  xor xor_6 (xor_6_out, sub, b3);
  xor xor_7 (xor_7_out, sub, b4);
  xor xor_8 (xor_8_out, sub, b5);
  xor xor_9 (xor_9_out, sub, b6);
  xor xor_10 (xor_10_out, sub, b7);
  Adder8 adder8_1 (
    .cin(xor_11_out), .a0(a0), .b0(xor_3_out), .a1(a1), .b1(xor_4_out), .a2(a2), .b2(xor_5_out), .a3(a3),
    .b3(xor_6_out), .a4(a4), .b4(xor_7_out), .a5(a5), .b5(xor_8_out), .a6(a6), .b6(xor_9_out), .a7(a7),
    .b7(xor_10_out), .out0(out0), .out1(out1), .out2(out2), .out3(out3), .out4(out4), .out5(out5),
    .out6(out6), .out7(out7), .ovcarry(adder8_1_ovcarry), .cout(adder8_1_cout));
  xor xor_11 (xor_11_out, sub, cin);
endmodule

module Inc8 (
  input  [7:0] in,
  output [7:0] in_2
);

  wire incrementer4_1_cout;

  Incrementer4 incrementer4_1 (
    .cin(1'b1), .in0(in[0]), .in1(in[1]), .in2(in[2]), .in3(in[3]), .out0(in_2[0]), .out1(in_2[1]),
    .out2(in_2[2]), .out3(in_2[3]), .cout(incrementer4_1_cout));
  Incrementer4 incrementer4_2 (
    .cin(incrementer4_1_cout), .in0(in[4]), .in1(in[5]), .in2(in[6]), .in3(in[7]), .out0(in_2[4]),
    .out1(in_2[5]), .out2(in_2[6]), .out3(in_2[7]));  // open: cout
endmodule

module Incrementer4 (
  input  cin,
  input  in0,
  input  in1,
  input  in2,
  input  in3,
  output out0,
  output out1,
  output out2,
  output out3,
  output cout
);

  wire and_1_out, and_2_out, and_3_out;

  and and_1 (and_1_out, in0, cin);
  and and_2 (and_2_out, in1, and_1_out);
  and and_3 (and_3_out, in2, and_2_out);
  and and_4 (cout, in3, and_3_out);
  xor xor_1 (out0, cin, in0);
  xor xor_2 (out1, and_1_out, in1);
  xor xor_3 (out2, and_2_out, in2);
  xor xor_4 (out3, and_3_out, in3);
endmodule

module BranchChecker (
  input  zero,
  input  sign,
  input  carry,
  input  overflow,
  input  op2,
  input  op1,
  input  op0,
  output result
);

  wire and_1_out, and_2_out, and_3_out, and_4_out, and_5_out, and_6_out, and_7_out, decoder_1_out0,
       decoder_1_out1, decoder_1_out2, decoder_1_out3, decoder_1_out4, decoder_1_out5, decoder_1_out6,
       decoder_1_out7, or_1_out, or_2_out, xor_1_out;

  Decoder #(.select(3), .enable("false")) decoder_1 (
    .out0(decoder_1_out0), .out1(decoder_1_out1), .out2(decoder_1_out2), .out3(decoder_1_out3),
    .out4(decoder_1_out4), .out5(decoder_1_out5), .out6(decoder_1_out6), .out7(decoder_1_out7),
    .sel({op2, op1, op0}));
  or or_1 (or_1_out, zero, xor_1_out);
  or or_2 (or_2_out, carry, zero);
  xor xor_1 (xor_1_out, overflow, sign);
  and and_1 (and_1_out, decoder_1_out1, zero);
  and and_2 (and_2_out, decoder_1_out2, sign);
  and and_3 (and_3_out, decoder_1_out3, overflow);
  and and_4 (and_4_out, decoder_1_out4, carry);
  and and_5 (and_5_out, decoder_1_out5, or_2_out);
  and and_6 (and_6_out, decoder_1_out6, xor_1_out);
  and and_7 (and_7_out, decoder_1_out7, or_1_out);
  or or_3 (result, and_7_out, and_6_out, and_5_out, and_4_out, and_3_out, and_2_out, and_1_out, decoder_1_out0);
endmodule
