// Logisim project cmos.circ as structural Verilog: 13 circuits, main circuit PMOS
module PMOS (
  input  G,
  input  S,
  output D
);

  Transistor transistor_1 (.in(S), .out(D), .gate(G));

  // Notes on the sheet:
  //   90 - 180 ns
  //   14 - 40 ns
  //   https://www.reichelt.de/MOSFET-Transistoren-IXYS/FDV-304P/3/index.html?ACTION=3&LA=2&ARTICLE=219238&GROUPID=4350&artnr=FDV+304P&trstct=pol_11
endmodule

module NMOS (
  input  G,
  input  S,
  output D
);

  Transistor #(.\type ("n")) transistor_1 (.in(S), .out(D), .gate(G));

  // Notes on the sheet:
  //   30 - 55 ns
  //   11.5 - 24 ns
  //   https://www.reichelt.de/MOSFET-Transistoren-IXYS/FDV-303N/3/index.html?ACTION=3&LA=2&ARTICLE=219237&GROUPID=4350&artnr=FDV+303N&trstct=pol_10
endmodule

module AOI2 (
  input  A,
  input  B,
  input  C,
  input  D,
  output nZ
);

  wire nmos_1_d, nmos_3_d, pmos_1_d;

  PMOS pmos_1 (.G(A), .S(1'b1), .D(pmos_1_d));
  NMOS nmos_1 (.G(A), .S(1'b0), .D(nmos_1_d));
  PMOS pmos_2 (.G(B), .S(1'b1), .D(pmos_1_d));
  NMOS nmos_2 (.G(B), .S(nmos_1_d), .D(nZ));
  PMOS pmos_3 (.G(C), .S(pmos_1_d), .D(nZ));
  NMOS nmos_3 (.G(C), .S(1'b0), .D(nmos_3_d));
  PMOS pmos_4 (.G(D), .S(pmos_1_d), .D(nZ));
  NMOS nmos_4 (.G(D), .S(nmos_3_d), .D(nZ));
endmodule

module NOT1 (
  input  A,
  output Z
);

  PMOS pmos_1 (.G(A), .S(1'b1), .D(Z));
  NMOS nmos_1 (.G(A), .S(1'b0), .D(Z));
endmodule

module NAND2 (
  input  A,
  input  B,
  output Z
);

  wire nmos_1_d;

  PMOS pmos_1 (.G(A), .S(1'b1), .D(Z));
  NMOS nmos_1 (.G(A), .S(1'b0), .D(nmos_1_d));
  PMOS pmos_2 (.G(B), .S(1'b1), .D(Z));
  NMOS nmos_2 (.G(B), .S(nmos_1_d), .D(Z));
endmodule

module NAND3 (
  input  A,
  input  B,
  input  C,
  output Z
);

  wire nmos_1_d, nmos_2_d;

  PMOS pmos_1 (.G(A), .S(1'b1), .D(Z));
  NMOS nmos_1 (.G(A), .S(1'b0), .D(nmos_1_d));
  PMOS pmos_2 (.G(B), .S(1'b1), .D(Z));
  NMOS nmos_2 (.G(B), .S(nmos_1_d), .D(nmos_2_d));
  PMOS pmos_3 (.G(C), .S(1'b1), .D(Z));
  NMOS nmos_3 (.G(C), .S(nmos_2_d), .D(Z));
endmodule

module NAND4 (
  input  A,
  input  B,
  input  C,
  input  D,
  output Z
);

  wire nmos_1_d, nmos_2_d, nmos_3_d;

  PMOS pmos_1 (.G(A), .S(1'b1), .D(Z));
  NMOS nmos_1 (.G(A), .S(1'b0), .D(nmos_1_d));
  PMOS pmos_2 (.G(B), .S(1'b1), .D(Z));
  NMOS nmos_2 (.G(B), .S(nmos_1_d), .D(nmos_2_d));
  PMOS pmos_3 (.G(C), .S(1'b1), .D(Z));
  NMOS nmos_3 (.G(C), .S(nmos_2_d), .D(nmos_3_d));
  PMOS pmos_4 (.G(D), .S(1'b1), .D(Z));
  NMOS nmos_4 (.G(D), .S(nmos_3_d), .D(Z));
endmodule

module NOR2 (
  input  A,
  input  B,
  output Z
);

  wire pmos_1_d;

  PMOS pmos_1 (.G(A), .S(1'b1), .D(pmos_1_d));
  NMOS nmos_1 (.G(A), .S(1'b0), .D(Z));
  PMOS pmos_2 (.G(B), .S(pmos_1_d), .D(Z));
  NMOS nmos_2 (.G(B), .S(1'b0), .D(Z));
endmodule

module NOR3 (
  input  A,
  input  B,
  input  C,
  output Z
);

  wire pmos_1_d, pmos_2_d;

  PMOS pmos_1 (.G(A), .S(1'b1), .D(pmos_1_d));
  NMOS nmos_1 (.G(A), .S(1'b0), .D(Z));
  PMOS pmos_2 (.G(B), .S(pmos_1_d), .D(pmos_2_d));
  NMOS nmos_2 (.G(B), .S(1'b0), .D(Z));
  PMOS pmos_3 (.G(C), .S(pmos_2_d), .D(Z));
  NMOS nmos_3 (.G(C), .S(1'b0), .D(Z));
endmodule

module NOR4 (
  input  A,
  input  B,
  input  C,
  input  D,
  output Z
);

  wire pmos_1_d, pmos_2_d, pmos_3_d;

  PMOS pmos_1 (.G(A), .S(1'b1), .D(pmos_1_d));
  NMOS nmos_1 (.G(A), .S(1'b0), .D(Z));
  PMOS pmos_2 (.G(B), .S(pmos_1_d), .D(pmos_2_d));
  NMOS nmos_2 (.G(B), .S(1'b0), .D(Z));
  PMOS pmos_3 (.G(C), .S(pmos_2_d), .D(pmos_3_d));
  NMOS nmos_3 (.G(C), .S(1'b0), .D(Z));
  PMOS pmos_4 (.G(D), .S(pmos_3_d), .D(Z));
  NMOS nmos_4 (.G(D), .S(1'b0), .D(Z));
endmodule

module EN1 (
  input  en,
  input  A,
  output Z
);

  wire pmos_1_d;

  PMOS pmos_1 (.G(en), .S(1'b1), .D(pmos_1_d));
  NMOS nmos_1 (.G(en), .S(1'b0), .D(pmos_1_d));
  PMOS pmos_2 (.G(pmos_1_d), .S(A), .D(Z));
  NMOS nmos_2 (.G(en), .S(A), .D(Z));
endmodule

module MUX2 (
  input  sel,
  input  A,
  input  B,
  output Z
);

  wire pmos_1_d;

  PMOS pmos_1 (.G(sel), .S(1'b1), .D(pmos_1_d));
  NMOS nmos_1 (.G(sel), .S(1'b0), .D(pmos_1_d));
  NMOS nmos_2 (.G(pmos_1_d), .S(A), .D(Z));
  PMOS pmos_2 (.G(sel), .S(A), .D(Z));
  PMOS pmos_3 (.G(pmos_1_d), .S(B), .D(Z));
  NMOS nmos_3 (.G(sel), .S(B), .D(Z));
endmodule

module XOR2 (
  input  A,
  input  B,
  output Z
);

  wire not_1_out;

  MUX2 mux2_1 (.A(B), .B(not_1_out), .sel(A), .Z(Z));
  not not_1 (not_1_out, B);
endmodule
